// Logisim project 8-BIT CPU IMPROVED orig.circ as structural Verilog: 42 circuits, main circuit CPU
module MAIN (
  input  START,
  input  RESET
);

  wire clock_1_out, cpu_1_i_o_clk, cpu_1_i_o_clr, cpu_1_i_o_r, cpu_1_i_o_w, cpu_1_mem_r_w, cpu_1_ram_r_w,
       cpu_1_w_clk, i_o_ctrl_1_i_o_clk_in, i_o_ctrl_1_i_o_clk_out, lcd_video_1_p1, lcd_video_1_p2,
       lcd_video_1_p3, lcd_video_1_p4, lcd_video_1_p5, lcd_video_1_p6, n2d_engine_1_p4, n2d_engine_1_p5,
       n2d_engine_1_p6, or_1_out;
  wire [2:0] cpu_1_rom_mem_rom;
  wire [6:0] i_o_ctrl_1_i_o_dev_out, keyboard_1_data;
  wire [7:0] cpu_1_address, cpu_1_d_bus_out, cpu_1_i_o_out, i_o_ctrl_1_i_o_out, multiplexer_1_out,
       n2d_engine_1_p1, n2d_engine_1_p3, n2d_engine_1_p7, ram_2_data_out, rom_1_data_out;

  I_O_CTRL i_o_ctrl_1 (
    .I_O_CLK(cpu_1_i_o_clk), .I_O_R(cpu_1_i_o_r), .I_O_IN(cpu_1_i_o_out), .I_O_OUT(i_o_ctrl_1_i_o_out),
    .I_O_W(cpu_1_i_o_w), .I_O_CLK_IN(i_o_ctrl_1_i_o_clk_in), .I_O_DEV_OUT(i_o_ctrl_1_i_o_dev_out),
    .I_O_DEV_IN(keyboard_1_data), .I_O_CLK_OUT(i_o_ctrl_1_i_o_clk_out));
  TTY #(.cols(38)) tty_1 (
    .data(i_o_ctrl_1_i_o_dev_out), .clk(i_o_ctrl_1_i_o_clk_out), .clr(cpu_1_i_o_clr));  // open: we
  Multiplexer #(.width(8), .enable("false")) multiplexer_1 (
    .in0(n2d_engine_1_p1), .in1(cpu_1_i_o_out), .out(multiplexer_1_out));  // open: sel
  Keyboard keyboard_1 (.clk(i_o_ctrl_1_i_o_clk_in), .clr(cpu_1_i_o_clr), .data(keyboard_1_data));  // open: re, avail
  // Probe on cpu_1_d_bus_out
  CPU cpu_1 (
    .D_BUS_IN(rom_1_data_out), .I_O_IN(i_o_ctrl_1_i_o_out), .SEL(START), .CLR(RESET), .CLK(clock_1_out),
    .D_BUS_OUT(cpu_1_d_bus_out), .I_O_OUT(cpu_1_i_o_out), .ADDRESS(cpu_1_address), .MEM_R_W(cpu_1_mem_r_w),
    .RAM_R_W(cpu_1_ram_r_w), .W_CLK(cpu_1_w_clk), .I_O_W(cpu_1_i_o_w), .I_O_R(cpu_1_i_o_r),
    .I_O_CLK(cpu_1_i_o_clk), .I_O_CLR(cpu_1_i_o_clr), .INT(2'b00), .ROM_MEM_ROM(cpu_1_rom_mem_rom));  // open: STATUS_INT_MIO
  Clock clock_1 (.out(clock_1_out));
  // _2D_ENGINE 2d_engine_1: pin names not known; wires that end beside it: n2d_engine_1_p1, multiplexer_1_out, n2d_engine_1_p3, n2d_engine_1_p4, n2d_engine_1_p5, n2d_engine_1_p6, n2d_engine_1_p7
  ROM rom_1 (.ADDRESS_IN(cpu_1_address), .DATA_OUT(rom_1_data_out), .SEL(cpu_1_rom_mem_rom[0]));
  MEM mem_1 (
    .ADDRESS(cpu_1_address), .DATA_IN(cpu_1_d_bus_out), .DATA_OUT(rom_1_data_out),
    .SEL(cpu_1_rom_mem_rom[1]), .CLK(cpu_1_w_clk), .R_W(cpu_1_mem_r_w), .prog(3'b000));
  RAM ram_1 (
    .ADDRESS(cpu_1_address), .DATA_IN(cpu_1_d_bus_out), .DATA_OUT(rom_1_data_out), .SEL(or_1_out),
    .CLK(cpu_1_w_clk), .R_W(cpu_1_ram_r_w), .CLR(RESET));
  buf or_1 (or_1_out, cpu_1_rom_mem_rom[2]);  // OR_Gate
  // LCD_Video lcd_video_1: pin names not known; wires that end beside it: lcd_video_1_p1, lcd_video_1_p2, lcd_video_1_p3, lcd_video_1_p4, lcd_video_1_p5, lcd_video_1_p6
  RAM ram_2 (
    .ADDRESS(n2d_engine_1_p3), .DATA_IN(n2d_engine_1_p7), .DATA_OUT(ram_2_data_out));  // open: SEL, CLK, R_W, CLR

  // Other names for the same wires on the sheet: RST = RESET; STRT = START
endmodule

module MAIN_2 (
);

  wire cpu_1_p1, cpu_1_p2, cpu_1_p3, cpu_1_p4, cpu_1_p5, cpu_1_p6, cpu_1_p7, cpu_1_p8, cpu_1_p9, cpu_1_p11,
       cpu_1_p12, cpu_1_p13;
  wire [1:0] cpu_1_p10;

  // CPU cpu_1: pin names not known; wires that end beside it: cpu_1_p1, cpu_1_p2, cpu_1_p3, cpu_1_p4, cpu_1_p5, cpu_1_p6, cpu_1_p7, cpu_1_p8, cpu_1_p9, cpu_1_p10, cpu_1_p11, cpu_1_p12, cpu_1_p13
  // NORTHBRIDGE northbridge_1: pin names not known; wires that end beside it: cpu_1_p8, cpu_1_p2
endmodule

module CPU (
  input  [7:0] D_BUS_IN,
  input  [7:0] I_O_IN,
  input  SEL,
  input  CLR,
  input  CLK,
  input  [1:0] INT,
  output [7:0] D_BUS_OUT,
  output [7:0] I_O_OUT,
  output [7:0] ADDRESS,
  output [2:0] STATUS_INT_MIO,
  output [2:0] ROM_MEM_ROM,
  output MEM_R_W,
  output RAM_R_W,
  output W_CLK,
  output I_O_W,
  output I_O_R,
  output I_O_CLK,
  output I_O_CLR
);

  wire alu_1_c_out, alu_1_equal, alu_1_hi, alu_1_lo, alu_1_zero, C, control_unit_1_alu_en,
       control_unit_1_c_en, control_unit_1_c_in, control_unit_1_clr_acc, control_unit_1_clr_pc,
       control_unit_1_clr_regs, control_unit_1_fence, control_unit_1_i_o_clr, control_unit_1_i_o_r,
       control_unit_1_i_o_r_w_clk, control_unit_1_i_o_w, control_unit_1_immed_en, control_unit_1_immed_sel,
       control_unit_1_loop_write, control_unit_1_ltsi_en, control_unit_1_mem_w_r, control_unit_1_pc_laod,
       control_unit_1_ram_w_r, control_unit_1_w_clk, d_ff_1_q, or_1_out, regsiter_file_1_break, tunnel,
       tunnel_t, tunnel_t_t, Z;
  wire [1:0] control_unit_1_d_bus_mux, control_unit_1_i_o_mux, control_unit_1_int_stat,
       control_unit_1_main_mux, control_unit_1_pc_load;
  wire [2:0] A_SEL, B_SEL, C_SEL, control_unit_1_ltsi, control_unit_1_rom;
  wire [3:0] control_unit_1_op;
  wire [7:0] accumilator_1_resault_2, alu_1_resault, control_unit_1_address, control_unit_1_brod, IMMED_q,
       IR_q, multiplexer_1_out, multiplexer_2_out, multiplexer_3_out, multiplexer_4_out, pc_1_address,
       register_1_q, register_2_q, register_3_q, register_4_q, regsiter_file_1_a, regsiter_file_1_b,
       regsiter_file_1_c, undriven;

  or or_1 (or_1_out, ~SEL, CLR);  // OR_Gate
  Register #(.trigger("high")) register_1 (.D(D_BUS_IN), .en(d_ff_1_q), .Q(register_1_q), .clk(CLK), .clr(CLR));
  Register #(.trigger("high")) register_2 (.D(I_O_IN), .en(d_ff_1_q), .Q(register_2_q), .clk(CLK), .clr(CLR));
  D_Flip_Flop d_ff_1 (.clk(CLK), .D(SEL), .Q(d_ff_1_q), .en(SEL), .reset(or_1_out));  // open: Qn, preset
  Multiplexer #(.select(2), .width(8), .enable("false")) multiplexer_1 (
    .in0(register_1_q), .in1(regsiter_file_1_c), .in2(register_2_q), .in3(accumilator_1_resault_2),
    .out(multiplexer_1_out), .sel(control_unit_1_main_mux));
  Register #(.trigger("high")) IR (.D(register_1_q), .en(control_unit_1_fence), .Q(IR_q), .clk(CLK), .clr(CLR));
  Register IMMED (.D(register_1_q), .en(control_unit_1_immed_en), .Q(IMMED_q), .clk(CLK), .clr(CLR));
  REGSITER_FILE regsiter_file_1 (
    .LTSI(control_unit_1_ltsi), .DATA_IN(multiplexer_1_out), .CLK(CLK), .CLR(control_unit_1_clr_regs),
    .ALU_EN(control_unit_1_alu_en), .C_EN(control_unit_1_c_en), .LTSI_SEL(control_unit_1_ltsi_en),
    .\break (regsiter_file_1_break), .loop_write(control_unit_1_loop_write), .A(regsiter_file_1_a),
    .C(regsiter_file_1_c), .B(regsiter_file_1_b), .A_SEL(A_SEL), .C_SEL(C_SEL), .B_SEL(B_SEL));
  Multiplexer #(.width(8), .enable("false")) multiplexer_2 (
    .in0(regsiter_file_1_b), .in1(IMMED_q), .out(multiplexer_2_out), .sel(control_unit_1_immed_sel));
  CONTROL_UNIT control_unit_1 (
    .IR_IN(IR_q), .SEL(d_ff_1_q), .CLR(CLR), .CLK(CLK), .PC_IN(pc_1_address), .BROD(control_unit_1_brod),
    .ADDRESS(control_unit_1_address), .LTSI_EN(control_unit_1_ltsi_en), .ALU_EN(control_unit_1_alu_en),
    .C_EN(control_unit_1_c_en), .IMMED_EN(control_unit_1_immed_en), .IMMED_SEL(control_unit_1_immed_sel),
    .LTSI(control_unit_1_ltsi), .C_SEL(C_SEL), .A_SEL(A_SEL), .B_SEL(B_SEL), .OP(control_unit_1_op),
    .ROM(control_unit_1_rom[0]), .MEM(control_unit_1_rom[1]), .RAM(control_unit_1_rom[2]),
    .CLR_ACC(control_unit_1_clr_acc), .CLR_REGS(control_unit_1_clr_regs), .MEM_W_R(control_unit_1_mem_w_r),
    .RAM_W_R(control_unit_1_ram_w_r), .W_CLK(control_unit_1_w_clk), .I_O_R(control_unit_1_i_o_r),
    .I_O_W(control_unit_1_i_o_w), .I_O_R_W_CLK(control_unit_1_i_o_r_w_clk), .PC_LOAD(control_unit_1_pc_load),
    .MAIN_MUX(control_unit_1_main_mux), .D_BUS_MUX(control_unit_1_d_bus_mux),
    .I_O_MUX(control_unit_1_i_o_mux), .Z(Z), .C(C), .LO(tunnel), .EQUAL(tunnel_t), .HI(tunnel_t_t),
    .I_O_CLR(control_unit_1_i_o_clr), .FENCE(control_unit_1_fence), .LOOP_WRITE(control_unit_1_loop_write),
    .C_IN(control_unit_1_c_in), .CLR_PC(control_unit_1_clr_pc), .BREAK(regsiter_file_1_break),
    .PC_LAOD(control_unit_1_pc_laod), .ACC_IN(accumilator_1_resault_2), .I_O_IN(register_2_q), .INT(INT),
    .INT_STAT(control_unit_1_int_stat));
  Pull_Resistor pull_resistor_1 (.node(STATUS_INT_MIO[0]));
  ALU alu_1 (
    .A(regsiter_file_1_a), .B(multiplexer_2_out), .OP(control_unit_1_op), .C_OUT(alu_1_c_out), .HI(alu_1_hi),
    .EQUAL(alu_1_equal), .LO(alu_1_lo), .ZERO(alu_1_zero), .RESAULT(alu_1_resault), .C_IN(control_unit_1_c_in));
  ACCUMILATOR accumilator_1 (
    .RESAULT(alu_1_resault), .RESAULT_2(accumilator_1_resault_2), .ZERO(alu_1_zero), .ZERO_2(Z),
    .C_OUT(alu_1_c_out), .C_OUT_2(C), .HI(alu_1_hi), .HI_2(tunnel_t_t), .EQUAL(alu_1_equal),
    .EQUAL_2(tunnel_t), .LO(alu_1_lo), .LO_2(tunnel), .CLR(CLR), .UPDATE(control_unit_1_clr_acc));
  PC pc_1 (
    ._1(control_unit_1_address), ._2(register_1_q), ._3(regsiter_file_1_c), .in_4(control_unit_1_pc_load),
    .PC_LOAD(control_unit_1_pc_laod), .CLK(CLK), .CLR(CLR), .ADDRESS(pc_1_address),
    .MANUAL_CLR(control_unit_1_clr_pc));
  Multiplexer #(.select(2), .width(8), .enable("false")) multiplexer_3 (
    .in0(control_unit_1_brod), .in1(regsiter_file_1_c), .in2(accumilator_1_resault_2),
    .in3(multiplexer_1_out), .out(multiplexer_3_out), .sel(control_unit_1_d_bus_mux));
  Multiplexer #(.select(2), .width(8), .enable("false")) multiplexer_4 (
    .in0({8{1'b0}}), .in1(regsiter_file_1_c), .in2(accumilator_1_resault_2), .in3(multiplexer_1_out),
    .out(multiplexer_4_out), .sel(control_unit_1_i_o_mux));
  Pull_Resistor pull_resistor_2 (.node(STATUS_INT_MIO[2:1]));
  Transistor #(.\type ("n"), .width(2)) transistor_1 (
    .in(control_unit_1_int_stat), .out(STATUS_INT_MIO[2:1]), .gate(d_ff_1_q));
  Transistor #(.\type ("n"), .width(3)) transistor_2 (.in(control_unit_1_rom), .out(ROM_MEM_ROM), .gate(d_ff_1_q));
  Pull_Resistor pull_resistor_3 (.node(ROM_MEM_ROM));
  Transistor #(.\type ("n")) transistor_3 (.in(control_unit_1_mem_w_r), .out(MEM_R_W), .gate(d_ff_1_q));
  Pull_Resistor pull_resistor_4 (.node(MEM_R_W));
  Pull_Resistor pull_resistor_5 (.node(RAM_R_W));
  Transistor #(.\type ("n")) transistor_4 (.in(control_unit_1_ram_w_r), .out(RAM_R_W), .gate(d_ff_1_q));
  Pull_Resistor pull_resistor_6 (.node(W_CLK));
  Transistor #(.\type ("n")) transistor_5 (.in(control_unit_1_w_clk), .out(W_CLK), .gate(d_ff_1_q));
  Pull_Resistor pull_resistor_7 (.node(I_O_W));
  Transistor #(.\type ("n")) transistor_6 (.in(control_unit_1_i_o_w), .out(I_O_W), .gate(d_ff_1_q));
  Pull_Resistor pull_resistor_8 (.node(I_O_R));
  Transistor #(.\type ("n")) transistor_7 (.in(control_unit_1_i_o_r), .out(I_O_R), .gate(d_ff_1_q));
  Transistor #(.\type ("n")) transistor_8 (.in(control_unit_1_i_o_r_w_clk), .out(I_O_CLK), .gate(d_ff_1_q));
  Pull_Resistor pull_resistor_9 (.node(I_O_CLK));
  Transistor #(.\type ("n")) transistor_9 (.in(control_unit_1_i_o_clr), .out(I_O_CLR), .gate(d_ff_1_q));
  Pull_Resistor pull_resistor_10 (.node(I_O_CLR));
  Pull_Resistor pull_resistor_11 (.node(D_BUS_OUT));
  Transistor #(.\type ("n"), .width(8)) transistor_10 (.in(register_3_q), .out(D_BUS_OUT), .gate(d_ff_1_q));
  Register #(.trigger("high")) register_3 (.D(multiplexer_3_out), .Q(register_3_q), .clk(CLK), .clr(CLR));  // open: en
  Register #(.trigger("high")) register_4 (.D(multiplexer_4_out), .Q(register_4_q), .clk(CLK), .clr(CLR));  // open: en
  Transistor #(.\type ("n"), .width(8)) transistor_11 (.in(register_4_q), .out(I_O_OUT), .gate(d_ff_1_q));
  Pull_Resistor pull_resistor_12 (.node(I_O_OUT));
  Multiplexer #(.width(8), .enable("false")) multiplexer_5 (
    .in0(pc_1_address), .in1(undriven), .out(ADDRESS), .sel(STATUS_INT_MIO[0]));
endmodule

module SOUTHBRIDGE (
  input  STAT,
  input  CLK,
  input  CLR,
  input  [7:0] DATA_BUS_IN,
  input  [7:0] I_O_IN_CPU,
  input  [7:0] ADDR_IN,
  input  [7:0] I_O_IN_PH,
  output [7:0] DATA_BUS_OUT,
  output [7:0] I_O_OUT_CPU,
  output [7:0] ADDR_OUT,
  output [7:0] I_O_OUT_PH
);

  wire and_1_out, and_2_out, and_3_out, bit_extender_1_out, bit_extender_2_out, bit_extender_3_out,
       bit_extender_4_out, comparator_1_eq, comparator_2_eq, counter_1_q, d_ff_1_q, d_ff_2_q, d_ff_3_q,
       d_ff_4_q, not_1_out, or_1_out, or_2_out;
  wire [1:0] register_3_q, register_4_q, register_5_q, register_6_q;
  wire [7:0] register_1_q, register_2_q;

  Register register_1 (.D(ADDR_IN), .en(STAT), .Q(register_1_q), .clk(CLK), .clr(or_1_out));
  or or_1 (or_1_out, CLR, ~STAT);  // OR_Gate
  and and_1 (and_1_out, comparator_1_eq, and_3_out);
  Comparator comparator_1 (.a(register_1_q), .b(8'h14), .eq(comparator_1_eq));  // open: gt, lt
  Comparator comparator_2 (.a(register_1_q), .b(8'h15), .eq(comparator_2_eq));  // open: gt, lt
  and and_2 (and_2_out, comparator_2_eq, and_3_out);
  and and_3 (and_3_out, STAT, ~counter_1_q);  // AND_Gate
  Counter #(.width(1), .max('h1)) counter_1 (
    .count(STAT), .Q(counter_1_q), .clk(CLK), .clr(or_2_out));  // open: load, D, carry
  or or_2 (or_2_out, not_1_out, CLR);
  not not_1 (not_1_out, STAT);
  Register register_2 (.D(ADDR_IN), .en(STAT), .Q(register_2_q), .clk(CLK), .clr(CLR));
  Register #(.width(2)) register_3 (.D(register_2_q[1:0]), .en(and_1_out), .Q(register_3_q), .clk(CLK), .clr(CLR));
  Multiplexer #(.select(2), .width(8)) multiplexer_1 (
    .in0(DATA_BUS_IN), .in1(I_O_IN_CPU), .in2(ADDR_IN), .in3(I_O_IN_PH), .out(DATA_BUS_OUT),
    .sel(register_3_q), .en(d_ff_2_q));
  Multiplexer #(.select(2), .width(8)) multiplexer_2 (
    .in0(DATA_BUS_IN), .in1(I_O_IN_CPU), .in2(ADDR_IN), .in3(I_O_IN_PH), .out(I_O_OUT_CPU),
    .sel(register_4_q), .en(d_ff_1_q));
  Multiplexer #(.select(2), .width(8)) multiplexer_3 (
    .in0(DATA_BUS_IN), .in1(I_O_IN_CPU), .in2(ADDR_IN), .in3(I_O_IN_PH), .out(ADDR_OUT), .sel(register_5_q),
    .en(d_ff_3_q));
  Multiplexer #(.select(2), .width(8)) multiplexer_4 (
    .in0(DATA_BUS_IN), .in1(I_O_IN_CPU), .in2(ADDR_IN), .in3(I_O_IN_PH), .out(I_O_OUT_PH),
    .sel(register_6_q), .en(d_ff_4_q));
  Bit_Extender #(.in_width(2), .out_width(1), .\type ("sign")) bit_extender_1 (
    .in(register_2_q[7:6]), .out(bit_extender_1_out));
  Bit_Extender #(.in_width(2), .out_width(1), .\type ("sign")) bit_extender_2 (
    .in(register_2_q[5:4]), .out(bit_extender_2_out));
  Bit_Extender #(.in_width(2), .out_width(1), .\type ("sign")) bit_extender_3 (
    .in(register_2_q[3:2]), .out(bit_extender_3_out));
  Bit_Extender #(.in_width(2), .out_width(1), .\type ("sign")) bit_extender_4 (
    .in(register_2_q[1:0]), .out(bit_extender_4_out));
  Register #(.width(2)) register_4 (.D(register_2_q[3:2]), .en(and_1_out), .Q(register_4_q), .clk(CLK), .clr(CLR));
  Pull_Resistor pull_resistor_1 (.node(DATA_BUS_OUT));
  Pull_Resistor pull_resistor_2 (.node(I_O_OUT_CPU));
  Pull_Resistor pull_resistor_3 (.node(ADDR_OUT));
  Pull_Resistor pull_resistor_4 (.node(I_O_OUT_PH));
  D_Flip_Flop d_ff_1 (
    .clk(CLK), .D(bit_extender_2_out), .Q(d_ff_1_q), .en(and_2_out), .reset(CLR));  // open: Qn, preset
  D_Flip_Flop d_ff_2 (
    .clk(CLK), .D(bit_extender_1_out), .Q(d_ff_2_q), .en(and_2_out), .reset(CLR));  // open: Qn, preset
  Register #(.width(2)) register_5 (.D(register_2_q[5:4]), .en(and_1_out), .Q(register_5_q), .clk(CLK), .clr(CLR));
  D_Flip_Flop d_ff_3 (
    .clk(CLK), .D(bit_extender_3_out), .Q(d_ff_3_q), .en(and_2_out), .reset(CLR));  // open: Qn, preset
  Register #(.width(2)) register_6 (.D(register_2_q[7:6]), .en(and_1_out), .Q(register_6_q), .clk(CLK), .clr(CLR));
  D_Flip_Flop d_ff_4 (
    .clk(CLK), .D(bit_extender_4_out), .Q(d_ff_4_q), .en(and_2_out), .reset(CLR));  // open: Qn, preset
endmodule

module NORTHBRIDGE (
  input  [7:0] ADDR_IN,
  input  [7:0] DATA_IN,
  input  in_3
);
endmodule

module ALU (
  input  C_IN,
  input  [7:0] A,
  input  [7:0] B,
  input  [3:0] OP,
  output C_OUT,
  output HI,
  output EQUAL,
  output LO,
  output ZERO,
  output [7:0] RESAULT
);

  wire adder_1_cout, subtractor_1_bout;
  wire [7:0] adder_1_out, and_1_out, ascii_1_out_3, divider_1_out, divider_1_rem, multiplier_1_cout,
       multiplier_1_out, not_1_out, or_1_out, shifter_1_out, shifter_2_out, shifter_3_out, shifter_4_out,
       shifter_5_out, subtractor_1_out, xor_1_out;

  assign and_1_out = A & B;  // AND_Gate and_1, 8 bits wide
  assign or_1_out = A | B;  // OR_Gate or_1, 8 bits wide
  assign not_1_out = ~A;  // NOT_Gate not_1, 8 bits wide
  Adder adder_1 (.a(A), .b(B), .out(adder_1_out), .cin(C_IN), .cout(adder_1_cout));
  Subtractor subtractor_1 (.a(A), .b(B), .out(subtractor_1_out), .bin(C_IN), .bout(subtractor_1_bout));
  Multiplier multiplier_1 (.a(A), .b(B), .out(multiplier_1_out), .cout(multiplier_1_cout));  // open: cin
  Divider divider_1 (.a(A), .b(B), .out(divider_1_out), .rem(divider_1_rem));  // open: upper
  Comparator comparator_1 (.a(A), .b(B), .gt(HI), .eq(EQUAL), .lt(LO));
  assign xor_1_out = A ^ B;  // XOR_Gate xor_1, 8 bits wide
  ASCII ascii_1 (.INP_1(A), .INP_2(B), .out_3(ascii_1_out_3));
  Shifter shifter_1 (.in(A), .\dist (B[2:0]), .out(shifter_1_out));
  Shifter #(.shift("lr")) shifter_2 (.in(A), .\dist (B[2:0]), .out(shifter_2_out));
  Shifter #(.shift("ar")) shifter_3 (.in(A), .\dist (B[2:0]), .out(shifter_3_out));
  Shifter #(.shift("rl")) shifter_4 (.in(A), .\dist (B[2:0]), .out(shifter_4_out));
  Shifter #(.shift("rr")) shifter_5 (.in(A), .\dist (B[2:0]), .out(shifter_5_out));
  Multiplexer #(.select(4), .width(8), .enable("false")) multiplexer_1 (
    .in0(adder_1_out), .in1(subtractor_1_out), .in2(multiplier_1_out), .in3(multiplier_1_cout),
    .in4(divider_1_out), .in5(divider_1_rem), .in6(and_1_out), .in7(xor_1_out), .in8(or_1_out),
    .in9(not_1_out), .in10(ascii_1_out_3), .in11(shifter_1_out), .in12(shifter_2_out), .in13(shifter_3_out),
    .in14(shifter_4_out), .in15(shifter_5_out), .out(RESAULT), .sel(OP));
  nor nor_1 (ZERO, RESAULT[0], RESAULT[1], RESAULT[2], RESAULT[3], RESAULT[4], RESAULT[5], RESAULT[6], RESAULT[7]);
  Multiplexer #(.select(4), .enable("false")) multiplexer_2 (
    .in0(adder_1_cout), .in1(subtractor_1_bout), .in2(1'b0), .in3(1'b0), .in4(1'b0), .in5(1'b0), .in6(1'b0),
    .in7(1'b0), .in8(1'b0), .in9(1'b0), .in10(1'b0), .in11(1'b0), .in12(1'b0), .in13(1'b0), .in14(1'b0),
    .in15(1'b0), .out(C_OUT), .sel(OP));

  // Other names for the same wires on the sheet: ALU_OP[3:0] = OP
endmodule

module ASCII (
  input  [7:0] INP_1,
  input  [7:0] INP_2,
  output [7:0] out_3
);

  wire nor_1_out, nor_2_out, nor_3_out, nor_4_out;
  wire [3:0] adder_1_out, adder_2_out, subtractor_1_out, subtractor_2_out, subtractor_3_out, subtractor_4_out;

  Subtractor #(.width(4)) subtractor_1 (.a(INP_1[7:4]), .b(4'b0011), .out(subtractor_1_out));  // open: bin, bout
  Subtractor #(.width(4)) subtractor_2 (.a(INP_1[7:4]), .b(4'b0100), .out(subtractor_2_out));  // open: bin, bout
  Subtractor #(.width(4)) subtractor_3 (.a(INP_2[7:4]), .b(4'b0011), .out(subtractor_3_out));  // open: bin, bout
  Subtractor #(.width(4)) subtractor_4 (.a(INP_2[7:4]), .b(4'b0100), .out(subtractor_4_out));  // open: bin, bout
  nor nor_1 (nor_1_out, subtractor_1_out[0], subtractor_1_out[1], subtractor_1_out[2], subtractor_1_out[3]);
  nor nor_2 (nor_2_out, subtractor_2_out[0], subtractor_2_out[1], subtractor_2_out[2], subtractor_2_out[3]);
  nor nor_3 (nor_3_out, subtractor_3_out[0], subtractor_3_out[1], subtractor_3_out[2], subtractor_3_out[3]);
  nor nor_4 (nor_4_out, subtractor_4_out[0], subtractor_4_out[1], subtractor_4_out[2], subtractor_4_out[3]);
  Adder #(.width(4)) adder_1 (.a(INP_2[3:0]), .b(4'b1001), .out(adder_1_out));  // open: cin, cout
  assign out_3[7:4] = nor_1_out ? INP_1[3:0] : 4'bz;  // Controlled_Buffer controlled_buffer_1
  assign out_3[7:4] = nor_2_out ? adder_2_out : 4'bz;  // Controlled_Buffer controlled_buffer_2
  Adder #(.width(4)) adder_2 (.a(INP_1[3:0]), .b(4'b1001), .out(adder_2_out));  // open: cin, cout
  assign out_3[3:0] = nor_3_out ? INP_2[3:0] : 4'bz;  // Controlled_Buffer controlled_buffer_3
  assign out_3[3:0] = nor_4_out ? adder_1_out : 4'bz;  // Controlled_Buffer controlled_buffer_4
  Pull_Resistor pull_resistor_1 (.node(out_3[7:4]));
  Pull_Resistor pull_resistor_2 (.node(out_3[3:0]));
  // Probe on out_3

  // Notes on the sheet:
  //   INP_1: pull=down
  //   INP_2: pull=down
endmodule

module REGSITER_FILE (
  input  LTSI_SEL,
  input  [2:0] LTSI,
  input  loop_write,
  input  [7:0] DATA_IN,
  input  CLK,
  input  CLR,
  input  ALU_EN,
  input  C_EN,
  input  [2:0] A_SEL,
  input  [2:0] C_SEL,
  input  [2:0] B_SEL,
  output \break ,
  output [7:0] A,
  output [7:0] C,
  output [7:0] B
);

  wire and_3_out, demultiplexer_1_out0, demultiplexer_1_out1, demultiplexer_1_out2, demultiplexer_1_out3,
       demultiplexer_1_out4, demultiplexer_1_out5, demultiplexer_1_out6, demultiplexer_1_out7, or_1_out;
  wire [7:0] adder_1_out, bit_extender_1_out, bit_extender_2_out, multiplexer_1_out, multiplexer_2_out,
       multiplexer_3_out, multiplexer_4_out, register_1_q, register_2_q, register_3_q, register_4_q,
       register_5_q, register_6_q, register_7_q, register_8_q;

  Demultiplexer #(.select(3), .enable("false")) demultiplexer_1 (
    .out0(demultiplexer_1_out0), .out1(demultiplexer_1_out1), .out2(demultiplexer_1_out2),
    .out3(demultiplexer_1_out3), .out4(demultiplexer_1_out4), .out5(demultiplexer_1_out5),
    .out6(demultiplexer_1_out6), .out7(demultiplexer_1_out7), .in(LTSI_SEL), .sel(LTSI));
  Register register_1 (.D(DATA_IN), .en(demultiplexer_1_out0), .Q(register_1_q), .clk(CLK), .clr(CLR));
  Register register_2 (.D(DATA_IN), .en(demultiplexer_1_out1), .Q(register_2_q), .clk(CLK), .clr(CLR));
  Register register_3 (.D(DATA_IN), .en(demultiplexer_1_out2), .Q(register_3_q), .clk(CLK), .clr(CLR));
  Register register_4 (.D(DATA_IN), .en(demultiplexer_1_out3), .Q(register_4_q), .clk(CLK), .clr(CLR));
  Register register_5 (.D(DATA_IN), .en(demultiplexer_1_out4), .Q(register_5_q), .clk(CLK), .clr(CLR));
  Register register_6 (.D(DATA_IN), .en(demultiplexer_1_out5), .Q(register_6_q), .clk(CLK), .clr(CLR));
  Register register_7 (.D(DATA_IN), .en(demultiplexer_1_out6), .Q(register_7_q), .clk(CLK), .clr(CLR));
  Register register_8 (.D(multiplexer_1_out), .en(or_1_out), .Q(register_8_q), .clk(CLK), .clr(CLR));
  Multiplexer #(.width(8), .enable("false")) multiplexer_1 (
    .in0(DATA_IN), .in1(adder_1_out), .out(multiplexer_1_out), .sel(and_3_out));
  or or_1 (or_1_out, loop_write, demultiplexer_1_out7);
  Multiplexer #(.select(3), .width(8), .enable("false")) multiplexer_2 (
    .in0(register_1_q), .in1(register_2_q), .in2(register_3_q), .in3(register_4_q), .in4(register_5_q),
    .in5(register_6_q), .in6(register_7_q), .in7(register_8_q), .out(multiplexer_2_out), .sel(A_SEL));
  assign bit_extender_1_out = {{7{ALU_EN}}, ALU_EN};  // Bit_Extender bit_extender_1
  assign bit_extender_2_out = {{7{C_EN}}, C_EN};  // Bit_Extender bit_extender_2
  assign A = bit_extender_1_out & multiplexer_2_out;  // AND_Gate and_1, 8 bits wide
  Comparator comparator_1 (.a(register_8_q), .b(register_7_q), .eq(\break ));  // open: gt, lt
  Multiplexer #(.select(3), .width(8), .enable("false")) multiplexer_3 (
    .in0(register_1_q), .in1(register_2_q), .in2(register_3_q), .in3(register_4_q), .in4(register_5_q),
    .in5(register_6_q), .in6(register_7_q), .in7(register_8_q), .out(multiplexer_3_out), .sel(C_SEL));
  assign C = bit_extender_2_out & multiplexer_3_out;  // AND_Gate and_2, 8 bits wide
  and and_3 (and_3_out, ~\break , loop_write);  // AND_Gate
  Adder adder_1 (.a(register_8_q), .b(8'h1), .out(adder_1_out));  // open: cin, cout
  Multiplexer #(.select(3), .width(8), .enable("false")) multiplexer_4 (
    .in0(register_1_q), .in1(register_2_q), .in2(register_3_q), .in3(register_4_q), .in4(register_5_q),
    .in5(register_6_q), .in6(register_7_q), .in7(register_8_q), .out(multiplexer_4_out), .sel(B_SEL));
  assign B = bit_extender_1_out & multiplexer_4_out;  // AND_Gate and_4, 8 bits wide

  // Other names for the same wires on the sheet: LW = loop_write
endmodule

module PC (
  input  [7:0] _1,
  input  [7:0] _2,
  input  [7:0] _3,
  input  [1:0] in_4,
  input  PC_LOAD,
  input  CLK,
  input  CLR,
  input  MANUAL_CLR,
  output [7:0] ADDRESS
);

  wire or_1_out;
  wire [7:0] adder_1_out, multiplexer_1_out;

  Multiplexer #(.select(2), .width(8), .enable("false")) multiplexer_1 (
    .in0(adder_1_out), .in1(_1), .in2(_2), .in3(_3), .out(multiplexer_1_out), .sel(in_4));
  Register PC (.D(multiplexer_1_out), .en(PC_LOAD), .Q(ADDRESS), .clk(CLK), .clr(or_1_out));
  or or_1 (or_1_out, CLR, MANUAL_CLR);
  Adder adder_1 (.a(ADDRESS), .b(8'h1), .out(adder_1_out));  // open: cin, cout
endmodule

module ACCUMILATOR (
  input  [7:0] RESAULT,
  input  ZERO,
  input  C_OUT,
  input  HI,
  input  EQUAL,
  input  LO,
  input  CLR,
  input  UPDATE,
  output [7:0] RESAULT_2,
  output ZERO_2,
  output C_OUT_2,
  output HI_2,
  output EQUAL_2,
  output LO_2
);

  wire or_1_out_2, or_2_out, or_3_out, or_4_out, or_5_out, or_6_out, or_7_out;

  OR or_1 (.in_1(RESAULT), .out_2(or_1_out_2));
  Register #(.trigger("high")) u_RESAULT (.D(RESAULT), .en(UPDATE), .Q(RESAULT_2), .clk(or_2_out), .clr(CLR));
  or or_2 (or_2_out, UPDATE, or_1_out_2);
  Register #(.width(1), .trigger("high")) u_ZERO (.D(ZERO), .en(UPDATE), .Q(ZERO_2), .clk(or_3_out), .clr(CLR));
  or or_3 (or_3_out, UPDATE, ZERO);
  Register #(.width(1), .trigger("high")) u_C_OUT (.D(C_OUT), .en(UPDATE), .Q(C_OUT_2), .clk(or_4_out), .clr(CLR));
  or or_4 (or_4_out, UPDATE, C_OUT);
  Register #(.width(1), .trigger("high")) u_HI (.D(HI), .en(UPDATE), .Q(HI_2), .clk(or_5_out), .clr(CLR));
  or or_5 (or_5_out, UPDATE, HI);
  Register #(.width(1), .trigger("high")) u_EQUAL (.D(EQUAL), .en(UPDATE), .Q(EQUAL_2), .clk(or_6_out), .clr(CLR));
  or or_6 (or_6_out, UPDATE, EQUAL);
  Register #(.width(1), .trigger("high")) u_LO (.D(LO), .en(UPDATE), .Q(LO_2), .clk(or_7_out), .clr(CLR));
  or or_7 (or_7_out, UPDATE, LO);
endmodule

module OR (
  input  [7:0] in_1,
  output out_2
);

  or or_1 (out_2, in_1[0], in_1[1], in_1[2], in_1[3], in_1[4], in_1[5], in_1[6], in_1[7]);
endmodule

module INSTRUCTION_REGISTERS (
  input  STATUS,
  input  [7:0] DATA_IN,
  input  CLR,
  input  CLK,
  output [31:0] DATA_OUT
);

  wire decoder_1_out0, decoder_1_out1, decoder_1_out2, decoder_1_out3, not_1_out, not_2_out, or_1_out,
       or_2_out, transistor_1_out;
  wire [1:0] counter_1_q;
  wire [7:0] register_1_q, register_2_q, register_3_q, register_4_q, transistor_2_out;

  Counter #(.width(2), .max('h3)) counter_1 (
    .Q(counter_1_q), .clk(transistor_1_out), .clr(or_1_out));  // open: load, D, count, carry
  Transistor #(.\type ("n")) transistor_1 (.in(CLK), .out(transistor_1_out), .gate(STATUS));
  or or_1 (or_1_out, CLR, not_1_out);
  Decoder #(.select(2), .enable("false")) decoder_1 (
    .out0(decoder_1_out0), .out1(decoder_1_out1), .out2(decoder_1_out2), .out3(decoder_1_out3),
    .sel(counter_1_q));
  not not_1 (not_1_out, STATUS);
  not not_2 (not_2_out, STATUS);
  Transistor #(.\type ("n"), .width(8)) transistor_2 (.in(DATA_IN), .out(transistor_2_out), .gate(STATUS));
  Register #(.trigger("high")) register_1 (
    .D(transistor_2_out), .en(decoder_1_out0), .Q(register_1_q), .clk(CLK), .clr(CLR));
  Register #(.trigger("high")) register_2 (
    .D(transistor_2_out), .en(decoder_1_out1), .Q(register_2_q), .clk(CLK), .clr(CLR));
  Register #(.trigger("high")) register_3 (
    .D(transistor_2_out), .en(decoder_1_out2), .Q(register_3_q), .clk(CLK), .clr(CLR));
  Register #(.trigger("high")) register_4 (
    .D(transistor_2_out), .en(decoder_1_out3), .Q(register_4_q), .clk(CLK), .clr(CLR));
  or or_2 (or_2_out, decoder_1_out3, not_2_out);
  Pull_Resistor pull_resistor_1 (.node(DATA_OUT));
  Transistor #(.\type ("n"), .gate("br"), .width(32)) transistor_3 (
    .in({register_1_q, register_2_q, register_3_q, register_4_q}), .out(DATA_OUT), .gate(or_2_out));
endmodule

module CONTROL_UNIT (
  input  Z,
  input  C,
  input  [7:0] IR_IN,
  input  SEL,
  input  CLR,
  input  BREAK,
  input  CLK,
  input  [7:0] PC_IN,
  input  LO,
  input  EQUAL,
  input  HI,
  input  [7:0] ACC_IN,
  input  [7:0] I_O_IN,
  input  [1:0] INT,
  output LOOP_WRITE,
  output [7:0] BROD,
  output [7:0] ADDRESS,
  output LTSI_EN,
  output ALU_EN,
  output C_EN,
  output IMMED_EN,
  output IMMED_SEL,
  output [2:0] LTSI,
  output [2:0] C_SEL,
  output [2:0] A_SEL,
  output [2:0] B_SEL,
  output [3:0] OP,
  output CLR_PC,
  output C_IN,
  output ROM,
  output MEM,
  output RAM,
  output CLR_ACC,
  output CLR_REGS,
  output MEM_W_R,
  output I_O_CLR,
  output RAM_W_R,
  output W_CLK,
  output PC_LAOD,
  output I_O_R,
  output FENCE,
  output I_O_W,
  output I_O_R_W_CLK,
  output [1:0] INT_STAT,
  output [1:0] PC_LOAD,
  output [1:0] MAIN_MUX,
  output [1:0] D_BUS_MUX,
  output [1:0] I_O_MUX
);

  wire and_1_out, and_2_out, and_3_out, and_4_out, and_5_out, and_6_out, and_7_out, and_8_out, and_21_out,
       and_22_out, and_23_out, bridge_ctrl_1_bridge_activate, BROD_SEL, D_BUS_0, hlt_fence_1_clr_ir,
       hlt_fence_1_fence, hlt_fence_1_pc_load, I_O_DEV_IN_CLK, I_O_DEV_OUT, I_O_DEV_OUT_1, I_O_DEV_OUT_2,
       I_O_IN_t, I_O_R_t, I_O_W_t, LOAD, logic_1_clr_accumilator, logic_1_clr_i_o, LTSI_EN_t, MAIN_0, MAIN_2,
       MAIN_2_1, MAIN_MUX_3, MEM_1, MEM_3, MEM_t, MEM_W, mov_b_1_c_en, mov_b_1_i_o_r, mov_b_1_ltsi_en,
       mov_b_1_mem_r, mov_b_1_ram_r, mov_b_1_rom, mov_b_1_status, MOV_OP, mov_op_1_c_en, mov_op_1_i_o_w,
       mov_op_1_ltsi_en, or_1_out, or_2_out, or_3_out, or_4_out, or_5_out_2, or_6_out, or_7_out, or_10_out_2,
       or_25_out, or_26_out, or_27_out, or_29_out, OUT_1, OUT_2, OUT_3, PC_LOAD_2, RAM_1, RAM_3, RAM_t,
       RAM_W, ROM_1, ROM_2, ROM_t, SEL_ADDR_2, SEL_ADDR_3, SEL_ADDR_4, SEL_ADDR_5, stack_engine_1_c_en,
       stack_engine_1_pc_load_2, stack_engine_1_ram_r, stack_engine_1_ram_w, stack_engine_1_status;
  wire [1:0] and_9_out, and_10_out, and_11_out, and_12_out, and_13_out, and_14_out, and_15_out, and_16_out,
       and_17_out, and_18_out, and_19_out, and_20_out, bit_extender_1_out, bit_extender_2_out,
       bit_extender_3_out, bit_extender_4_out, bit_extender_5_out, bit_extender_6_out, bit_extender_7_out,
       bit_extender_8_out, bit_extender_9_out, bit_extender_10_out, bit_extender_11_out, bit_extender_12_out,
       or_15_out, stack_engine_1_pc_load;
  wire [2:0] LTSI_t, mov_b_1_c_sel, mov_b_1_ltsi, mov_op_1_c_sel, mov_op_1_ltsi, stack_engine_1_c_sel;
  wire [7:0] ADDR_INT, branch_1_addr, bridge_ctrl_1_brod, BROD_t, hlt_fence_1_address, mov_b_1_address,
       mov_b_1_brod, stack_engine_1_addr;
  wire [31:0] instruction_registers_1_data_out, pull_resistor_1_node;

  INSTRUCTION_REGISTERS instruction_registers_1 (
    .STATUS(and_1_out), .DATA_IN(IR_IN), .CLR(or_1_out), .CLK(CLK),
    .DATA_OUT(instruction_registers_1_data_out));
  or or_1 (or_1_out, CLR, hlt_fence_1_clr_ir);
  and and_1 (and_1_out, SEL, and_2_out, mov_b_1_status);
  or or_2 (or_2_out, and_1_out, ~stack_engine_1_status);  // OR_Gate
  and and_2 (and_2_out, FENCE, stack_engine_1_status);
  Pull_Resistor pull_resistor_1 (.node(pull_resistor_1_node));
  Transistor #(.\type ("n"), .width(32)) transistor_1 (
    .in(instruction_registers_1_data_out), .out(pull_resistor_1_node), .gate(or_2_out));
  or or_3 (or_3_out, SEL_ADDR_5, PC_LOAD_2);
  or or_4 (or_4_out, SEL_ADDR_3, or_3_out, SEL_ADDR_4);
  OR or_5 (.in_1(ADDRESS), .out_2(or_5_out_2));
  or or_6 (or_6_out, MAIN_2, I_O_IN_t, MAIN_2_1);
  BRANCH branch_1 (
    .in_1(pull_resistor_1_node), .ZERO_FLAG(Z), .SEL(or_2_out), .Hi(HI), .EQUAL(EQUAL), .Lo(LO),
    .ADDR(branch_1_addr), .SEL_ADDR(SEL_ADDR_2), .LOAD(LOAD), .\break (BREAK), .loop_write(LOOP_WRITE),
    .MEM(MEM_3), .RAM(RAM_3), .ROM(ROM_2), .CLR(CLR), .CLK(CLK), .PC_IN(PC_IN), .CARRY_FLAG(C));  // open: C_SEL
  MOV_OP mov_op_1 (
    .DATA_IN(pull_resistor_1_node), .I_O_W(mov_op_1_i_o_w), .I_O_MUX_2(I_O_DEV_OUT_2),
    .I_O_MUX_1(I_O_DEV_OUT_1), .IMMED_SEL(IMMED_SEL), .ALU_EN(ALU_EN), .IMMED_EN(IMMED_EN), .A_SEL(A_SEL),
    .OP(OP), .B_SEL(B_SEL), .C_SEL(mov_op_1_c_sel), .LTSI(mov_op_1_ltsi), .C_EN(mov_op_1_c_en),
    .LTSI_EN(mov_op_1_ltsi_en), .MAIN_MUX_1(MOV_OP), .I_O_IN(MAIN_2_1), .MAIN_3(MAIN_MUX_3), .CLK(CLK),
    .CLR(CLR), .I_O_DEV_IN(I_O_IN_t), .I_O_DEV_IN_CLK(I_O_DEV_IN_CLK), .I_O_R(I_O_R_t));  // open: PC_LOAD
  MOV_B mov_b_1 (
    .DATA_IN(pull_resistor_1_node), .PC_IN(PC_IN), .CLR(CLR), .CLK(CLK), .BROD(mov_b_1_brod),
    .STATUS(mov_b_1_status), .ROM(mov_b_1_rom), .MEM_R(mov_b_1_mem_r), .RAM_R(mov_b_1_ram_r),
    .I_O_R(mov_b_1_i_o_r), .MEM_W(MEM_W), .RAM_W(RAM_W), .I_O_W(I_O_W_t), .LTSI(mov_b_1_ltsi),
    .C_SEL(mov_b_1_c_sel), .C_EN(mov_b_1_c_en), .LTSI_EN(mov_b_1_ltsi_en), .ADDRESS(mov_b_1_address),
    .MAIN_0(MAIN_0), .D_BUS_3(OUT_3), .MAIN_2(MAIN_2), .I_O_3(I_O_DEV_OUT), .D_BUS_2(OUT_2), .D_BUS_1(OUT_1),
    .PC_LOAD_2(PC_LOAD_2), .sel_addr(SEL_ADDR_4), .ACC_IN(ACC_IN));
  LOGIC logic_1 (
    .DATA_IN(pull_resistor_1_node), .PC_IN(PC_IN), .CLR(CLR), .CLK(CLK), .RAM_WRITE(1'b0), .MEM_WRITE(1'b0),
    .CLR_I_O(logic_1_clr_i_o), .CLR_ACCUMILATOR(logic_1_clr_accumilator), .CLR_REGS(CLR_REGS),
    .SEL_BIOS(ROM_t), .SEL_RAM(RAM_t), .SEL_MEM(MEM_t), .C_IN(C_IN), .ROM_2(ROM_2), .RAM_3(RAM_3),
    .MEM_3(MEM_3));  // open: MAIN_MUX, ADDR, CLR_X, CLR_PC, CLK_KYBD, CLK_RAM, CLK_MEM, CLR_PC_ALL
  STACK_ENGINE stack_engine_1 (
    .DATA_IN(pull_resistor_1_node), .PC_IN(PC_IN), .C_EN(stack_engine_1_c_en), .C_SEL(stack_engine_1_c_sel),
    .ADDR(stack_engine_1_addr), .RAM(RAM_1), .MEM(MEM_1), .ROM(ROM_1), .CLR(CLR), .CLK(CLK),
    .SEL_ADDR(SEL_ADDR_3), .carry(C), .zero(Z), .STACK_SEGMENT_IN({8{1'b0}}), .BROD(BROD_t),
    .RAM_W(stack_engine_1_ram_w), .LTSI_EN(LTSI_EN_t), .RAM_R(stack_engine_1_ram_r), .LTSI_SEL(LTSI_t),
    .STATUS(stack_engine_1_status), .BROD_2(BROD_SEL), .PC_LOAD(stack_engine_1_pc_load),
    .PC_LOAD_2(stack_engine_1_pc_load_2), .SEL(SEL));
  HLT_FENCE hlt_fence_1 (
    .DATA_IN(pull_resistor_1_node), .PC_IN(PC_IN), .CLK(CLK), .CLR(CLR), .FENCE(hlt_fence_1_fence),
    .I_O_IN(I_O_IN), .ADDRESS(hlt_fence_1_address), .PC_LOAD(hlt_fence_1_pc_load), .CLR_PC(CLR_PC),
    .CLR_IR(hlt_fence_1_clr_ir));
  not not_1 (FENCE, hlt_fence_1_fence);
  INT int_1 (
    .in_1(pull_resistor_1_node), .SEL_ADDR(SEL_ADDR_5), .ADDR(ADDR_INT), .EN(1'b1), .CLK(CLK), .CLR(CLR),
    .INT_STAT(INT_STAT), .ZERO(Z), .CARRY(C), .INT(INT));  // open: M_IO_ADDR, M_IO
  assign bit_extender_1_out = {{1{or_7_out}}, or_7_out};  // Bit_Extender bit_extender_1
  or or_7 (or_7_out, or_4_out, SEL_ADDR_2, or_5_out_2);
  assign bit_extender_2_out = {{1{1'b0}}, 1'b0};  // Bit_Extender bit_extender_2
  assign bit_extender_3_out = {{1{LOAD}}, LOAD};  // Bit_Extender bit_extender_3
  and and_3 (and_3_out, MOV_OP, ~MAIN_0);  // AND_Gate
  assign bit_extender_4_out = {{1{and_3_out}}, and_3_out};  // Bit_Extender bit_extender_4
  assign bit_extender_5_out = {{1{and_4_out}}, and_4_out};  // Bit_Extender bit_extender_5
  and and_4 (and_4_out, or_6_out, ~MAIN_0);  // AND_Gate
  and and_5 (and_5_out, MAIN_MUX_3, ~MAIN_0);  // AND_Gate
  assign bit_extender_6_out = {{1{and_5_out}}, and_5_out};  // Bit_Extender bit_extender_6
  and and_6 (and_6_out, ~D_BUS_0, OUT_1);  // AND_Gate
  assign bit_extender_7_out = {{1{and_6_out}}, and_6_out};  // Bit_Extender bit_extender_7
  assign bit_extender_8_out = {{1{and_7_out}}, and_7_out};  // Bit_Extender bit_extender_8
  and and_7 (and_7_out, ~D_BUS_0, OUT_2);  // AND_Gate
  and and_8 (and_8_out, ~D_BUS_0, OUT_3);  // AND_Gate
  assign bit_extender_9_out = {{1{and_8_out}}, and_8_out};  // Bit_Extender bit_extender_9
  assign bit_extender_10_out = {{1{I_O_DEV_OUT_1}}, I_O_DEV_OUT_1};  // Bit_Extender bit_extender_10
  assign bit_extender_11_out = {{1{I_O_DEV_OUT_2}}, I_O_DEV_OUT_2};  // Bit_Extender bit_extender_11
  assign bit_extender_12_out = {{1{I_O_DEV_OUT}}, I_O_DEV_OUT};  // Bit_Extender bit_extender_12
  BRIDGE_CTRL bridge_ctrl_1 (
    .in_1(pull_resistor_1_node), .BROD(bridge_ctrl_1_brod), .bridge_activate(bridge_ctrl_1_bridge_activate));
  or or_8 (CLR_ACC, ALU_EN, logic_1_clr_accumilator);
  or or_9 (I_O_CLR, logic_1_clr_i_o, CLR);
  assign and_9_out = bit_extender_1_out & 2'b01;  // AND_Gate and_9, 2 bits wide
  assign and_10_out = bit_extender_2_out & 2'b10;  // AND_Gate and_10, 2 bits wide
  assign and_11_out = bit_extender_3_out & 2'b11;  // AND_Gate and_11, 2 bits wide
  assign and_12_out = bit_extender_4_out & 2'b01;  // AND_Gate and_12, 2 bits wide
  assign and_13_out = bit_extender_5_out & 2'b10;  // AND_Gate and_13, 2 bits wide
  assign and_14_out = bit_extender_6_out & 2'b11;  // AND_Gate and_14, 2 bits wide
  assign and_15_out = bit_extender_7_out & 2'b01;  // AND_Gate and_15, 2 bits wide
  assign and_16_out = bit_extender_8_out & 2'b10;  // AND_Gate and_16, 2 bits wide
  assign and_17_out = bit_extender_9_out & 2'b11;  // AND_Gate and_17, 2 bits wide
  assign and_18_out = bit_extender_10_out & 2'b01;  // AND_Gate and_18, 2 bits wide
  assign and_19_out = bit_extender_11_out & 2'b10;  // AND_Gate and_19, 2 bits wide
  assign and_20_out = bit_extender_12_out & 2'b11;  // AND_Gate and_20, 2 bits wide
  OR or_10 (.in_1(BROD), .out_2(or_10_out_2));
  assign BROD = bridge_ctrl_1_brod | BROD_t | mov_b_1_brod;  // OR_Gate or_11, 8 bits wide
  and and_21 (and_21_out, stack_engine_1_pc_load_2, SEL);
  Pull_Resistor pull_resistor_2 (.node(PC_LAOD));
  Transistor #(.\type ("n")) transistor_2 (.in(hlt_fence_1_pc_load), .out(PC_LAOD), .gate(and_21_out));
  or or_12 (I_O_R, I_O_R_t, mov_b_1_i_o_r);
  or or_13 (I_O_W, I_O_W_t, mov_op_1_i_o_w);
  assign PC_LOAD = stack_engine_1_pc_load | or_15_out;  // OR_Gate or_14, 2 bits wide
  assign or_15_out = and_9_out | and_10_out | and_11_out;  // OR_Gate or_15, 2 bits wide
  assign MAIN_MUX = and_12_out | and_13_out | and_14_out;  // OR_Gate or_16, 2 bits wide
  assign D_BUS_MUX = and_15_out | and_16_out | and_17_out;  // OR_Gate or_17, 2 bits wide
  assign I_O_MUX = and_18_out | and_19_out | and_20_out;  // OR_Gate or_18, 2 bits wide
  or or_19 (D_BUS_0, BROD_SEL, or_10_out_2);
  assign ADDRESS = hlt_fence_1_address | branch_1_addr | ADDR_INT | stack_engine_1_addr | mov_b_1_address;  // OR_Gate or_20, 8 bits wide
  or or_21 (LTSI_EN, mov_b_1_ltsi_en, LTSI_EN_t, mov_op_1_ltsi_en);
  or or_22 (C_EN, mov_op_1_c_en, stack_engine_1_c_en, mov_b_1_c_en);
  assign LTSI = mov_op_1_ltsi | LTSI_t | mov_b_1_ltsi;  // OR_Gate or_23, 3 bits wide
  assign C_SEL = mov_op_1_c_sel | stack_engine_1_c_sel | mov_b_1_c_sel;  // OR_Gate or_24, 3 bits wide
  or or_25 (or_25_out, mov_b_1_ram_r, stack_engine_1_ram_r);
  MEMORY_CTRL memory_ctrl_1 (
    .ROM_SEL(ROM_1), .ROM_R(mov_b_1_rom), .MEM_SEL(MEM_1), .MEM_R(mov_b_1_mem_r), .MEM_W(MEM_W),
    .RAM_SEL(RAM_1), .RAM_R(or_25_out), .RAM_W(or_26_out), .ROM_SEL_2(ROM), .MEM_SEL_2(MEM), .RAM_SEL_2(RAM),
    .RAM_SEL_LOGIC(RAM_t), .MEM_SEL_LOGIC(MEM_t), .ROM_SEL_LOGIC(ROM_t),
    .bridge_activate(bridge_ctrl_1_bridge_activate));  // open: MEMORY_CTRL_ERROR
  or or_26 (or_26_out, stack_engine_1_ram_w, RAM_W);
  or or_27 (or_27_out, I_O_R, I_O_W);
  and and_22 (and_22_out, or_27_out, CLK);
  and and_23 (and_23_out, I_O_DEV_IN_CLK, CLK);
  and and_24 (MEM_W_R, ~mov_b_1_mem_r, MEM_W);  // AND_Gate
  and and_25 (RAM_W_R, ~or_25_out, or_26_out);  // AND_Gate
  and and_26 (W_CLK, CLK, or_29_out);
  or or_28 (I_O_R_W_CLK, and_22_out, and_23_out);
  or or_29 (or_29_out, MEM_W_R, RAM_W_R);

  // Other names for the same wires on the sheet: ADDR[7:0] = ADDRESS
endmodule

module INT (
  input  [31:0] in_1,
  input  EN,
  input  CLK,
  input  CLR,
  input  ZERO,
  input  CARRY,
  input  [1:0] INT,
  output M_IO,
  output [7:0] M_IO_ADDR,
  output [1:0] INT_STAT,
  output SEL_ADDR,
  output [7:0] ADDR
);

  wire and_1_out, and_2_out, and_3_out, and_4_out, and_5_out, comparator_1_eq, comparator_2_eq,
       comparator_3_eq, comparator_4_eq, comparator_5_eq, comparator_6_eq, comparator_7_eq, comparator_8_eq,
       comparator_9_eq, comparator_10_eq, comparator_11_eq, comparator_12_eq, comparator_13_eq,
       comparator_14_eq, comparator_15_eq, comparator_17_eq, comparator_18_eq, decoder_1_out1,
       decoder_1_out2, decoder_1_out3, demultiplexer_1_out1, demultiplexer_1_out2, demultiplexer_1_out3,
       not_1_out, not_2_out, or_1_out, or_2_out, or_3_out, or_4_out, or_5_out, or_6_out, or_7_out,
       pull_resistor_1_node, pull_resistor_8_node, pull_resistor_9_node, pull_resistor_10_node,
       pull_resistor_12_node, pull_resistor_14_node, pull_resistor_15_node, pull_resistor_16_node,
       pull_resistor_17_node, pull_resistor_19_node, pull_resistor_21_node, transistor_2_out,
       transistor_3_out, transistor_4_out, transistor_5_out, transistor_6_out, transistor_7_out,
       transistor_11_out, transistor_13_out, transistor_18_out;
  wire [7:0] register_1_q, register_2_q, register_3_q, transistor_22_out;

  Comparator comparator_1 (.a(in_1[7:0]), .b(8'h11), .eq(comparator_1_eq));  // open: gt, lt
  Comparator comparator_2 (.a(in_1[15:8]), .b(8'h57), .eq(comparator_2_eq));  // open: gt, lt
  Comparator comparator_3 (.a(in_1[23:16]), .b(8'he8), .eq(comparator_3_eq));  // open: gt, lt
  Pull_Resistor pull_resistor_1 (.node(pull_resistor_1_node));
  Comparator comparator_4 (.a(in_1[31:24]), .b(8'h21), .eq(comparator_4_eq));  // open: gt, lt
  Transistor #(.\type ("n")) transistor_1 (
    .in(comparator_4_eq), .out(pull_resistor_1_node), .gate(pull_resistor_10_node));
  Transistor #(.\type ("n")) transistor_2 (.in(comparator_5_eq), .out(transistor_2_out), .gate(pull_resistor_10_node));
  Comparator comparator_5 (.a(in_1[31:24]), .b(8'h31), .eq(comparator_5_eq));  // open: gt, lt
  Pull_Resistor pull_resistor_2 (.node(transistor_2_out));
  Transistor #(.\type ("n")) transistor_3 (.in(comparator_6_eq), .out(transistor_3_out), .gate(pull_resistor_19_node));
  Comparator comparator_6 (.a(in_1[31:24]), .b(8'h21), .eq(comparator_6_eq));  // open: gt, lt
  Pull_Resistor pull_resistor_3 (.node(transistor_3_out));
  Comparator comparator_7 (.a(in_1[31:24]), .b(8'h31), .eq(comparator_7_eq));  // open: gt, lt
  Transistor #(.\type ("n")) transistor_4 (.in(comparator_7_eq), .out(transistor_4_out), .gate(pull_resistor_19_node));
  Pull_Resistor pull_resistor_4 (.node(transistor_4_out));
  Comparator comparator_8 (.a(in_1[31:24]), .b(8'h22), .eq(comparator_8_eq));  // open: gt, lt
  Transistor #(.\type ("n")) transistor_5 (.in(comparator_8_eq), .out(transistor_5_out), .gate(pull_resistor_10_node));
  Pull_Resistor pull_resistor_5 (.node(transistor_5_out));
  Transistor #(.\type ("n")) transistor_6 (.in(comparator_9_eq), .out(transistor_6_out), .gate(pull_resistor_10_node));
  Pull_Resistor pull_resistor_6 (.node(transistor_6_out));
  Comparator comparator_9 (.a(in_1[31:24]), .b(8'h35), .eq(comparator_9_eq));  // open: gt, lt
  Transistor #(.\type ("n")) transistor_7 (.in(comparator_10_eq), .out(transistor_7_out), .gate(pull_resistor_19_node));
  Comparator comparator_10 (.a(in_1[31:24]), .b(8'h22), .eq(comparator_10_eq));  // open: gt, lt
  Pull_Resistor pull_resistor_7 (.node(transistor_7_out));
  Comparator comparator_11 (.a(in_1[31:24]), .b(8'h35), .eq(comparator_11_eq));  // open: gt, lt
  Pull_Resistor pull_resistor_8 (.node(pull_resistor_8_node));
  Transistor #(.\type ("n")) transistor_8 (
    .in(comparator_11_eq), .out(pull_resistor_8_node), .gate(pull_resistor_19_node));
  or or_1 (or_1_out, pull_resistor_19_node, pull_resistor_10_node);
  Pull_Resistor pull_resistor_9 (.node(pull_resistor_9_node));
  Transistor #(.\type ("n")) transistor_9 (.in(comparator_12_eq), .out(pull_resistor_9_node), .gate(or_1_out));
  Comparator comparator_12 (.a(in_1[31:24]), .b(8'he8), .eq(comparator_12_eq));  // open: gt, lt
  Comparator comparator_13 (.a(in_1[7:0]), .b(8'h12), .eq(comparator_13_eq));  // open: gt, lt
  Comparator comparator_14 (.a(in_1[15:8]), .b(8'h89), .eq(comparator_14_eq));  // open: gt, lt
  Comparator comparator_15 (.a(in_1[23:16]), .b(8'hf8), .eq(comparator_15_eq));  // open: gt, lt
  and and_1 (and_1_out, comparator_1_eq, comparator_2_eq, comparator_3_eq);
  Pull_Resistor pull_resistor_10 (.node(pull_resistor_10_node));
  Transistor #(.\type ("n")) transistor_10 (.in(and_1_out), .out(pull_resistor_10_node), .gate(EN));
  Transistor #(.\type ("n")) transistor_11 (.in(pull_resistor_1_node), .out(transistor_11_out), .gate(ZERO));
  Pull_Resistor pull_resistor_11 (.node(transistor_11_out));
  or or_2 (or_2_out, transistor_11_out, pull_resistor_12_node);
  Pull_Resistor pull_resistor_12 (.node(pull_resistor_12_node));
  Transistor #(.\type ("n")) transistor_12 (.in(transistor_2_out), .out(pull_resistor_12_node), .gate(CARRY));
  Transistor #(.\type ("n")) transistor_13 (.in(transistor_3_out), .out(transistor_13_out), .gate(ZERO));
  Pull_Resistor pull_resistor_13 (.node(transistor_13_out));
  or or_3 (or_3_out, transistor_13_out, pull_resistor_14_node);
  Pull_Resistor pull_resistor_14 (.node(pull_resistor_14_node));
  Transistor #(.\type ("n")) transistor_14 (.in(transistor_4_out), .out(pull_resistor_14_node), .gate(CARRY));
  not not_1 (not_1_out, CARRY);
  not not_2 (not_2_out, ZERO);
  Pull_Resistor pull_resistor_15 (.node(pull_resistor_15_node));
  Transistor #(.\type ("n")) transistor_15 (.in(transistor_5_out), .out(pull_resistor_15_node), .gate(not_2_out));
  or or_4 (or_4_out, pull_resistor_15_node, pull_resistor_16_node);
  Pull_Resistor pull_resistor_16 (.node(pull_resistor_16_node));
  Transistor #(.\type ("n")) transistor_16 (.in(transistor_6_out), .out(pull_resistor_16_node), .gate(not_1_out));
  Pull_Resistor pull_resistor_17 (.node(pull_resistor_17_node));
  Transistor #(.\type ("n")) transistor_17 (.in(transistor_7_out), .out(pull_resistor_17_node), .gate(not_2_out));
  or or_5 (or_5_out, pull_resistor_17_node, transistor_18_out);
  Transistor #(.\type ("n")) transistor_18 (.in(pull_resistor_8_node), .out(transistor_18_out), .gate(not_1_out));
  Pull_Resistor pull_resistor_18 (.node(transistor_18_out));
  and and_2 (and_2_out, pull_resistor_9_node, pull_resistor_10_node);
  and and_3 (and_3_out, pull_resistor_19_node, pull_resistor_9_node);
  Comparator #(.width(24)) comparator_16 (.a(in_1[23:0]), .b(24'h3ecfff), .eq(M_IO));  // open: gt, lt
  and and_4 (and_4_out, comparator_13_eq, comparator_14_eq, comparator_15_eq);
  Pull_Resistor pull_resistor_19 (.node(pull_resistor_19_node));
  Transistor #(.\type ("n")) transistor_19 (.in(and_4_out), .out(pull_resistor_19_node), .gate(EN));
  or or_6 (or_6_out, or_2_out, and_2_out, or_4_out);
  or or_7 (or_7_out, or_3_out, and_3_out, or_5_out);
  Transistor #(.\type ("n"), .width(8)) transistor_20 (.in(in_1[31:24]), .out(M_IO_ADDR), .gate(M_IO));
  Pull_Resistor pull_resistor_20 (.node(M_IO_ADDR));
  Comparator comparator_17 (.a(in_1[7:0]), .b(8'h13), .eq(comparator_17_eq));  // open: gt, lt
  Comparator comparator_18 (.a(in_1[15:8]), .b(8'h71), .eq(comparator_18_eq));  // open: gt, lt
  and and_5 (and_5_out, comparator_17_eq, comparator_18_eq);
  Pull_Resistor pull_resistor_21 (.node(pull_resistor_21_node));
  Transistor #(.\type ("n")) transistor_21 (.in(and_5_out), .out(pull_resistor_21_node), .gate(EN));
  Demultiplexer #(.select(2), .enable("false")) demultiplexer_1 (
    .out1(demultiplexer_1_out1), .out2(demultiplexer_1_out2), .out3(demultiplexer_1_out3),
    .in(pull_resistor_21_node), .sel(in_1[17:16]));  // open: out0
  Register register_1 (.D(in_1[31:24]), .en(demultiplexer_1_out1), .Q(register_1_q), .clk(CLK), .clr(CLR));
  D_Flip_Flop d_ff_1 (.clk(CLK), .D(or_6_out), .Q(INT_STAT[0]), .en(EN), .reset(CLR));  // open: Qn, preset
  D_Flip_Flop d_ff_2 (.clk(CLK), .D(or_7_out), .Q(INT_STAT[1]), .en(EN), .reset(CLR));  // open: Qn, preset
  Decoder #(.select(2), .enable("false")) decoder_1 (
    .out1(decoder_1_out1), .out2(decoder_1_out2), .out3(decoder_1_out3), .sel(INT));  // open: out0
  or or_8 (SEL_ADDR, INT[0], INT[1]);
  Register register_2 (.D(in_1[31:24]), .en(demultiplexer_1_out2), .Q(register_2_q), .clk(CLK), .clr(CLR));
  Transistor #(.\type ("n"), .width(8)) transistor_22 (
    .in(register_2_q), .out(transistor_22_out), .gate(decoder_1_out2));
  Transistor #(.\type ("n"), .width(8)) transistor_23 (
    .in(register_1_q), .out(transistor_22_out), .gate(decoder_1_out1));
  Register register_3 (.D(in_1[31:24]), .en(demultiplexer_1_out3), .Q(register_3_q), .clk(CLK), .clr(CLR));
  Transistor #(.\type ("n"), .width(8)) transistor_24 (
    .in(register_3_q), .out(transistor_22_out), .gate(decoder_1_out3));
  Pull_Resistor pull_resistor_22 (.node(ADDR));
  Transistor #(.\type ("n"), .width(8)) transistor_25 (.in(transistor_22_out), .out(ADDR), .gate(SEL_ADDR));
endmodule

module BRANCH (
  input  [31:0] in_1,
  input  CARRY_FLAG,
  input  CLR,
  input  ZERO_FLAG,
  input  CLK,
  input  SEL,
  input  [7:0] PC_IN,
  input  Hi,
  input  EQUAL,
  input  Lo,
  input  \break ,
  output loop_write,
  output LOAD,
  output SEL_ADDR,
  output [2:0] C_SEL,
  output [7:0] ADDR,
  output MEM,
  output RAM,
  output ROM
);

  wire and_1_out, and_2_out, and_4_out, and_5_out, and_6_out, and_8_out, and_9_out, and_11_out, and_12_out,
       and_13_out, and_64_out, comparator_1_eq, comparator_2_eq, comparator_3_eq, comparator_4_eq,
       comparator_5_eq, comparator_7_eq, comparator_8_eq, comparator_9_eq, comparator_10_eq,
       comparator_11_eq, comparator_12_eq, comparator_13_eq, comparator_14_eq, comparator_15_eq,
       comparator_16_eq, comparator_17_eq, comparator_18_eq, comparator_19_eq, comparator_20_eq,
       comparator_21_eq, comparator_22_eq, comparator_23_eq, d_ff_1_q, d_ff_2_q, d_ff_3_q, decoder_1_out2,
       not_1_out, not_2_out, not_9_out, not_10_out, or_1_out, or_2_out, or_3_out, or_4_out, or_5_out,
       or_6_out, or_7_out, or_8_out_2, or_10_out, or_11_out, or_15_out_2, pull_resistor_3_node,
       pull_resistor_5_node, pull_resistor_8_node, pull_resistor_9_node, transistor_2_out, transistor_4_out,
       transistor_6_out, transistor_7_out;
  wire [1:0] counter_1_q;
  wire [7:0] and_14_out, and_15_out, and_16_out, and_17_out, and_18_out, and_19_out, and_20_out, and_21_out,
       and_22_out, and_23_out, and_24_out, and_25_out, and_26_out, and_27_out, and_28_out, and_29_out,
       and_30_out, and_31_out, and_32_out, and_33_out, and_34_out, and_35_out, and_36_out, and_37_out,
       and_38_out, and_39_out, and_40_out, and_41_out, and_42_out, and_43_out, and_44_out, and_45_out,
       and_46_out, and_47_out, and_48_out, and_49_out, and_50_out, and_51_out, and_52_out, and_53_out,
       and_54_out, and_55_out, and_56_out, and_57_out, and_58_out, and_59_out, and_60_out, and_61_out,
       and_62_out, bit_extender_1_out, bit_extender_2_out, bit_extender_3_out, bit_extender_4_out,
       bit_extender_5_out, bit_extender_6_out, bit_extender_7_out, bit_extender_8_out, bit_extender_9_out,
       bit_extender_10_out, bit_extender_11_out, bit_extender_12_out, bit_extender_13_out,
       bit_extender_14_out, bit_extender_15_out, bit_extender_16_out, bit_extender_17_out,
       bit_extender_18_out, bit_extender_19_out, bit_extender_20_out, bit_extender_21_out, multiplexer_1_out,
       not_3_out, not_4_out, not_5_out, not_6_out, not_7_out, not_8_out, or_12_out, or_13_out, or_14_out,
       pull_resistor_1_node, subtractor_1_out, transistor_10_out;
  wire [31:0] register_1_q;
  wire [31:8] pull_resistor_1_node_2;

  and and_1 (and_1_out, ~CLK, ~comparator_2_eq, ~or_4_out);  // AND_Gate
  Counter #(.width(2), .max('h3)) counter_1 (
    .Q(counter_1_q), .clk(and_2_out), .clr(or_1_out));  // open: load, D, count, carry
  and and_2 (and_2_out, CLK, comparator_2_eq, or_4_out);
  Decoder #(.select(2), .enable("false")) decoder_1 (
    .out2(decoder_1_out2), .sel(counter_1_q));  // open: out0, out1, out3
  or or_1 (or_1_out, and_1_out, CLR);
  Comparator #(.width(32)) comparator_1 (.a(register_1_q), .b(in_1), .eq(comparator_1_eq));  // open: gt, lt
  Comparator comparator_2 (.a(pull_resistor_1_node), .b(PC_IN), .eq(comparator_2_eq));  // open: gt, lt
  D_Flip_Flop d_ff_1 (.clk(and_6_out), .D(and_6_out), .Q(d_ff_1_q), .reset(or_2_out));  // open: Qn, preset, en
  or or_2 (or_2_out, decoder_1_out2, CLR);
  and and_3 (MEM, comparator_2_eq, d_ff_1_q);
  Pull_Resistor pull_resistor_1 (.node({pull_resistor_1_node_2, pull_resistor_1_node}));
  Transistor #(.\type ("n"), .width(32)) transistor_1 (
    .in(register_1_q), .out({pull_resistor_1_node_2, pull_resistor_1_node}), .gate(comparator_1_eq));
  Register #(.width(32), .trigger("high")) register_1 (
    .D(in_1), .Q(register_1_q), .clk(and_4_out), .clr(or_3_out));  // open: en
  or or_3 (or_3_out, CLR, decoder_1_out2);
  buf and_4 (and_4_out, CLK);  // AND_Gate
  or or_4 (or_4_out, and_13_out, and_12_out);
  and and_5 (and_5_out, or_6_out, comparator_9_eq);
  or or_5 (or_5_out, and_5_out, SEL_ADDR);
  Comparator comparator_3 (.a(pull_resistor_1_node_2[23:16]), .b(8'h6), .eq(comparator_3_eq));  // open: gt, lt
  Comparator comparator_4 (.a(pull_resistor_1_node_2[23:16]), .b(8'h5), .eq(comparator_4_eq));  // open: gt, lt
  Comparator comparator_5 (.a(pull_resistor_1_node_2[23:16]), .b(8'h4), .eq(comparator_5_eq));  // open: gt, lt
  and and_6 (and_6_out, or_5_out, comparator_5_eq);
  D_Flip_Flop d_ff_2 (.clk(and_8_out), .D(and_8_out), .Q(d_ff_2_q), .reset(or_2_out));  // open: Qn, preset, en
  and and_7 (RAM, comparator_2_eq, d_ff_2_q);
  Comparator #(.width(32)) comparator_6 (
    .a({pull_resistor_1_node_2, pull_resistor_1_node}), .b(32'hbcf78659), .eq(loop_write));  // open: gt, lt
  Comparator comparator_7 (.a(pull_resistor_1_node_2[31:24]), .b(8'hac), .eq(comparator_7_eq));  // open: gt, lt
  Comparator comparator_8 (.a(pull_resistor_1_node_2[31:24]), .b(8'hdc), .eq(comparator_8_eq));  // open: gt, lt
  Multiplexer #(.width(8), .enable("false")) multiplexer_1 (
    .in0(pull_resistor_1_node), .in1(8'h1), .out(multiplexer_1_out), .sel(and_11_out));
  or or_6 (or_6_out, comparator_5_eq, comparator_4_eq, comparator_3_eq);
  or or_7 (or_7_out, or_6_out, comparator_11_eq);
  Comparator comparator_9 (.a(pull_resistor_1_node_2[15:8]), .b(8'h40), .eq(comparator_9_eq));  // open: gt, lt
  and and_8 (and_8_out, or_5_out, comparator_4_eq);
  and and_9 (and_9_out, or_5_out, comparator_3_eq);
  D_Flip_Flop d_ff_3 (.clk(and_9_out), .D(and_9_out), .Q(d_ff_3_q), .reset(or_2_out));  // open: Qn, preset, en
  and and_10 (ROM, comparator_2_eq, d_ff_3_q);
  not not_1 (not_1_out, ZERO_FLAG);
  not not_2 (not_2_out, CARRY_FLAG);
  assign bit_extender_1_out = {{7{CARRY_FLAG}}, CARRY_FLAG};  // Bit_Extender bit_extender_1
  assign bit_extender_2_out = {{7{ZERO_FLAG}}, ZERO_FLAG};  // Bit_Extender bit_extender_2
  assign bit_extender_3_out = {{7{SEL}}, SEL};  // Bit_Extender bit_extender_3
  Comparator comparator_10 (.a(pull_resistor_1_node_2[23:16]), .b(8'h20), .eq(comparator_10_eq));  // open: gt, lt
  Comparator comparator_11 (.a(pull_resistor_1_node_2[23:16]), .b(8'h30), .eq(comparator_11_eq));  // open: gt, lt
  and and_11 (and_11_out, comparator_8_eq, and_12_out, ~or_8_out_2);  // AND_Gate
  OR or_8 (.in_1(pull_resistor_1_node), .out_2(or_8_out_2));
  and and_12 (and_12_out, or_7_out, comparator_9_eq);
  assign bit_extender_4_out = {{7{and_12_out}}, and_12_out};  // Bit_Extender bit_extender_4
  Comparator comparator_12 (.a(pull_resistor_1_node_2[15:8]), .b(8'h31), .eq(comparator_12_eq));  // open: gt, lt
  Comparator comparator_13 (.a(pull_resistor_1_node_2[15:8]), .b(8'h35), .eq(comparator_13_eq));  // open: gt, lt
  Comparator comparator_14 (.a(pull_resistor_1_node_2[15:8]), .b(8'h21), .eq(comparator_14_eq));  // open: gt, lt
  Comparator comparator_15 (.a(pull_resistor_1_node_2[15:8]), .b(8'h22), .eq(comparator_15_eq));  // open: gt, lt
  Comparator comparator_16 (.a(pull_resistor_1_node_2[15:8]), .b(8'hd1), .eq(comparator_16_eq));  // open: gt, lt
  Comparator comparator_17 (.a(pull_resistor_1_node_2[15:8]), .b(8'hd5), .eq(comparator_17_eq));  // open: gt, lt
  Comparator comparator_18 (.a(pull_resistor_1_node_2[15:8]), .b(8'hd2), .eq(comparator_18_eq));  // open: gt, lt
  Comparator comparator_19 (.a(pull_resistor_1_node_2[15:8]), .b(8'hc1), .eq(comparator_19_eq));  // open: gt, lt
  Comparator comparator_20 (.a(pull_resistor_1_node_2[15:8]), .b(8'hc5), .eq(comparator_20_eq));  // open: gt, lt
  Comparator comparator_21 (.a(pull_resistor_1_node_2[15:8]), .b(8'hc2), .eq(comparator_21_eq));  // open: gt, lt
  Comparator comparator_22 (.a(pull_resistor_1_node_2[15:8]), .b(8'he1), .eq(comparator_22_eq));  // open: gt, lt
  Comparator comparator_23 (.a(pull_resistor_1_node_2[15:8]), .b(8'he2), .eq(comparator_23_eq));  // open: gt, lt
  assign bit_extender_5_out = {{7{Hi}}, Hi};  // Bit_Extender bit_extender_5
  assign bit_extender_6_out = {{7{EQUAL}}, EQUAL};  // Bit_Extender bit_extender_6
  assign bit_extender_7_out = {{7{Lo}}, Lo};  // Bit_Extender bit_extender_7
  assign bit_extender_8_out = {{7{\break }}, \break };  // Bit_Extender bit_extender_8
  Transistor #(.\type ("n")) transistor_2 (.in(not_1_out), .out(transistor_2_out), .gate(comparator_7_eq));
  Pull_Resistor pull_resistor_2 (.node(transistor_2_out));
  Pull_Resistor pull_resistor_3 (.node(pull_resistor_3_node));
  Transistor #(.\type ("n")) transistor_3 (.in(not_2_out), .out(pull_resistor_3_node), .gate(comparator_7_eq));
  OR or_9 (.in_1(or_14_out), .out_2(SEL_ADDR));
  assign bit_extender_9_out = {{7{and_13_out}}, and_13_out};  // Bit_Extender bit_extender_9
  and and_13 (and_13_out, comparator_8_eq, or_10_out);
  or or_10 (or_10_out, comparator_10_eq, or_6_out);
  assign and_14_out = bit_extender_3_out & multiplexer_1_out;  // AND_Gate and_14, 8 bits wide
  assign and_15_out = bit_extender_3_out & multiplexer_1_out;  // AND_Gate and_15, 8 bits wide
  assign and_16_out = bit_extender_3_out & multiplexer_1_out;  // AND_Gate and_16, 8 bits wide
  assign and_17_out = bit_extender_3_out & multiplexer_1_out;  // AND_Gate and_17, 8 bits wide
  assign bit_extender_10_out = {{7{comparator_12_eq}}, comparator_12_eq};  // Bit_Extender bit_extender_10
  assign bit_extender_11_out = {{7{comparator_13_eq}}, comparator_13_eq};  // Bit_Extender bit_extender_11
  assign bit_extender_12_out = {{7{comparator_14_eq}}, comparator_14_eq};  // Bit_Extender bit_extender_12
  assign bit_extender_13_out = {{7{comparator_15_eq}}, comparator_15_eq};  // Bit_Extender bit_extender_13
  assign bit_extender_14_out = {{7{comparator_16_eq}}, comparator_16_eq};  // Bit_Extender bit_extender_14
  assign bit_extender_15_out = {{7{comparator_17_eq}}, comparator_17_eq};  // Bit_Extender bit_extender_15
  assign bit_extender_16_out = {{7{comparator_18_eq}}, comparator_18_eq};  // Bit_Extender bit_extender_16
  assign bit_extender_17_out = {{7{comparator_19_eq}}, comparator_19_eq};  // Bit_Extender bit_extender_17
  assign bit_extender_18_out = {{7{comparator_20_eq}}, comparator_20_eq};  // Bit_Extender bit_extender_18
  assign bit_extender_19_out = {{7{comparator_21_eq}}, comparator_21_eq};  // Bit_Extender bit_extender_19
  assign bit_extender_20_out = {{7{comparator_22_eq}}, comparator_22_eq};  // Bit_Extender bit_extender_20
  assign bit_extender_21_out = {{7{comparator_23_eq}}, comparator_23_eq};  // Bit_Extender bit_extender_21
  assign and_18_out = bit_extender_3_out & multiplexer_1_out;  // AND_Gate and_18, 8 bits wide
  assign and_19_out = bit_extender_3_out & multiplexer_1_out;  // AND_Gate and_19, 8 bits wide
  assign and_20_out = bit_extender_3_out & multiplexer_1_out;  // AND_Gate and_20, 8 bits wide
  assign and_21_out = bit_extender_3_out & multiplexer_1_out;  // AND_Gate and_21, 8 bits wide
  assign and_22_out = bit_extender_3_out & multiplexer_1_out;  // AND_Gate and_22, 8 bits wide
  assign and_23_out = bit_extender_3_out & multiplexer_1_out;  // AND_Gate and_23, 8 bits wide
  assign and_24_out = bit_extender_3_out & multiplexer_1_out;  // AND_Gate and_24, 8 bits wide
  assign and_25_out = bit_extender_3_out & multiplexer_1_out;  // AND_Gate and_25, 8 bits wide
  Transistor #(.\type ("n")) transistor_4 (.in(ZERO_FLAG), .out(transistor_4_out), .gate(comparator_7_eq));
  Pull_Resistor pull_resistor_4 (.node(transistor_4_out));
  Pull_Resistor pull_resistor_5 (.node(pull_resistor_5_node));
  Transistor #(.\type ("n")) transistor_5 (.in(CARRY_FLAG), .out(pull_resistor_5_node), .gate(comparator_7_eq));
  assign and_26_out = bit_extender_9_out & and_14_out;  // AND_Gate and_26, 8 bits wide
  assign and_27_out = bit_extender_2_out & and_26_out;  // AND_Gate and_27, 8 bits wide
  assign and_28_out = bit_extender_9_out & and_15_out;  // AND_Gate and_28, 8 bits wide
  assign and_29_out = bit_extender_1_out & and_28_out;  // AND_Gate and_29, 8 bits wide
  assign not_3_out = ~bit_extender_2_out;  // NOT_Gate not_3, 8 bits wide
  assign and_30_out = bit_extender_9_out & and_16_out;  // AND_Gate and_30, 8 bits wide
  assign not_4_out = ~bit_extender_1_out;  // NOT_Gate not_4, 8 bits wide
  assign and_31_out = bit_extender_9_out & and_17_out;  // AND_Gate and_31, 8 bits wide
  assign and_32_out = bit_extender_9_out & and_18_out;  // AND_Gate and_32, 8 bits wide
  assign and_33_out = bit_extender_5_out & and_32_out;  // AND_Gate and_33, 8 bits wide
  assign and_34_out = bit_extender_6_out & and_35_out;  // AND_Gate and_34, 8 bits wide
  assign and_35_out = bit_extender_9_out & and_19_out;  // AND_Gate and_35, 8 bits wide
  assign and_36_out = bit_extender_7_out & and_37_out;  // AND_Gate and_36, 8 bits wide
  assign and_37_out = bit_extender_9_out & and_20_out;  // AND_Gate and_37, 8 bits wide
  assign not_5_out = ~bit_extender_5_out;  // NOT_Gate not_5, 8 bits wide
  assign and_38_out = bit_extender_9_out & and_21_out;  // AND_Gate and_38, 8 bits wide
  assign not_6_out = ~bit_extender_6_out;  // NOT_Gate not_6, 8 bits wide
  assign and_39_out = bit_extender_9_out & and_22_out;  // AND_Gate and_39, 8 bits wide
  assign not_7_out = ~bit_extender_7_out;  // NOT_Gate not_7, 8 bits wide
  assign and_40_out = bit_extender_9_out & and_23_out;  // AND_Gate and_40, 8 bits wide
  assign and_41_out = bit_extender_8_out & and_42_out;  // AND_Gate and_41, 8 bits wide
  assign and_42_out = bit_extender_9_out & and_24_out;  // AND_Gate and_42, 8 bits wide
  assign not_8_out = ~bit_extender_8_out;  // NOT_Gate not_8, 8 bits wide
  assign and_43_out = bit_extender_9_out & and_25_out;  // AND_Gate and_43, 8 bits wide
  not not_9 (not_9_out, comparator_14_eq);
  Transistor #(.\type ("n")) transistor_6 (.in(transistor_4_out), .out(transistor_6_out), .gate(comparator_14_eq));
  Pull_Resistor pull_resistor_6 (.node(transistor_6_out));
  assign and_44_out = bit_extender_12_out & and_27_out;  // AND_Gate and_44, 8 bits wide
  assign and_45_out = bit_extender_10_out & and_29_out;  // AND_Gate and_45, 8 bits wide
  assign and_46_out = not_3_out & and_30_out;  // AND_Gate and_46, 8 bits wide
  assign and_47_out = bit_extender_13_out & and_46_out;  // AND_Gate and_47, 8 bits wide
  assign and_48_out = not_4_out & and_31_out;  // AND_Gate and_48, 8 bits wide
  assign and_49_out = bit_extender_11_out & and_48_out;  // AND_Gate and_49, 8 bits wide
  assign and_50_out = bit_extender_14_out & and_33_out;  // AND_Gate and_50, 8 bits wide
  assign and_51_out = bit_extender_15_out & and_34_out;  // AND_Gate and_51, 8 bits wide
  assign and_52_out = bit_extender_16_out & and_36_out;  // AND_Gate and_52, 8 bits wide
  assign and_53_out = not_5_out & and_38_out;  // AND_Gate and_53, 8 bits wide
  assign and_54_out = bit_extender_17_out & and_53_out;  // AND_Gate and_54, 8 bits wide
  assign and_55_out = bit_extender_18_out & and_56_out;  // AND_Gate and_55, 8 bits wide
  assign and_56_out = not_6_out & and_39_out;  // AND_Gate and_56, 8 bits wide
  assign and_57_out = not_7_out & and_40_out;  // AND_Gate and_57, 8 bits wide
  assign and_58_out = bit_extender_19_out & and_57_out;  // AND_Gate and_58, 8 bits wide
  assign and_59_out = bit_extender_20_out & and_41_out;  // AND_Gate and_59, 8 bits wide
  assign and_60_out = bit_extender_21_out & and_61_out;  // AND_Gate and_60, 8 bits wide
  assign and_61_out = not_8_out & and_43_out;  // AND_Gate and_61, 8 bits wide
  not not_10 (not_10_out, comparator_12_eq);
  Transistor #(.\type ("n")) transistor_7 (.in(pull_resistor_5_node), .out(transistor_7_out), .gate(comparator_12_eq));
  Pull_Resistor pull_resistor_7 (.node(transistor_7_out));
  Pull_Resistor pull_resistor_8 (.node(pull_resistor_8_node));
  Transistor #(.\type ("n")) transistor_8 (.in(transistor_2_out), .out(pull_resistor_8_node), .gate(not_9_out));
  assign and_62_out = multiplexer_1_out & bit_extender_4_out;  // AND_Gate and_62, 8 bits wide
  or or_11 (or_11_out, transistor_6_out, transistor_7_out, pull_resistor_8_node, pull_resistor_9_node);
  and and_63 (LOAD, or_11_out, or_10_out);
  Pull_Resistor pull_resistor_9 (.node(pull_resistor_9_node));
  Transistor #(.\type ("n")) transistor_9 (.in(pull_resistor_3_node), .out(pull_resistor_9_node), .gate(not_10_out));
  assign or_12_out = and_44_out | and_45_out | and_62_out | and_47_out | and_49_out;  // OR_Gate or_12, 8 bits wide
  assign or_13_out = and_50_out | and_51_out | and_52_out | and_54_out | and_55_out | and_58_out | and_59_out | and_60_out;  // OR_Gate or_13, 8 bits wide
  Bit_Extender #(.out_width(3)) bit_extender_22 (.in(transistor_10_out), .out(C_SEL));
  Transistor #(.\type ("n"), .width(8)) transistor_10 (.in(ADDR), .out(transistor_10_out), .gate(LOAD));
  Pull_Resistor pull_resistor_10 (.node(transistor_10_out));
  assign or_14_out = or_12_out | or_13_out;  // OR_Gate or_14, 8 bits wide
  Multiplexer #(.width(8), .enable("false")) multiplexer_2 (
    .in0(or_14_out), .in1(subtractor_1_out), .out(ADDR), .sel(and_64_out));
  Subtractor subtractor_1 (.a(or_14_out), .b(8'h1), .out(subtractor_1_out));  // open: bin, bout
  OR or_15 (.in_1(or_14_out), .out_2(or_15_out_2));
  and and_64 (and_64_out, or_15_out_2, and_11_out);
endmodule

module STACK_ENGINE (
  input  zero,
  input  carry,
  input  [7:0] PC_IN,
  input  SEL,
  input  [31:0] DATA_IN,
  input  [7:0] STACK_SEGMENT_IN,
  input  CLR,
  input  CLK,
  output [2:0] LTSI_SEL,
  output LTSI_EN,
  output C_EN,
  output [2:0] C_SEL,
  output [7:0] BROD,
  output BROD_2,
  output [7:0] ADDR,
  output [1:0] PC_LOAD,
  output SEL_ADDR,
  output PC_LOAD_2,
  output RAM_R,
  output RAM_W,
  output RAM,
  output STATUS,
  output MEM,
  output ROM
);

  wire and_1_out, and_2_out, and_3_out, and_4_out, and_5_out, and_6_out, and_7_out, and_11_out, and_12_out,
       and_13_out, and_15_out, and_16_out, comparator_1_eq, comparator_2_eq, comparator_3_eq,
       comparator_4_eq, comparator_5_eq, comparator_6_eq, comparator_7_eq, comparator_8_eq, comparator_9_eq,
       comparator_10_eq, comparator_11_eq, comparator_12_eq, comparator_13_eq, comparator_14_eq,
       comparator_15_eq, comparator_16_eq, comparator_17_eq, comparator_18_gt, comparator_18_lt,
       decoder_1_out0, decoder_1_out1, decoder_1_out2, decoder_1_out3, decoder_1_out4, decoder_1_out5,
       not_1_out, not_2_out, not_3_out, not_4_out, not_5_out, or_1_out, or_2_out, or_3_out, or_4_out,
       or_5_out, or_6_out, or_7_out, or_8_out, or_10_out, or_11_out, or_12_out, or_13_out, or_14_out,
       or_15_out, or_16_out, or_17_out, or_18_out, or_19_out, pull_resistor_2_node, pull_resistor_3_node,
       pull_resistor_6_node, pull_resistor_9_node, pull_resistor_14_node, pull_resistor_17_node,
       register_5_q, transistor_4_out, transistor_5_out, transistor_7_out, transistor_8_out,
       transistor_10_out, transistor_11_out;
  wire [2:0] adder_2_out, bit_extender_1_out, register_2_q;
  wire [7:0] adder_1_out, adder_3_out, DI_q, multiplexer_1_out, multiplexer_2_out, multiplexer_3_out,
       multiplexer_4_out, register_1_q, register_3_q, register_4_q, SP_q, subtractor_1_out, transistor_20_out;
  wire [31:0] transistor_1_out;

  Transistor #(.\type ("n"), .width(32)) transistor_1 (.in(DATA_IN), .out(transistor_1_out), .gate(SEL));
  Pull_Resistor pull_resistor_1 (.node(transistor_1_out));
  not not_1 (not_1_out, zero);
  Comparator #(.width(16)) comparator_1 (
    .a(transistor_1_out[31:16]), .b(16'he05b), .eq(comparator_1_eq));  // open: gt, lt
  Pull_Resistor pull_resistor_2 (.node(pull_resistor_2_node));
  Transistor #(.\type ("n")) transistor_2 (.in(comparator_1_eq), .out(pull_resistor_2_node), .gate(not_1_out));
  Comparator #(.width(16)) comparator_2 (
    .a(transistor_1_out[31:16]), .b(16'he05a), .eq(comparator_2_eq));  // open: gt, lt
  not not_2 (not_2_out, carry);
  Pull_Resistor pull_resistor_3 (.node(pull_resistor_3_node));
  Comparator #(.width(16)) comparator_3 (
    .a(transistor_1_out[31:16]), .b(16'he059), .eq(comparator_3_eq));  // open: gt, lt
  Transistor #(.\type ("n")) transistor_3 (.in(comparator_3_eq), .out(pull_resistor_3_node), .gate(not_2_out));
  Comparator #(.width(16)) comparator_4 (
    .a(transistor_1_out[31:16]), .b(16'he058), .eq(comparator_4_eq));  // open: gt, lt
  not not_3 (not_3_out, zero);
  Transistor #(.\type ("n")) transistor_4 (.in(comparator_5_eq), .out(transistor_4_out), .gate(not_3_out));
  Pull_Resistor pull_resistor_4 (.node(transistor_4_out));
  Comparator #(.width(16)) comparator_5 (
    .a(transistor_1_out[31:16]), .b(16'hfffd), .eq(comparator_5_eq));  // open: gt, lt
  Comparator #(.width(16)) comparator_6 (
    .a(transistor_1_out[31:16]), .b(16'hfffc), .eq(comparator_6_eq));  // open: gt, lt
  not not_4 (not_4_out, carry);
  Comparator #(.width(16)) comparator_7 (
    .a(transistor_1_out[31:16]), .b(16'hfffb), .eq(comparator_7_eq));  // open: gt, lt
  Transistor #(.\type ("n")) transistor_5 (.in(comparator_7_eq), .out(transistor_5_out), .gate(not_4_out));
  Pull_Resistor pull_resistor_5 (.node(transistor_5_out));
  Comparator #(.width(16)) comparator_8 (
    .a(transistor_1_out[31:16]), .b(16'hfffa), .eq(comparator_8_eq));  // open: gt, lt
  Comparator #(.width(16)) comparator_9 (
    .a(transistor_1_out[31:16]), .b(16'hb4d7), .eq(comparator_9_eq));  // open: gt, lt
  Comparator #(.width(16)) comparator_10 (
    .a(transistor_1_out[31:16]), .b(16'hb4b6), .eq(comparator_10_eq));  // open: gt, lt
  Comparator #(.width(16)) comparator_11 (
    .a(transistor_1_out[31:16]), .b(16'he057), .eq(comparator_11_eq));  // open: gt, lt
  or or_1 (or_1_out, comparator_11_eq, comparator_9_eq, or_6_out);
  Comparator #(.width(16)) comparator_12 (
    .a(transistor_1_out[31:16]), .b({16{1'b1}}), .eq(comparator_12_eq));  // open: gt, lt
  or or_2 (or_2_out, comparator_12_eq, comparator_10_eq, or_7_out);
  and and_1 (and_1_out, decoder_1_out0, or_2_out);
  and and_2 (and_2_out, ~or_17_out, or_5_out);  // AND_Gate
  Register DI (.D(transistor_1_out[15:8]), .en(and_1_out), .Q(DI_q), .clk(CLK), .clr(or_3_out));
  Pull_Resistor pull_resistor_6 (.node(pull_resistor_6_node));
  Transistor transistor_6 (.in(and_1_out), .out(pull_resistor_6_node), .gate(or_17_out));
  and and_3 (and_3_out, or_1_out, decoder_1_out2);
  or or_3 (or_3_out, or_12_out, CLR);
  Comparator #(.width(32)) comparator_13 (
    .a(transistor_1_out), .b(32'h4b4676fd), .eq(comparator_13_eq));  // open: gt, lt
  Register register_1 (.D(transistor_1_out[7:0]), .en(and_1_out), .Q(register_1_q), .clk(CLK), .clr(or_3_out));
  Transistor #(.\type ("n")) transistor_7 (.in(comparator_2_eq), .out(transistor_7_out), .gate(zero));
  Pull_Resistor pull_resistor_7 (.node(transistor_7_out));
  Transistor #(.\type ("n")) transistor_8 (.in(comparator_4_eq), .out(transistor_8_out), .gate(carry));
  Pull_Resistor pull_resistor_8 (.node(transistor_8_out));
  Pull_Resistor pull_resistor_9 (.node(pull_resistor_9_node));
  Transistor #(.\type ("n")) transistor_9 (.in(comparator_6_eq), .out(pull_resistor_9_node), .gate(zero));
  Transistor #(.\type ("n")) transistor_10 (.in(comparator_8_eq), .out(transistor_10_out), .gate(carry));
  Pull_Resistor pull_resistor_10 (.node(transistor_10_out));
  Multiplexer #(.width(8), .enable("false")) multiplexer_1 (
    .in0(multiplexer_3_out), .in1(STACK_SEGMENT_IN), .out(multiplexer_1_out), .sel(comparator_13_eq));
  Register SP (.D(multiplexer_1_out), .en(or_4_out), .Q(SP_q), .clk(CLK), .clr(CLR));
  or or_4 (or_4_out, and_2_out, comparator_13_eq);
  or or_5 (or_5_out, and_3_out, pull_resistor_6_node);
  Transistor #(.\type ("n")) transistor_11 (.in(comparator_14_eq), .out(transistor_11_out), .gate(or_19_out));
  Comparator comparator_14 (.a(register_1_q), .b(8'h55), .eq(comparator_14_eq));  // open: gt, lt
  Pull_Resistor pull_resistor_11 (.node(transistor_11_out));
  Comparator comparator_15 (.a(register_1_q), .b(8'h56), .eq(comparator_15_eq));  // open: gt, lt
  Transistor #(.\type ("n")) transistor_12 (.in(comparator_15_eq), .out(MEM), .gate(or_19_out));
  Pull_Resistor pull_resistor_12 (.node(MEM));
  Pull_Resistor pull_resistor_13 (.node(ROM));
  Comparator comparator_16 (.a(register_1_q), .b(8'h57), .eq(comparator_16_eq));  // open: gt, lt
  Transistor #(.\type ("n")) transistor_13 (.in(comparator_16_eq), .out(ROM), .gate(or_19_out));
  or or_6 (or_6_out, pull_resistor_2_node, transistor_7_out, pull_resistor_3_node, transistor_8_out);
  or or_7 (or_7_out, transistor_4_out, pull_resistor_9_node, transistor_5_out, transistor_10_out);
  Multiplexer #(.width(8), .enable("false")) multiplexer_2 (
    .in0({8{1'b0}}), .in1(DI_q), .out(multiplexer_2_out), .sel(or_2_out));
  Subtractor subtractor_1 (.a(SP_q), .b(8'h1), .out(subtractor_1_out));  // open: bin, bout
  Adder adder_1 (.a(SP_q), .b(8'h1), .out(adder_1_out));  // open: cin, cout
  Pull_Resistor pull_resistor_14 (.node(pull_resistor_14_node));
  Transistor #(.gate("br")) transistor_14 (.in(and_3_out), .out(pull_resistor_14_node), .gate(comparator_17_eq));
  or or_8 (or_8_out, LTSI_EN, or_1_out);
  Pull_Resistor pull_resistor_15 (.node(RAM_R));
  Transistor #(.\type ("n")) transistor_15 (.in(or_16_out), .out(RAM_R), .gate(or_8_out));
  Transistor transistor_16 (.in(or_16_out), .out(RAM_W), .gate(or_8_out));
  Pull_Resistor pull_resistor_16 (.node(RAM_W));
  or or_9 (RAM, or_16_out, transistor_11_out);
  Bit_Extender #(.out_width(3)) bit_extender_1 (.in(register_1_q), .out(bit_extender_1_out));
  or or_10 (or_10_out, or_1_out, or_2_out);
  Comparator comparator_17 (.a({8{1'b0}}), .b(SP_q), .eq(comparator_17_eq));  // open: gt, lt
  Multiplexer #(.width(8), .enable("false")) multiplexer_3 (
    .in0(subtractor_1_out), .in1(adder_1_out), .out(multiplexer_3_out), .sel(pull_resistor_14_node));
  Register #(.width(3)) register_2 (.D(adder_2_out), .en(or_10_out), .Q(register_2_q), .clk(CLK), .clr(or_11_out));
  Adder #(.width(3)) adder_2 (.a(register_2_q), .b(3'b001), .out(adder_2_out));  // open: cin, cout
  or or_11 (or_11_out, CLR, or_12_out);
  Pull_Resistor pull_resistor_17 (.node(pull_resistor_17_node));
  or or_12 (or_12_out, decoder_1_out5, pull_resistor_17_node, and_15_out);
  Transistor #(.\type ("n"), .gate("br")) transistor_17 (
    .in(decoder_1_out3), .out(pull_resistor_17_node), .gate(and_4_out));
  and and_4 (and_4_out, or_1_out, register_5_q);
  or or_13 (or_13_out, CLR, ~or_1_out);  // OR_Gate
  Transistor #(.\type ("n"), .gate("br"), .width(3)) transistor_18 (
    .in(bit_extender_1_out), .out(LTSI_SEL), .gate(LTSI_EN));
  Pull_Resistor pull_resistor_18 (.node(LTSI_SEL));
  Pull_Resistor pull_resistor_19 (.node(C_SEL));
  Transistor #(.\type ("n"), .width(3)) transistor_19 (.in(bit_extender_1_out), .out(C_SEL), .gate(comparator_10_eq));
  Register register_3 (.D(PC_IN), .en(and_16_out), .Q(register_3_q), .clk(not_5_out), .clr(CLR));
  Transistor #(.\type ("n"), .gate("br"), .width(8)) transistor_20 (
    .in(SP_q), .out(transistor_20_out), .gate(or_18_out));
  Register register_4 (.D(SP_q), .en(and_5_out), .Q(register_4_q), .clk(not_5_out), .clr(CLR));
  and and_5 (and_5_out, or_17_out, ~or_14_out);  // AND_Gate
  not not_5 (not_5_out, CLK);
  or or_14 (or_14_out, pull_resistor_6_node, and_3_out);
  or or_15 (or_15_out, pull_resistor_6_node, and_11_out);
  Decoder #(.select(3), .enable("false")) decoder_1 (
    .out0(decoder_1_out0), .out1(decoder_1_out1), .out2(decoder_1_out2), .out3(decoder_1_out3),
    .out4(decoder_1_out4), .out5(decoder_1_out5), .sel(register_2_q));  // open: out6, out7
  or or_16 (or_16_out, decoder_1_out2, and_12_out, and_6_out);
  and and_6 (and_6_out, decoder_1_out3, ~or_1_out);  // AND_Gate
  and and_7 (and_7_out, decoder_1_out3, or_1_out);
  Register #(.width(1), .trigger("high")) register_5 (
    .D(and_7_out), .Q(register_5_q), .clk(CLK), .clr(or_13_out));  // open: en
  and and_8 (LTSI_EN, decoder_1_out4, comparator_9_eq);
  and and_9 (C_EN, decoder_1_out4, comparator_10_eq);
  Transistor #(.\type ("n"), .gate("br"), .width(8)) transistor_21 (.in(adder_3_out), .out(BROD), .gate(BROD_2));
  Adder adder_3 (.a(register_3_q), .b(8'h1), .out(adder_3_out));  // open: cin, cout
  Pull_Resistor pull_resistor_20 (.node(BROD));
  and and_10 (BROD_2, or_18_out, ~or_1_out);  // AND_Gate
  Multiplexer #(.width(8), .enable("false")) multiplexer_4 (
    .in0(multiplexer_2_out), .in1(transistor_20_out), .out(multiplexer_4_out), .sel(or_18_out));
  Pull_Resistor pull_resistor_21 (.node(multiplexer_4_out));
  or or_17 (or_17_out, comparator_18_gt, comparator_18_lt);
  Comparator comparator_18 (.a(SP_q), .b(register_4_q), .gt(comparator_18_gt), .lt(comparator_18_lt));  // open: eq
  or or_18 (or_18_out, decoder_1_out1, decoder_1_out2);
  or or_19 (or_19_out, decoder_1_out3, decoder_1_out4);
  and and_11 (and_11_out, or_1_out, ~register_5_q, decoder_1_out0);  // AND_Gate
  and and_12 (and_12_out, decoder_1_out2, or_1_out);
  Transistor #(.gate("br"), .width(8)) transistor_22 (.in(multiplexer_4_out), .out(ADDR), .gate(and_13_out));
  Pull_Resistor pull_resistor_22 (.node(ADDR));
  and and_13 (and_13_out, or_1_out, decoder_1_out2);
  Pull_Resistor pull_resistor_23 (.node(PC_LOAD));
  Transistor #(.\type ("n"), .width(2)) transistor_23 (.in(2'b10), .out(PC_LOAD), .gate(and_13_out));
  and and_14 (SEL_ADDR, decoder_1_out4, ~or_1_out);  // AND_Gate
  and and_15 (and_15_out, decoder_1_out4, or_1_out);
  and and_16 (and_16_out, or_15_out, decoder_1_out0);
  not not_6 (PC_LOAD_2, and_16_out);
  nor nor_1 (STATUS, and_11_out, or_18_out, or_14_out, or_19_out);

  // Notes on the sheet:
  //   RET
  //   RET
  //   RET
  //   RET
  //   CALL
  //   CALL
  //   CALL
  //   CALL
  //   POP
  //   PUSH
  //   RET
  //   CALL
endmodule

module MOV_B (
  input  [31:0] DATA_IN,
  input  [7:0] PC_IN,
  input  CLR,
  input  CLK,
  input  [7:0] ACC_IN,
  output [7:0] BROD,
  output STATUS,
  output ROM,
  output MEM_R,
  output RAM_R,
  output I_O_R,
  output MEM_W,
  output RAM_W,
  output I_O_W,
  output [2:0] LTSI,
  output MAIN_0,
  output [2:0] C_SEL,
  output D_BUS_3,
  output C_EN,
  output MAIN_2,
  output LTSI_EN,
  output I_O_3,
  output D_BUS_1,
  output D_BUS_2,
  output PC_LOAD_2,
  output [7:0] ADDRESS,
  output sel_addr
);

  wire ALU_W_q, and_1_out, and_2_out, and_3_out, and_4_out, and_5_out, and_6_out, and_7_out, and_11_out,
       and_12_out, and_13_out, and_14_out, and_15_out, and_16_out, and_17_out, and_18_out, and_19_out,
       and_20_out, and_21_out, and_22_out, and_23_out, and_24_out, and_25_out, and_26_out, C_EN_q,
       comparator_1_eq, comparator_2_eq, comparator_3_eq, comparator_4_eq, comparator_5_eq, comparator_6_eq,
       comparator_7_eq, comparator_8_eq, comparator_9_eq, comparator_10_eq, comparator_10_gt,
       comparator_10_lt, comparator_11_eq, comparator_11_gt, comparator_11_lt, comparator_12_eq,
       comparator_13_eq, comparator_13_gt, comparator_13_lt, comparator_14_eq, comparator_14_gt,
       comparator_14_lt, comparator_15_eq, comparator_15_gt, comparator_15_lt, comparator_16_eq,
       comparator_16_gt, comparator_16_lt, comparator_17_eq, comparator_18_eq, comparator_19_eq,
       comparator_20_eq, comparator_21_eq, comparator_22_eq, comparator_22_gt, comparator_22_lt,
       comparator_23_eq, comparator_23_gt, comparator_23_lt, comparator_24_eq, comparator_24_gt,
       comparator_24_lt, comparator_25_eq, counter_1_q, d_ff_1_q, d_ff_2_q, d_ff_3_q, decoder_1_out1,
       decoder_1_out2, decoder_1_out4, decoder_1_out5, I_O_2_out, I_O_out, LTSI_EN_q, MEM_2_out, MEM_out,
       not_1_out, not_2_out, not_3_out, not_4_out, not_6_out, not_7_out, or_1_out, or_2_out, or_3_out,
       or_4_out, or_5_out, or_6_out, or_7_out, or_8_out, or_9_out, or_10_out, or_11_out, or_12_out,
       or_13_out_2, or_14_out, or_15_out, or_18_out, or_19_out, or_20_out, or_21_out, or_22_out, or_23_out,
       or_24_out, or_25_out, or_26_out, or_27_out, or_28_out, or_30_out, or_31_out, or_32_out, or_33_out,
       or_34_out, or_35_out, or_36_out, or_37_out, or_38_out, or_39_out, or_40_out, or_41_out, or_42_out,
       or_43_out, or_44_out, or_45_out, pull_resistor_9_node, pull_resistor_10_node, pull_resistor_11_node,
       pull_resistor_12_node, pull_resistor_14_node, pull_resistor_15_node, pull_resistor_16_node, RAM_2_out,
       RAM_out, register_1_q, ROM_out, t_ff_1_q, transistor_1_out, transistor_3_out, transistor_4_out;
  wire [2:0] counter_2_q;
  wire [3:0] bit_extender_1_out, bit_extender_2_out, C_q, DEV_q, LTSI_q, multiplexer_1_out,
       multiplexer_3_out, pull_resistor_3_node, pull_resistor_5_node, transistor_6_out;
  wire [7:0] adder_1_out, ADDR, and_9_out, and_10_out, bit_extender_3_out, bit_extender_4_out,
       bit_extender_7_out, GO_TO_q, multiplexer_2_out, or_17_out, RET_q, transistor_19_out,
       transistor_20_out, xor_1_out;
  wire [11:0] START_q, STOP_q;

  Comparator comparator_1 (.a(DATA_IN[31:24]), .b(8'h7), .eq(comparator_1_eq));  // open: gt, lt
  or or_1 (or_1_out, and_7_out, and_26_out, CLR);
  and and_1 (and_1_out, ~counter_1_q, comparator_1_eq);  // AND_Gate
  Transistor #(.\type ("n")) transistor_1 (.in(CLK), .out(transistor_1_out), .gate(comparator_1_eq));
  Comparator comparator_2 (.a(RET_q), .b({8{1'b0}}), .eq(comparator_2_eq));  // open: gt, lt
  and and_2 (and_2_out, comparator_2_eq, comparator_3_eq);
  Comparator comparator_3 (.a(GO_TO_q), .b({8{1'b0}}), .eq(comparator_3_eq));  // open: gt, lt
  Counter #(.width(1), .max('h1)) counter_1 (
    .Q(counter_1_q), .clk(transistor_1_out), .clr(or_1_out));  // open: load, D, count, carry
  Comparator comparator_4 (.a(PC_IN), .b({8{1'b0}}), .eq(comparator_4_eq));  // open: gt, lt
  Bit_Extender #(.out_width(4)) bit_extender_1 (.in(DATA_IN[15:8]), .out(bit_extender_1_out));
  Bit_Extender #(.out_width(4)) bit_extender_2 (.in(DATA_IN[23:16]), .out(bit_extender_2_out));
  Comparator comparator_5 (.a(DATA_IN[31:24]), .b(8'h8), .eq(comparator_5_eq));  // open: gt, lt
  Comparator comparator_6 (.a(DATA_IN[31:24]), .b(8'h9), .eq(comparator_6_eq));  // open: gt, lt
  Comparator comparator_7 (.a(DATA_IN[31:24]), .b(8'h5), .eq(comparator_7_eq));  // open: gt, lt
  Comparator comparator_8 (.a(DATA_IN[31:24]), .b(8'ha), .eq(comparator_8_eq));  // open: gt, lt
  Adder adder_1 (.a(PC_IN), .b(8'h1), .out(adder_1_out));  // open: cin, cout
  not not_1 (not_1_out, and_2_out);
  or or_2 (or_2_out, CLR, or_26_out);
  D_Flip_Flop d_ff_1 (
    .clk(comparator_8_eq), .D(comparator_8_eq), .Q(d_ff_1_q), .reset(or_14_out));  // open: Qn, preset, en
  Transistor #(.\type ("n"), .width(8)) transistor_2 (.in(START_q[11:4]), .out(ADDR), .gate(and_1_out));
  Pull_Resistor pull_resistor_1 (.node(ADDR));
  Register #(.width(12), .trigger("high")) START (
    .D(DATA_IN[11:0]), .en(and_1_out), .Q(START_q), .clk(CLK), .clr(or_1_out));
  Register #(.width(12), .trigger("high")) STOP (
    .D(DATA_IN[23:12]), .en(and_1_out), .Q(STOP_q), .clk(CLK), .clr(or_1_out));
  D_Flip_Flop d_ff_2 (.clk(and_1_out), .D(and_1_out), .Q(d_ff_2_q), .reset(or_1_out));  // open: Qn, preset, en
  or or_3 (or_3_out, and_6_out, or_25_out);
  Comparator #(.width(4)) comparator_9 (.a(DATA_IN[11:8]), .b(4'b1111), .eq(comparator_9_eq));  // open: gt, lt
  or or_4 (or_4_out, comparator_12_eq, comparator_9_eq);
  Multiplexer #(.width(4), .enable("false")) multiplexer_1 (
    .in0(4'b0101), .in1(bit_extender_1_out), .out(multiplexer_1_out), .sel(not_2_out));
  not not_2 (not_2_out, comparator_9_eq);
  or or_5 (or_5_out, comparator_8_eq, or_6_out);
  or or_6 (or_6_out, and_3_out, comparator_7_eq, comparator_5_eq);
  buf and_3 (and_3_out, comparator_6_eq);  // AND_Gate
  or or_7 (or_7_out, and_3_out, comparator_7_eq, comparator_5_eq);
  not not_3 (not_3_out, or_4_out);
  or or_8 (or_8_out, comparator_8_eq, or_7_out);
  and and_4 (and_4_out, comparator_8_eq, not_3_out);
  assign bit_extender_3_out = {{7{or_4_out}}, or_4_out};  // Bit_Extender bit_extender_3
  assign bit_extender_4_out = {{7{comparator_8_eq}}, comparator_8_eq};  // Bit_Extender bit_extender_4
  and and_5 (and_5_out, not_6_out, or_8_out);
  Multiplexer #(.width(8), .enable("false")) multiplexer_2 (
    .in0(DATA_IN[7:0]), .in1(ACC_IN), .out(multiplexer_2_out), .sel(and_4_out));
  Transistor #(.\type ("n")) transistor_3 (.in(or_8_out), .out(transistor_3_out), .gate(not_1_out));
  Register #(.width(1), .trigger("high")) register_1 (
    .D(transistor_3_out), .Q(register_1_q), .clk(transistor_3_out), .clr(or_14_out));  // open: en
  Pull_Resistor pull_resistor_2 (.node(transistor_3_out));
  Comparator comparator_10 (
    .a(START_q[11:4]), .b(PC_IN), .gt(comparator_10_gt), .eq(comparator_10_eq), .lt(comparator_10_lt));
  or or_9 (or_9_out, comparator_10_gt, comparator_10_lt);
  Comparator comparator_11 (
    .a(STOP_q[11:4]), .b(PC_IN), .gt(comparator_11_gt), .eq(comparator_11_eq), .lt(comparator_11_lt));
  or or_10 (or_10_out, comparator_11_gt, comparator_11_lt);
  not not_4 (not_4_out, comparator_4_eq);
  and and_6 (and_6_out, comparator_10_eq, not_4_out, d_ff_2_q);
  and and_7 (and_7_out, comparator_11_eq, not_4_out, d_ff_2_q);
  T_Flip_Flop t_ff_1 (.clk(or_3_out), .T(or_3_out), .Q(t_ff_1_q), .reset(or_11_out));  // open: Qn, preset, en
  not not_5 (STATUS, t_ff_1_q);
  or or_11 (or_11_out, and_7_out, CLR, or_2_out);
  Comparator #(.width(4)) comparator_12 (.a(DATA_IN[11:8]), .b(4'b1110), .eq(comparator_12_eq));  // open: gt, lt
  Register #(.width(4)) DEV (.D(multiplexer_3_out), .en(or_5_out), .Q(DEV_q), .clk(CLK), .clr(or_2_out));
  Register #(.width(4)) u_LTSI (.D(bit_extender_2_out), .en(comparator_5_eq), .Q(LTSI_q), .clk(CLK), .clr(or_2_out));
  Register #(.width(4)) C (.D(bit_extender_2_out), .en(or_12_out), .Q(C_q), .clk(CLK), .clr(or_2_out));
  or or_12 (or_12_out, and_3_out, comparator_8_eq);
  D_Flip_Flop u_C_EN (.clk(or_12_out), .D(or_12_out), .Q(C_EN_q), .reset(or_2_out));  // open: Qn, preset, en
  D_Flip_Flop u_LTSI_EN (
    .clk(comparator_5_eq), .D(comparator_5_eq), .Q(LTSI_EN_q), .reset(or_2_out));  // open: Qn, preset, en
  D_Flip_Flop ALU_W (
    .clk(comparator_7_eq), .D(comparator_7_eq), .Q(ALU_W_q), .reset(or_2_out));  // open: Qn, preset, en
  OR or_13 (.in_1(RET_q), .out_2(or_13_out_2));
  Register RET (.D(adder_1_out), .en(and_5_out), .Q(RET_q), .clk(CLK), .clr(or_2_out));
  Register GO_TO (.D(multiplexer_2_out), .en(or_8_out), .Q(GO_TO_q), .clk(CLK), .clr(or_2_out));
  Counter #(.width(3), .max('h7)) counter_2 (
    .Q(counter_2_q), .clk(transistor_4_out), .clr(or_14_out));  // open: load, D, count, carry
  or or_14 (or_14_out, or_2_out, or_26_out);
  Transistor #(.\type ("n")) transistor_4 (.in(CLK), .out(transistor_4_out), .gate(or_19_out));
  and and_8 (sel_addr, register_1_q, ~transistor_3_out);  // AND_Gate
  Comparator #(.width(4)) comparator_13 (
    .a(START_q[3:0]), .b(4'b0110), .gt(comparator_13_gt), .eq(comparator_13_eq), .lt(comparator_13_lt));
  Comparator #(.width(4)) comparator_14 (
    .a(START_q[3:0]), .b(4'b1000), .gt(comparator_14_gt), .eq(comparator_14_eq), .lt(comparator_14_lt));
  Comparator #(.width(4)) comparator_15 (
    .a(START_q[3:0]), .b(4'b0100), .gt(comparator_15_gt), .eq(comparator_15_eq), .lt(comparator_15_lt));
  Comparator #(.width(4)) comparator_16 (
    .a(START_q[3:0]), .b(4'b0101), .gt(comparator_16_gt), .eq(comparator_16_eq), .lt(comparator_16_lt));
  or or_15 (or_15_out, or_9_out, or_10_out);
  and RAM (RAM_out, ~STATUS, comparator_16_eq);  // AND_Gate
  Multiplexer #(.width(4), .enable("false")) multiplexer_3 (
    .in0(multiplexer_1_out), .in1(4'b0100), .out(multiplexer_3_out), .sel(comparator_12_eq));
  Pull_Resistor pull_resistor_3 (.node(pull_resistor_3_node));
  Transistor #(.\type ("n"), .width(4)) transistor_5 (.in(DEV_q), .out(pull_resistor_3_node), .gate(or_25_out));
  Bit_Extender #(.in_width(4), .out_width(3)) bit_extender_5 (.in(transistor_6_out), .out(LTSI));
  Transistor #(.\type ("n"), .width(4)) transistor_6 (.in(LTSI_q), .out(transistor_6_out), .gate(or_25_out));
  Pull_Resistor pull_resistor_4 (.node(transistor_6_out));
  Pull_Resistor pull_resistor_5 (.node(pull_resistor_5_node));
  Bit_Extender #(.in_width(4), .out_width(3)) bit_extender_6 (.in(pull_resistor_5_node), .out(C_SEL));
  Transistor #(.\type ("n"), .width(4)) transistor_7 (.in(C_q), .out(pull_resistor_5_node), .gate(or_25_out));
  Pull_Resistor pull_resistor_6 (.node(C_EN));
  Transistor #(.\type ("n")) transistor_8 (.in(C_EN_q), .out(C_EN), .gate(or_25_out));
  Transistor #(.\type ("n")) transistor_9 (.in(LTSI_EN_q), .out(LTSI_EN), .gate(or_25_out));
  Pull_Resistor pull_resistor_7 (.node(LTSI_EN));
  Transistor #(.\type ("n")) transistor_10 (.in(ALU_W_q), .out(D_BUS_2), .gate(or_25_out));
  Pull_Resistor pull_resistor_8 (.node(D_BUS_2));
  not not_6 (not_6_out, or_13_out_2);
  assign and_9_out = RET_q & bit_extender_7_out;  // AND_Gate and_9, 8 bits wide
  assign ADDRESS = ADDR | or_17_out;  // OR_Gate or_16, 8 bits wide
  assign or_17_out = and_9_out | and_10_out;  // OR_Gate or_17, 8 bits wide
  assign and_10_out = ~bit_extender_7_out & GO_TO_q;  // AND_Gate and_10, 8 bits wide
  Comparator comparator_17 (.a(GO_TO_q), .b(PC_IN), .eq(comparator_17_eq));  // open: gt, lt
  or or_18 (or_18_out, and_11_out, or_30_out);
  and and_11 (and_11_out, comparator_17_eq, register_1_q);
  and and_12 (and_12_out, comparator_17_eq, register_1_q, or_30_out);
  Decoder #(.select(3), .enable("false")) decoder_1 (
    .out1(decoder_1_out1), .out2(decoder_1_out2), .out4(decoder_1_out4), .out5(decoder_1_out5),
    .sel(counter_2_q));  // open: out0, out3, out6, out7
  or or_19 (or_19_out, and_16_out, d_ff_1_q);
  and and_13 (and_13_out, d_ff_1_q, decoder_1_out5);
  or or_20 (or_20_out, comparator_13_gt, comparator_13_lt);
  or or_21 (or_21_out, comparator_14_gt, comparator_14_lt);
  or or_22 (or_22_out, comparator_15_gt, comparator_15_lt);
  or or_23 (or_23_out, comparator_16_gt, comparator_16_lt);
  and I_O (I_O_out, ~STATUS, comparator_14_eq);  // AND_Gate
  and MEM (MEM_out, ~STATUS, comparator_15_eq);  // AND_Gate
  Comparator #(.width(4)) comparator_18 (.a(pull_resistor_3_node), .b(4'b0110), .eq(comparator_18_eq));  // open: gt, lt
  Comparator #(.width(4)) comparator_19 (.a(pull_resistor_3_node), .b(4'b0100), .eq(comparator_19_eq));  // open: gt, lt
  Comparator #(.width(4)) comparator_20 (.a(pull_resistor_3_node), .b(4'b0101), .eq(comparator_20_eq));  // open: gt, lt
  Comparator #(.width(4)) comparator_21 (.a(pull_resistor_3_node), .b(4'b1000), .eq(comparator_21_eq));  // open: gt, lt
  or or_24 (or_24_out, D_BUS_2, C_EN, PC_LOAD_2);
  D_Flip_Flop d_ff_3 (
    .clk(comparator_8_eq), .D(comparator_8_eq), .Q(d_ff_3_q), .reset(or_2_out));  // open: Qn, preset, en
  assign bit_extender_7_out = {{7{and_12_out}}, and_12_out};  // Bit_Extender bit_extender_7
  or or_25 (or_25_out, or_30_out, and_16_out);
  and and_14 (and_14_out, decoder_1_out2, ~d_ff_1_q);  // AND_Gate
  or or_26 (or_26_out, and_13_out, and_14_out);
  Comparator #(.width(4)) comparator_22 (
    .a(STOP_q[3:0]), .b(4'b1000), .gt(comparator_22_gt), .eq(comparator_22_eq), .lt(comparator_22_lt));
  Comparator #(.width(4)) comparator_23 (
    .a(STOP_q[3:0]), .b(4'b0100), .gt(comparator_23_gt), .eq(comparator_23_eq), .lt(comparator_23_lt));
  and and_15 (and_15_out, or_20_out, or_21_out, or_22_out, or_23_out);
  Comparator #(.width(4)) comparator_24 (
    .a(STOP_q[3:0]), .b(4'b0101), .gt(comparator_24_gt), .eq(comparator_24_eq), .lt(comparator_24_lt));
  or or_27 (or_27_out, and_15_out, or_15_out);
  and u_ROM (ROM_out, ~STATUS, comparator_13_eq);  // AND_Gate
  or or_28 (or_28_out, RAM_out, MEM_out, ROM_out);
  Pull_Resistor pull_resistor_9 (.node(pull_resistor_9_node));
  Transistor #(.\type ("n")) transistor_11 (.in(comparator_18_eq), .out(pull_resistor_9_node), .gate(LTSI_EN));
  Pull_Resistor pull_resistor_10 (.node(pull_resistor_10_node));
  Transistor #(.\type ("n")) transistor_12 (.in(comparator_19_eq), .out(pull_resistor_10_node), .gate(LTSI_EN));
  Pull_Resistor pull_resistor_11 (.node(pull_resistor_11_node));
  Transistor #(.\type ("n")) transistor_13 (.in(comparator_20_eq), .out(pull_resistor_11_node), .gate(LTSI_EN));
  Pull_Resistor pull_resistor_12 (.node(pull_resistor_12_node));
  Transistor #(.\type ("n")) transistor_14 (.in(comparator_21_eq), .out(pull_resistor_12_node), .gate(LTSI_EN));
  or or_29 (D_BUS_1, C_EN, PC_LOAD_2);
  Pull_Resistor pull_resistor_13 (.node(PC_LOAD_2));
  Transistor #(.\type ("n")) transistor_15 (.in(d_ff_3_q), .out(PC_LOAD_2), .gate(or_25_out));
  and and_16 (and_16_out, or_18_out, ~d_ff_1_q);  // AND_Gate
  and and_17 (and_17_out, decoder_1_out4, d_ff_1_q);
  or or_30 (or_30_out, and_17_out, and_18_out);
  and and_18 (and_18_out, ~d_ff_1_q, decoder_1_out1);  // AND_Gate
  or or_31 (or_31_out, comparator_22_gt, comparator_22_lt);
  or or_32 (or_32_out, comparator_23_gt, comparator_23_lt);
  or or_33 (or_33_out, comparator_24_gt, comparator_24_lt);
  and MEM_2 (MEM_2_out, ~STATUS, comparator_23_eq);  // AND_Gate
  and RAM_2 (RAM_2_out, ~STATUS, comparator_24_eq);  // AND_Gate
  Pull_Resistor pull_resistor_14 (.node(pull_resistor_14_node));
  Transistor #(.\type ("n")) transistor_16 (.in(comparator_19_eq), .out(pull_resistor_14_node), .gate(or_24_out));
  Pull_Resistor pull_resistor_15 (.node(pull_resistor_15_node));
  Transistor #(.\type ("n")) transistor_17 (.in(comparator_20_eq), .out(pull_resistor_15_node), .gate(or_24_out));
  Pull_Resistor pull_resistor_16 (.node(pull_resistor_16_node));
  Transistor #(.\type ("n")) transistor_18 (.in(comparator_21_eq), .out(pull_resistor_16_node), .gate(or_24_out));
  or or_34 (or_34_out, pull_resistor_9_node, pull_resistor_10_node, pull_resistor_11_node);
  and and_19 (and_19_out, or_31_out, or_32_out, or_33_out);
  or or_35 (or_35_out, and_19_out, or_27_out);
  and I_O_2 (I_O_2_out, ~STATUS, comparator_22_eq);  // AND_Gate
  or or_36 (or_36_out, RAM_2_out, MEM_2_out);
  or or_37 (or_37_out, pull_resistor_9_node, ROM_out);
  or or_38 (or_38_out, pull_resistor_10_node, MEM_out);
  or or_39 (or_39_out, pull_resistor_11_node, RAM_out);
  or or_40 (or_40_out, pull_resistor_12_node, I_O_out);
  or or_41 (or_41_out, pull_resistor_14_node, MEM_2_out);
  or or_42 (or_42_out, pull_resistor_15_node, RAM_2_out);
  or or_43 (or_43_out, pull_resistor_16_node, I_O_2_out);
  or or_44 (or_44_out, or_28_out, and_20_out);
  and and_20 (and_20_out, or_34_out, LTSI_EN);
  or or_45 (or_45_out, I_O_out, and_21_out);
  and and_21 (and_21_out, pull_resistor_12_node, LTSI_EN);
  and and_22 (and_22_out, ~and_15_out, and_24_out, and_19_out);  // AND_Gate
  and and_23 (and_23_out, ~and_19_out, and_24_out, and_15_out);  // AND_Gate
  and and_24 (and_24_out, d_ff_2_q, or_35_out);
  Transistor #(.\type ("n"), .width(8)) transistor_19 (
    .in({4'b0110, START_q[3:0]}), .out(transistor_19_out), .gate(and_22_out));
  Transistor #(.\type ("n"), .width(8)) transistor_20 (
    .in({4'b0101, STOP_q[3:0]}), .out(transistor_20_out), .gate(and_23_out));
  T_Flip_Flop ROM_2 (.clk(or_37_out), .T(or_37_out), .Q(ROM), .reset(or_11_out));  // open: Qn, preset, en
  T_Flip_Flop u_MEM_R (.clk(or_38_out), .T(or_38_out), .Q(MEM_R), .reset(or_11_out));  // open: Qn, preset, en
  T_Flip_Flop u_RAM_R (.clk(or_39_out), .T(or_39_out), .Q(RAM_R), .reset(or_11_out));  // open: Qn, preset, en
  T_Flip_Flop u_I_O_R (.clk(or_40_out), .T(or_40_out), .Q(I_O_R), .reset(or_11_out));  // open: Qn, preset, en
  T_Flip_Flop u_MEM_W (.clk(or_41_out), .T(or_41_out), .Q(MEM_W), .reset(or_11_out));  // open: Qn, preset, en
  T_Flip_Flop u_RAM_W (.clk(or_42_out), .T(or_42_out), .Q(RAM_W), .reset(or_11_out));  // open: Qn, preset, en
  T_Flip_Flop u_I_O_W (.clk(or_43_out), .T(or_43_out), .Q(I_O_W), .reset(or_11_out));  // open: Qn, preset, en
  T_Flip_Flop t_ff_2 (.clk(or_44_out), .T(or_44_out), .Q(MAIN_0), .reset(or_11_out));  // open: Qn, preset, en
  T_Flip_Flop t_ff_3 (.clk(or_36_out), .T(or_36_out), .Q(D_BUS_3), .reset(or_11_out));  // open: Qn, preset, en
  T_Flip_Flop t_ff_4 (.clk(or_45_out), .T(or_45_out), .Q(MAIN_2), .reset(or_11_out));  // open: Qn, preset, en
  T_Flip_Flop t_ff_5 (.clk(I_O_2_out), .T(I_O_2_out), .Q(I_O_3), .reset(or_11_out));  // open: Qn, preset, en
  and and_25 (and_25_out, and_23_out, and_22_out);
  Pull_Resistor pull_resistor_17 (.node(transistor_19_out));
  assign xor_1_out = transistor_19_out ^ transistor_20_out;  // XOR_Gate xor_1, 8 bits wide
  Pull_Resistor pull_resistor_18 (.node(transistor_20_out));
  Comparator comparator_25 (.a(xor_1_out), .b({8{1'b0}}), .eq(comparator_25_eq));  // open: gt, lt
  and and_26 (and_26_out, and_25_out, comparator_25_eq);
  not not_7 (not_7_out, and_26_out);
  Transistor #(.\type ("n"), .width(8)) transistor_21 (.in(xor_1_out), .out(BROD), .gate(not_7_out));
  Pull_Resistor pull_resistor_19 (.node(BROD));

  // Notes on the sheet:
  //   READ
  //   WRITE
endmodule
module MOV_OP (
  input  [31:0] DATA_IN,
  input  CLK,
  input  CLR,
  output I_O_W,
  output I_O_MUX_2,
  output I_O_MUX_1,
  output IMMED_SEL,
  output ALU_EN,
  output IMMED_EN,
  output [2:0] A_SEL,
  output [3:0] OP,
  output [2:0] B_SEL,
  output [2:0] C_SEL,
  output [2:0] LTSI,
  output C_EN,
  output LTSI_EN,
  output MAIN_MUX_1,
  output I_O_IN,
  output MAIN_3,
  output PC_LOAD,
  output I_O_DEV_IN,
  output I_O_DEV_IN_CLK,
  output I_O_R
);

  wire and_6_out, comparator_3_eq, comparator_4_eq, comparator_5_eq, comparator_6_eq, comparator_7_eq,
       decoder_1_out0, decoder_1_out2, not_1_out, not_2_out, or_1_out, or_4_out, or_5_out, or_9_out,
       t_ff_1_q, transistor_8_out;
  wire [1:0] counter_1_q;
  wire [2:0] bit_extender_3_out, bit_extender_4_out, bit_extender_5_out, bit_extender_7_out,
       pull_resistor_8_node;
  wire [3:0] bit_extender_2_out;
  wire [7:0] pull_resistor_1_node, pull_resistor_4_node, pull_resistor_6_node, transistor_2_out,
       transistor_3_out, transistor_5_out, transistor_7_out;

  // Probe on DATA_IN[31:8]
  Comparator #(.width(16)) comparator_1 (.a(DATA_IN[31:16]), .b(16'h9a5a), .eq(I_O_IN));  // open: gt, lt
  Comparator #(.width(24)) comparator_2 (.a(DATA_IN[31:8]), .b(24'h36f152), .eq(MAIN_3));  // open: gt, lt
  Comparator #(.width(24)) comparator_3 (.a(DATA_IN[31:8]), .b(24'h82d741), .eq(comparator_3_eq));  // open: gt, lt
  Comparator #(.width(24)) comparator_4 (.a(24'h23a1c2), .b(DATA_IN[31:8]), .eq(comparator_4_eq));  // open: gt, lt
  Comparator comparator_5 (.a(DATA_IN[7:0]), .b(8'h8), .eq(comparator_5_eq));  // open: gt, lt
  Comparator comparator_6 (.a(DATA_IN[31:24]), .b(8'h3), .eq(comparator_6_eq));  // open: gt, lt
  or or_1 (or_1_out, comparator_6_eq, comparator_7_eq);
  Comparator comparator_7 (.a(DATA_IN[31:24]), .b(8'h2), .eq(comparator_7_eq));  // open: gt, lt
  Pull_Resistor pull_resistor_1 (.node(pull_resistor_1_node));
  Transistor #(.\type ("n"), .width(8)) transistor_1 (.in(DATA_IN[23:16]), .out(pull_resistor_1_node), .gate(or_1_out));
  Transistor #(.\type ("n"), .width(8)) transistor_2 (.in(DATA_IN[15:8]), .out(transistor_2_out), .gate(or_1_out));
  Pull_Resistor pull_resistor_2 (.node(transistor_2_out));
  Transistor #(.\type ("n"), .width(8)) transistor_3 (
    .in(DATA_IN[7:0]), .out(transistor_3_out), .gate(comparator_7_eq));
  Pull_Resistor pull_resistor_3 (.node(transistor_3_out));
  T_Flip_Flop t_ff_1 (
    .clk(comparator_3_eq), .T(comparator_3_eq), .Q(t_ff_1_q), .reset(or_5_out));  // open: Qn, preset, en
  or or_2 (I_O_W, I_O_MUX_1, I_O_MUX_2);
  and and_1 (I_O_MUX_1, comparator_4_eq, not_2_out);
  not not_1 (not_1_out, not_2_out);
  not not_2 (not_2_out, comparator_5_eq);
  Pull_Resistor pull_resistor_4 (.node(pull_resistor_4_node));
  Transistor #(.\type ("n"), .width(8)) transistor_4 (
    .in(DATA_IN[7:0]), .out(pull_resistor_4_node), .gate(comparator_4_eq));
  Transistor #(.\type ("n"), .width(8)) transistor_5 (
    .in(pull_resistor_4_node), .out(transistor_5_out), .gate(not_2_out));
  Pull_Resistor pull_resistor_5 (.node(transistor_5_out));
  and and_2 (IMMED_EN, or_1_out, ~comparator_7_eq);  // AND_Gate
  or or_3 (ALU_EN, IMMED_EN, comparator_7_eq);
  Bit_Extender #(.out_width(3)) bit_extender_1 (.in(pull_resistor_1_node), .out(A_SEL));
  Bit_Extender #(.out_width(4)) bit_extender_2 (.in(transistor_2_out), .out(bit_extender_2_out));
  Pull_Resistor pull_resistor_6 (.node(pull_resistor_6_node));
  Transistor #(.\type ("n"), .width(8)) transistor_6 (.in(DATA_IN[7:0]), .out(pull_resistor_6_node), .gate(MAIN_MUX_1));
  Bit_Extender #(.out_width(3)) bit_extender_3 (.in(pull_resistor_6_node), .out(bit_extender_3_out));
  Transistor #(.\type ("n"), .width(8)) transistor_7 (.in(DATA_IN[15:8]), .out(transistor_7_out), .gate(MAIN_MUX_1));
  Pull_Resistor pull_resistor_7 (.node(transistor_7_out));
  Bit_Extender #(.out_width(3)) bit_extender_4 (.in(DATA_IN[7:0]), .out(bit_extender_4_out));
  Comparator #(.width(16)) comparator_8 (.a(DATA_IN[31:16]), .b(16'h12e6), .eq(MAIN_MUX_1));  // open: gt, lt
  or or_4 (or_4_out, MAIN_3, I_O_DEV_IN);
  Counter #(.width(2), .max('h3)) counter_1 (
    .Q(counter_1_q), .clk(transistor_8_out), .clr(or_5_out));  // open: load, D, count, carry
  Decoder #(.select(2), .enable("false")) decoder_1 (
    .out0(decoder_1_out0), .out1(I_O_DEV_IN_CLK), .out2(decoder_1_out2), .sel(counter_1_q));  // open: out3
  or or_5 (or_5_out, CLR, decoder_1_out2);
  Transistor #(.\type ("n")) transistor_8 (.in(CLK), .out(transistor_8_out), .gate(t_ff_1_q));
  and and_3 (I_O_MUX_2, comparator_4_eq, not_1_out);
  Bit_Extender #(.out_width(3)) bit_extender_5 (.in(transistor_5_out), .out(bit_extender_5_out));
  Bit_Extender #(.out_width(3)) bit_extender_6 (.in(transistor_3_out), .out(B_SEL));
  assign C_SEL = bit_extender_5_out | bit_extender_3_out;  // OR_Gate or_6, 3 bits wide
  Bit_Extender #(.out_width(3)) bit_extender_7 (.in(transistor_7_out), .out(bit_extender_7_out));
  or or_7 (C_EN, I_O_MUX_1, MAIN_MUX_1);
  or or_8 (LTSI_EN, I_O_IN, or_4_out, MAIN_MUX_1);
  or or_9 (or_9_out, MAIN_3, I_O_DEV_IN);
  and and_4 (PC_LOAD, t_ff_1_q, decoder_1_out0);
  Register #(.width(4)) register_1 (.D(bit_extender_2_out), .Q(OP), .clk(CLK), .clr(CLR));  // open: en
  assign LTSI = bit_extender_7_out | pull_resistor_8_node;  // OR_Gate or_10, 3 bits wide
  Pull_Resistor pull_resistor_8 (.node(pull_resistor_8_node));
  Transistor #(.\type ("n"), .width(3)) transistor_9 (
    .in(bit_extender_4_out), .out(pull_resistor_8_node), .gate(or_9_out));
  and and_5 (I_O_DEV_IN, t_ff_1_q, ~and_6_out);  // AND_Gate
  and and_6 (and_6_out, I_O_DEV_IN_CLK, ~CLK);  // AND_Gate

  assign I_O_R = I_O_DEV_IN_CLK;
  assign IMMED_SEL = IMMED_EN;
endmodule

module HLT_FENCE (
  input  [31:0] DATA_IN,
  input  [7:0] PC_IN,
  input  CLK,
  input  CLR,
  input  [7:0] I_O_IN,
  output FENCE,
  output PC_LOAD,
  output CLR_IR,
  output CLR_PC,
  output [7:0] ADDRESS
);

  wire and_1_out, and_2_out, and_3_out, and_4_out, comparator_1_eq, comparator_2_eq, comparator_3_eq,
       comparator_4_eq, comparator_5_eq, d_ff_1_q, decoder_1_out1, decoder_1_out2, decoder_2_out3,
       decoder_2_out4, decoder_2_out5, demultiplexer_1_out0, demultiplexer_1_out1, not_1_out, or_1_out,
       or_2_out_2, or_3_out, or_4_out, or_5_out_2, or_6_out_2, or_8_out, or_9_out, or_11_out, t_ff_1_q,
       t_ff_2_q, t_ff_3_q, transistor_3_out, transistor_4_out, transistor_6_out;
  wire [1:0] counter_1_q;
  wire [2:0] counter_2_q;
  wire [7:0] FROM_q, register_1_q, register_2_q, TO_q, transistor_1_out, transistor_2_out;

  Demultiplexer #(.enable("false")) demultiplexer_1 (
    .out0(demultiplexer_1_out0), .out1(demultiplexer_1_out1), .in(transistor_4_out), .sel(d_ff_1_q));
  Comparator #(.width(16)) comparator_1 (.a(DATA_IN[31:16]), .b(16'h5a9b), .eq(comparator_1_eq));  // open: gt, lt
  Register FROM (.D(DATA_IN[15:8]), .en(comparator_1_eq), .Q(FROM_q), .clk(CLK), .clr(or_1_out));
  Register TO (.D(DATA_IN[7:0]), .en(comparator_1_eq), .Q(TO_q), .clk(CLK), .clr(or_1_out));
  or or_1 (or_1_out, CLR, decoder_1_out1);
  Register register_1 (.D(I_O_IN), .en(demultiplexer_1_out0), .Q(register_1_q), .clk(CLK), .clr(or_3_out));
  Register register_2 (.D(I_O_IN), .en(demultiplexer_1_out1), .Q(register_2_q), .clk(CLK), .clr(or_3_out));
  OR or_2 (.in_1(I_O_IN), .out_2(or_2_out_2));
  or or_3 (or_3_out, and_1_out, CLR);
  Comparator comparator_2 (.a(FROM_q), .b(PC_IN), .eq(comparator_2_eq));  // open: gt, lt
  Comparator comparator_3 (.a(TO_q), .b(PC_IN), .eq(comparator_3_eq));  // open: gt, lt
  T_Flip_Flop t_ff_1 (
    .clk(comparator_3_eq), .T(comparator_3_eq), .Q(t_ff_1_q), .reset(or_4_out));  // open: Qn, preset, en
  Transistor #(.\type ("n"), .width(8)) transistor_1 (.in(register_1_q), .out(transistor_1_out), .gate(decoder_2_out3));
  Pull_Resistor pull_resistor_1 (.node(transistor_1_out));
  Transistor #(.\type ("n"), .width(8)) transistor_2 (.in(register_2_q), .out(transistor_2_out), .gate(decoder_2_out3));
  Pull_Resistor pull_resistor_2 (.node(transistor_2_out));
  Comparator comparator_4 (.a(PC_IN), .b(ADDRESS), .eq(comparator_4_eq));  // open: gt, lt
  and and_1 (and_1_out, comparator_4_eq, or_11_out);
  T_Flip_Flop t_ff_2 (
    .clk(comparator_2_eq), .T(comparator_2_eq), .Q(t_ff_2_q), .reset(comparator_3_eq));  // open: Qn, preset, en
  Counter #(.width(2), .max('h3)) counter_1 (
    .Q(counter_1_q), .clk(transistor_3_out), .clr(or_4_out));  // open: load, D, count, carry
  or or_4 (or_4_out, CLR, decoder_1_out2);
  Transistor #(.\type ("n")) transistor_3 (.in(CLK), .out(transistor_3_out), .gate(t_ff_1_q));
  Transistor #(.\type ("n")) transistor_4 (.in(t_ff_3_q), .out(transistor_4_out), .gate(not_1_out));
  Pull_Resistor pull_resistor_3 (.node(transistor_4_out));
  Comparator comparator_5 (.a(transistor_1_out), .b(8'hfc), .eq(comparator_5_eq));  // open: gt, lt
  Pull_Resistor pull_resistor_4 (.node(ADDRESS));
  Transistor #(.\type ("n"), .width(8)) transistor_5 (.in(transistor_2_out), .out(ADDRESS), .gate(comparator_5_eq));
  OR or_5 (.in_1(register_1_q), .out_2(or_5_out_2));
  OR or_6 (.in_1(register_2_q), .out_2(or_6_out_2));
  and and_2 (and_2_out, or_5_out_2, or_6_out_2);
  Decoder #(.select(2), .enable("false")) decoder_1 (
    .out1(decoder_1_out1), .out2(decoder_1_out2), .sel(counter_1_q));  // open: out0, out3
  not not_1 (not_1_out, and_2_out);
  or or_7 (CLR_IR, comparator_5_eq, or_3_out);
  or or_8 (or_8_out, t_ff_3_q, decoder_2_out3);
  or or_9 (or_9_out, or_2_out_2, or_5_out_2);
  and and_3 (and_3_out, or_9_out, or_8_out);
  Transistor #(.\type ("n")) transistor_6 (.in(CLK), .out(transistor_6_out), .gate(and_3_out));
  or or_10 (FENCE, t_ff_2_q, t_ff_3_q);
  T_Flip_Flop t_ff_3 (.clk(CLR_PC), .T(CLR_PC), .Q(t_ff_3_q), .reset(CLR_IR));  // open: Qn, preset, en
  Comparator #(.width(32)) comparator_6 (.a(DATA_IN), .b(32'h38513b89), .eq(CLR_PC));  // open: gt, lt
  and and_4 (and_4_out, or_5_out_2, or_2_out_2);
  Counter #(.width(3), .max('h7)) counter_2 (
    .Q(counter_2_q), .clk(transistor_6_out), .clr(or_3_out));  // open: load, D, count, carry
  Decoder #(.select(3), .enable("false")) decoder_2 (
    .out3(decoder_2_out3), .out4(decoder_2_out4), .out5(decoder_2_out5), .sel(counter_2_q));  // open: out0, out1, out2, out6, out7
  not not_2 (PC_LOAD, t_ff_3_q);
  D_Flip_Flop d_ff_1 (.clk(and_4_out), .D(and_4_out), .Q(d_ff_1_q), .reset(CLR_IR));  // open: Qn, preset, en
  or or_11 (or_11_out, decoder_2_out4, decoder_2_out5);
endmodule

module BRIDGE_CTRL (
  input  [31:0] in_1,
  output [7:0] BROD,
  output bridge_activate
);

  Comparator #(.width(24)) comparator_1 (
    .a({in_1[15:8], in_1[23:16], in_1[31:24]}), .b(24'h4ed5fa), .eq(bridge_activate));  // open: gt, lt
  Pull_Resistor pull_resistor_1 (.node(BROD));
  Transistor #(.\type ("n"), .width(8)) transistor_1 (.in(in_1[7:0]), .out(BROD), .gate(bridge_activate));
endmodule

module LOGIC (
  input  [31:0] DATA_IN,
  input  [7:0] PC_IN,
  input  CLR,
  input  CLK,
  input  RAM_WRITE,
  input  MEM_WRITE,
  input  ROM_2,
  input  RAM_3,
  input  MEM_3,
  output MAIN_MUX,
  output [7:0] ADDR,
  output CLR_X,
  output CLR_PC,
  output CLK_KYBD,
  output CLR_I_O,
  output CLK_RAM,
  output CLR_ACCUMILATOR,
  output CLK_MEM,
  output CLR_REGS,
  output SEL_BIOS,
  output SEL_RAM,
  output SEL_MEM,
  output CLR_PC_ALL,
  output C_IN
);

  wire and_1_out, and_2_out, and_3_out, and_4_out, and_5_out, and_6_out, and_7_out, and_8_out, and_9_out,
       and_10_out, and_11_out, and_12_out, and_13_out, and_16_out, and_17_out, and_18_out, and_19_out,
       and_20_out, and_21_out, and_22_out, and_23_out, and_24_out, and_25_out, and_26_out, and_27_out,
       and_28_out, and_29_out, and_30_out, and_31_out, and_32_out, and_33_out, and_36_out, and_37_out,
       and_38_out, and_40_out, comparator_1_eq, comparator_2_eq, comparator_3_eq, comparator_4_eq,
       comparator_5_eq, comparator_6_eq, comparator_7_eq, comparator_8_eq, comparator_9_eq, comparator_10_eq,
       comparator_11_eq, comparator_12_eq, comparator_13_eq, comparator_14_eq, comparator_15_eq,
       comparator_16_eq, comparator_17_eq, comparator_18_eq, comparator_19_eq, comparator_20_eq,
       comparator_21_eq, comparator_22_eq, comparator_23_eq, comparator_24_eq, comparator_25_eq,
       comparator_26_eq, comparator_27_eq, comparator_28_eq, not_1_out, or_1_out, or_2_out, or_3_out,
       or_4_out, or_5_out, or_6_out, or_7_out, or_10_out_2, or_12_out, t_ff_2_q, transistor_1_out;
  wire [1:0] counter_1_q, counter_2_q;
  wire [7:0] bit_extender_1_out;

  Comparator comparator_1 (.a(DATA_IN[31:24]), .b(8'hf1), .eq(comparator_1_eq));  // open: gt, lt
  Comparator comparator_2 (.a(DATA_IN[31:24]), .b(8'hf2), .eq(comparator_2_eq));  // open: gt, lt
  Comparator comparator_3 (.a(DATA_IN[31:24]), .b(8'hf3), .eq(comparator_3_eq));  // open: gt, lt
  Comparator comparator_4 (.a(DATA_IN[31:24]), .b(8'hf4), .eq(comparator_4_eq));  // open: gt, lt
  Comparator comparator_5 (.a(DATA_IN[31:24]), .b(8'hf5), .eq(comparator_5_eq));  // open: gt, lt
  Comparator comparator_6 (.a(PC_IN), .b({8{1'b0}}), .eq(comparator_6_eq));  // open: gt, lt
  Comparator comparator_7 (.a(DATA_IN[23:16]), .b(8'h40), .eq(comparator_7_eq));  // open: gt, lt
  Comparator comparator_8 (.a(DATA_IN[23:16]), .b(8'h50), .eq(comparator_8_eq));  // open: gt, lt
  Comparator comparator_9 (.a(DATA_IN[23:16]), .b(8'h60), .eq(comparator_9_eq));  // open: gt, lt
  Comparator comparator_10 (.a(DATA_IN[15:8]), .b(8'h45), .eq(comparator_10_eq));  // open: gt, lt
  Comparator comparator_11 (.a(DATA_IN[15:8]), .b(8'h55), .eq(comparator_11_eq));  // open: gt, lt
  Comparator comparator_12 (.a(DATA_IN[15:8]), .b(8'h65), .eq(comparator_12_eq));  // open: gt, lt
  Comparator comparator_13 (.a(DATA_IN[7:0]), .b(8'h43), .eq(comparator_13_eq));  // open: gt, lt
  Comparator comparator_14 (.a(DATA_IN[7:0]), .b(8'h44), .eq(comparator_14_eq));  // open: gt, lt
  Comparator comparator_15 (.a(DATA_IN[7:0]), .b(8'h47), .eq(comparator_15_eq));  // open: gt, lt
  Comparator comparator_16 (.a(DATA_IN[7:0]), .b(8'h53), .eq(comparator_16_eq));  // open: gt, lt
  Comparator comparator_17 (.a(DATA_IN[7:0]), .b(8'h54), .eq(comparator_17_eq));  // open: gt, lt
  Comparator comparator_18 (.a(DATA_IN[7:0]), .b(8'h57), .eq(comparator_18_eq));  // open: gt, lt
  not not_1 (not_1_out, or_1_out);
  and and_1 (and_1_out, not_1_out, comparator_6_eq);
  Comparator comparator_19 (.a(DATA_IN[23:16]), .b(8'h90), .eq(comparator_19_eq));  // open: gt, lt
  Comparator comparator_20 (.a(DATA_IN[15:8]), .b(8'h95), .eq(comparator_20_eq));  // open: gt, lt
  and and_2 (and_2_out, comparator_13_eq, comparator_2_eq);
  and and_3 (and_3_out, and_2_out, comparator_7_eq);
  and and_4 (and_4_out, comparator_14_eq, comparator_2_eq);
  and and_5 (and_5_out, and_4_out, comparator_7_eq);
  and and_6 (and_6_out, comparator_15_eq, comparator_2_eq);
  and and_7 (and_7_out, and_6_out, comparator_7_eq);
  and and_8 (and_8_out, comparator_16_eq, comparator_3_eq);
  and and_9 (and_9_out, and_8_out, comparator_8_eq);
  and and_10 (and_10_out, comparator_17_eq, comparator_3_eq);
  and and_11 (and_11_out, and_10_out, comparator_8_eq);
  and and_12 (and_12_out, comparator_18_eq, comparator_3_eq);
  and and_13 (and_13_out, and_12_out, comparator_8_eq);
  or or_1 (or_1_out, SEL_BIOS, SEL_RAM, SEL_MEM);
  Comparator comparator_21 (.a(DATA_IN[7:0]), .b(8'h93), .eq(comparator_21_eq));  // open: gt, lt
  Comparator comparator_22 (.a(DATA_IN[23:16]), .b(8'h70), .eq(comparator_22_eq));  // open: gt, lt
  Comparator comparator_23 (.a(DATA_IN[15:8]), .b(8'h75), .eq(comparator_23_eq));  // open: gt, lt
  and and_14 (CLR_I_O, and_3_out, comparator_10_eq);
  and and_15 (CLR_ACCUMILATOR, and_5_out, comparator_10_eq);
  and and_16 (and_16_out, and_7_out, comparator_10_eq);
  and and_17 (and_17_out, and_9_out, comparator_11_eq);
  or or_2 (or_2_out, and_17_out, ROM_2, and_1_out);
  or or_3 (or_3_out, and_18_out, RAM_3);
  and and_18 (and_18_out, and_11_out, comparator_11_eq);
  or or_4 (or_4_out, MEM_3, and_19_out);
  and and_19 (and_19_out, and_13_out, comparator_11_eq);
  or or_5 (or_5_out, or_4_out, CLR, or_2_out);
  or or_6 (or_6_out, or_3_out, CLR, or_2_out);
  or or_7 (or_7_out, or_4_out, CLR, or_3_out);
  and and_20 (and_20_out, SEL_MEM, or_2_out);
  and and_21 (and_21_out, SEL_RAM, or_3_out);
  and and_22 (and_22_out, SEL_MEM, or_4_out);
  and and_23 (and_23_out, comparator_21_eq, comparator_5_eq);
  Comparator comparator_24 (.a(DATA_IN[7:0]), .b(8'h63), .eq(comparator_24_eq));  // open: gt, lt
  Comparator comparator_25 (.a(DATA_IN[7:0]), .b(8'h64), .eq(comparator_25_eq));  // open: gt, lt
  Comparator comparator_26 (.a(DATA_IN[7:0]), .b(8'h67), .eq(comparator_26_eq));  // open: gt, lt
  or or_8 (CLR_REGS, and_16_out, CLR);
  Register #(.width(1), .trigger("high")) register_1 (
    .D(or_2_out), .Q(SEL_BIOS), .clk(or_2_out), .clr(or_7_out));  // open: en
  Register #(.width(1), .trigger("high")) register_2 (
    .D(or_3_out), .Q(SEL_RAM), .clk(or_3_out), .clr(or_5_out));  // open: en
  Register #(.width(1), .trigger("high")) register_3 (
    .D(or_4_out), .Q(SEL_MEM), .clk(or_4_out), .clr(or_6_out));  // open: en
  or or_9 (CLR_PC_ALL, and_20_out, and_21_out, and_22_out, CLR);
  and and_24 (and_24_out, and_23_out, comparator_19_eq);
  and and_25 (and_25_out, and_24_out, comparator_20_eq);
  Comparator comparator_27 (.a(DATA_IN[7:0]), .b(8'h73), .eq(comparator_27_eq));  // open: gt, lt
  and and_26 (and_26_out, comparator_27_eq, comparator_4_eq);
  and and_27 (and_27_out, comparator_24_eq, comparator_1_eq);
  and and_28 (and_28_out, comparator_25_eq, comparator_1_eq);
  and and_29 (and_29_out, comparator_26_eq, comparator_1_eq);
  J_K_Flip_Flop j_k_ff_1 (
    .J(and_25_out), .clk(and_25_out), .K(and_25_out), .Q(C_IN), .reset(CLR));  // open: Qn, preset, en
  and and_30 (and_30_out, and_26_out, comparator_22_eq);
  OR or_10 (.in_1(PC_IN), .out_2(or_10_out_2));
  and and_31 (and_31_out, and_27_out, comparator_9_eq);
  and and_32 (and_32_out, and_28_out, comparator_9_eq);
  and and_33 (and_33_out, and_29_out, comparator_9_eq);
  and and_34 (CLK_RAM, RAM_WRITE, CLK);
  and and_35 (CLK_MEM, MEM_WRITE, CLK);
  and and_36 (and_36_out, and_30_out, comparator_23_eq);
  Counter #(.width(2), .max('h3)) counter_1 (
    .Q(counter_1_q), .clk(transistor_1_out), .clr(and_37_out));  // open: load, D, count, carry
  Transistor #(.\type ("n")) transistor_1 (.in(or_10_out_2), .out(transistor_1_out), .gate(MAIN_MUX));
  and and_37 (and_37_out, counter_1_q[1], counter_1_q[0]);
  and and_38 (and_38_out, and_31_out, comparator_12_eq);
  or or_11 (CLR_PC, and_38_out, CLR);
  assign bit_extender_1_out = {{7{CLR_X}}, CLR_X};  // Bit_Extender bit_extender_1
  and and_39 (CLR_X, and_32_out, comparator_12_eq);
  and and_40 (and_40_out, and_33_out, comparator_12_eq);
  or or_12 (or_12_out, CLR, comparator_28_eq);
  T_Flip_Flop t_ff_1 (.clk(and_36_out), .T(and_36_out), .Q(MAIN_MUX), .reset(counter_1_q[1]));  // open: Qn, preset, en
  assign ADDR = DATA_IN[15:8] & bit_extender_1_out;  // AND_Gate and_41, 8 bits wide
  T_Flip_Flop t_ff_2 (.clk(and_40_out), .T(and_40_out), .Q(t_ff_2_q), .reset(or_12_out));  // open: Qn, preset, en
  and and_42 (CLK_KYBD, t_ff_2_q, CLK);
  Counter #(.width(2), .max('h3)) counter_2 (
    .Q(counter_2_q), .clk(and_40_out), .clr(comparator_28_eq));  // open: load, D, count, carry
  Comparator #(.width(2)) comparator_28 (.a(counter_2_q), .b(2'b10), .eq(comparator_28_eq));  // open: gt, lt
endmodule

module TEST (
  input  in_1,
  input  in_2,
  input  [7:0] in_3
);

  wire and_1_out, and_2_out, clock_1_out, cpu_1_i_o_clk, cpu_1_i_o_clr, cpu_1_i_o_r, cpu_1_i_o_w,
       cpu_1_ram_r_w, cpu_1_w_clk, not_1_out;
  wire [2:0] cpu_1_rom_mem_rom;
  wire [6:0] bit_extender_1_out, keyboard_1_data;
  wire [7:0] ascii_1_out_3, cpu_1_address, cpu_1_d_bus_out, cpu_1_i_o_out, ram_1_data;

  STACK_ENGINE stack_engine_1 ();  // open: DATA_IN, PC_IN, C_EN, C_SEL, ADDR, RAM, MEM, ROM, CLR, CLK, SEL_ADDR, carry, zero, STACK_SEGMENT_IN, BROD, RAM_W, LTSI_EN, RAM_R, LTSI_SEL, STATUS, BROD_2, PC_LOAD, PC_LOAD_2, SEL
  ROM_part rom_1 ();  // open: addr, data, sel
  ROM_part rom_2 ();  // open: addr, data, sel
  ROM_part rom_3 ();  // open: addr, data, sel
  Clock clock_1 (.out(clock_1_out));
  CPU cpu_1 (
    .D_BUS_IN(ram_1_data), .I_O_IN({1'b0, keyboard_1_data}), .SEL(in_1), .CLR(in_2), .CLK(clock_1_out),
    .D_BUS_OUT(cpu_1_d_bus_out), .I_O_OUT(cpu_1_i_o_out), .ADDRESS(cpu_1_address), .RAM_R_W(cpu_1_ram_r_w),
    .W_CLK(cpu_1_w_clk), .I_O_W(cpu_1_i_o_w), .I_O_R(cpu_1_i_o_r), .I_O_CLK(cpu_1_i_o_clk),
    .I_O_CLR(cpu_1_i_o_clr), .INT(2'b00), .ROM_MEM_ROM(cpu_1_rom_mem_rom));  // open: MEM_R_W, STATUS_INT_MIO
  and and_1 (and_1_out, cpu_1_i_o_clk, cpu_1_i_o_w);
  Keyboard #(.trigger("falling")) keyboard_1 (
    .clk(and_1_out), .clr(cpu_1_i_o_clr), .data(keyboard_1_data));  // open: re, avail
  // Probe on ascii_1_out_3
  ASCII ascii_1 (.INP_1(in_3), .INP_2(in_3), .out_3(ascii_1_out_3));
  Bit_Extender #(.out_width(7)) bit_extender_1 (.in(cpu_1_i_o_out), .out(bit_extender_1_out));
  TTY tty_1 (.data(bit_extender_1_out), .clk(and_2_out), .clr(cpu_1_i_o_clr));  // open: we
  and and_2 (and_2_out, cpu_1_i_o_clk, cpu_1_i_o_r);
  ROM_part rom_4 ();  // open: addr, data, sel
  not not_1 (not_1_out, cpu_1_ram_r_w);
  RAM_part #(.bus("separate")) ram_1 (
    .addr(cpu_1_address), .din(cpu_1_d_bus_out), .data(ram_1_data), .str(cpu_1_ram_r_w),
    .sel(cpu_1_rom_mem_rom[2]), .clk(cpu_1_w_clk), .ld(not_1_out));  // open: clr
  ROM_part rom_5 (.addr(cpu_1_address), .data(ram_1_data), .sel(cpu_1_rom_mem_rom[0]));
  ROM_part rom_6 ();  // open: addr, data, sel
  ROM_part rom_7 ();  // open: addr, data, sel
  ROM_part rom_8 ();  // open: addr, data, sel
  ROM_part rom_9 ();  // open: addr, data, sel
  ROM_part rom_10 ();  // open: addr, data, sel
  ROM_part rom_11 ();  // open: addr, data, sel

  // Notes on the sheet:
  //   contents of rom_1 (hex, n*v repeats v):
  //   f2 40 45 43 7 60 80 86 57 68 65 6e 20 64 6f 6e 65 20 77 69 74 68 20 74 68 65 20 64 6f 63 75 6d 65 6e
  //   74 20 70 72 65 73 73 20 22 2a 22 a 4f 6e 6c 79 20 31 32 38 20 63 68 61 72 61 63 74 65 72 73 20 61 6e
  //   79 20 61 62 6f 76 65 20 77 69 6c 6c 20 6e 6f 74 20 62 65 20 73 61 76 65 64 0 0 0 f2 40 45 47 8 1 6
  //   70 8 2 6 71 5a 9b 70 74 42 1 0 0 f2 40 45 43 82 d7 41 0 2 0 0 4 dc 20 21 78 2 0 1 1 dc 20 21 a4 23
  //   a1 c2 0 f2 40 45 44 2 3 0 2 a 0 5 0 36 f1 52 3 dc 30 40 78
  //   contents of rom_2 (hex, n*v repeats v):
  //   7 38 80 46 4*5f 57 65 6c 63 6f 6d 65 4*5f 20 a a 38 2d 42 49 54 20 43 50 55 20 a 56 2e 31 2e 37 a 47
  //   65 74 74 69 6e 67 20 52 65 61 64 79 2e 2e 2e 0 5a 9b 8 10 0 31 32 33 34 35 36 37 8 1 6 3d 8 2 6 3e 8
  //   3 6 3f 8 4 6 40 8 5 6 41 8 6 6 42 8 7 6 43 f2 40 45 43 7 bc 86 86 43 48 4f 4f 53 45 20 50 52 4f 47
  //   52 41 4d 3a a 31 2e 20 43 41 4c 43 55 4c 41 54 4f 52 a 32 2e 20 43 50 55 20 53 50 45 43 53 a 33 2e
  //   20 44 45 56 20 43 4f 4d 4d 45 4e 54 53 a 34 2e 20 54 45 58 54 20 45 44 49 54 4f 52 a a 4e 55 4d 42
  //   45 52 3a a 0 82 d7 41 0 23 a1 c2 0 2 0 0 1 dc 20 d5 e8 2 0 0 2 dc 20 d5 0 2 0 0 3 dc 20 d5 0 2 0 0 4
  //   dc 20 d5 e8 dc 20 c5 bc ff ff 0 56 ff ff
  //   contents of rom_3 (hex, n*v repeats v):
  //   7 38 80 46 4*5f 57 65 6c 63 6f 6d 65 4*5f 20 a a 38 2d 42 49 54 20 43 50 55 20 a 56 2e 31 2e 37 a 47
  //   65 74 74 69 6e 67 20 52 65 61 64 79 2e 2e 2e 0 5a 9b 3c 44 0 31 32 33 34 35 36 37 8 1 6 3d 8 2 6 3e
  //   8 3 6 3f 8 4 6 40 8 5 6 41 8 6 6 42 8 7 6 43 f2 40 45 43 7 bc 86 86 43 48 4f 4f 53 45 20 50 52 4f 47
  //   52 41 4d 3a a 31 2e 20 43 41 4c 43 55 4c 41 54 4f 52 a 32 2e 20 43 50 55 20 53 50 45 43 53 a 33 2e
  //   20 44 45 56 20 43 4f 4d 4d 45 4e 54 53 a 34 2e 20 54 45 58 54 20 45 44 49 54 4f 52 a a 4e 55 4d 42
  //   45 52 3a a 0 82 d7 41 0 23 a1 c2 0 2 0 0 1 dc 20 d5 0 2 0 0 2 dc 20 d5 0 2 0 0 3 dc 20 d5 0 2 0 0 4
  //   dc 20 d5 e8 dc 20 c5 bc dc 4 40 0 ff ff
  //   contents of rom_4 (hex, n*v repeats v):
  //   5a 9b 4 c 31 32 33 34 35 36 37 38 8 1 6 9 8 2 6 a 9 2 5
  //   contents of rom_5 (hex, n*v repeats v):
  //   ff ff c 57 12*0 e0 57
  //   contents of rom_6 (hex, n*v repeats v):
  //   5a 9b 8 c 31 32 33 34 35 36 37 38 8 1 6 9 8 2 6 a 8 3 6 b 8 4 6 c 8 5 6 d 8 6 6 e 8 7 6 f f2 40 45
  //   43
  //   contents of rom_7 (hex, n*v repeats v):
  //   5a 9b 4 9 0 31 32 33 34 35 36 37 8 1 6 3d 8 2 6 3e 8 3 6 3f 8 4 6 40 8 5 6 41 8 6 6 42 8 7 6 43
  //   MOV B AND I/O(2)
  //   I/O TEST(1)
  //   R/W FROM AND TO I/O
  //   MOV B AND ALU TEST(1)
  //   LOAD/STORE AND IMMED
  //   WRITE REG TO RAM ALU= ADDRESS DONE PASSED
  //   MEMORY SWITCHING PASSED
  //   CALL/RET AND JUMP(CZEHL) PASSED
  //   PASSED
  //   contents of rom_8 (hex, n*v repeats v):
  //   7 c 50 48 78 0 66 5 65 0 5 65 76 46 66 57
  //   PASSED
  //   contents of rom_9 (hex, n*v repeats v):
  //   82 d7 41 1 23 a1 c2 1
  //   contents of rom_10 (hex, n*v repeats v):
  //   8 0 6 8 5a 9b 8 c 5 9 0 0 8 1 6 9 2 0 0 1 36 f1 52 3 8*0 36 f1 52 4 9 4 5 2 2 a 0 b
  //   PASSED
  //   contents of rom_11 (hex, n*v repeats v):
  //   8 5 6 c a 5 5 0 f3 50 55 54 8
  //   FENCE PASSED
  //    READY FOR GENERAL USE
endmodule

module MEMORY_CTRL (
  input  MEM_SEL_LOGIC,
  input  RAM_SEL_LOGIC,
  input  ROM_SEL_LOGIC,
  input  ROM_SEL,
  input  ROM_R,
  input  MEM_SEL,
  input  MEM_R,
  input  MEM_W,
  input  RAM_SEL,
  input  RAM_R,
  input  RAM_W,
  input  bridge_activate,
  output MEMORY_CTRL_ERROR,
  output ROM_SEL_2,
  output MEM_SEL_2,
  output RAM_SEL_2
);

  wire and_1_out, and_2_out, and_3_out, and_4_out, and_5_out, and_6_out, and_7_out, and_8_out, and_9_out,
       and_10_out, and_11_out, and_12_out, nor_1_out, not_1_out, or_1_out, or_2_out, or_3_out, or_4_out,
       or_5_out, or_6_out, or_7_out, or_8_out, or_9_out, or_10_out, or_11_out, or_12_out, or_13_out,
       or_14_out, or_15_out, or_16_out, or_17_out;

  or or_1 (or_1_out, ROM_SEL, ROM_R);
  not not_1 (not_1_out, or_2_out);
  or or_2 (or_2_out, RAM_W, RAM_R, RAM_SEL, MEM_W, MEM_R, MEM_SEL);
  or or_3 (or_3_out, or_2_out, or_1_out);
  and and_1 (and_1_out, RAM_SEL_LOGIC, not_1_out);
  and and_2 (and_2_out, not_1_out, MEM_SEL_LOGIC);
  and and_3 (and_3_out, not_1_out, ROM_SEL_LOGIC);
  or or_4 (or_4_out, ROM_SEL, ROM_R);
  or or_5 (or_5_out, MEM_SEL, or_6_out);
  or or_6 (or_6_out, MEM_R, MEM_W);
  or or_7 (or_7_out, ROM_SEL, or_9_out);
  or or_8 (or_8_out, RAM_SEL, or_9_out);
  or or_9 (or_9_out, RAM_R, RAM_W);
  or or_10 (or_10_out, or_6_out, ROM_SEL);
  and and_4 (and_4_out, ROM_SEL, ~or_12_out, ~and_3_out);  // AND_Gate
  or or_11 (or_11_out, and_3_out, or_4_out);
  or or_12 (or_12_out, RAM_SEL, or_6_out);
  and and_5 (and_5_out, MEM_SEL, ~or_7_out, ~and_2_out);  // AND_Gate
  or or_13 (or_13_out, and_2_out, or_5_out);
  and and_6 (and_6_out, RAM_SEL, ~or_10_out, ~and_1_out);  // AND_Gate
  or or_14 (or_14_out, and_1_out, or_8_out);
  nor nor_1 (nor_1_out, and_11_out, and_9_out, and_7_out);
  or or_15 (or_15_out, and_6_out, and_5_out);
  and and_7 (and_7_out, ~or_15_out, and_8_out);  // AND_Gate
  and and_8 (and_8_out, or_11_out, ~or_12_out);  // AND_Gate
  or or_16 (or_16_out, and_4_out, and_6_out);
  and and_9 (and_9_out, ~or_16_out, and_10_out);  // AND_Gate
  and and_10 (and_10_out, or_13_out, ~or_7_out);  // AND_Gate
  or or_17 (or_17_out, and_5_out, and_4_out);
  and and_11 (and_11_out, ~or_17_out, and_12_out);  // AND_Gate
  and and_12 (and_12_out, or_14_out, ~or_10_out);  // AND_Gate
  and and_13 (MEMORY_CTRL_ERROR, or_3_out, nor_1_out);
  or or_18 (ROM_SEL_2, and_7_out, bridge_activate);
  or or_19 (MEM_SEL_2, and_9_out, bridge_activate);
  or or_20 (RAM_SEL_2, and_11_out, bridge_activate);

  // Notes on the sheet:
  //   WRITE/READ OP = PRIORITY
endmodule

module TEST_2 (
);

  wire or_1_out, or_2_out, texture_mapping_1_done, texture_mapping_1_sel_data, texture_mapping_1_sel_texture,
       undriven, undriven_2, undriven_3, undriven_4, undriven_5, undriven_7;
  wire [7:0] texture_mapping_1_address_data, texture_mapping_1_texture_cache_address, texture_mapping_1_x,
       texture_mapping_1_y;
  wire [15:0] texture_cache_1_data_1, texture_cache_1_data_2, texture_cache_1_texture_data,
       texture_mapping_1_colour;
  wire [19:0] undriven_6;

  or or_1 (or_1_out, texture_mapping_1_sel_data, undriven);
  TEXTURE_CACHE texture_cache_1 (
    .W_CLK(undriven_4), .R_W(undriven_3), .CLR(undriven_2), .DATA_2(texture_cache_1_data_2),
    .ADDRESS_DATA(texture_mapping_1_address_data), .DATA_1(texture_cache_1_data_1), .SEL_DATA(or_1_out),
    .ADDRESS_TEXTURE(texture_mapping_1_texture_cache_address), .TEXTURE_DATA(texture_cache_1_texture_data),
    .SEL_TEXTURE(or_2_out));  // open: FROM_LD, FROM_TEXTURE_MEM, DIFFRENT_LINE
  or or_2 (or_2_out, texture_mapping_1_sel_texture, undriven_5);
  TEXTURE_MAPPING texture_mapping_1 (
    .DTATA_IN_2(texture_cache_1_data_2), .DATA_IN(texture_cache_1_data_1),
    .TEXTURE_IN(texture_cache_1_texture_data), .INSTR(undriven_6), .EN(undriven_7), .X(texture_mapping_1_x),
    .Y(texture_mapping_1_y), .DONE(texture_mapping_1_done), .COLOUR(texture_mapping_1_colour),
    .TEXTURE_CACHE_ADDRESS(texture_mapping_1_texture_cache_address),
    .ADDRESS_DATA(texture_mapping_1_address_data), .SEL_DATA(texture_mapping_1_sel_data),
    .SEL_TEXTURE(texture_mapping_1_sel_texture), .CLR(undriven_2), .CLK(undriven_4));
endmodule

module RAM (
  input  [7:0] ADDRESS,
  input  [7:0] DATA_IN,
  input  SEL,
  input  CLK,
  input  R_W,
  input  CLR,
  output [7:0] DATA_OUT
);

  wire not_1_out;

  RAM_part #(.bus("separate")) ram_1 (
    .addr(ADDRESS), .din(DATA_IN), .data(DATA_OUT), .str(R_W), .sel(SEL), .clk(CLK), .ld(not_1_out), .clr(CLR));
  not not_1 (not_1_out, R_W);
endmodule

module ROM (
  input  [7:0] ADDRESS_IN,
  input  SEL,
  output [7:0] DATA_OUT
);

  ROM_part rom_1 (.addr(ADDRESS_IN), .data(DATA_OUT), .sel(SEL));

  // Notes on the sheet:
  //   contents of rom_1 (hex, n*v repeats v):
  //   7 38 80 46 4*5f 57 65 6c 63 6f 6d 65 4*5f 20 a a 38 2d 42 49 54 20 43 50 55 20 a 56 2e 31 2e 37 a 47
  //   65 74 74 69 6e 67 20 52 65 61 64 79 2e 2e 2e 0 5a 9b 3c 44 0 31 32 33 34 35 36 37 8 1 6 3d 8 2 6 3e
  //   8 3 6 3f 8 4 6 40 8 5 6 41 8 6 6 42 8 7 6 43 f2 40 45 43 7 bc 86 86 43 48 4f 4f 53 45 20 50 52 4f 47
  //   52 41 4d 3a a 31 2e 20 43 41 4c 43 55 4c 41 54 4f 52 a 32 2e 20 43 50 55 20 53 50 45 43 53 a 33 2e
  //   20 44 45 56 20 43 4f 4d 4d 45 4e 54 53 a 34 2e 20 54 45 58 54 20 45 44 49 54 4f 52 a a 4e 55 4d 42
  //   45 52 3a a 0 82 d7 41 0 23 a1 c2 0 2 0 0 1 dc 20 d5 0 2 0 0 2 dc 20 d5 0 2 0 0 3 dc 20 d5 0 2 0 0 4
  //   dc 20 d5 e8 dc 20 c5 bc dc 4 40 0 ff ff
endmodule

module MEM (
  input  R_W,
  input  CLK,
  input  [7:0] ADDRESS,
  input  [7:0] DATA_IN,
  input  SEL,
  input  [2:0] prog,
  output [7:0] DATA_OUT
);

  wire demultiplexer_1_out0, demultiplexer_1_out1, demultiplexer_1_out2, demultiplexer_1_out3,
       demultiplexer_1_out4, demultiplexer_1_out5, demultiplexer_1_out6, demultiplexer_1_out7, not_1_out,
       not_2_out, not_3_out, not_4_out;
  wire [7:0] undriven;

  Demultiplexer #(.select(3), .enable("false")) demultiplexer_1 (
    .out0(demultiplexer_1_out0), .out1(demultiplexer_1_out1), .out2(demultiplexer_1_out2),
    .out3(demultiplexer_1_out3), .out4(demultiplexer_1_out4), .out5(demultiplexer_1_out5),
    .out6(demultiplexer_1_out6), .out7(demultiplexer_1_out7), .in(SEL), .sel(prog));
  ROM_part rom_1 (.addr(ADDRESS), .data(DATA_OUT), .sel(demultiplexer_1_out0));
  ROM_part rom_2 (.addr(ADDRESS), .data(DATA_OUT), .sel(demultiplexer_1_out1));
  ROM_part rom_3 (.addr(ADDRESS), .data(DATA_OUT), .sel(demultiplexer_1_out2));
  ROM_part rom_4 (.addr(ADDRESS), .data(DATA_OUT), .sel(demultiplexer_1_out3));
  RAM_part #(.bus("separate")) ram_1 (
    .addr(ADDRESS), .din(DATA_IN), .data(DATA_OUT), .str(R_W), .sel(demultiplexer_1_out4), .clk(CLK),
    .ld(not_1_out));  // open: clr
  not not_1 (not_1_out, R_W);
  RAM_part #(.bus("separate")) ram_2 (
    .addr(ADDRESS), .din(DATA_IN), .data(DATA_OUT), .str(R_W), .sel(demultiplexer_1_out5), .clk(CLK),
    .ld(not_2_out));  // open: clr
  not not_2 (not_2_out, R_W);
  RAM_part #(.bus("separate")) ram_3 (
    .addr(undriven), .din(DATA_IN), .data(DATA_OUT), .str(R_W), .sel(demultiplexer_1_out6), .clk(CLK),
    .ld(not_3_out));  // open: clr
  not not_3 (not_3_out, R_W);
  RAM_part #(.bus("separate")) ram_4 (
    .addr(undriven), .din(DATA_IN), .data(DATA_OUT), .str(R_W), .sel(demultiplexer_1_out7), .clk(CLK),
    .ld(not_4_out));  // open: clr
  not not_4 (not_4_out, R_W);

  // Notes on the sheet:
  //   contents of rom_1 (hex, n*v repeats v):
  //   f2 40 45 43 7 60 80 84 57 68 65 6e 20 64 6f 6e 65 20 77 69 74 68 20 74 68 65 20 64 6f 63 75 6d 65 6e
  //   74 20 70 72 65 73 73 20 22 2a 22 a 4f 6e 6c 79 20 31 32 38 20 63 68 61 72 61 63 74 65 72 73 20 61 6e
  //   79 20 61 62 6f 76 65 20 77 69 6c 6c 20 6e 6f 74 20 62 65 20 73 61 76 65 64 0 0 0 f2 40 45 47 8 1 4
  //   70 8 2 4 71 5a 9b 70 74 2a 1 0 0 f2 40 45 43 82 d7 41 0 2 0 0 4 dc 20 21 78 2 0 1 1 dc 20 21 a4 23
  //   a1 c2 0 f2 40 45 44 2 3 0 2 a 0 5 0 36 f1 52 3 dc 30 40 78 85*0 c
endmodule

module I_O_CTRL (
  input  I_O_CLK,
  input  I_O_R,
  input  [7:0] I_O_IN,
  input  [6:0] I_O_DEV_IN,
  input  I_O_W,
  output I_O_CLK_IN,
  output [6:0] I_O_DEV_OUT,
  output [7:0] I_O_OUT,
  output I_O_CLK_OUT
);

  and and_1 (I_O_CLK_IN, I_O_CLK, I_O_R);
  and and_2 (I_O_CLK_OUT, I_O_CLK, I_O_W);

  assign I_O_DEV_OUT = I_O_IN[6:0];
  assign I_O_OUT = {I_O_IN[7], I_O_DEV_IN};
  // also tied to GND on the sheet: I_O_IN[7]
endmodule

module PC2 (
  input  [7:0] DATA_IN,
  input  MUX,
  input  LOAD,
  input  CLK,
  input  CLR,
  output [7:0] ADDRESS
);

  wire [7:0] adder_1_out, multiplexer_1_out, PC_q;

  Multiplexer #(.width(8), .enable("false")) multiplexer_1 (
    .in0(adder_1_out), .in1(DATA_IN), .out(multiplexer_1_out), .sel(MUX));
  Register PC (.D(multiplexer_1_out), .en(LOAD), .Q(PC_q), .clk(CLK), .clr(CLR));
  Adder adder_1 (.a(PC_q), .b(8'h1), .out(adder_1_out));  // open: cin, cout
  Pull_Resistor pull_resistor_1 (.node(ADDRESS));
  Transistor #(.\type ("n"), .gate("br"), .width(8)) transistor_1 (.in(PC_q), .out(ADDRESS), .gate(LOAD));
endmodule

module CTRL_MANAGEMENT (
  input  [31:0] DATA_IN,
  output [31:0] VFU_1,
  output [31:0] VFU_2,
  output [31:0] VFU_3,
  output [31:0] VFU_4,
  output [31:0] MOV_B_1,
  output [31:0] MOV_B_2,
  output [31:0] MOV_B_3,
  output [31:0] MOV_B_4
);

  wire and_1_out, comparator_1_eq, comparator_2_eq, comparator_3_eq, comparator_4_eq, comparator_5_eq,
       comparator_6_eq, comparator_7_eq, comparator_8_eq, not_1_out, or_1_out, or_2_out,
       pull_resistor_1_node, pull_resistor_2_node, pull_resistor_13_node, pull_resistor_15_node,
       pull_resistor_17_node, pull_resistor_19_node, pull_resistor_25_node, pull_resistor_26_node,
       pull_resistor_28_node, transistor_3_out, transistor_4_out, transistor_5_out, transistor_6_out,
       transistor_7_out, transistor_8_out, transistor_14_out, transistor_16_out, transistor_18_out,
       transistor_20_out, transistor_27_out;
  wire [7:0] pull_resistor_9_node, pull_resistor_10_node, pull_resistor_29_node, pull_resistor_30_node,
       pull_resistor_32_node, pull_resistor_38_node, pull_resistor_40_node, pull_resistor_41_node,
       pull_resistor_45_node, pull_resistor_53_node, pull_resistor_54_node, transistor_11_out,
       transistor_12_out, transistor_31_out, transistor_37_out, transistor_39_out, transistor_43_out,
       transistor_47_out, transistor_55_out, transistor_56_out;
  wire [31:0] pull_resistor_22_node, pull_resistor_23_node, pull_resistor_24_node, pull_resistor_34_node,
       pull_resistor_42_node, pull_resistor_44_node, pull_resistor_46_node, pull_resistor_51_node,
       pull_resistor_59_node, transistor_21_out, transistor_33_out, transistor_35_out, transistor_36_out,
       transistor_48_out, transistor_49_out, transistor_50_out, transistor_52_out, transistor_57_out,
       transistor_58_out, transistor_60_out;

  Pull_Resistor pull_resistor_1 (.node(pull_resistor_1_node));
  Transistor #(.\type ("n")) transistor_1 (.in(comparator_1_eq), .out(pull_resistor_1_node), .gate(comparator_5_eq));
  Comparator comparator_1 (.a(DATA_IN[31:24]), .b(8'h1), .eq(comparator_1_eq));  // open: gt, lt
  Pull_Resistor pull_resistor_2 (.node(pull_resistor_2_node));
  Transistor #(.\type ("n")) transistor_2 (.in(comparator_2_eq), .out(pull_resistor_2_node), .gate(comparator_5_eq));
  Comparator comparator_2 (.a(DATA_IN[31:24]), .b(8'h2), .eq(comparator_2_eq));  // open: gt, lt
  Transistor #(.\type ("n")) transistor_3 (.in(comparator_3_eq), .out(transistor_3_out), .gate(comparator_5_eq));
  Pull_Resistor pull_resistor_3 (.node(transistor_3_out));
  Comparator comparator_3 (.a(DATA_IN[31:24]), .b(8'h3), .eq(comparator_3_eq));  // open: gt, lt
  Comparator comparator_4 (.a(DATA_IN[31:24]), .b(8'h4), .eq(comparator_4_eq));  // open: gt, lt
  Transistor #(.\type ("n")) transistor_4 (.in(comparator_4_eq), .out(transistor_4_out), .gate(comparator_5_eq));
  Pull_Resistor pull_resistor_4 (.node(transistor_4_out));
  or or_1 (or_1_out, comparator_5_eq, comparator_8_eq, comparator_7_eq, comparator_6_eq);
  Comparator #(.width(16)) comparator_5 (
    .a({DATA_IN[15:8], DATA_IN[23:16]}), .b(16'hd741), .eq(comparator_5_eq));  // open: gt, lt
  Comparator #(.width(16)) comparator_6 (
    .a({DATA_IN[15:8], DATA_IN[23:16]}), .b(16'hd741), .eq(comparator_6_eq));  // open: gt, lt
  Comparator #(.width(4)) comparator_7 (.a(DATA_IN[3:0]), .b(4'b0101), .eq(comparator_7_eq));  // open: gt, lt
  Comparator #(.width(4)) comparator_8 (.a(DATA_IN[3:0]), .b(4'b0100), .eq(comparator_8_eq));  // open: gt, lt
  or or_2 (or_2_out, comparator_1_eq, comparator_2_eq, comparator_3_eq, comparator_4_eq);
  not not_1 (not_1_out, or_1_out);
  Transistor #(.\type ("n")) transistor_5 (.in(comparator_1_eq), .out(transistor_5_out), .gate(and_1_out));
  Pull_Resistor pull_resistor_5 (.node(transistor_5_out));
  Transistor #(.\type ("n")) transistor_6 (.in(comparator_1_eq), .out(transistor_6_out), .gate(comparator_6_eq));
  Pull_Resistor pull_resistor_6 (.node(transistor_6_out));
  Transistor #(.\type ("n")) transistor_7 (.in(comparator_1_eq), .out(transistor_7_out), .gate(comparator_7_eq));
  Pull_Resistor pull_resistor_7 (.node(transistor_7_out));
  Transistor #(.\type ("n")) transistor_8 (.in(comparator_1_eq), .out(transistor_8_out), .gate(comparator_8_eq));
  Pull_Resistor pull_resistor_8 (.node(transistor_8_out));
  Pull_Resistor pull_resistor_9 (.node(pull_resistor_9_node));
  Transistor #(.\type ("n"), .width(8)) transistor_9 (
    .in(8'h82), .out(pull_resistor_9_node), .gate(pull_resistor_1_node));
  Pull_Resistor pull_resistor_10 (.node(pull_resistor_10_node));
  Transistor #(.\type ("n"), .width(8)) transistor_10 (
    .in(8'h82), .out(pull_resistor_10_node), .gate(pull_resistor_2_node));
  Transistor #(.\type ("n"), .width(8)) transistor_11 (.in(8'h82), .out(transistor_11_out), .gate(transistor_3_out));
  Pull_Resistor pull_resistor_11 (.node(transistor_11_out));
  Transistor #(.\type ("n"), .width(8)) transistor_12 (.in(8'h82), .out(transistor_12_out), .gate(transistor_4_out));
  Pull_Resistor pull_resistor_12 (.node(transistor_12_out));
  and and_1 (and_1_out, or_2_out, not_1_out);
  Pull_Resistor pull_resistor_13 (.node(pull_resistor_13_node));
  Transistor #(.\type ("n")) transistor_13 (.in(comparator_2_eq), .out(pull_resistor_13_node), .gate(and_1_out));
  Transistor #(.\type ("n")) transistor_14 (.in(comparator_3_eq), .out(transistor_14_out), .gate(and_1_out));
  Pull_Resistor pull_resistor_14 (.node(transistor_14_out));
  Pull_Resistor pull_resistor_15 (.node(pull_resistor_15_node));
  Transistor #(.\type ("n")) transistor_15 (.in(comparator_2_eq), .out(pull_resistor_15_node), .gate(comparator_6_eq));
  Transistor #(.\type ("n")) transistor_16 (.in(comparator_3_eq), .out(transistor_16_out), .gate(comparator_6_eq));
  Pull_Resistor pull_resistor_16 (.node(transistor_16_out));
  Pull_Resistor pull_resistor_17 (.node(pull_resistor_17_node));
  Transistor #(.\type ("n")) transistor_17 (.in(comparator_2_eq), .out(pull_resistor_17_node), .gate(comparator_7_eq));
  Transistor #(.\type ("n")) transistor_18 (.in(comparator_3_eq), .out(transistor_18_out), .gate(comparator_7_eq));
  Pull_Resistor pull_resistor_18 (.node(transistor_18_out));
  Pull_Resistor pull_resistor_19 (.node(pull_resistor_19_node));
  Transistor #(.\type ("n")) transistor_19 (.in(comparator_2_eq), .out(pull_resistor_19_node), .gate(comparator_8_eq));
  Transistor #(.\type ("n")) transistor_20 (.in(comparator_3_eq), .out(transistor_20_out), .gate(comparator_8_eq));
  Pull_Resistor pull_resistor_20 (.node(transistor_20_out));
  Transistor #(.\type ("n"), .width(32)) transistor_21 (
    .in({pull_resistor_9_node, DATA_IN[23:0]}), .out(transistor_21_out), .gate(pull_resistor_1_node));
  Pull_Resistor pull_resistor_21 (.node(transistor_21_out));
  Pull_Resistor pull_resistor_22 (.node(pull_resistor_22_node));
  Transistor #(.\type ("n"), .width(32)) transistor_22 (
    .in({pull_resistor_10_node, DATA_IN[23:0]}), .out(pull_resistor_22_node), .gate(pull_resistor_2_node));
  Pull_Resistor pull_resistor_23 (.node(pull_resistor_23_node));
  Transistor #(.\type ("n"), .width(32)) transistor_23 (
    .in({transistor_11_out, DATA_IN[23:0]}), .out(pull_resistor_23_node), .gate(transistor_3_out));
  Pull_Resistor pull_resistor_24 (.node(pull_resistor_24_node));
  Transistor #(.\type ("n"), .width(32)) transistor_24 (
    .in({transistor_12_out, DATA_IN[23:0]}), .out(pull_resistor_24_node), .gate(transistor_4_out));
  Pull_Resistor pull_resistor_25 (.node(pull_resistor_25_node));
  Transistor #(.\type ("n")) transistor_25 (.in(comparator_4_eq), .out(pull_resistor_25_node), .gate(and_1_out));
  Pull_Resistor pull_resistor_26 (.node(pull_resistor_26_node));
  Transistor #(.\type ("n")) transistor_26 (.in(comparator_4_eq), .out(pull_resistor_26_node), .gate(comparator_6_eq));
  Transistor #(.\type ("n")) transistor_27 (.in(comparator_4_eq), .out(transistor_27_out), .gate(comparator_7_eq));
  Pull_Resistor pull_resistor_27 (.node(transistor_27_out));
  Pull_Resistor pull_resistor_28 (.node(pull_resistor_28_node));
  Transistor #(.\type ("n")) transistor_28 (.in(comparator_4_eq), .out(pull_resistor_28_node), .gate(comparator_8_eq));
  Pull_Resistor pull_resistor_29 (.node(pull_resistor_29_node));
  Transistor #(.\type ("n"), .width(8)) transistor_29 (.in(8'h2), .out(pull_resistor_29_node), .gate(transistor_5_out));
  Pull_Resistor pull_resistor_30 (.node(pull_resistor_30_node));
  Transistor #(.\type ("n"), .width(8)) transistor_30 (
    .in(8'h2), .out(pull_resistor_30_node), .gate(pull_resistor_13_node));
  Transistor #(.\type ("n"), .width(8)) transistor_31 (.in(8'h2), .out(transistor_31_out), .gate(transistor_14_out));
  Pull_Resistor pull_resistor_31 (.node(transistor_31_out));
  Pull_Resistor pull_resistor_32 (.node(pull_resistor_32_node));
  Transistor #(.\type ("n"), .width(8)) transistor_32 (
    .in(8'h2), .out(pull_resistor_32_node), .gate(pull_resistor_25_node));
  Transistor #(.\type ("n"), .width(32)) transistor_33 (
    .in({pull_resistor_29_node, DATA_IN[23:0]}), .out(transistor_33_out), .gate(transistor_5_out));
  Pull_Resistor pull_resistor_33 (.node(transistor_33_out));
  Pull_Resistor pull_resistor_34 (.node(pull_resistor_34_node));
  Transistor #(.\type ("n"), .width(32)) transistor_34 (
    .in({pull_resistor_30_node, DATA_IN[23:0]}), .out(pull_resistor_34_node), .gate(pull_resistor_13_node));
  Transistor #(.\type ("n"), .width(32)) transistor_35 (
    .in({transistor_31_out, DATA_IN[23:0]}), .out(transistor_35_out), .gate(transistor_14_out));
  Pull_Resistor pull_resistor_35 (.node(transistor_35_out));
  Transistor #(.\type ("n"), .width(32)) transistor_36 (
    .in({pull_resistor_32_node, DATA_IN[23:0]}), .out(transistor_36_out), .gate(pull_resistor_25_node));
  Pull_Resistor pull_resistor_36 (.node(transistor_36_out));
  Transistor #(.\type ("n"), .width(8)) transistor_37 (.in(8'hd4), .out(transistor_37_out), .gate(transistor_6_out));
  Pull_Resistor pull_resistor_37 (.node(transistor_37_out));
  Pull_Resistor pull_resistor_38 (.node(pull_resistor_38_node));
  Transistor #(.\type ("n"), .width(8)) transistor_38 (
    .in(8'hd4), .out(pull_resistor_38_node), .gate(pull_resistor_15_node));
  Transistor #(.\type ("n"), .width(8)) transistor_39 (.in(8'hd4), .out(transistor_39_out), .gate(transistor_16_out));
  Pull_Resistor pull_resistor_39 (.node(transistor_39_out));
  Pull_Resistor pull_resistor_40 (.node(pull_resistor_40_node));
  Transistor #(.\type ("n"), .width(8)) transistor_40 (
    .in(8'hd4), .out(pull_resistor_40_node), .gate(pull_resistor_26_node));
  Pull_Resistor pull_resistor_41 (.node(pull_resistor_41_node));
  Transistor #(.\type ("n"), .width(8)) transistor_41 (.in(8'h7), .out(pull_resistor_41_node), .gate(transistor_8_out));
  Pull_Resistor pull_resistor_42 (.node(pull_resistor_42_node));
  Transistor #(.\type ("n"), .width(32)) transistor_42 (
    .in({pull_resistor_41_node, DATA_IN[23:0]}), .out(pull_resistor_42_node), .gate(transistor_8_out));
  Transistor #(.\type ("n"), .width(8)) transistor_43 (
    .in(8'h7), .out(transistor_43_out), .gate(pull_resistor_19_node));
  Pull_Resistor pull_resistor_43 (.node(transistor_43_out));
  Pull_Resistor pull_resistor_44 (.node(pull_resistor_44_node));
  Transistor #(.\type ("n"), .width(32)) transistor_44 (
    .in({transistor_43_out, DATA_IN[23:0]}), .out(pull_resistor_44_node), .gate(pull_resistor_19_node));
  Pull_Resistor pull_resistor_45 (.node(pull_resistor_45_node));
  Transistor #(.\type ("n"), .width(8)) transistor_45 (
    .in(8'h7), .out(pull_resistor_45_node), .gate(transistor_20_out));
  Pull_Resistor pull_resistor_46 (.node(pull_resistor_46_node));
  Transistor #(.\type ("n"), .width(32)) transistor_46 (
    .in({pull_resistor_45_node, DATA_IN[23:0]}), .out(pull_resistor_46_node), .gate(transistor_20_out));
  Transistor #(.\type ("n"), .width(8)) transistor_47 (
    .in(8'h7), .out(transistor_47_out), .gate(pull_resistor_28_node));
  Pull_Resistor pull_resistor_47 (.node(transistor_47_out));
  Transistor #(.\type ("n"), .width(32)) transistor_48 (
    .in({transistor_47_out, DATA_IN[23:0]}), .out(transistor_48_out), .gate(pull_resistor_28_node));
  Pull_Resistor pull_resistor_48 (.node(transistor_48_out));
  Transistor #(.\type ("n"), .width(32)) transistor_49 (
    .in({transistor_37_out, DATA_IN[23:0]}), .out(transistor_49_out), .gate(transistor_6_out));
  Pull_Resistor pull_resistor_49 (.node(transistor_49_out));
  assign VFU_1 = transistor_49_out | transistor_33_out | transistor_21_out;  // OR_Gate or_3, 32 bits wide
  Transistor #(.\type ("n"), .width(32)) transistor_50 (
    .in({pull_resistor_38_node, DATA_IN[23:0]}), .out(transistor_50_out), .gate(pull_resistor_15_node));
  Pull_Resistor pull_resistor_50 (.node(transistor_50_out));
  assign VFU_2 = transistor_50_out | pull_resistor_34_node | pull_resistor_22_node;  // OR_Gate or_4, 32 bits wide
  Pull_Resistor pull_resistor_51 (.node(pull_resistor_51_node));
  Transistor #(.\type ("n"), .width(32)) transistor_51 (
    .in({transistor_39_out, DATA_IN[23:0]}), .out(pull_resistor_51_node), .gate(transistor_16_out));
  assign VFU_3 = pull_resistor_51_node | transistor_35_out | pull_resistor_23_node;  // OR_Gate or_5, 32 bits wide
  Transistor #(.\type ("n"), .width(32)) transistor_52 (
    .in({pull_resistor_40_node, DATA_IN[23:0]}), .out(transistor_52_out), .gate(pull_resistor_26_node));
  Pull_Resistor pull_resistor_52 (.node(transistor_52_out));
  assign VFU_4 = transistor_52_out | transistor_36_out | pull_resistor_24_node;  // OR_Gate or_6, 32 bits wide
  Pull_Resistor pull_resistor_53 (.node(pull_resistor_53_node));
  Transistor #(.\type ("n"), .width(8)) transistor_53 (.in(8'h7), .out(pull_resistor_53_node), .gate(transistor_7_out));
  Pull_Resistor pull_resistor_54 (.node(pull_resistor_54_node));
  Transistor #(.\type ("n"), .width(8)) transistor_54 (
    .in(8'h7), .out(pull_resistor_54_node), .gate(pull_resistor_17_node));
  Transistor #(.\type ("n"), .width(8)) transistor_55 (.in(8'h7), .out(transistor_55_out), .gate(transistor_18_out));
  Pull_Resistor pull_resistor_55 (.node(transistor_55_out));
  Transistor #(.\type ("n"), .width(8)) transistor_56 (.in(8'h7), .out(transistor_56_out), .gate(transistor_27_out));
  Pull_Resistor pull_resistor_56 (.node(transistor_56_out));
  Transistor #(.\type ("n"), .width(32)) transistor_57 (
    .in({pull_resistor_53_node, DATA_IN[23:0]}), .out(transistor_57_out), .gate(transistor_7_out));
  Pull_Resistor pull_resistor_57 (.node(transistor_57_out));
  assign MOV_B_1 = transistor_57_out | pull_resistor_42_node;  // OR_Gate or_7, 32 bits wide
  Transistor #(.\type ("n"), .width(32)) transistor_58 (
    .in({pull_resistor_54_node, DATA_IN[23:0]}), .out(transistor_58_out), .gate(pull_resistor_17_node));
  Pull_Resistor pull_resistor_58 (.node(transistor_58_out));
  assign MOV_B_2 = transistor_58_out | pull_resistor_44_node;  // OR_Gate or_8, 32 bits wide
  Pull_Resistor pull_resistor_59 (.node(pull_resistor_59_node));
  Transistor #(.\type ("n"), .width(32)) transistor_59 (
    .in({transistor_55_out, DATA_IN[23:0]}), .out(pull_resistor_59_node), .gate(transistor_18_out));
  assign MOV_B_3 = pull_resistor_59_node | pull_resistor_46_node;  // OR_Gate or_9, 32 bits wide
  Transistor #(.\type ("n"), .width(32)) transistor_60 (
    .in({transistor_56_out, DATA_IN[23:0]}), .out(transistor_60_out), .gate(transistor_27_out));
  Pull_Resistor pull_resistor_60 (.node(transistor_60_out));
  assign MOV_B_4 = transistor_60_out | transistor_48_out;  // OR_Gate or_10, 32 bits wide
endmodule

module LINE_DRAWER (
  input  [7:0] X1,
  input  [7:0] Y1,
  input  [7:0] X2,
  input  [7:0] Y2,
  input  EN,
  input  CLK,
  input  CLR,
  output LINE_IS_VERTICAL,
  output X_Y,
  output SETTING_UP,
  output [7:0] Y,
  output [7:0] X,
  output DONE
);

  wire and_1_out, and_2_out, and_4_out, and_5_out, and_7_out, and_8_out, comparator_1_eq, comparator_2_eq,
       comparator_2_gt, comparator_2_lt, comparator_3_gt, comparator_3_lt, comparator_4_eq, comparator_5_eq,
       comparator_7_gt, comparator_8_eq, comparator_9_eq, d_ff_1_q, d_ff_2_q, E1, multiplexer_4_out,
       not_1_out, not_2_out, not_3_out, not_4_out, not_5_out, not_6_out, not_7_out, or16x_1_out_2, or_1_out,
       or_2_out, or_4_out, or_5_out, or_6_out, or_7_out, register_6_q, SUB, t_ff_1_q, t_ff_1_qn, tunnel,
       X_Y_Y_X;
  wire [7:0] adder_1_out, adder_2_out, adder_3_out, divider_1_out, divider_1_rem, multiplexer_1_out,
       multiplexer_2_out, multiplexer_3_out, multiplexer_5_out, multiplexer_6_out, multiplier_1_out,
       multiplier_2_out, part_1_out_5, register_5_q, subtractor_1_out_4, subtractor_2_out_4,
       subtractor_3_out_4, XX;
  wire [15:0] bit_extender_1_out, X_t, Y_t;

  Register register_1 (.D(X1), .en(EN), .Q(X_t[7:0]), .clk(CLK), .clr(CLR));
  Register register_2 (.D(Y1), .en(EN), .Q(Y_t[7:0]), .clk(CLK), .clr(CLR));
  Register register_3 (.D(X2), .en(EN), .Q(X_t[15:8]), .clk(CLK), .clr(CLR));
  Register register_4 (.D(Y2), .en(EN), .Q(Y_t[15:8]), .clk(CLK), .clr(CLR));
  Comparator #(.width(32)) comparator_1 (.a({Y2, Y1, X2, X1}), .b({Y_t, X_t}), .eq(comparator_1_eq));  // open: gt, lt
  Comparator #(.mode("unsigned")) comparator_2 (
    .a(Y_t[7:0]), .b(Y_t[15:8]), .gt(comparator_2_gt), .eq(comparator_2_eq), .lt(comparator_2_lt));
  and and_1 (and_1_out, comparator_2_gt, comparator_3_gt);
  Comparator #(.mode("unsigned")) comparator_3 (
    .a(X_t[7:0]), .b(X_t[15:8]), .gt(comparator_3_gt), .eq(E1), .lt(comparator_3_lt));
  SUBTRACTOR subtractor_1 (.in_1(X_t[7:0]), .in_3(X_t[15:8]), .out_4(subtractor_1_out_4));  // open: in_2, out_5
  Multiplexer #(.width(8), .enable("false")) multiplexer_1 (
    .in0(X_t[7:0]), .in1(Y_t[7:0]), .out(multiplexer_1_out), .sel(X_Y_Y_X));
  Multiplexer #(.width(8), .enable("false")) multiplexer_2 (
    .in0(part_1_out_5), .in1(X_t[7:0]), .out(multiplexer_2_out), .sel(not_6_out));
  SUBTRACTOR subtractor_2 (.in_1(Y_t[7:0]), .in_3(Y_t[15:8]), .out_4(subtractor_2_out_4));  // open: in_2, out_5
  and and_2 (and_2_out, EN, not_1_out);
  not not_1 (not_1_out, DONE);
  Comparator #(.width(16)) comparator_4 (.a({Y_t[15:8], X_t[15:8]}), .b({Y, X}), .eq(comparator_4_eq));  // open: gt, lt
  and and_3 (DONE, comparator_1_eq, comparator_4_eq);
  or or_1 (or_1_out, comparator_2_eq, comparator_2_lt);
  and and_4 (and_4_out, or_1_out, comparator_3_gt);
  and and_5 (and_5_out, comparator_2_gt, or_2_out);
  or or_2 (or_2_out, E1, comparator_3_lt);
  Pull_Resistor pull_resistor_1 (.node(XX));
  Transistor #(.\type ("n"), .width(8)) transistor_1 (.in(X_t[7:0]), .out(XX), .gate(E1));
  Comparator comparator_5 (.a(subtractor_1_out_4), .b({8{1'b0}}), .eq(comparator_5_eq));  // open: gt, lt
  Multiplexer #(.width(8), .enable("false")) multiplexer_3 (
    .in0(divider_1_out), .in1({8{1'b0}}), .out(multiplexer_3_out), .sel(comparator_5_eq));
  Divider divider_1 (
    .a(subtractor_2_out_4), .b(subtractor_1_out_4), .out(divider_1_out), .rem(divider_1_rem));  // open: upper
  Comparator comparator_6 (.a(multiplexer_1_out), .b(register_5_q), .eq(tunnel));  // open: gt, lt
  not not_2 (not_2_out, tunnel);
  and and_6 (SETTING_UP, not_2_out, not_1_out, not_6_out);
  Register register_5 (.D(multiplexer_2_out), .en(and_2_out), .Q(register_5_q), .clk(CLK), .clr(CLR));
  circuit part_1 (
    .COUNTER_IN(register_5_q), .CONSTANT(8'h1), .out_5(part_1_out_5), .C_B_IN(not_6_out), .SUB(SUB));  // open: C_B_OUT
  Register #(.width(1), .trigger("high")) register_6 (
    .D(tunnel), .en(not_3_out), .Q(register_6_q), .clk(tunnel), .clr(comparator_4_eq));
  not not_3 (not_3_out, comparator_4_eq);
  not not_4 (not_4_out, not_2_out);
  or or_3 (SUB, and_4_out, and_5_out, and_1_out);
  D_Flip_Flop d_ff_1 (.clk(CLK), .D(comparator_5_eq), .Q(d_ff_1_q), .reset(or_4_out));  // open: Qn, preset, en
  or or_4 (or_4_out, CLR, not_5_out);
  not not_5 (not_5_out, comparator_5_eq);
  OR16x or16x_1 (.in_1(bit_extender_1_out), .out_2(or16x_1_out_2));
  assign bit_extender_1_out = {{8{1'b0}}, divider_1_rem};  // Bit_Extender bit_extender_1
  Adder adder_1 (.a(multiplier_1_out), .b(divider_1_rem), .out(adder_1_out));  // open: cin, cout
  Multiplier multiplier_1 (.a(multiplexer_3_out), .b(X_t[7:0]), .out(multiplier_1_out));  // open: cin, cout
  Adder adder_2 (.a(Y_t[7:0]), .b(adder_1_out), .out(adder_2_out));  // open: cin, cout
  SUBTRACTOR subtractor_3 (.in_1(Y_t[7:0]), .in_3(adder_1_out), .out_4(subtractor_3_out_4));  // open: in_2, out_5
  Multiplier multiplier_2 (.a(register_5_q), .b(multiplexer_5_out), .out(multiplier_2_out));  // open: cin, cout
  not not_6 (not_6_out, multiplexer_4_out);
  Multiplexer #(.enable("false")) multiplexer_4 (
    .in0(t_ff_1_q), .in1(t_ff_1_qn), .out(multiplexer_4_out), .sel(or_6_out));
  T_Flip_Flop t_ff_1 (.clk(not_4_out), .T(not_4_out), .Q(t_ff_1_q), .Qn(t_ff_1_qn), .reset(DONE));  // open: preset, en
  and and_7 (and_7_out, or_5_out, ~not_1_out, t_ff_1_qn);  // AND_Gate
  Multiplexer #(.width(8), .enable("false")) multiplexer_5 (
    .in0(multiplexer_3_out), .in1(adder_1_out), .out(multiplexer_5_out), .sel(or16x_1_out_2));
  Comparator comparator_7 (.a(adder_1_out), .b(8'h80), .gt(comparator_7_gt));  // open: eq, lt
  Multiplexer #(.width(8), .enable("false")) multiplexer_6 (
    .in0(adder_2_out), .in1(subtractor_3_out_4), .out(multiplexer_6_out), .sel(comparator_7_gt));
  Adder adder_3 (.a(multiplier_2_out), .b(multiplexer_6_out), .out(adder_3_out));  // open: cin, cout
  Multiplexer #(.width(8), .enable("false")) multiplexer_7 (.in0(register_5_q), .in1(XX), .out(X), .sel(or_5_out));
  Comparator #(.width(16)) comparator_8 (.a(X_t), .b({16{1'b0}}), .eq(comparator_8_eq));  // open: gt, lt
  or or_5 (or_5_out, comparator_8_eq, E1);
  or or_6 (or_6_out, and_7_out, and_8_out);
  and and_8 (and_8_out, register_6_q, t_ff_1_qn);
  and and_9 (X_Y_Y_X, d_ff_1_q, ~DONE);  // AND_Gate
  and and_10 (LINE_IS_VERTICAL, d_ff_1_q, ~DONE);  // AND_Gate
  or or_7 (or_7_out, CLR, not_7_out);
  Multiplexer #(.width(8), .enable("false")) multiplexer_8 (
    .in0(adder_3_out), .in1(register_5_q), .out(Y), .sel(d_ff_1_q));
  and and_11 (X_Y, d_ff_2_q, ~DONE);  // AND_Gate
  D_Flip_Flop d_ff_2 (.clk(CLK), .D(comparator_9_eq), .Q(d_ff_2_q), .reset(or_7_out));  // open: Qn, preset, en
  not not_7 (not_7_out, CLK);
  Comparator comparator_9 (.a(Y), .b(X), .eq(comparator_9_eq));  // open: gt, lt

  // Notes on the sheet:
  //   HLT
endmodule

module SUBTRACTOR (
  input  [7:0] in_1,
  input  in_2,
  input  [7:0] in_3,
  output [7:0] out_4,
  output out_5
);

  wire comparator_1_gt;
  wire [7:0] multiplexer_1_out, multiplexer_2_out;

  Multiplexer #(.width(8), .enable("false")) multiplexer_1 (
    .in0(in_1), .in1(in_3), .out(multiplexer_1_out), .sel(comparator_1_gt));
  Subtractor subtractor_1 (.a(multiplexer_1_out), .b(multiplexer_2_out), .out(out_4), .bin(in_2), .bout(out_5));
  Multiplexer #(.width(8), .enable("false")) multiplexer_2 (
    .in0(in_3), .in1(in_1), .out(multiplexer_2_out), .sel(comparator_1_gt));
  Comparator comparator_1 (.a(in_3), .b(in_1), .gt(comparator_1_gt));  // open: eq, lt
endmodule

module OR16x (
  input  [15:0] in_1,
  output out_2
);

  or or_1 (out_2, in_1[0], in_1[1], in_1[2], in_1[3], in_1[4], in_1[5], in_1[6], in_1[7], in_1[8], in_1[9], in_1[10], in_1[11], in_1[12], in_1[13], in_1[14], in_1[15]);
endmodule

module circuit (
  input  C_B_IN,
  input  SUB,
  input  [7:0] COUNTER_IN,
  input  [7:0] CONSTANT,
  output [7:0] out_5,
  output C_B_OUT
);

  wire adder_1_cout, demultiplexer_1_out0, demultiplexer_1_out1, subtractor_1_bout;
  wire [7:0] adder_1_out, subtractor_1_out;

  Demultiplexer #(.enable("false")) demultiplexer_1 (
    .out0(demultiplexer_1_out0), .out1(demultiplexer_1_out1), .in(C_B_IN), .sel(SUB));
  Adder adder_1 (.a(COUNTER_IN), .b(CONSTANT), .out(adder_1_out), .cin(demultiplexer_1_out0), .cout(adder_1_cout));
  Subtractor subtractor_1 (
    .a(COUNTER_IN), .b(CONSTANT), .out(subtractor_1_out), .bin(demultiplexer_1_out1), .bout(subtractor_1_bout));
  Multiplexer #(.width(8), .enable("false")) multiplexer_1 (
    .in0(adder_1_out), .in1(subtractor_1_out), .out(out_5), .sel(SUB));
  Multiplexer #(.enable("false")) multiplexer_2 (.in0(adder_1_cout), .in1(subtractor_1_bout), .out(C_B_OUT), .sel(SUB));
endmodule

module JOYSTICK (
  input  [4:0] JOYSTICK_X,
  input  [4:0] JOYSTICK_Y,
  input  [7:0] SENSITIVITY,
  input  EN,
  input  CLK,
  input  CLR,
  input  [7:0] SCREEN_SIZE,
  output [7:0] X,
  output [7:0] Y
);

  wire and_1_out, and_2_out, and_3_out, and_4_out, comparator_1_gt, comparator_1_lt, comparator_2_gt,
       comparator_2_lt, comparator_3_eq, comparator_4_eq, comparator_6_lt, comparator_7_eq, comparator_8_eq,
       comparator_9_eq, comparator_10_eq, comparator_11_eq, comparator_12_eq, comparator_13_eq,
       multiplexer_5_out, multiplexer_6_out, multiplexer_7_out, multiplexer_8_out, not_1_out, not_2_out,
       not_3_out, not_5_out, not_6_out, not_7_out, or_1_out, or_2_out, or_3_out, or_4_out, or_5_out, sub,
       sub_2, t_ff_1_q, t_ff_2_q;
  wire [4:0] adder_2_out, adder_3_out, multiplexer_1_out, multiplexer_2_out, multiplexer_3_out,
       multiplexer_4_out, X_q, Y_q;
  wire [7:0] adder_1_out, bit_extender_1_out, bit_extender_2_out, bit_extender_3_out, bit_extender_4_out,
       multiplier_1_out, multiplier_2_out, part_1_out_5, part_2_out_5, SPEED_CONTROL_q;

  and and_1 (and_1_out, not_5_out, not_1_out);
  or or_1 (or_1_out, comparator_1_gt, comparator_1_lt);
  Comparator #(.width(5)) comparator_1 (
    .a(JOYSTICK_X), .b(X_q), .gt(comparator_1_gt), .lt(comparator_1_lt));  // open: eq
  Comparator #(.width(5)) comparator_2 (
    .a(JOYSTICK_Y), .b(Y_q), .gt(comparator_2_gt), .lt(comparator_2_lt));  // open: eq
  or or_2 (or_2_out, comparator_2_gt, comparator_2_lt);
  Comparator #(.width(5)) comparator_3 (.a(X_q), .b(5'b10000), .eq(comparator_3_eq));  // open: gt, lt
  Register #(.width(5)) u_X (.D(JOYSTICK_X), .en(EN), .Q(X_q), .clk(CLK), .clr(CLR));
  Register #(.width(5)) u_Y (.D(JOYSTICK_Y), .en(EN), .Q(Y_q), .clk(CLK), .clr(CLR));
  or or_3 (or_3_out, or_1_out, or_2_out);
  not not_1 (not_1_out, or_3_out);
  and and_2 (and_2_out, comparator_3_eq, comparator_4_eq);
  Comparator #(.width(5)) comparator_4 (.a(Y_q), .b(5'b10000), .eq(comparator_4_eq));  // open: gt, lt
  not not_2 (not_2_out, comparator_4_eq);
  not not_3 (not_3_out, comparator_3_eq);
  Register SPEED_CONTROL (.D(adder_1_out), .en(and_1_out), .Q(SPEED_CONTROL_q), .clk(CLK), .clr(or_4_out));
  Adder adder_1 (.a(SPEED_CONTROL_q), .b(8'h1), .out(adder_1_out));  // open: cin, cout
  or or_4 (or_4_out, CLR, comparator_11_eq);
  Comparator #(.width(5), .mode("unsigned")) comparator_5 (.a(X_q), .b(5'b10000), .lt(sub));  // open: gt, eq
  Multiplexer #(.width(5), .enable("false")) multiplexer_1 (
    .in0(X_q), .in1(5'b10000), .out(multiplexer_1_out), .sel(sub));
  Multiplexer #(.width(5), .enable("false")) multiplexer_2 (
    .in0(5'b10000), .in1(X_q), .out(multiplexer_2_out), .sel(sub));
  Multiplexer #(.width(5), .enable("false")) multiplexer_3 (
    .in0(Y_q), .in1(5'b10000), .out(multiplexer_3_out), .sel(comparator_6_lt));
  Multiplexer #(.width(5), .enable("false")) multiplexer_4 (
    .in0(5'b10000), .in1(Y_q), .out(multiplexer_4_out), .sel(comparator_6_lt));
  not not_4 (sub_2, comparator_6_lt);
  Comparator #(.width(5), .mode("unsigned")) comparator_6 (
    .a(Y_q), .b(5'b10000), .lt(comparator_6_lt));  // open: gt, eq
  Comparator comparator_7 (.a(X), .b(bit_extender_4_out), .eq(comparator_7_eq));  // open: gt, lt
  not not_5 (not_5_out, and_2_out);
  assign bit_extender_1_out = {{3{1'b0}}, adder_2_out};  // Bit_Extender bit_extender_1
  Adder #(.width(5)) adder_2 (.a(multiplexer_1_out), .b(multiplexer_2_out), .out(adder_2_out));  // open: cin, cout
  assign bit_extender_2_out = {{3{1'b0}}, adder_3_out};  // Bit_Extender bit_extender_2
  Adder #(.width(5)) adder_3 (.a(multiplexer_3_out), .b(multiplexer_4_out), .out(adder_3_out));  // open: cin, cout
  assign bit_extender_3_out = {{3{1'b0}}, Y_q};  // Bit_Extender bit_extender_3
  assign bit_extender_4_out = {{3{1'b0}}, X_q};  // Bit_Extender bit_extender_4
  T_Flip_Flop t_ff_1 (.clk(not_1_out), .T(not_1_out), .Q(t_ff_1_q), .reset(comparator_7_eq));  // open: Qn, preset, en
  and and_3 (and_3_out, not_3_out, multiplexer_5_out, not_5_out);
  Multiplexer #(.enable("false")) multiplexer_5 (.in0(1'b1), .in1(not_6_out), .out(multiplexer_5_out), .sel(1'b0));
  not not_6 (not_6_out, comparator_9_eq);
  Multiplier multiplier_1 (.a(bit_extender_1_out), .b(8'h1), .out(multiplier_1_out));  // open: cin, cout
  Multiplier multiplier_2 (.a(bit_extender_2_out), .b(8'h1), .out(multiplier_2_out));  // open: cin, cout
  Register X_POS (.D(part_1_out_5), .en(and_3_out), .Q(X), .clk(multiplexer_7_out), .clr(CLR));
  circuit part_1 (.COUNTER_IN(X), .CONSTANT(8'h1), .out_5(part_1_out_5), .SUB(sub));  // open: C_B_IN, C_B_OUT
  Comparator comparator_8 (.a(Y), .b(bit_extender_3_out), .eq(comparator_8_eq));  // open: gt, lt
  Comparator comparator_9 (.a(X), .b(SCREEN_SIZE), .eq(comparator_9_eq));  // open: gt, lt
  T_Flip_Flop t_ff_2 (.clk(not_1_out), .T(not_1_out), .Q(t_ff_2_q), .reset(comparator_8_eq));  // open: Qn, preset, en
  Comparator #(.mode("unsigned")) comparator_10 (
    .a(SPEED_CONTROL_q), .b(multiplier_1_out), .eq(comparator_10_eq));  // open: gt, lt
  Comparator comparator_11 (.a(SPEED_CONTROL_q), .b(SENSITIVITY), .eq(comparator_11_eq));  // open: gt, lt
  Register Y_POS (.D(part_2_out_5), .en(and_4_out), .Q(Y), .clk(multiplexer_8_out), .clr(CLR));
  or or_5 (or_5_out, t_ff_2_q, t_ff_1_q);
  and and_4 (and_4_out, not_5_out, multiplexer_6_out, not_2_out);
  Multiplexer #(.enable("false")) multiplexer_6 (.in0(1'b1), .in1(not_7_out), .out(multiplexer_6_out), .sel(1'b0));
  not not_7 (not_7_out, comparator_13_eq);
  Comparator #(.mode("unsigned")) comparator_12 (
    .a(multiplier_2_out), .b(SPEED_CONTROL_q), .eq(comparator_12_eq));  // open: gt, lt
  circuit part_2 (.COUNTER_IN(Y), .CONSTANT(8'h1), .out_5(part_2_out_5), .SUB(sub_2));  // open: C_B_IN, C_B_OUT
  Multiplexer #(.enable("false")) multiplexer_7 (
    .in0(comparator_12_eq), .in1(CLK), .out(multiplexer_7_out), .sel(1'b0));
  Comparator comparator_13 (.a(Y), .b(SCREEN_SIZE), .eq(comparator_13_eq));  // open: gt, lt
  Multiplexer #(.enable("false")) multiplexer_8 (
    .in0(comparator_10_eq), .in1(CLK), .out(multiplexer_8_out), .sel(1'b0));
endmodule

module TEXTURE_MAPPING (
  input  [15:0] DTATA_IN_2,
  input  [15:0] DATA_IN,
  input  [15:0] TEXTURE_IN,
  input  CLR,
  input  CLK,
  input  [19:0] INSTR,
  input  EN,
  output [7:0] X,
  output [7:0] Y,
  output DONE,
  output [15:0] COLOUR,
  output [7:0] TEXTURE_CACHE_ADDRESS,
  output SEL_TEXTURE,
  output [7:0] ADDRESS_DATA,
  output SEL_DATA
);

  wire and_1_out, and_2_out, and_3_out, and_4_out, and_5_out, and_6_out, and_7_out, and_8_out, and_9_out,
       and_10_out, and_11_out, and_12_out, and_13_out, and_14_out, and_15_out, and_16_out, and_17_out,
       and_18_out, and_19_out, and_20_out, and_21_out, and_22_out, comparator_1_gt, comparator_2_eq,
       comparator_2_gt, comparator_2_lt, comparator_3_eq, comparator_4_eq, comparator_5_eq, comparator_6_gt,
       comparator_6_lt, comparator_7_eq, comparator_7_gt, comparator_7_lt, comparator_8_gt, comparator_9_eq,
       comparator_10_eq, comparator_11_eq, comparator_12_eq, comparator_13_eq, comparator_13_lt,
       comparator_14_eq, comparator_15_eq, comparator_16_eq, comparator_16_gt, comparator_17_eq, d_ff_1_q,
       d_ff_2_q, d_ff_3_q, demultiplexer_1_out0, demultiplexer_1_out1, j_k_ff_1_q, multiplexer_1_out,
       multiplexer_4_out, not_1_out, not_2_out, not_3_out, not_4_out, not_5_out, not_6_out, not_7_out,
       not_8_out, or16x_1_out_2, or_1_out, or_2_out, or_3_out, or_4_out, or_5_out, or_6_out, or_7_out,
       or_8_out, or_10_out, or_11_out, or_12_out, or_13_out, or_14_out, or_15_out, or_16_out, t_ff_1_q,
       t_ff_2_q;
  wire [7:0] adder_1_out, adder_3_out, END_2_q, END_q, multiplexer_2_out, multiplexer_5_out,
       multiplexer_6_out, part_1_out_5, register_1_q, register_4_q, START_2_q, START_q;
  wire [15:0] adder_2_out, COMPARE_END_2_q, COMPARE_END_q, HIGHEST_VALUE_q, LOWEST_VALUE_q, PROGRAM_CTRL_q,
       register_2_q, subtractor_1_out;
  wire [19:0] IR_q;

  Register #(.width(16), .trigger("high")) COMPARE_END (
    .D(DATA_IN), .en(d_ff_1_q), .Q(COMPARE_END_q), .clk(and_1_out), .clr(CLR));
  Register #(.width(16), .trigger("high")) HIGHEST_VALUE (
    .D(COMPARE_END_q), .en(comparator_1_gt), .Q(HIGHEST_VALUE_q), .clk(and_1_out), .clr(CLR));
  and and_1 (and_1_out, CLK, EN);
  Register #(.width(20)) IR (.D(INSTR), .en(EN), .Q(IR_q), .clk(and_1_out), .clr(CLR));
  Comparator comparator_1 (.a(COMPARE_END_q[15:8]), .b(HIGHEST_VALUE_q[15:8]), .gt(comparator_1_gt));  // open: eq, lt
  and and_2 (and_2_out, ~comparator_1_gt, comparator_2_eq);  // AND_Gate
  Comparator #(.width(16)) comparator_2 (
    .a(COMPARE_END_q), .b(HIGHEST_VALUE_q), .gt(comparator_2_gt), .eq(comparator_2_eq), .lt(comparator_2_lt));
  or or_1 (or_1_out, comparator_2_gt, comparator_2_lt);
  not not_1 (not_1_out, and_3_out);
  and and_3 (and_3_out, and_2_out, comparator_3_eq);
  Comparator #(.width(4), .mode("unsigned")) comparator_3 (
    .a(IR_q[19:16]), .b(4'b0010), .eq(comparator_3_eq));  // open: gt, lt
  Comparator #(.width(4)) comparator_4 (.a(IR_q[19:16]), .b(4'b0001), .eq(comparator_4_eq));  // open: gt, lt
  and and_4 (and_4_out, and_1_out, comparator_15_eq);
  Register #(.width(16), .trigger("high")) COMPARE_END_2 (
    .D(DATA_IN), .en(d_ff_2_q), .Q(COMPARE_END_2_q), .clk(and_1_out), .clr(CLR));
  Register #(.width(16), .trigger("high")) LOWEST_VALUE (
    .D(COMPARE_END_2_q), .en(multiplexer_1_out), .Q(LOWEST_VALUE_q), .clk(and_1_out), .clr(CLR));
  and and_5 (and_5_out, comparator_1_gt, or_1_out);
  or or_2 (or_2_out, and_5_out, not_1_out, CLR);
  Register START (.D(IR_q[15:8]), .en(comparator_3_eq), .Q(START_q), .clk(and_1_out), .clr(CLR));
  Comparator #(.width(4)) comparator_5 (.a(IR_q[19:16]), .b(4'b0011), .eq(comparator_5_eq));  // open: gt, lt
  Demultiplexer #(.enable("false")) demultiplexer_1 (
    .out0(demultiplexer_1_out0), .out1(demultiplexer_1_out1), .in(and_17_out), .sel(j_k_ff_1_q));
  J_K_Flip_Flop j_k_ff_1 (
    .J(and_17_out), .clk(and_4_out), .K(and_17_out), .Q(j_k_ff_1_q), .reset(CLR));  // open: Qn, preset, en
  Comparator comparator_6 (
    .a(COMPARE_END_2_q[15:8]), .b(LOWEST_VALUE_q[15:8]), .gt(comparator_6_gt), .lt(comparator_6_lt));  // open: eq
  Multiplexer #(.enable("false")) multiplexer_1 (
    .in0(comparator_6_gt), .in1(comparator_6_lt), .out(multiplexer_1_out), .sel(not_5_out));
  Comparator #(.width(16)) comparator_7 (
    .a(COMPARE_END_2_q), .b(LOWEST_VALUE_q), .gt(comparator_7_gt), .eq(comparator_7_eq), .lt(comparator_7_lt));
  or or_3 (or_3_out, comparator_7_gt, comparator_7_lt);
  D_Flip_Flop d_ff_1 (
    .clk(and_1_out), .D(and_2_out), .Q(d_ff_1_q), .en(and_3_out), .reset(or_2_out));  // open: Qn, preset
  and and_6 (and_6_out, or_5_out, not_6_out);
  Register END (.D(IR_q[7:0]), .en(comparator_3_eq), .Q(END_q), .clk(and_1_out), .clr(CLR));
  not not_2 (not_2_out, not_4_out);
  or or_4 (or_4_out, and_7_out, and_20_out);
  and and_7 (and_7_out, not_4_out, or_5_out);
  or or_5 (or_5_out, comparator_3_eq, comparator_5_eq);
  or or_6 (or_6_out, or_5_out, comparator_5_eq, comparator_4_eq);
  Register #(.width(16), .trigger("high")) register_1 (
    .D(DATA_IN), .en(demultiplexer_1_out0), .Q({Y, register_1_q}), .clk(and_1_out), .clr(CLR));
  Register #(.width(16), .trigger("high")) register_2 (
    .D(DTATA_IN_2), .en(demultiplexer_1_out1), .Q(register_2_q), .clk(and_1_out), .clr(CLR));
  Subtractor #(.width(16)) subtractor_1 (
    .a(LOWEST_VALUE_q), .b(HIGHEST_VALUE_q), .out(subtractor_1_out));  // open: bin, bout
  and and_8 (and_8_out, ~multiplexer_1_out, comparator_7_eq);  // AND_Gate
  and and_9 (and_9_out, multiplexer_1_out, or_3_out);
  or or_7 (or_7_out, and_9_out, not_3_out, CLR);
  Multiplexer #(.width(8), .enable("false")) multiplexer_2 (
    .in0(adder_1_out), .in1(START_q), .out(multiplexer_2_out), .sel(or_4_out));
  Register COUNTER (.D(multiplexer_2_out), .en(SEL_DATA), .Q(ADDRESS_DATA), .clk(multiplexer_4_out), .clr(or_8_out));
  Multiplexer #(.enable("false")) multiplexer_3 (.in0(and_6_out), .in1(t_ff_1_q), .out(SEL_DATA), .sel(not_2_out));
  or or_8 (or_8_out, CLR, and_10_out);
  and and_10 (and_10_out, comparator_11_eq, comparator_5_eq);
  Multiplexer #(.enable("false")) multiplexer_4 (
    .in0(and_1_out), .in1(and_11_out), .out(multiplexer_4_out), .sel(and_19_out));
  and and_11 (and_11_out, and_1_out, comparator_15_eq);
  Comparator #(.width(16)) comparator_8 (
    .a({Y, register_1_q}), .b(register_2_q), .gt(comparator_8_gt));  // open: eq, lt
  and and_12 (and_12_out, comparator_9_eq, comparator_11_eq);
  or or_9 (DONE, and_12_out, and_14_out);
  Comparator #(.width(16)) comparator_9 (
    .a(PROGRAM_CTRL_q), .b(subtractor_1_out), .eq(comparator_9_eq));  // open: gt, lt
  D_Flip_Flop d_ff_2 (
    .clk(and_1_out), .D(and_8_out), .Q(d_ff_2_q), .en(and_13_out), .reset(or_7_out));  // open: Qn, preset
  not not_3 (not_3_out, and_13_out);
  Adder adder_1 (.a(ADDRESS_DATA), .b(8'h1), .out(adder_1_out));  // open: cin, cout
  not not_4 (not_4_out, t_ff_1_q);
  OR16x or16x_1 (.in_1({Y, register_1_q}), .out_2(or16x_1_out_2));
  Register X_COUNTER (.D(multiplexer_5_out), .en(and_17_out), .Q(X), .clk(and_1_out), .clr(CLR));
  Multiplexer #(.width(8), .enable("false")) multiplexer_5 (
    .in0(register_1_q), .in1(part_1_out_5), .out(multiplexer_5_out), .sel(and_16_out));
  Comparator comparator_10 (.a(register_1_q), .b(X), .eq(comparator_10_eq));  // open: gt, lt
  or or_10 (or_10_out, comparator_15_eq, CLR);
  and and_13 (and_13_out, and_8_out, or_5_out);
  and and_14 (and_14_out, or_5_out, comparator_11_eq);
  Comparator comparator_11 (.a(ADDRESS_DATA), .b(END_q), .eq(comparator_11_eq));  // open: gt, lt
  Comparator comparator_12 (.a(START_q), .b(ADDRESS_DATA), .eq(comparator_12_eq));  // open: gt, lt
  and and_15 (and_15_out, comparator_12_eq, or_5_out);
  Comparator #(.mode("unsigned")) comparator_13 (
    .a(ADDRESS_DATA), .b(8'h1), .eq(comparator_13_eq), .lt(comparator_13_lt));  // open: gt
  or or_11 (or_11_out, comparator_13_eq, comparator_13_lt);
  not not_5 (not_5_out, or_11_out);
  and and_16 (and_16_out, d_ff_3_q, or16x_1_out_2);
  circuit part_1 (
    .COUNTER_IN(X), .CONSTANT(8'h1), .out_5(part_1_out_5), .SUB(comparator_8_gt));  // open: C_B_IN, C_B_OUT
  D_Flip_Flop d_ff_3 (.clk(and_1_out), .D(comparator_10_eq), .Q(d_ff_3_q), .reset(or_10_out));  // open: Qn, preset, en
  and and_17 (and_17_out, or_6_out, t_ff_1_q, or_12_out);
  or or_12 (or_12_out, d_ff_3_q, comparator_5_eq, and_18_out);
  and and_18 (and_18_out, ~comparator_14_eq, comparator_11_eq);  // AND_Gate
  T_Flip_Flop t_ff_1 (.clk(and_15_out), .T(and_15_out), .Q(t_ff_1_q), .reset(or_13_out));  // open: Qn, preset, en
  or or_13 (or_13_out, CLR, comparator_11_eq);
  not not_6 (not_6_out, comparator_11_eq);
  Comparator comparator_14 (.a(END_q), .b({8{1'b0}}), .eq(comparator_14_eq));  // open: gt, lt
  and and_19 (and_19_out, t_ff_1_q, or_14_out);
  Comparator comparator_15 (.a(X), .b(register_2_q[7:0]), .eq(comparator_15_eq));  // open: gt, lt
  Register #(.width(16), .trigger("high")) register_3 (
    .D(TEXTURE_IN), .en(or_14_out), .Q(COLOUR), .clk(and_1_out), .clr(CLR));
  or or_14 (or_14_out, comparator_4_eq, comparator_5_eq);
  and and_20 (and_20_out, d_ff_2_q, comparator_11_eq);
  Register #(.width(16)) PROGRAM_CTRL (
    .D(adder_2_out), .en(comparator_11_eq), .Q(PROGRAM_CTRL_q), .clk(demultiplexer_1_out1), .clr(CLR));
  Register START_2 (.D(IR_q[15:8]), .en(or_14_out), .Q(START_2_q), .clk(and_1_out), .clr(CLR));
  Adder #(.width(16)) adder_2 (.a(PROGRAM_CTRL_q), .out(adder_2_out));  // open: b, cin, cout
  Register END_2 (.D(IR_q[7:0]), .en(comparator_5_eq), .Q(END_2_q), .clk(and_1_out), .clr(CLR));
  and and_21 (and_21_out, not_8_out, not_7_out);
  Multiplexer #(.width(8), .enable("false")) multiplexer_6 (
    .in0(adder_3_out), .in1(START_2_q), .out(multiplexer_6_out), .sel(and_21_out));
  Register register_4 (.D(multiplexer_6_out), .en(SEL_TEXTURE), .Q(register_4_q), .clk(and_1_out), .clr(or_15_out));
  Multiplexer #(.enable("false")) multiplexer_7 (.in0(and_22_out), .in1(t_ff_2_q), .out(SEL_TEXTURE), .sel(t_ff_2_q));
  or or_15 (or_15_out, CLR, comparator_17_eq);
  and and_22 (and_22_out, or_14_out, not_8_out);
  not not_7 (not_7_out, t_ff_2_q);
  Adder adder_3 (.a(register_4_q), .b(8'h1), .out(adder_3_out));  // open: cin, cout
  Transistor #(.\type ("n"), .gate("br"), .width(8)) transistor_1 (
    .in(register_4_q), .out(TEXTURE_CACHE_ADDRESS), .gate(or_16_out));
  or or_16 (or_16_out, comparator_16_gt, comparator_16_eq);
  Comparator #(.mode("unsigned")) comparator_16 (
    .a(register_4_q), .b(START_2_q), .gt(comparator_16_gt), .eq(comparator_16_eq));  // open: lt
  Comparator comparator_17 (.a(register_4_q), .b(END_2_q), .eq(comparator_17_eq));  // open: gt, lt
  not not_8 (not_8_out, t_ff_2_q);
  T_Flip_Flop t_ff_2 (.clk(comparator_16_eq), .T(comparator_16_eq), .Q(t_ff_2_q), .reset(CLR));  // open: Qn, preset, en
endmodule

module TEXTURE_CACHE (
  input  [7:0] ADDRESS_DATA,
  input  DIFFRENT_LINE,
  input  [15:0] FROM_LD,
  input  SEL_DATA,
  input  [7:0] ADDRESS_TEXTURE,
  input  [15:0] FROM_TEXTURE_MEM,
  input  W_CLK,
  input  R_W,
  input  SEL_TEXTURE,
  input  CLR,
  output [15:0] DATA_2,
  output [15:0] DATA_1,
  output [15:0] TEXTURE_DATA
);

  wire not_1_out, not_2_out;
  wire [15:0] demultiplexer_1_out0, demultiplexer_1_out1;

  Demultiplexer #(.width(16), .enable("false")) demultiplexer_1 (
    .out0(demultiplexer_1_out0), .out1(demultiplexer_1_out1), .in(FROM_LD), .sel(not_1_out));
  not not_1 (not_1_out, DIFFRENT_LINE);
  not not_2 (not_2_out, R_W);
  RAM_part #(.dataWidth(16), .bus("separate")) ram_1 (
    .addr(ADDRESS_DATA), .din(demultiplexer_1_out0), .data(DATA_2), .str(SEL_DATA), .sel(R_W), .clk(W_CLK),
    .ld(not_2_out), .clr(CLR));
  RAM_part #(.dataWidth(16), .bus("separate")) ram_2 (
    .addr(ADDRESS_DATA), .din(demultiplexer_1_out1), .data(DATA_1), .str(R_W), .sel(SEL_DATA), .clk(W_CLK),
    .ld(not_2_out), .clr(CLR));
  RAM_part #(.dataWidth(16), .bus("separate")) ram_3 (
    .addr(ADDRESS_TEXTURE), .din(FROM_TEXTURE_MEM), .data(TEXTURE_DATA), .str(R_W), .sel(SEL_TEXTURE),
    .clk(W_CLK), .ld(not_2_out), .clr(CLR));
endmodule

module _2D_ENGINE_CONTROL_UNIT (
  input  [7:0] DATA_IN,
  input  EN,
  input  SETTING_UP,
  input  DONE,
  input  CLR,
  input  CLK,
  input  [7:0] PC_IN,
  input  in_8,
  input  [1:0] in_9,
  output [7:0] X1,
  output [7:0] Y1,
  output [7:0] X2,
  output [7:0] Y2,
  output EN_JOYSTICK,
  output JS_AND_LD,
  output [7:0] SENSITIVITY,
  output LD_EN,
  output [7:0] SCREEN_SIZE,
  output SEL_LD,
  output [15:0] COLOUR,
  output MAINBOARD_RAM_R_W,
  output [7:0] JMP,
  output MUX,
  output [7:0] BROD,
  output CRAM,
  output PC_EN,
  output VRAM,
  output CLR_PC,
  output VMEM
);

  wire and_1_out, and_2_out, and_3_out, and_4_out, and_6_out, and_7_out, and_8_out, and_9_out, and_10_out,
       and_14_out, comparator_1_eq, comparator_2_eq, comparator_3_eq, comparator_4_eq, comparator_5_eq,
       comparator_7_eq, comparator_8_eq, comparator_9_eq, comparator_9_gt, comparator_9_lt, comparator_10_eq,
       comparator_10_gt, comparator_10_lt, comparator_11_eq, comparator_11_gt, comparator_11_lt,
       comparator_12_eq, comparator_12_gt, comparator_12_lt, comparator_13_eq, comparator_13_gt,
       comparator_13_lt, comparator_14_eq, comparator_14_gt, comparator_14_lt, comparator_15_eq,
       comparator_16_eq, comparator_18_eq, comparator_18_gt, comparator_18_lt, comparator_19_eq,
       comparator_19_gt, comparator_19_lt, comparator_20_eq, comparator_20_gt, comparator_20_lt,
       comparator_21_eq, counter_1_q, d_ff_1_q, I_O_2_out, I_O_out, MEM_2_out, MEM_out, not_1_out, not_3_out,
       or_2_out, or_3_out, or_4_out, or_7_out, or_8_out, or_9_out, or_10_out, or_11_out, or_12_out,
       or_14_out, or_15_out, or_16_out, or_17_out, or_18_out, or_19_out, or_20_out, or_21_out, or_22_out,
       RAM_2_out, RAM_out, ROM_out, transistor_1_out, undriven, undriven_2;
  wire [7:0] ADDR, and_11_out, and_12_out, and_13_out, bit_extender_1_out, bit_extender_2_out,
       bit_extender_3_out, or_23_out, pull_resistor_4_node, register_1_q, register_2_q, register_5_q,
       register_6_q, transistor_3_out, transistor_4_out, xor_1_out;
  wire [11:0] START_q, STOP_q;
  wire [31:0] instruction_registers_1_data_out;

  Comparator comparator_1 (
    .a(instruction_registers_1_data_out[31:24]), .b(8'h7), .eq(comparator_1_eq));  // open: gt, lt
  INSTRUCTION_REGISTERS instruction_registers_1 (
    .STATUS(EN), .DATA_IN(DATA_IN), .CLR(CLR), .CLK(CLK), .DATA_OUT(instruction_registers_1_data_out));
  Comparator #(.width(16)) comparator_2 (
    .a(instruction_registers_1_data_out[31:16]), .b(16'he68e), .eq(comparator_2_eq));  // open: gt, lt
  Comparator #(.width(16)) comparator_3 (
    .a(instruction_registers_1_data_out[31:16]), .b(16'he908), .eq(comparator_3_eq));  // open: gt, lt
  Comparator #(.width(16)) comparator_4 (
    .a(instruction_registers_1_data_out[31:16]), .b(16'hd55b), .eq(comparator_4_eq));  // open: gt, lt
  or or_1 (LD_EN, comparator_3_eq, comparator_2_eq);
  Comparator #(.width(16)) comparator_5 (
    .a(instruction_registers_1_data_out[31:16]), .b(16'hede6), .eq(comparator_5_eq));  // open: gt, lt
  Comparator #(.width(24)) comparator_6 (
    .a(instruction_registers_1_data_out[23:0]), .b(24'hffede6), .eq(MUX));  // open: gt, lt
  Comparator #(.width(16)) comparator_7 (
    .a(instruction_registers_1_data_out[31:16]), .b(16'he408), .eq(comparator_7_eq));  // open: gt, lt
  or or_2 (or_2_out, and_2_out, and_14_out, CLR);
  and and_1 (and_1_out, ~counter_1_q, comparator_1_eq);  // AND_Gate
  Counter #(.width(1), .max('h1)) counter_1 (
    .Q(counter_1_q), .clk(transistor_1_out), .clr(or_2_out));  // open: load, D, count, carry
  Transistor #(.\type ("n")) transistor_1 (.in(CLK), .out(transistor_1_out), .gate(comparator_1_eq));
  Comparator comparator_8 (.a(PC_IN), .b({8{1'b0}}), .eq(comparator_8_eq));  // open: gt, lt
  Register register_1 (
    .D(instruction_registers_1_data_out[15:8]), .en(comparator_7_eq), .Q(register_1_q), .clk(undriven),
    .clr(undriven_2));
  Register register_2 (
    .D(instruction_registers_1_data_out[7:0]), .en(comparator_7_eq), .Q(register_2_q), .clk(undriven),
    .clr(undriven_2));
  Register #(.width(12), .trigger("high")) START (
    .D(instruction_registers_1_data_out[11:0]), .en(and_1_out), .Q(START_q), .clk(CLK), .clr(or_2_out));
  Register #(.width(12), .trigger("high")) STOP (
    .D(instruction_registers_1_data_out[23:12]), .en(and_1_out), .Q(STOP_q), .clk(CLK), .clr(or_2_out));
  D_Flip_Flop d_ff_1 (.clk(and_1_out), .D(and_1_out), .Q(d_ff_1_q), .reset(or_2_out));  // open: Qn, preset, en
  Register register_3 (.D(instruction_registers_1_data_out[7:0]), .en(comparator_2_eq), .Q(X1), .clk(CLK), .clr(CLR));
  Register register_4 (.D(instruction_registers_1_data_out[15:8]), .en(comparator_2_eq), .Q(Y1), .clk(CLK), .clr(CLR));
  Register register_5 (
    .D(instruction_registers_1_data_out[7:0]), .en(comparator_3_eq), .Q(register_5_q), .clk(CLK), .clr(CLR));
  Register register_6 (
    .D(instruction_registers_1_data_out[15:8]), .en(comparator_3_eq), .Q(register_6_q), .clk(CLK), .clr(CLR));
  Register #(.width(16)) register_7 (
    .D({instruction_registers_1_data_out[7:0], instruction_registers_1_data_out[15:8]}),
    .en(comparator_4_eq), .Q(COLOUR), .clk(CLK), .clr(CLR));
  Transistor #(.\type ("n"), .width(8)) transistor_2 (.in(START_q[11:4]), .out(ADDR), .gate(and_1_out));
  Pull_Resistor pull_resistor_1 (.node(ADDR));
  Comparator comparator_9 (
    .a(START_q[11:4]), .b(PC_IN), .gt(comparator_9_gt), .eq(comparator_9_eq), .lt(comparator_9_lt));
  or or_3 (or_3_out, comparator_9_gt, comparator_9_lt);
  Comparator comparator_10 (
    .a(STOP_q[11:4]), .b(PC_IN), .gt(comparator_10_gt), .eq(comparator_10_eq), .lt(comparator_10_lt));
  or or_4 (or_4_out, comparator_10_gt, comparator_10_lt);
  not not_1 (not_1_out, comparator_8_eq);
  and and_2 (and_2_out, comparator_10_eq, not_1_out, d_ff_1_q);
  assign Y2 = register_5_q | register_2_q;  // OR_Gate or_5, 8 bits wide
  assign X2 = register_6_q | register_1_q;  // OR_Gate or_6, 8 bits wide
  Comparator #(.width(4)) comparator_11 (
    .a(START_q[3:0]), .b(4'b0110), .gt(comparator_11_gt), .eq(comparator_11_eq), .lt(comparator_11_lt));
  Comparator #(.width(4)) comparator_12 (
    .a(START_q[3:0]), .b(4'b1000), .gt(comparator_12_gt), .eq(comparator_12_eq), .lt(comparator_12_lt));
  Comparator #(.width(4)) comparator_13 (
    .a(START_q[3:0]), .b(4'b0100), .gt(comparator_13_gt), .eq(comparator_13_eq), .lt(comparator_13_lt));
  Comparator #(.width(4)) comparator_14 (
    .a(START_q[3:0]), .b(4'b0101), .gt(comparator_14_gt), .eq(comparator_14_eq), .lt(comparator_14_lt));
  or or_7 (or_7_out, or_3_out, or_4_out);
  and and_3 (and_3_out, comparator_9_eq, not_1_out, d_ff_1_q);
  T_Flip_Flop t_ff_1 (.clk(and_3_out), .T(and_3_out), .Q(PC_EN), .reset(or_8_out));  // open: Qn, preset, en
  or or_8 (or_8_out, and_2_out, CLR);
  not not_2 (CLR_PC, PC_EN);
  Comparator #(.width(32)) comparator_15 (
    .a(instruction_registers_1_data_out), .b(32'hffffe68e), .eq(comparator_15_eq));  // open: gt, lt
  Comparator #(.width(32)) comparator_16 (
    .a(instruction_registers_1_data_out), .b(32'hffffe908), .eq(comparator_16_eq));  // open: gt, lt
  Comparator #(.width(32)) comparator_17 (.a(instruction_registers_1_data_out), .b(32'hffffd55b));  // open: gt, eq, lt
  Register #(.trigger("high")) register_8 (
    .D(instruction_registers_1_data_out[31:24]), .en(MUX), .Q(JMP), .clk(CLK), .clr(CLR));
  or or_9 (or_9_out, comparator_11_gt, comparator_11_lt);
  or or_10 (or_10_out, comparator_12_gt, comparator_12_lt);
  or or_11 (or_11_out, comparator_13_gt, comparator_13_lt);
  or or_12 (or_12_out, comparator_14_gt, comparator_14_lt);
  and RAM (RAM_out, PC_EN, comparator_14_eq);
  and MEM (MEM_out, PC_EN, comparator_13_eq);
  J_K_Flip_Flop j_k_ff_1 (
    .J(comparator_15_eq), .clk(CLK), .K(comparator_15_eq), .Q(EN_JOYSTICK), .reset(CLR));  // open: Qn, preset, en
  J_K_Flip_Flop j_k_ff_2 (
    .J(comparator_16_eq), .clk(CLK), .K(comparator_16_eq), .Q(JS_AND_LD), .reset(CLR));  // open: Qn, preset, en
  Register SENS (.D(instruction_registers_1_data_out[7:0]), .en(comparator_5_eq), .Q(SENSITIVITY));  // open: clk, clr
  Register SCREEN (
    .D(instruction_registers_1_data_out[15:8]), .en(comparator_5_eq), .Q(SCREEN_SIZE), .clk(CLR), .clr(CLK));
  and and_4 (and_4_out, or_9_out, or_10_out, or_11_out, or_12_out);
  and ROM (ROM_out, PC_EN, comparator_11_eq);
  and I_O (I_O_out, PC_EN, comparator_12_eq);
  // OR_Gate or_13 has open pins: in0=RAM_out, in1=MEM_out, in2=ROM_out, out=open
  and and_5 (MAINBOARD_RAM_R_W, ~SETTING_UP, ~DONE);  // AND_Gate
  Comparator #(.width(4)) comparator_18 (
    .a(STOP_q[3:0]), .b(4'b1000), .gt(comparator_18_gt), .eq(comparator_18_eq), .lt(comparator_18_lt));
  Comparator #(.width(4)) comparator_19 (
    .a(STOP_q[3:0]), .b(4'b0100), .gt(comparator_19_gt), .eq(comparator_19_eq), .lt(comparator_19_lt));
  Comparator #(.width(4)) comparator_20 (
    .a(STOP_q[3:0]), .b(4'b0101), .gt(comparator_20_gt), .eq(comparator_20_eq), .lt(comparator_20_lt));
  or or_14 (or_14_out, and_4_out, or_7_out);
  and RAM_2 (RAM_2_out, PC_EN, comparator_20_eq);
  or or_15 (or_15_out, comparator_18_gt, comparator_18_lt);
  or or_16 (or_16_out, comparator_19_gt, comparator_19_lt);
  and and_6 (and_6_out, or_15_out, or_16_out, or_17_out);
  or or_17 (or_17_out, comparator_20_gt, comparator_20_lt);
  and I_O_2 (I_O_2_out, PC_EN, comparator_18_eq);
  and MEM_2 (MEM_2_out, PC_EN, comparator_19_eq);
  or or_18 (or_18_out, RAM_2_out, MEM_2_out);
  and and_7 (and_7_out, d_ff_1_q, or_19_out);
  or or_19 (or_19_out, and_6_out, or_14_out);
  Transistor #(.\type ("n"), .width(8)) transistor_3 (
    .in({4'b0110, START_q[3:0]}), .out(transistor_3_out), .gate(and_8_out));
  Transistor #(.\type ("n"), .width(8)) transistor_4 (
    .in({4'b0101, STOP_q[3:0]}), .out(transistor_4_out), .gate(and_9_out));
  T_Flip_Flop ROM_2 (.clk(or_20_out), .T(or_20_out), .Q(CRAM), .reset(or_8_out));  // open: Qn, preset, en
  or or_20 (or_20_out, ROM_out, ROM_out);
  T_Flip_Flop RAM_3 (.clk(or_21_out), .T(or_21_out), .Q(VRAM), .reset(or_8_out));  // open: Qn, preset, en
  or or_21 (or_21_out, ROM_out, RAM_2_out);
  T_Flip_Flop ROM_3 (.clk(or_22_out), .T(or_22_out), .Q(VMEM), .reset(or_8_out));  // open: Qn, preset, en
  or or_22 (or_22_out, I_O_2_out, I_O_out);
  and and_8 (and_8_out, ~and_4_out, and_7_out, and_6_out);  // AND_Gate
  and and_9 (and_9_out, ~and_6_out, and_7_out, and_4_out);  // AND_Gate
  and and_10 (and_10_out, and_9_out, and_8_out);
  Pull_Resistor pull_resistor_2 (.node(transistor_3_out));
  assign xor_1_out = transistor_3_out ^ transistor_4_out;  // XOR_Gate xor_1, 8 bits wide
  Pull_Resistor pull_resistor_3 (.node(transistor_4_out));
  Comparator comparator_21 (.a(xor_1_out), .b({8{1'b0}}), .eq(comparator_21_eq));  // open: gt, lt
  assign bit_extender_1_out = {{7{in_8}}, in_8};  // Bit_Extender bit_extender_1
  assign and_11_out = bit_extender_1_out & {8{1'b1}};  // AND_Gate and_11, 8 bits wide
  assign bit_extender_2_out = {{7{in_9[0]}}, in_9[0]};  // Bit_Extender bit_extender_2
  assign and_12_out = bit_extender_2_out & 8'hf;  // AND_Gate and_12, 8 bits wide
  assign bit_extender_3_out = {{7{in_9[1]}}, in_9[1]};  // Bit_Extender bit_extender_3
  assign and_13_out = bit_extender_3_out & 8'hf0;  // AND_Gate and_13, 8 bits wide
  and and_14 (and_14_out, and_10_out, comparator_21_eq);
  not not_3 (not_3_out, and_14_out);
  assign or_23_out = and_11_out | and_12_out | and_13_out;  // OR_Gate or_23, 8 bits wide
  Multiplexer #(.width(8), .enable("false")) multiplexer_1 (
    .in0(or_23_out), .in1(pull_resistor_4_node), .out(BROD));  // open: sel
  Pull_Resistor pull_resistor_4 (.node(pull_resistor_4_node));
  Transistor #(.\type ("n"), .width(8)) transistor_5 (.in(xor_1_out), .out(pull_resistor_4_node), .gate(not_3_out));

  assign SEL_LD = MAINBOARD_RAM_R_W;

  // Notes on the sheet:
  //   READ
  //   WRITE
endmodule

module SCREEN_LATCH (
  input  LD_SEL,
  input  [7:0] in_2,
  input  [7:0] in_3,
  input  [7:0] in_4,
  input  [7:0] in_5,
  output [7:0] X,
  output [7:0] Y
);

  wire not_1_out;

  Transistor #(.\type ("n"), .width(8)) transistor_1 (.in(in_2), .out(X), .gate(LD_SEL));
  not not_1 (not_1_out, LD_SEL);
  Transistor #(.\type ("n"), .width(8)) transistor_2 (.in(in_3), .out(Y), .gate(LD_SEL));
  Transistor #(.\type ("n"), .width(8)) transistor_3 (.in(in_4), .out(X), .gate(not_1_out));
  Transistor #(.\type ("n"), .width(8)) transistor_4 (.in(in_5), .out(Y), .gate(not_1_out));
endmodule

module _2D_ENGINE (
  input  [7:0] I_O_IN,
  input  EN,
  input  CLK,
  input  CLR,
  input  [4:0] JOYSTICK_X,
  input  [4:0] JOYSTICK_Y,
  input  [7:0] X_DATA,
  input  [7:0] Y_DATA,
  output [7:0] I_O_OUT,
  output VMEM,
  output VRAM,
  output VROM,
  output [15:0] COLOUR,
  output MAINBOARD_RAM_R_W,
  output [7:0] X,
  output [7:0] Y,
  output [7:0] ADDRESS
);

  wire line_drawer_1_done, line_drawer_1_setting_up, n2d_engine_control_unit_1_clr_pc,
       n2d_engine_control_unit_1_en_joystick, n2d_engine_control_unit_1_js_and_ld,
       n2d_engine_control_unit_1_ld_en, n2d_engine_control_unit_1_mux, n2d_engine_control_unit_1_pc_en,
       n2d_engine_control_unit_1_sel_ld, vector_alu_1_xy_equal;
  wire [1:0] undriven_2, vector_alu_1_x_c_out, vector_alu_1_y_equal;
  wire [7:0] IR_q, line_drawer_1_x, multiplexer_1_out, multiplexer_2_out, n2d_engine_control_unit_1_jmp,
       n2d_engine_control_unit_1_screen_size, n2d_engine_control_unit_1_sensitivity,
       n2d_engine_control_unit_1_x1, n2d_engine_control_unit_1_x2, n2d_engine_control_unit_1_y1,
       n2d_engine_control_unit_1_y2, undriven, vector_alu_1_x_out, vector_alu_1_y_out;

  Register #(.trigger("high")) IR (.D(I_O_IN), .en(EN), .Q(IR_q), .clk(CLK), .clr(CLR));
  Multiplexer #(.width(8), .enable("false")) multiplexer_1 (
    .in0(n2d_engine_control_unit_1_x1), .in1(X_DATA), .out(multiplexer_1_out),
    .sel(n2d_engine_control_unit_1_js_and_ld));
  Multiplexer #(.width(8), .enable("false")) multiplexer_2 (
    .in0(n2d_engine_control_unit_1_y1), .in1(Y_DATA), .out(multiplexer_2_out),
    .sel(n2d_engine_control_unit_1_js_and_ld));
  VECTOR_ALU vector_alu_1 (
    .X(X_DATA), .Y(Y_DATA), .X_CONSTANT(n2d_engine_control_unit_1_x2),
    .Y_CONSTANT(n2d_engine_control_unit_1_y2), .X_OP(undriven[3:0]), .Y_OP(undriven[7:4]),
    .X_C_OUT(vector_alu_1_x_c_out[0]), .Y_C_OUT(vector_alu_1_x_c_out[1]), .X_EQUAL(vector_alu_1_y_equal[1]),
    .Y_EQUAL(vector_alu_1_y_equal[0]), .X_OUT(vector_alu_1_x_out), .Y_OUT(vector_alu_1_y_out),
    .XY_EQUAL(vector_alu_1_xy_equal), .X_C_IN(undriven_2[1]), .Y_C_IN(undriven_2[0]));
  _2D_ENGINE_CONTROL_UNIT u_2d_engine_control_unit_1 (
    .DATA_IN(IR_q), .X1(n2d_engine_control_unit_1_x1), .EN_JOYSTICK(n2d_engine_control_unit_1_en_joystick),
    .JS_AND_LD(n2d_engine_control_unit_1_js_and_ld), .Y1(n2d_engine_control_unit_1_y1),
    .X2(n2d_engine_control_unit_1_x2), .Y2(n2d_engine_control_unit_1_y2), .COLOUR(COLOUR),
    .LD_EN(n2d_engine_control_unit_1_ld_en), .CLR(CLR), .CLK(CLK), .SETTING_UP(line_drawer_1_setting_up),
    .DONE(line_drawer_1_done), .SEL_LD(n2d_engine_control_unit_1_sel_ld),
    .SCREEN_SIZE(n2d_engine_control_unit_1_screen_size), .SENSITIVITY(n2d_engine_control_unit_1_sensitivity),
    .EN(EN), .MAINBOARD_RAM_R_W(MAINBOARD_RAM_R_W), .JMP(n2d_engine_control_unit_1_jmp),
    .MUX(n2d_engine_control_unit_1_mux), .PC_IN(ADDRESS), .BROD(I_O_OUT),
    .PC_EN(n2d_engine_control_unit_1_pc_en), .CLR_PC(n2d_engine_control_unit_1_clr_pc), .CRAM(VROM),
    .VRAM(VRAM), .VMEM(VMEM), .in_8(vector_alu_1_xy_equal), .in_9(vector_alu_1_y_equal));
  LINE_DRAWER line_drawer_1 (
    .X1(multiplexer_1_out), .Y1(multiplexer_2_out), .X2(n2d_engine_control_unit_1_x2),
    .Y2(n2d_engine_control_unit_1_y2), .EN(n2d_engine_control_unit_1_ld_en), .CLK(CLK), .CLR(CLR),
    .SETTING_UP(line_drawer_1_setting_up), .Y(n2d_engine_control_unit_1_screen_size), .X(line_drawer_1_x),
    .DONE(line_drawer_1_done));  // open: LINE_IS_VERTICAL, X_Y
  JOYSTICK joystick_1 (
    .JOYSTICK_X(JOYSTICK_X), .JOYSTICK_Y(JOYSTICK_Y), .SENSITIVITY(n2d_engine_control_unit_1_sensitivity),
    .EN(n2d_engine_control_unit_1_en_joystick), .SCREEN_SIZE(n2d_engine_control_unit_1_screen_size),
    .CLK(CLK), .CLR(CLR));  // open: X, Y
  PC2 pc2_1 (
    .DATA_IN(n2d_engine_control_unit_1_jmp), .ADDRESS(ADDRESS), .MUX(n2d_engine_control_unit_1_mux),
    .LOAD(n2d_engine_control_unit_1_pc_en), .CLK(CLK), .CLR(n2d_engine_control_unit_1_clr_pc));
  SCREEN_LATCH screen_latch_1 (
    .in_2(n2d_engine_control_unit_1_screen_size), .in_3(line_drawer_1_x), .in_4(vector_alu_1_x_out),
    .in_5(vector_alu_1_y_out), .X(X), .Y(Y), .LD_SEL(n2d_engine_control_unit_1_sel_ld));
endmodule

module VECTOR_ALU (
  input  X_C_IN,
  input  Y_C_IN,
  input  [7:0] X,
  input  [7:0] Y,
  input  [7:0] X_CONSTANT,
  input  [7:0] Y_CONSTANT,
  input  [3:0] X_OP,
  input  [3:0] Y_OP,
  output X_C_OUT,
  output Y_C_OUT,
  output X_EQUAL,
  output Y_EQUAL,
  output [7:0] X_OUT,
  output [7:0] Y_OUT,
  output XY_EQUAL
);

  wire adder_1_cout, adder_2_cout, subtractor_1_bout, subtractor_2_bout;
  wire [7:0] adder_1_out, adder_2_out, and_1_out, and_2_out, divider_1_out, divider_1_rem, divider_2_out,
       divider_2_rem, multiplier_1_cout, multiplier_1_out, multiplier_2_cout, multiplier_2_out, not_1_out,
       not_2_out, or_1_out, or_2_out, shifter_1_out, shifter_2_out, shifter_3_out, shifter_4_out,
       shifter_5_out, shifter_6_out, shifter_7_out, shifter_8_out, shifter_9_out, shifter_10_out,
       subtractor_1_out, subtractor_2_out, xor_1_out, xor_2_out;

  Adder adder_1 (.a(X), .b(X_CONSTANT), .out(adder_1_out), .cin(X_C_IN), .cout(adder_1_cout));
  Subtractor subtractor_1 (.a(X), .b(X_CONSTANT), .out(subtractor_1_out), .bin(X_C_IN), .bout(subtractor_1_bout));
  Multiplier multiplier_1 (.a(X), .b(X_CONSTANT), .out(multiplier_1_out), .cout(multiplier_1_cout));  // open: cin
  Divider divider_1 (.a(X), .b(X_CONSTANT), .out(divider_1_out), .rem(divider_1_rem));  // open: upper
  Comparator comparator_1 (.a(X), .b(X_CONSTANT), .eq(X_EQUAL));  // open: gt, lt
  assign and_1_out = X & X_CONSTANT;  // AND_Gate and_1, 8 bits wide
  assign or_1_out = X | X_CONSTANT;  // OR_Gate or_1, 8 bits wide
  assign xor_1_out = X ^ X_CONSTANT;  // XOR_Gate xor_1, 8 bits wide
  assign not_1_out = ~X;  // NOT_Gate not_1, 8 bits wide
  Shifter shifter_1 (.in(X), .\dist (X_CONSTANT[2:0]), .out(shifter_1_out));
  Shifter #(.shift("lr")) shifter_2 (.in(X), .\dist (X_CONSTANT[2:0]), .out(shifter_2_out));
  Shifter #(.shift("ar")) shifter_3 (.in(X), .\dist (X_CONSTANT[2:0]), .out(shifter_3_out));
  Shifter #(.shift("rl")) shifter_4 (.in(X), .\dist (X_CONSTANT[2:0]), .out(shifter_4_out));
  Shifter #(.shift("rr")) shifter_5 (.in(X), .\dist (X_CONSTANT[2:0]), .out(shifter_5_out));
  Multiplexer #(.select(4), .width(8), .enable("false")) multiplexer_1 (
    .in0(adder_1_out), .in1(subtractor_1_out), .in2(multiplier_1_out), .in3(multiplier_1_cout),
    .in4(divider_1_out), .in5(divider_1_rem), .in6(and_1_out), .in7(or_1_out), .in8(xor_1_out),
    .in9(not_1_out), .in10(shifter_1_out), .in11(shifter_2_out), .in12(shifter_3_out), .in13(shifter_4_out),
    .in14(shifter_5_out), .out(X_OUT), .sel(X_OP));  // open: in15
  Multiplexer #(.select(4), .enable("false")) multiplexer_2 (
    .in0(adder_1_cout), .in1(subtractor_1_bout), .in2(1'b0), .in3(1'b0), .in4(1'b0), .in5(1'b0), .in6(1'b0),
    .in7(1'b0), .in8(1'b0), .in9(1'b0), .in10(1'b0), .in11(1'b0), .in12(1'b0), .in13(1'b0), .in14(1'b0),
    .in15(1'b0), .out(X_C_OUT), .sel(X_OP));
  assign and_2_out = Y & Y_CONSTANT;  // AND_Gate and_2, 8 bits wide
  assign or_2_out = Y | Y_CONSTANT;  // OR_Gate or_2, 8 bits wide
  assign not_2_out = ~Y;  // NOT_Gate not_2, 8 bits wide
  Adder adder_2 (.a(Y), .b(Y_CONSTANT), .out(adder_2_out), .cin(Y_C_IN), .cout(adder_2_cout));
  Subtractor subtractor_2 (.a(Y), .b(Y_CONSTANT), .out(subtractor_2_out), .bin(Y_C_IN), .bout(subtractor_2_bout));
  Multiplier multiplier_2 (.a(Y), .b(Y_CONSTANT), .out(multiplier_2_out), .cout(multiplier_2_cout));  // open: cin
  Divider divider_2 (.a(Y), .b(Y_CONSTANT), .out(divider_2_out), .rem(divider_2_rem));  // open: upper
  Comparator comparator_2 (.a(Y), .b(Y_CONSTANT), .eq(Y_EQUAL));  // open: gt, lt
  assign xor_2_out = Y ^ Y_CONSTANT;  // XOR_Gate xor_2, 8 bits wide
  Shifter shifter_6 (.in(Y), .\dist (Y_CONSTANT[2:0]), .out(shifter_6_out));
  Shifter #(.shift("lr")) shifter_7 (.in(Y), .\dist (Y_CONSTANT[2:0]), .out(shifter_7_out));
  Shifter #(.shift("ar")) shifter_8 (.in(Y), .\dist (Y_CONSTANT[2:0]), .out(shifter_8_out));
  Shifter #(.shift("rl")) shifter_9 (.in(Y), .\dist (Y_CONSTANT[2:0]), .out(shifter_9_out));
  Shifter #(.shift("rr")) shifter_10 (.in(Y), .\dist (Y_CONSTANT[2:0]), .out(shifter_10_out));
  Multiplexer #(.select(4), .width(8), .enable("false")) multiplexer_3 (
    .in0(adder_2_out), .in1(subtractor_2_out), .in2(multiplier_2_out), .in3(multiplier_2_cout),
    .in4(divider_2_out), .in5(divider_2_rem), .in6(and_2_out), .in7(or_2_out), .in8(xor_2_out),
    .in9(not_2_out), .in10(shifter_6_out), .in11(shifter_7_out), .in12(shifter_8_out), .in13(shifter_9_out),
    .in14(shifter_10_out), .out(Y_OUT), .sel(Y_OP));  // open: in15
  Comparator comparator_3 (.a(Y_OUT), .b(X_OUT), .eq(XY_EQUAL));  // open: gt, lt
  Multiplexer #(.select(4), .enable("false")) multiplexer_4 (
    .in0(adder_2_cout), .in1(subtractor_2_bout), .in2(1'b0), .in3(1'b0), .in4(1'b0), .in5(1'b0), .in6(1'b0),
    .in7(1'b0), .in8(1'b0), .in9(1'b0), .in10(1'b0), .in11(1'b0), .in12(1'b0), .in13(1'b0), .in14(1'b0),
    .in15(1'b0), .out(Y_C_OUT), .sel(Y_OP));
endmodule
module _2D_ENGINE_CU (
  input  [7:0] in_1,
  input  [7:0] PC_IN
);

  wire comparator_1_eq, comparator_2_eq, comparator_3_eq, comparator_4_eq, comparator_5_eq, comparator_6_eq,
       demultiplexer_1_out0, demultiplexer_1_out1, demultiplexer_1_out2, demultiplexer_1_out3, not_1_out,
       not_2_out, not_3_out, not_4_out, or_1_out, or_2_out, or_3_out, or_6_out_2, or_7_out_2, or_8_out_2,
       or_9_out_2, or_10_out, undriven, undriven_2;
  wire [7:0] register_1_q, register_2_q, register_3_q, register_4_q, register_5_q, register_6_q,
       register_7_q, register_8_q, register_9_q, register_10_q, register_11_q, register_12_q;

  Demultiplexer #(.select(2), .enable("false")) demultiplexer_1 (
    .out0(demultiplexer_1_out0), .out1(demultiplexer_1_out1), .out2(demultiplexer_1_out2),
    .out3(demultiplexer_1_out3));  // open: in, sel
  Register register_1 (.D(in_1), .en(demultiplexer_1_out0), .Q(register_1_q), .clk(undriven_2), .clr(undriven));
  Register register_2 (.D(in_1), .en(demultiplexer_1_out1), .Q(register_2_q), .clk(undriven_2), .clr(undriven));
  Register register_3 (.D(in_1), .en(demultiplexer_1_out2), .Q(register_3_q), .clk(undriven_2), .clr(undriven));
  Register register_4 (.D(in_1), .en(demultiplexer_1_out3), .Q(register_4_q), .clk(undriven_2), .clr(undriven));
  Comparator #(.width(16)) comparator_1 (
    .a({register_2_q, register_1_q}), .b(16'he078), .eq(comparator_1_eq));  // open: gt, lt
  Comparator #(.width(16)) comparator_2 (
    .a({register_2_q, register_1_q}), .b(16'he079), .eq(comparator_2_eq));  // open: gt, lt
  Comparator #(.width(16)) comparator_3 (
    .a({register_2_q, register_1_q}), .b(16'he080), .eq(comparator_3_eq));  // open: gt, lt
  not not_1 (not_1_out, or_1_out);
  or or_1 (or_1_out, comparator_1_eq, comparator_3_eq);
  not not_2 (not_2_out, comparator_2_eq);
  Register register_5 (.D(register_3_q), .en(or_1_out), .Q(register_5_q), .clk(undriven_2), .clr(undriven));
  Register register_6 (.D(register_4_q), .en(or_1_out), .Q(register_6_q), .clk(undriven_2), .clr(undriven));
  Register register_7 (.D(register_3_q), .en(comparator_2_eq), .Q(register_7_q), .clk(undriven_2), .clr(undriven));
  Register register_8 (.D(register_4_q), .en(comparator_2_eq), .Q(register_8_q), .clk(undriven_2), .clr(undriven));
  // AND_Gate and_1 has open pins: in0=or_2_out, in1=or_10_out, out=open
  or or_2 (or_2_out, not_1_out, not_2_out, not_3_out, not_4_out);
  Comparator #(.width(16)) comparator_4 (
    .a({register_2_q, register_1_q}), .b(16'he081), .eq(comparator_4_eq));  // open: gt, lt
  Comparator #(.width(16)) comparator_5 (
    .a({register_2_q, register_1_q}), .b(16'he082), .eq(comparator_5_eq));  // open: gt, lt
  Comparator #(.width(16)) comparator_6 (
    .a({register_2_q, register_1_q}), .b(16'he083), .eq(comparator_6_eq));  // open: gt, lt
  not not_3 (not_3_out, or_3_out);
  or or_3 (or_3_out, comparator_4_eq, comparator_6_eq);
  Register register_9 (.D(register_3_q), .en(or_3_out), .Q(register_9_q), .clk(undriven_2), .clr(undriven));
  Register register_10 (.D(register_4_q), .en(or_3_out), .Q(register_10_q), .clk(undriven_2), .clr(undriven));
  // OR_Gate or_4 has open pins: in0=comparator_1_eq, in1=comparator_4_eq, out=open
  // OR_Gate or_5 has open pins: in0=comparator_3_eq, in1=comparator_6_eq, out=open
  not not_4 (not_4_out, comparator_5_eq);
  Register register_11 (.D(register_3_q), .en(comparator_5_eq), .Q(register_11_q), .clk(undriven_2), .clr(undriven));
  OR or_6 (.in_1(register_2_q), .out_2(or_6_out_2));
  OR or_7 (.in_1(register_1_q), .out_2(or_7_out_2));
  Register register_12 (.D(register_4_q), .en(comparator_5_eq), .Q(register_12_q), .clk(undriven_2), .clr(undriven));
  OR or_8 (.in_1(register_3_q), .out_2(or_8_out_2));
  OR or_9 (.in_1(register_4_q), .out_2(or_9_out_2));
  or or_10 (or_10_out, or_9_out_2, or_8_out_2, or_7_out_2, or_6_out_2);
endmodule
