// Logisim project CPU.circ as structural Verilog
module ALU (
  input  [7:0] C_IN,
  input  [7:0] A,
  input  [7:0] B,
  input  [3:0] OP,
  output [7:0] RESULT,
  output ZERO,
  output Hi,
  output EQUAL,
  output Lo,
  output C_OUT,
  output [7:0] C_OUT_2
);

  wire adder_1_cout, bit_extender_1_out, bit_extender_2_out, subtractor_1_bout;
  wire [1:0] bit_extender_6_out;
  wire [2:0] bit_extender_3_out;
  wire [7:0] adder_1_out, and_1_out, ascii_1_out_3, bit_extender_4_out, bit_extender_5_out,
       demultiplexer_1_out0, demultiplexer_1_out1, demultiplexer_2_out0, demultiplexer_2_out1, divider_1_out,
       divider_1_rem, multiplier_1_cout, multiplier_1_out, not_1_out, not_2_out, or_2_out, shifter_1_out,
       shifter_2_out, shifter_3_out, shifter_4_out, shifter_5_out, subtractor_1_out, xor_1_out;

  Bit_Extender #(.out_width(1)) bit_extender_1 (.in(demultiplexer_1_out0), .out(bit_extender_1_out));
  Bit_Extender #(.out_width(1)) bit_extender_2 (.in(demultiplexer_1_out1), .out(bit_extender_2_out));
  Bit_Extender #(.out_width(3)) bit_extender_3 (.in(B), .out(bit_extender_3_out));
  assign bit_extender_4_out = {{7{1'b0}}, adder_1_cout};  // Bit_Extender bit_extender_4
  assign bit_extender_5_out = {{7{1'b0}}, subtractor_1_bout};  // Bit_Extender bit_extender_5
  or or_1 (C_OUT, subtractor_1_bout, adder_1_cout);
  Adder adder_1 (.a(A), .b(B), .out(adder_1_out), .cin(bit_extender_1_out), .cout(adder_1_cout));
  Subtractor subtractor_1 (.a(A), .b(B), .out(subtractor_1_out), .bin(bit_extender_2_out), .bout(subtractor_1_bout));
  Multiplier multiplier_1 (.a(A), .b(B), .out(multiplier_1_out), .cin(demultiplexer_2_out0), .cout(multiplier_1_cout));
  Divider divider_1 (.a(A), .b(B), .out(divider_1_out), .upper(demultiplexer_2_out1), .rem(divider_1_rem));
  Shifter shifter_1 (.in(A), .\dist (bit_extender_3_out), .out(shifter_1_out));
  Shifter #(.shift("lr")) shifter_2 (.in(A), .\dist (bit_extender_3_out), .out(shifter_2_out));
  Shifter #(.shift("ar")) shifter_3 (.in(A), .\dist (bit_extender_3_out), .out(shifter_3_out));
  Shifter #(.shift("rl")) shifter_4 (.in(A), .\dist (bit_extender_3_out), .out(shifter_4_out));
  Shifter #(.shift("rr")) shifter_5 (.in(A), .\dist (bit_extender_3_out), .out(shifter_5_out));
  Comparator comparator_1 (.a(A), .b(B), .gt(Hi), .eq(EQUAL), .lt(Lo));
  assign and_1_out = A & B;  // AND_Gate and_1, 8 bits wide
  assign or_2_out = A | B;  // OR_Gate or_2, 8 bits wide
  assign xor_1_out = A ^ B;  // XOR_Gate xor_1, 8 bits wide
  assign not_1_out = ~A;  // NOT_Gate not_1, 8 bits wide
  assign not_2_out = ~B;  // NOT_Gate not_2, 8 bits wide
  ASCII ascii_1 (.INP_1(A), .INP_2(B), .out_3(ascii_1_out_3));
  Multiplexer #(.select(2), .width(8), .enable("false")) multiplexer_1 (
    .in0(bit_extender_4_out), .in1(bit_extender_5_out), .in2(multiplier_1_cout), .in3(divider_1_rem),
    .out(C_OUT_2), .sel(bit_extender_6_out));
  Demultiplexer #(.width(8), .enable("false")) demultiplexer_1 (
    .out0(demultiplexer_1_out0), .out1(demultiplexer_1_out1), .in(C_IN), .sel(bit_extender_6_out[0]));
  Demultiplexer #(.width(8), .enable("false")) demultiplexer_2 (
    .out0(demultiplexer_2_out0), .out1(demultiplexer_2_out1), .in(C_IN), .sel(bit_extender_6_out[1]));
  Multiplexer #(.select(4), .width(8), .enable("false")) multiplexer_2 (
    .in0(adder_1_out), .in1(subtractor_1_out), .in2(multiplier_1_out), .in3(divider_1_out),
    .in4(shifter_1_out), .in5(shifter_2_out), .in6(shifter_3_out), .in7(shifter_4_out), .in8(shifter_5_out),
    .in9(and_1_out), .in10(or_2_out), .in11(xor_1_out), .in12(not_1_out), .in13(ascii_1_out_3),
    .in14(not_2_out), .out(RESULT), .sel(OP));  // open: in15
  Bit_Extender #(.in_width(4), .out_width(2)) bit_extender_6 (.in(OP), .out(bit_extender_6_out));
  nor nor_1 (ZERO, RESULT[0], RESULT[1], RESULT[2], RESULT[3], RESULT[4], RESULT[5], RESULT[6], RESULT[7]);
endmodule

module ASCII (
  input  [7:0] INP_1,
  input  [7:0] INP_2,
  output [7:0] out_3
);

  wire nor_1_out, nor_2_out, nor_3_out, nor_4_out;
  wire [3:0] adder_1_out, adder_2_out, subtractor_1_out, subtractor_2_out, subtractor_3_out, subtractor_4_out;

  Subtractor #(.width(4)) subtractor_1 (.a(INP_1[7:4]), .b(4'b0011), .out(subtractor_1_out));  // open: bin, bout
  Subtractor #(.width(4)) subtractor_2 (.a(INP_1[7:4]), .b(4'b0100), .out(subtractor_2_out));  // open: bin, bout
  Subtractor #(.width(4)) subtractor_3 (.a(INP_2[7:4]), .b(4'b0011), .out(subtractor_3_out));  // open: bin, bout
  Subtractor #(.width(4)) subtractor_4 (.a(INP_2[7:4]), .b(4'b0100), .out(subtractor_4_out));  // open: bin, bout
  nor nor_1 (nor_1_out, subtractor_1_out[0], subtractor_1_out[1], subtractor_1_out[2], subtractor_1_out[3]);
  nor nor_2 (nor_2_out, subtractor_2_out[0], subtractor_2_out[1], subtractor_2_out[2], subtractor_2_out[3]);
  nor nor_3 (nor_3_out, subtractor_3_out[0], subtractor_3_out[1], subtractor_3_out[2], subtractor_3_out[3]);
  nor nor_4 (nor_4_out, subtractor_4_out[0], subtractor_4_out[1], subtractor_4_out[2], subtractor_4_out[3]);
  Adder #(.width(4)) adder_1 (.a(INP_2[3:0]), .b(4'b1001), .out(adder_1_out));  // open: cin, cout
  assign out_3[7:4] = nor_1_out ? INP_1[3:0] : 4'bz;  // Controlled_Buffer controlled_buffer_1
  assign out_3[7:4] = nor_2_out ? adder_2_out : 4'bz;  // Controlled_Buffer controlled_buffer_2
  Adder #(.width(4)) adder_2 (.a(INP_1[3:0]), .b(4'b1001), .out(adder_2_out));  // open: cin, cout
  assign out_3[3:0] = nor_3_out ? INP_2[3:0] : 4'bz;  // Controlled_Buffer controlled_buffer_3
  assign out_3[3:0] = nor_4_out ? adder_1_out : 4'bz;  // Controlled_Buffer controlled_buffer_4
  // Probe on out_3

  // Notes on the sheet:
  //   INP_1: pull=down
  //   INP_2: pull=down
endmodule

module REGISTERS (
  input  SEL_REGS,
  input  [1:0] SEL_1,
  input  [1:0] A_SEL,
  input  [7:0] D_BUS_IN,
  input  [1:0] REGS,
  input  SEL_A_B,
  input  SEL_REG,
  input  CLR,
  input  [1:0] B_SEL,
  input  CLK,
  output [7:0] A,
  output [7:0] C,
  output SUM_UPDATE,
  output [7:0] B
);

  wire demultiplexer_1_out0, demultiplexer_1_out1, demultiplexer_1_out2, demultiplexer_1_out3, or_1_out_2,
       or_2_out_2;
  wire [7:0] A_q, B_q, bit_extender_1_out, bit_extender_2_out, C_q, multiplexer_1_out, multiplexer_2_out,
       multiplexer_3_out, undriven;

  Demultiplexer #(.select(2), .enable("false")) demultiplexer_1 (
    .out0(demultiplexer_1_out0), .out1(demultiplexer_1_out1), .out2(demultiplexer_1_out2),
    .out3(demultiplexer_1_out3), .in(SEL_REGS), .sel(SEL_1));
  Register #(.trigger("high")) u_A (.D(D_BUS_IN), .en(demultiplexer_1_out0), .Q(A_q), .clk(CLK), .clr(CLR));
  Register #(.trigger("high")) u_B (.D(D_BUS_IN), .en(demultiplexer_1_out1), .Q(B_q), .clk(CLK), .clr(CLR));
  Register #(.trigger("high")) u_C (.D(D_BUS_IN), .en(demultiplexer_1_out2), .Q(C_q), .clk(CLK), .clr(CLR));
  Register #(.trigger("high")) D (.D(D_BUS_IN), .en(demultiplexer_1_out3), .clk(CLK), .clr(CLR));  // open: Q
  Multiplexer #(.select(2), .width(8), .enable("false")) multiplexer_1 (
    .in0(A_q), .in1(B_q), .in2(C_q), .in3(undriven), .out(multiplexer_1_out), .sel(A_SEL));
  assign A = multiplexer_1_out & bit_extender_2_out;  // AND_Gate and_1, 8 bits wide
  assign bit_extender_1_out = {{7{SEL_REG}}, SEL_REG};  // Bit_Extender bit_extender_1
  Multiplexer #(.select(2), .width(8), .enable("false")) multiplexer_2 (
    .in0(A_q), .in1(B_q), .in2(C_q), .in3(undriven), .out(multiplexer_2_out), .sel(REGS));
  Multiplexer #(.select(2), .width(8), .enable("false")) multiplexer_3 (
    .in0(A_q), .in1(B_q), .in2(C_q), .in3(undriven), .out(multiplexer_3_out), .sel(B_SEL));
  assign B = bit_extender_2_out & multiplexer_3_out;  // AND_Gate and_2, 8 bits wide
  OR or_1 (.in_1(A), .out_2(or_1_out_2));
  assign C = bit_extender_1_out & multiplexer_2_out;  // AND_Gate and_3, 8 bits wide
  assign bit_extender_2_out = {{7{SEL_A_B}}, SEL_A_B};  // Bit_Extender bit_extender_2
  OR or_2 (.in_1(B), .out_2(or_2_out_2));
  or or_3 (SUM_UPDATE, or_1_out_2, or_2_out_2);
endmodule

module PC (
  input  [7:0] PC_IN_2,
  input  SEL,
  input  [1:0] LOAD,
  input  [7:0] PC_IN_1,
  input  CLR_PC,
  input  CLK,
  input  D_BUS_ENABLE,
  input  [7:0] D_BUS_IN,
  input  SEL_2,
  input  CLR_ALL,
  output [7:0] ADDRESS,
  output [7:0] OUT_1,
  output [7:0] OUT_2,
  output [7:0] OUT_3,
  output [7:0] OUT_4
);

  wire and_1_out, and_2_out, and_3_out, and_4_out, and_5_out, and_6_out, and_10_out, comparator_1_eq,
       comparator_2_eq, comparator_3_eq, comparator_4_eq, demultiplexer_1_out0, demultiplexer_1_out1,
       demultiplexer_1_out2, demultiplexer_1_out3, demultiplexer_2_out0, demultiplexer_2_out1,
       demultiplexer_2_out2, demultiplexer_2_out3, demultiplexer_2_out4, demultiplexer_2_out5,
       demultiplexer_2_out6, demultiplexer_2_out7, demultiplexer_2_out8, demultiplexer_2_out9,
       demultiplexer_2_out10, not_1_out, not_2_out, not_3_out, not_4_out, not_5_out, not_6_out, or_1_out,
       or_2_out, or_3_out, or_4_out, or_5_out_2, or_6_out_2, or_7_out_2, or_8_out_2, or_9_out_2, or_11_out,
       or_12_out, or_14_out, or_15_out_2, or_16_out_2, transistor_1_out, transistor_3_out;
  wire [1:0] counter_1_q;
  wire [3:0] counter_2_q;
  wire [7:0] and_7_out, and_8_out, and_9_out, bit_extender_1_out, bit_extender_2_out, bit_extender_3_out,
       CS_q, DS_q, ES_q, multiplexer_1_out, or_10_out, or_13_out, or_17_out, register_1_q, SS_q,
       transistor_2_out;

  Demultiplexer #(.select(2), .enable("false")) demultiplexer_1 (
    .out0(demultiplexer_1_out0), .out1(demultiplexer_1_out1), .out2(demultiplexer_1_out2),
    .out3(demultiplexer_1_out3), .in(SEL), .sel(counter_1_q));
  Counter #(.width(2), .max('h3)) counter_1 (
    .Q(counter_1_q), .clk(or_12_out), .clr(or_1_out));  // open: load, D, count, carry
  // Probe on PC_IN_1
  or or_1 (or_1_out, CLR_PC, CLR_ALL);
  and and_1 (and_1_out, D_BUS_ENABLE, SEL_2);
  Register CS (.D(PC_IN_1), .en(demultiplexer_1_out0), .Q(CS_q), .clk(demultiplexer_1_out0), .clr(or_1_out));
  Register DS (.D(PC_IN_1), .en(demultiplexer_1_out1), .Q(DS_q), .clk(demultiplexer_1_out1), .clr(or_1_out));
  Register ES (.D(PC_IN_1), .en(demultiplexer_1_out2), .Q(ES_q), .clk(demultiplexer_1_out2), .clr(or_1_out));
  Register SS (.D(PC_IN_1), .en(demultiplexer_1_out3), .Q(SS_q), .clk(demultiplexer_1_out3), .clr(or_1_out));
  Demultiplexer #(.select(4), .enable("false")) demultiplexer_2 (
    .out0(demultiplexer_2_out0), .out1(demultiplexer_2_out1), .out2(demultiplexer_2_out2),
    .out3(demultiplexer_2_out3), .out4(demultiplexer_2_out4), .out5(demultiplexer_2_out5),
    .out6(demultiplexer_2_out6), .out7(demultiplexer_2_out7), .out8(demultiplexer_2_out8),
    .out9(demultiplexer_2_out9), .out10(demultiplexer_2_out10), .in(1'b1), .sel(counter_2_q));  // open: out11, out12, out13, out14, out15
  Counter #(.width(4), .max('hf)) counter_2 (
    .Q(counter_2_q), .clk(transistor_1_out), .clr(or_2_out));  // open: load, D, count, carry
  Transistor #(.\type ("n")) transistor_1 (.in(CLK), .out(transistor_1_out), .gate(and_1_out));
  or or_2 (or_2_out, CLR_ALL, and_2_out, or_4_out);
  not not_1 (not_1_out, D_BUS_ENABLE);
  and and_2 (and_2_out, not_1_out, comparator_1_eq);
  or or_3 (or_3_out, and_2_out, or_4_out);
  or or_4 (or_4_out, CLR_ALL, CLR_PC, and_10_out);
  OR or_5 (.in_1(SS_q), .out_2(or_5_out_2));
  OR or_6 (.in_1(ES_q), .out_2(or_6_out_2));
  OR or_7 (.in_1(DS_q), .out_2(or_7_out_2));
  and and_3 (and_3_out, demultiplexer_1_out0, or_8_out_2);
  OR or_8 (.in_1(CS_q), .out_2(or_8_out_2));
  OR or_9 (.in_1(CS_q), .out_2(or_9_out_2));
  Multiplexer #(.select(2), .width(8), .enable("false")) multiplexer_1 (
    .in0(CS_q), .in1(DS_q), .in2(ES_q), .in3(SS_q), .out(multiplexer_1_out), .sel(LOAD));
  assign or_10_out = and_8_out | PC_IN_2;  // OR_Gate or_10, 8 bits wide
  or or_11 (or_11_out, demultiplexer_2_out0, demultiplexer_2_out1);
  Transistor #(.\type ("n"), .width(8)) transistor_2 (.in(D_BUS_IN), .out(transistor_2_out), .gate(D_BUS_ENABLE));
  and and_4 (and_4_out, demultiplexer_1_out3, or_5_out_2);
  and and_5 (and_5_out, demultiplexer_1_out2, or_6_out_2);
  or or_12 (or_12_out, and_4_out, and_5_out, and_6_out, and_3_out);
  and and_6 (and_6_out, demultiplexer_1_out1, or_7_out_2);
  assign bit_extender_1_out = {{7{or_9_out_2}}, or_9_out_2};  // Bit_Extender bit_extender_1
  assign and_7_out = bit_extender_1_out & multiplexer_1_out;  // AND_Gate and_7, 8 bits wide
  assign or_13_out = and_7_out | PC_IN_2;  // OR_Gate or_13, 8 bits wide
  not not_2 (not_2_out, or_11_out);
  or or_14 (or_14_out, demultiplexer_2_out1, demultiplexer_2_out3, demultiplexer_2_out5, demultiplexer_2_out7, demultiplexer_2_out9);
  OR or_15 (.in_1(PC_IN_2), .out_2(or_15_out_2));
  not not_3 (not_3_out, or_15_out_2);
  Register register_1 (.D(or_10_out), .Q(register_1_q), .clk(transistor_3_out), .clr(or_1_out));  // open: en
  Counter counter_3 (
    .load(or_11_out), .D(or_17_out), .count(not_2_out), .Q(ADDRESS), .clk(or_14_out), .clr(or_1_out));  // open: carry
  Transistor #(.\type ("n")) transistor_3 (.in(demultiplexer_2_out10), .out(transistor_3_out), .gate(SEL_2));
  Register register_2 (.D(transistor_2_out), .Q(OUT_1), .clk(demultiplexer_2_out2), .clr(or_3_out));  // open: en
  Comparator comparator_1 (.a(OUT_1), .b(8'he), .eq(comparator_1_eq));  // open: gt, lt
  Register register_3 (.D(transistor_2_out), .Q(OUT_2), .clk(demultiplexer_2_out4), .clr(or_3_out));  // open: en
  Register register_4 (.D(transistor_2_out), .Q(OUT_3), .clk(demultiplexer_2_out6), .clr(or_3_out));  // open: en
  Register register_5 (.D(transistor_2_out), .Q(OUT_4), .clk(demultiplexer_2_out8), .clr(or_3_out));  // open: en
  assign bit_extender_2_out = {{7{not_3_out}}, not_3_out};  // Bit_Extender bit_extender_2
  assign and_8_out = bit_extender_2_out & ADDRESS;  // AND_Gate and_8, 8 bits wide
  OR or_16 (.in_1(PC_IN_2), .out_2(or_16_out_2));
  not not_4 (not_4_out, or_16_out_2);
  assign bit_extender_3_out = {{7{not_4_out}}, not_4_out};  // Bit_Extender bit_extender_3
  assign and_9_out = bit_extender_3_out & register_1_q;  // AND_Gate and_9, 8 bits wide
  assign or_17_out = PC_IN_2 | and_9_out;  // OR_Gate or_17, 8 bits wide
  Comparator comparator_2 (.a(PC_IN_2), .b(ADDRESS), .eq(comparator_2_eq));  // open: gt, lt
  Comparator comparator_3 (.a(PC_IN_2), .b({8{1'b0}}), .eq(comparator_3_eq));  // open: gt, lt
  Comparator comparator_4 (.a(ADDRESS), .b({8{1'b0}}), .eq(comparator_4_eq));  // open: gt, lt
  and and_10 (and_10_out, comparator_2_eq, not_5_out, not_6_out);
  not not_5 (not_5_out, comparator_3_eq);
  not not_6 (not_6_out, comparator_4_eq);
endmodule

module OR (
  input  [7:0] in_1,
  output out_2
);

  or or_1 (out_2, in_1[0], in_1[1], in_1[2], in_1[3], in_1[4], in_1[5], in_1[6], in_1[7]);
endmodule

module MOV_OP (
  input  SEL_MOV,
  input  SEL_ALU,
  input  [7:0] DATA_1,
  input  [7:0] DATA,
  input  [7:0] DATA_2,
  output [3:0] OP,
  output SEL_REG,
  output SEL_TEMP,
  output [1:0] REG,
  output OP_MUX,
  output [1:0] A_SEL,
  output [1:0] TEMP,
  output KYBD_ENABLE,
  output SEL_ACC,
  output SEL_A_B,
  output [1:0] B_SEL,
  output SEL_REGS,
  output SEL_TEMP_2,
  output [1:0] SEL_1,
  output [1:0] SEL_2,
  output TTY_ENABLE,
  output SEL_PC,
  output ENABLE_MATRIX
);

  wire and_11_out, comparator_1_eq, comparator_2_eq, comparator_3_eq, comparator_4_eq, comparator_5_eq,
       comparator_6_eq, comparator_7_eq, comparator_8_eq, comparator_9_eq, comparator_10_eq,
       comparator_11_eq, comparator_12_eq, comparator_13_eq, comparator_14_eq, comparator_15_eq,
       comparator_16_eq, comparator_17_eq, comparator_18_eq, comparator_19_eq, comparator_22_eq,
       comparator_23_eq, comparator_24_eq, comparator_25_eq, comparator_26_eq, comparator_27_eq,
       comparator_28_eq, comparator_29_eq, comparator_30_eq, comparator_33_eq, not_1_out, or_1_out,
       or_2_1_out_2, or_2_2_out_2, or_2_out, or_3_out, or_4_out, or_6_out, or_10_out, undriven;
  wire [1:0] and_3_out, and_4_out, and_5_out, and_6_out, and_7_out, and_8_out, and_9_out, and_10_out,
       and_16_out, and_17_out, bit_extender_2_out, bit_extender_3_out, bit_extender_4_out,
       bit_extender_5_out, bit_extender_6_out, bit_extender_7_out, bit_extender_8_out, bit_extender_9_out,
       bit_extender_10_out, bit_extender_13_out, bit_extender_14_out, bit_extender_15_out,
       bit_extender_16_out, bit_extender_17_out, bit_extender_18_out, bit_extender_19_out,
       bit_extender_20_out, bit_extender_21_out, bit_extender_22_out, bit_extender_23_out,
       bit_extender_24_out, bit_extender_25_out, bit_extender_26_out, bit_extender_27_out,
       bit_extender_28_out, counter_1_q, or_5_out, or_7_out, or_9_out, or_11_out, or_12_out, or_13_out;
  wire [3:0] bit_extender_1_out;
  wire [7:0] and_12_out, and_13_out, and_14_out, and_15_out, bit_extender_11_out, bit_extender_12_out;

  Comparator comparator_1 (.a(DATA), .b(8'hf3), .eq(comparator_1_eq));  // open: gt, lt
  Comparator comparator_2 (.a(DATA_2), .b(8'hf5), .eq(comparator_2_eq));  // open: gt, lt
  assign bit_extender_1_out = {{3{SEL_ALU}}, SEL_ALU};  // Bit_Extender bit_extender_1
  and and_1 (OP_MUX, comparator_1_eq, SEL_MOV, comparator_2_eq);
  assign OP = bit_extender_1_out & DATA[3:0];  // AND_Gate and_2, 4 bits wide
  assign bit_extender_2_out = {{1{SEL_ALU}}, SEL_ALU};  // Bit_Extender bit_extender_2
  Comparator comparator_3 (.a(DATA_1), .b(8'ha), .eq(comparator_3_eq));  // open: gt, lt
  Comparator comparator_4 (.a(DATA_1), .b(8'hb), .eq(comparator_4_eq));  // open: gt, lt
  Comparator comparator_5 (.a(DATA_1), .b(8'hc), .eq(comparator_5_eq));  // open: gt, lt
  Comparator comparator_6 (.a(DATA_1), .b(8'hd), .eq(comparator_6_eq));  // open: gt, lt
  Comparator comparator_7 (.a(DATA_2), .b(8'ha), .eq(comparator_7_eq));  // open: gt, lt
  Comparator comparator_8 (.a(DATA_2), .b(8'hb), .eq(comparator_8_eq));  // open: gt, lt
  Comparator comparator_9 (.a(DATA_2), .b(8'hc), .eq(comparator_9_eq));  // open: gt, lt
  Comparator comparator_10 (.a(DATA_2), .b(8'hd), .eq(comparator_10_eq));  // open: gt, lt
  not not_1 (not_1_out, DATA[1]);
  assign and_3_out = 2'b00 & bit_extender_3_out;  // AND_Gate and_3, 2 bits wide
  assign bit_extender_3_out = {{1{comparator_3_eq}}, comparator_3_eq};  // Bit_Extender bit_extender_3
  or or_1 (or_1_out, comparator_3_eq, comparator_4_eq);
  assign and_4_out = 2'b01 & bit_extender_4_out;  // AND_Gate and_4, 2 bits wide
  assign bit_extender_4_out = {{1{comparator_4_eq}}, comparator_4_eq};  // Bit_Extender bit_extender_4
  assign and_5_out = 2'b10 & bit_extender_5_out;  // AND_Gate and_5, 2 bits wide
  assign bit_extender_5_out = {{1{comparator_5_eq}}, comparator_5_eq};  // Bit_Extender bit_extender_5
  or or_2 (or_2_out, comparator_5_eq, comparator_6_eq);
  assign and_6_out = 2'b11 & bit_extender_6_out;  // AND_Gate and_6, 2 bits wide
  assign bit_extender_6_out = {{1{comparator_6_eq}}, comparator_6_eq};  // Bit_Extender bit_extender_6
  assign and_7_out = 2'b00 & bit_extender_7_out;  // AND_Gate and_7, 2 bits wide
  assign bit_extender_7_out = {{1{comparator_7_eq}}, comparator_7_eq};  // Bit_Extender bit_extender_7
  or or_3 (or_3_out, comparator_7_eq, comparator_8_eq);
  assign and_8_out = 2'b01 & bit_extender_8_out;  // AND_Gate and_8, 2 bits wide
  assign bit_extender_8_out = {{1{comparator_8_eq}}, comparator_8_eq};  // Bit_Extender bit_extender_8
  assign and_9_out = 2'b10 & bit_extender_9_out;  // AND_Gate and_9, 2 bits wide
  assign bit_extender_9_out = {{1{comparator_9_eq}}, comparator_9_eq};  // Bit_Extender bit_extender_9
  or or_4 (or_4_out, comparator_9_eq, comparator_10_eq);
  assign and_10_out = 2'b11 & bit_extender_10_out;  // AND_Gate and_10, 2 bits wide
  assign bit_extender_10_out = {{1{comparator_10_eq}}, comparator_10_eq};  // Bit_Extender bit_extender_10
  and and_11 (and_11_out, DATA[0], not_1_out, DATA[2]);
  assign bit_extender_11_out = {{7{and_11_out}}, and_11_out};  // Bit_Extender bit_extender_11
  assign and_12_out = DATA_1 & bit_extender_11_out;  // AND_Gate and_12, 8 bits wide
  assign and_13_out = DATA_2 & bit_extender_11_out;  // AND_Gate and_13, 8 bits wide
  assign or_5_out = and_3_out | and_4_out;  // OR_Gate or_5, 2 bits wide
  or or_6 (or_6_out, or_1_out, or_2_out);
  assign or_7_out = and_5_out | and_6_out;  // OR_Gate or_7, 2 bits wide
  or or_8 (SEL_A_B, or_6_out, or_10_out);
  assign or_9_out = and_7_out | and_8_out;  // OR_Gate or_9, 2 bits wide
  or or_10 (or_10_out, or_3_out, or_4_out);
  assign or_11_out = and_9_out | and_10_out;  // OR_Gate or_11, 2 bits wide
  assign bit_extender_12_out = {{7{SEL_MOV}}, SEL_MOV};  // Bit_Extender bit_extender_12
  assign and_14_out = and_12_out & bit_extender_12_out;  // AND_Gate and_14, 8 bits wide
  assign and_15_out = and_13_out & bit_extender_12_out;  // AND_Gate and_15, 8 bits wide
  assign and_16_out = bit_extender_2_out & or_12_out;  // AND_Gate and_16, 2 bits wide
  assign or_12_out = or_5_out | or_7_out;  // OR_Gate or_12, 2 bits wide
  OR_2 or_2_1 (.in_1(and_16_out), .out_2(or_2_1_out_2));
  assign and_17_out = bit_extender_2_out & or_13_out;  // AND_Gate and_17, 2 bits wide
  assign or_13_out = or_9_out | or_11_out;  // OR_Gate or_13, 2 bits wide
  OR_2 or_2_2 (.in_1(and_17_out), .out_2(or_2_2_out_2));
  Register #(.width(2), .trigger("high")) register_1 (
    .D(and_16_out), .Q(A_SEL), .clk(or_2_1_out_2), .clr(undriven));  // open: en
  Register #(.width(2), .trigger("high")) register_2 (
    .D(and_17_out), .Q(B_SEL), .clk(or_2_2_out_2), .clr(undriven));  // open: en
  Comparator comparator_11 (.a(and_15_out), .b(8'ha), .eq(comparator_11_eq));  // open: gt, lt
  Comparator comparator_12 (.a(and_15_out), .b(8'hb), .eq(comparator_12_eq));  // open: gt, lt
  Comparator comparator_13 (.a(and_15_out), .b(8'hc), .eq(comparator_13_eq));  // open: gt, lt
  Comparator comparator_14 (.a(and_15_out), .b(8'hd), .eq(comparator_14_eq));  // open: gt, lt
  Comparator comparator_15 (.a(and_15_out), .b(8'he), .eq(comparator_15_eq));  // open: gt, lt
  Comparator comparator_16 (.a(and_15_out), .b(8'hf), .eq(comparator_16_eq));  // open: gt, lt
  Comparator comparator_17 (.a(and_15_out), .b(8'h11), .eq(comparator_17_eq));  // open: gt, lt
  Comparator comparator_18 (.a(and_15_out), .b(8'h12), .eq(comparator_18_eq));  // open: gt, lt
  Comparator comparator_19 (.a(and_15_out), .b(8'h14), .eq(comparator_19_eq));  // open: gt, lt
  Comparator comparator_20 (.a(and_15_out), .b(8'h15), .eq(SEL_PC));  // open: gt, lt
  Comparator comparator_21 (.a(and_15_out), .b(8'h70), .eq(ENABLE_MATRIX));  // open: gt, lt
  Comparator comparator_22 (.a(and_15_out), .b(8'h97), .eq(comparator_22_eq));  // open: gt, lt
  Comparator comparator_23 (.a(and_14_out), .b(8'ha), .eq(comparator_23_eq));  // open: gt, lt
  assign bit_extender_13_out = {{1{comparator_23_eq}}, comparator_23_eq};  // Bit_Extender bit_extender_13
  Comparator comparator_24 (.a(and_14_out), .b(8'hb), .eq(comparator_24_eq));  // open: gt, lt
  assign bit_extender_14_out = {{1{comparator_24_eq}}, comparator_24_eq};  // Bit_Extender bit_extender_14
  assign bit_extender_15_out = {{1{comparator_25_eq}}, comparator_25_eq};  // Bit_Extender bit_extender_15
  Comparator comparator_25 (.a(and_14_out), .b(8'hc), .eq(comparator_25_eq));  // open: gt, lt
  assign bit_extender_16_out = {{1{comparator_26_eq}}, comparator_26_eq};  // Bit_Extender bit_extender_16
  Comparator comparator_26 (.a(and_14_out), .b(8'hd), .eq(comparator_26_eq));  // open: gt, lt
  assign bit_extender_17_out = {{1{comparator_27_eq}}, comparator_27_eq};  // Bit_Extender bit_extender_17
  Comparator comparator_27 (.a(and_14_out), .b(8'he), .eq(comparator_27_eq));  // open: gt, lt
  Comparator comparator_28 (.a(and_14_out), .b(8'hf), .eq(comparator_28_eq));  // open: gt, lt
  assign bit_extender_18_out = {{1{comparator_28_eq}}, comparator_28_eq};  // Bit_Extender bit_extender_18
  Comparator comparator_29 (.a(and_14_out), .b(8'h11), .eq(comparator_29_eq));  // open: gt, lt
  assign bit_extender_19_out = {{1{comparator_29_eq}}, comparator_29_eq};  // Bit_Extender bit_extender_19
  Comparator comparator_30 (.a(and_14_out), .b(8'h12), .eq(comparator_30_eq));  // open: gt, lt
  assign bit_extender_20_out = {{1{comparator_30_eq}}, comparator_30_eq};  // Bit_Extender bit_extender_20
  Comparator comparator_31 (.a(and_14_out), .b(8'h13), .eq(KYBD_ENABLE));  // open: gt, lt
  Comparator comparator_32 (.a(and_14_out), .b(8'h80), .eq(SEL_ACC));  // open: gt, lt
  assign SEL_1 = 2'b00 & bit_extender_21_out;  // AND_Gate and_18, 2 bits wide
  assign bit_extender_21_out = {{1{comparator_11_eq}}, comparator_11_eq};  // Bit_Extender bit_extender_21
  assign SEL_1 = 2'b01 & bit_extender_22_out;  // AND_Gate and_19, 2 bits wide
  assign bit_extender_22_out = {{1{comparator_12_eq}}, comparator_12_eq};  // Bit_Extender bit_extender_22
  assign SEL_1 = 2'b10 & bit_extender_23_out;  // AND_Gate and_20, 2 bits wide
  assign bit_extender_23_out = {{1{comparator_13_eq}}, comparator_13_eq};  // Bit_Extender bit_extender_23
  assign SEL_1 = 2'b11 & bit_extender_24_out;  // AND_Gate and_21, 2 bits wide
  assign bit_extender_24_out = {{1{comparator_14_eq}}, comparator_14_eq};  // Bit_Extender bit_extender_24
  assign SEL_2 = 2'b00 & bit_extender_25_out;  // AND_Gate and_22, 2 bits wide
  assign bit_extender_25_out = {{1{comparator_15_eq}}, comparator_15_eq};  // Bit_Extender bit_extender_25
  assign SEL_2 = 2'b01 & bit_extender_26_out;  // AND_Gate and_23, 2 bits wide
  assign bit_extender_26_out = {{1{comparator_16_eq}}, comparator_16_eq};  // Bit_Extender bit_extender_26
  assign SEL_2 = 2'b10 & bit_extender_27_out;  // AND_Gate and_24, 2 bits wide
  assign bit_extender_27_out = {{1{comparator_17_eq}}, comparator_17_eq};  // Bit_Extender bit_extender_27
  assign SEL_2 = 2'b11 & bit_extender_28_out;  // AND_Gate and_25, 2 bits wide
  assign bit_extender_28_out = {{1{comparator_18_eq}}, comparator_18_eq};  // Bit_Extender bit_extender_28
  assign REG = 2'b00 & bit_extender_13_out;  // AND_Gate and_26, 2 bits wide
  assign REG = 2'b01 & bit_extender_14_out;  // AND_Gate and_27, 2 bits wide
  assign REG = 2'b10 & bit_extender_15_out;  // AND_Gate and_28, 2 bits wide
  assign REG = 2'b11 & bit_extender_16_out;  // AND_Gate and_29, 2 bits wide
  assign TEMP = 2'b00 & bit_extender_17_out;  // AND_Gate and_30, 2 bits wide
  assign TEMP = 2'b01 & bit_extender_18_out;  // AND_Gate and_31, 2 bits wide
  assign TEMP = 2'b10 & bit_extender_19_out;  // AND_Gate and_32, 2 bits wide
  assign TEMP = 2'b11 & bit_extender_20_out;  // AND_Gate and_33, 2 bits wide
  T_Flip_Flop t_ff_1 (
    .clk(comparator_19_eq), .T(comparator_19_eq), .Q(TTY_ENABLE), .reset(comparator_33_eq));  // open: Qn, preset, en
  Counter #(.width(2), .max('h3)) counter_1 (
    .Q(counter_1_q), .clk(comparator_19_eq), .clr(comparator_33_eq));  // open: load, D, count, carry
  or or_14 (SEL_REGS, SEL_1[0], SEL_1[1], SEL_1[0], SEL_1[1], SEL_1[0], SEL_1[1], SEL_1[0], SEL_1[1]);
  or or_15 (SEL_TEMP_2, SEL_2[0], SEL_2[1], SEL_2[0], SEL_2[1], SEL_2[0], SEL_2[1], SEL_2[0], SEL_2[1]);
  Comparator #(.width(2)) comparator_33 (.a(counter_1_q), .b(2'b10), .eq(comparator_33_eq));  // open: gt, lt
  or or_16 (SEL_REG, REG[0], REG[1], REG[0], REG[1], REG[0], REG[1], REG[0], REG[1]);
  or or_17 (SEL_TEMP, TEMP[0], TEMP[1], TEMP[0], TEMP[1], TEMP[0], TEMP[1], TEMP[0], TEMP[1]);
endmodule

module CONTROL_UNIT (
  input  [7:0] D_BUS_IN,
  input  CLK,
  input  CLR,
  input  SELECT,
  input  ZERO,
  input  CARRY,
  input  Hi,
  input  EQUAL,
  input  Lo,
  output [7:0] ADDRESS,
  output [1:0] TTY_ENABLE_AND_MATRX,
  output [1:0] TTY_MUX,
  output [1:0] TEMP,
  output SEL_A_B,
  output [3:0] OP,
  output [1:0] A_SEL,
  output [1:0] B_SEL,
  output [1:0] REGS,
  output SEL_REGS,
  output SEL_TEMPs,
  output OP_MUX,
  output SEL_BIOS,
  output SEL_RAM,
  output SELMEM,
  output SEL_REG,
  output [1:0] SEL_1,
  output [1:0] SEL_2,
  output CLK_KYBD,
  output CLR_TTY,
  output CLR_LED_MATRIX,
  output CLR_REGS,
  output SEL_TEMP,
  output CLR_X,
  output CLK_RAM,
  output CLK_MEM,
  output MAIN_MUX,
  output ADDR_SEL,
  output MEM_READ,
  output RAM_READ,
  output RAM_WRITE,
  output MEM_WRITE,
  output [1:0] MUX_1,
  output [1:0] MUX_2
);

  wire and_1_out, and_2_out, and_6_out, and_7_out, and_8_out, and_9_out, and_13_out, and_15_out, and_18_out,
       demultiplexer_1_out1, demultiplexer_1_out2, demultiplexer_1_out3, demultiplexer_1_out4,
       demultiplexer_1_out5, demultiplexer_1_out6, demultiplexer_1_out7, demultiplexer_1_out9,
       demultiplexer_1_out10, demultiplexer_1_out11, demultiplexer_1_out12, demultiplexer_1_out13, KKYBD_2,
       logic_1_clr_pc, logic_1_clr_pc_all, logic_1_sel_bios, logic_1_sel_mem, logic_1_sel_ram,
       mov_batch_1_bios, mov_batch_1_enable_matrix, mov_batch_1_mem, mov_batch_1_pc_enable, mov_batch_1_ram,
       mov_batch_1_status, MOV_DATA, mov_op_1_enable_matrix, mov_op_1_kybd_enable, mov_op_1_sel_acc,
       mov_op_1_sel_pc, mov_op_1_sel_regs, mov_op_1_sel_temp_2, mov_op_1_tty_enable, or_1_out, or_2_1_out_2,
       or_2_2_out_2, or_2_3_out_2, or_2_4_out_2, or_3_out, or_5_out, or_7_out, or_8_out, or_16_out,
       or_24_out, or_25_out, PC_2, REGS_t, SEL_REG_t, SEL_REGS_t, SEL_TEMP_t, SEL_TEMPS_t, TEMP_t, TTY;
  wire [1:0] and_3_out, and_4_out, and_5_out, and_10_out, and_11_out, and_12_out, and_16_out, and_17_out,
       bit_extender_1_out, bit_extender_2_out, bit_extender_3_out, bit_extender_4_out, bit_extender_5_out,
       bit_extender_6_out, bit_extender_8_out, bit_extender_9_out, mov_batch_1_regs, mov_batch_1_sel_1,
       mov_batch_1_sel_2, mov_batch_1_temp, mov_op_1_reg, mov_op_1_sel_1, mov_op_1_sel_2, mov_op_1_temp;
  wire [7:0] and_14_out, bit_extender_7_out, call_ret_1_p10, jump_1_addr, logic_1_addr, MB, mov_batch_1_addr,
       or_4_out, pc_1_address, pc_1_out_1, pc_1_out_2, pc_1_out_3, pc_1_out_4, pc_2_1_address;

  Demultiplexer #(.select(4), .enable("false")) demultiplexer_1 (
    .out1(demultiplexer_1_out1), .out2(demultiplexer_1_out2), .out3(demultiplexer_1_out3),
    .out4(demultiplexer_1_out4), .out5(demultiplexer_1_out5), .out6(demultiplexer_1_out6),
    .out7(demultiplexer_1_out7), .out9(demultiplexer_1_out9), .out10(demultiplexer_1_out10),
    .out11(demultiplexer_1_out11), .out12(demultiplexer_1_out12), .out13(demultiplexer_1_out13),
    .out14(MOV_DATA), .in(SELECT), .sel(pc_1_out_1[3:0]));  // open: out0, out8, out15
  or or_1 (or_1_out, logic_1_clr_pc_all, logic_1_clr_pc);
  or or_2 (TTY_ENABLE_AND_MATRX[1], mov_op_1_enable_matrix, mov_batch_1_enable_matrix);
  // Probe on or_4_out
  MOV_OP mov_op_1 (
    .SEL_MOV(demultiplexer_1_out1), .SEL_ALU(demultiplexer_1_out2), .DATA_1(pc_1_out_3), .DATA(pc_1_out_2),
    .DATA_2(pc_1_out_4), .OP(OP), .REG(mov_op_1_reg), .A_SEL(A_SEL), .TEMP(mov_op_1_temp),
    .KYBD_ENABLE(mov_op_1_kybd_enable), .B_SEL(B_SEL), .SEL_REGS(mov_op_1_sel_regs),
    .SEL_TEMP_2(mov_op_1_sel_temp_2), .SEL_1(mov_op_1_sel_1), .SEL_2(mov_op_1_sel_2),
    .TTY_ENABLE(mov_op_1_tty_enable), .SEL_PC(mov_op_1_sel_pc), .ENABLE_MATRIX(mov_op_1_enable_matrix),
    .SEL_ACC(mov_op_1_sel_acc), .SEL_A_B(SEL_A_B), .SEL_TEMP(SEL_TEMP_t), .SEL_REG(SEL_REGS_t),
    .OP_MUX(OP_MUX));
  MOV_BATCH mov_batch_1 (
    .MOV_B_TO(demultiplexer_1_out3), .MOV_B_FROM(demultiplexer_1_out4), .DATA(pc_1_out_2),
    .DATA_1(pc_1_out_3), .DATA_2(pc_1_out_4), .ADDR(mov_batch_1_addr), .BIOS(mov_batch_1_bios),
    .RAM(mov_batch_1_ram), .MEM(mov_batch_1_mem), .SEL_1(mov_batch_1_sel_1), .REGS(mov_batch_1_regs),
    .SEL_2(mov_batch_1_sel_2), .TEMP(mov_batch_1_temp), .TTY_ENABLE(TTY), .PC_ENABLE(mov_batch_1_pc_enable),
    .ENABLE_MATRIX(mov_batch_1_enable_matrix), .SEL_TEMP_2(TEMP_t), .SEL_REGS(REGS_t),
    .STATUS(mov_batch_1_status), .PC_IN(ADDRESS), .CLR(CLR), .CLK(CLK), .MOV_DATA(MOV_DATA),
    .RAM_WRITE(RAM_WRITE), .MEM_WRITE(MEM_WRITE), .RAM_READ(RAM_READ), .MEM_READ(MEM_READ),
    .SEL_TEMP(SEL_TEMPS_t), .SEL_REGS_2(SEL_REG_t), .KYBD_ENABLE(KKYBD_2), .PC_1(MB), .PC_2_EN(PC_2));
  LOGIC logic_1 (
    .SEL_5(demultiplexer_1_out10), .SEL_1(demultiplexer_1_out9), .SEL_2(SELECT), .DATA(pc_1_out_2),
    .DATA_2(pc_1_out_3), .DATA_3(pc_1_out_4), .PC_IN(ADDRESS), .CLR(CLR), .ADDR(logic_1_addr),
    .CLR_TTY(CLR_TTY), .CLR_LED_MATRIX(CLR_LED_MATRIX), .CLR_REGS(CLR_REGS), .SEL_BIOS(logic_1_sel_bios),
    .SEL_MEM(logic_1_sel_mem), .CLR_PC_ALL(logic_1_clr_pc_all), .CLK_KYBD(CLK_KYBD), .CLR_X(CLR_X),
    .CLK_RAM(CLK_RAM), .CLK_MEM(CLK_MEM), .CLK(CLK), .SEL_3(demultiplexer_1_out11), .MAIN_MUX(MAIN_MUX),
    .SEL_4(demultiplexer_1_out12), .ADDR_SEL(ADDR_SEL), .CLR_PC(logic_1_clr_pc), .MEM_WRITE(MEM_WRITE),
    .RAM_WRITE(RAM_WRITE), .SEL_RAM(logic_1_sel_ram));
  and and_1 (and_1_out, or_24_out, and_18_out);
  or or_3 (or_3_out, mov_op_1_kybd_enable, KKYBD_2);
  and and_2 (and_2_out, and_15_out, and_18_out);
  PC_2 pc_2_1 (
    .ENABLE(mov_batch_1_status), .PC_IN(mov_batch_1_addr), .CLK(CLK), .ADDRESS(pc_2_1_address),
    .SELECT(SELECT), .CLR(CLR), .PC_2_EN(PC_2));
  assign or_4_out = logic_1_addr | jump_1_addr | call_ret_1_p10 | MB;  // OR_Gate or_4, 8 bits wide
  PC pc_1 (
    .PC_IN_1(D_BUS_IN), .CLR_PC(or_1_out), .CLK(CLK), .D_BUS_IN(D_BUS_IN), .SEL_2(SELECT),
    .ADDRESS(pc_1_address), .OUT_1(pc_1_out_1), .OUT_2(pc_1_out_2), .OUT_3(pc_1_out_3), .OUT_4(pc_1_out_4),
    .SEL(or_5_out), .PC_IN_2(or_4_out), .CLR_ALL(CLR), .D_BUS_ENABLE(mov_batch_1_status));  // open: LOAD
  // CALL_RET call_ret_1: pin names not known; wires that end beside it: pc_1_out_2, pc_1_out_3, pc_1_out_4, ADDRESS, CLR, CLK, demultiplexer_1_out5, demultiplexer_1_out13, demultiplexer_1_out6, call_ret_1_p10
  JUMP jump_1 (
    .CARRY_FLAG(CARRY), .ZERO_FLAG(ZERO), .SEL(demultiplexer_1_out7), .DATA(pc_1_out_2), .DATA_1(pc_1_out_3),
    .DATA_2(pc_1_out_4), .ADDR(jump_1_addr), .Hi(Hi), .EQUAL(EQUAL), .Lo(Lo));
  assign bit_extender_1_out = {{1{and_1_out}}, and_1_out};  // Bit_Extender bit_extender_1
  assign bit_extender_2_out = {{1{or_3_out}}, or_3_out};  // Bit_Extender bit_extender_2
  assign bit_extender_3_out = {{1{and_2_out}}, and_2_out};  // Bit_Extender bit_extender_3
  or or_5 (or_5_out, mov_batch_1_pc_enable, mov_op_1_sel_pc);
  assign and_3_out = bit_extender_1_out & 2'b11;  // AND_Gate and_3, 2 bits wide
  assign and_4_out = bit_extender_2_out & 2'b01;  // AND_Gate and_4, 2 bits wide
  assign MUX_1 = and_4_out | and_3_out | and_5_out;  // OR_Gate or_6, 2 bits wide
  assign and_5_out = bit_extender_3_out & 2'b10;  // AND_Gate and_5, 2 bits wide
  or or_7 (or_7_out, RAM_WRITE, MEM_WRITE);
  or or_8 (or_8_out, MEM_READ, RAM_READ);
  or or_9 (TTY_ENABLE_AND_MATRX[0], TTY, mov_op_1_tty_enable);
  assign TEMP = mov_batch_1_temp | mov_op_1_temp;  // OR_Gate or_10, 2 bits wide
  assign REGS = mov_batch_1_regs | mov_op_1_reg;  // OR_Gate or_11, 2 bits wide
  or or_12 (SEL_BIOS, mov_batch_1_bios, logic_1_sel_bios);
  or or_13 (SEL_RAM, mov_batch_1_ram, logic_1_sel_ram);
  or or_14 (SELMEM, mov_batch_1_mem, logic_1_sel_mem);
  assign SEL_1 = mov_batch_1_sel_1 | mov_op_1_sel_1;  // OR_Gate or_15, 2 bits wide
  or or_16 (or_16_out, KKYBD_2, and_8_out);
  and and_6 (and_6_out, or_24_out, or_7_out);
  and and_7 (and_7_out, and_15_out, or_7_out);
  and and_8 (and_8_out, or_7_out, or_8_out);
  and and_9 (and_9_out, mov_op_1_tty_enable, and_15_out);
  OR_2 or_2_1 (.in_1(REGS), .out_2(or_2_1_out_2));
  assign SEL_2 = mov_batch_1_sel_2 | mov_op_1_sel_2;  // OR_Gate or_17, 2 bits wide
  assign bit_extender_4_out = {{1{or_16_out}}, or_16_out};  // Bit_Extender bit_extender_4
  assign and_10_out = bit_extender_4_out & 2'b11;  // AND_Gate and_10, 2 bits wide
  assign bit_extender_5_out = {{1{and_6_out}}, and_6_out};  // Bit_Extender bit_extender_5
  assign and_11_out = bit_extender_5_out & 2'b01;  // AND_Gate and_11, 2 bits wide
  assign bit_extender_6_out = {{1{and_7_out}}, and_7_out};  // Bit_Extender bit_extender_6
  assign and_12_out = bit_extender_6_out & 2'b10;  // AND_Gate and_12, 2 bits wide
  assign bit_extender_7_out = {{7{mov_batch_1_status}}, mov_batch_1_status};  // Bit_Extender bit_extender_7
  and and_13 (and_13_out, mov_op_1_tty_enable, or_24_out);
  OR_2 or_2_2 (.in_1(TEMP), .out_2(or_2_2_out_2));
  or or_18 (SEL_REGS, REGS_t, mov_op_1_sel_regs);
  or or_19 (SEL_TEMPs, mov_op_1_sel_temp_2, TEMP_t);
  or or_20 (SEL_REG, SEL_REGS_t, SEL_REG_t);
  OR_2 or_2_3 (.in_1(SEL_2), .out_2(or_2_3_out_2));
  OR_2 or_2_4 (.in_1(SEL_1), .out_2(or_2_4_out_2));
  or or_21 (SEL_TEMP, SEL_TEMP_t, SEL_TEMPS_t);
  assign MUX_2 = and_11_out | and_10_out | and_12_out;  // OR_Gate or_22, 2 bits wide
  assign and_14_out = bit_extender_7_out & pc_1_address;  // AND_Gate and_14, 8 bits wide
  assign ADDRESS = and_14_out | pc_2_1_address;  // OR_Gate or_23, 8 bits wide
  assign bit_extender_8_out = {{1{and_9_out}}, and_9_out};  // Bit_Extender bit_extender_8
  assign bit_extender_9_out = {{1{and_13_out}}, and_13_out};  // Bit_Extender bit_extender_9
  or or_24 (or_24_out, or_2_2_out_2, SEL_TEMPs);
  and and_15 (and_15_out, or_2_1_out_2, SEL_REGS);
  or or_25 (or_25_out, or_2_1_out_2, or_2_3_out_2);
  assign and_16_out = bit_extender_8_out & 2'b01;  // AND_Gate and_16, 2 bits wide
  assign and_17_out = bit_extender_9_out & 2'b10;  // AND_Gate and_17, 2 bits wide
  and and_18 (and_18_out, or_25_out, or_2_4_out_2);
  assign TTY_MUX = and_16_out | and_17_out;  // OR_Gate or_26, 2 bits wide

  // Other names for the same wires on the sheet: _1 = MEM_READ; _2 = RAM_READ; _3 = RAM_WRITE; _4 = MEM_WRITE;
  //   A_B = SEL_A_B
endmodule

module ACCUMIALTOR (
  input  SUM_UPDATE,
  input  [7:0] ALU_IN,
  input  CLR,
  input  ZERO_IN,
  input  CARRY_IN,
  input  Hi_IN,
  input  EQUAL_IN,
  input  Lo_IN,
  output [7:0] ALU_OUT,
  output ZERO_OUT,
  output CARRY_OUT,
  output Hi_OUT,
  output EQUAL_OUT,
  output Lo_OUT
);

  wire or_1_out_2, or_2_out;

  OR or_1 (.in_1(ALU_IN), .out_2(or_1_out_2));
  Register RESAULT (.D(ALU_IN), .en(or_1_out_2), .Q(ALU_OUT), .clk(or_1_out_2), .clr(or_2_out));
  or or_2 (or_2_out, CLR, SUM_UPDATE);
  Register #(.width(1), .trigger("high")) ZERO (.D(ZERO_IN), .Q(ZERO_OUT), .clk(ZERO_IN), .clr(or_2_out));  // open: en
  Register #(.width(1), .trigger("high")) u_CARRY_OUT (
    .D(CARRY_IN), .Q(CARRY_OUT), .clk(CARRY_IN), .clr(or_2_out));  // open: en
  Register #(.width(1), .trigger("high")) Hi (.D(Hi_IN), .Q(Hi_OUT), .clk(Hi_IN), .clr(or_2_out));  // open: en
  Register #(.width(1), .trigger("high")) EQUAL (
    .D(EQUAL_IN), .Q(EQUAL_OUT), .clk(EQUAL_IN), .clr(or_2_out));  // open: en
  Register #(.width(1), .trigger("high")) Lo (.D(Lo_IN), .Q(Lo_OUT), .clk(Lo_IN));  // open: en, clr
endmodule

module MOV_BATCH (
  input  MOV_B_TO,
  input  MOV_B_FROM,
  input  [7:0] DATA,
  input  [7:0] DATA_1,
  input  [7:0] DATA_2,
  input  [7:0] PC_IN,
  input  CLR,
  input  CLK,
  input  MOV_DATA,
  output [7:0] ADDR,
  output STATUS,
  output [1:0] SEL_1,
  output [1:0] REGS,
  output SEL_REGS,
  output SEL_REGS_2,
  output SEL_TEMP,
  output SEL_TEMP_2,
  output [1:0] TEMP,
  output [1:0] SEL_2,
  output [7:0] PC_1,
  output PC_ENABLE,
  output TTY_ENABLE,
  output PC_2_EN,
  output BIOS,
  output RAM,
  output MEM,
  output RAM_WRITE,
  output MEM_WRITE,
  output ENABLE_MATRIX,
  output RAM_READ,
  output MEM_READ,
  output KYBD_ENABLE
);

  wire _13, and_1_out, and_4_out, and_5_out, and_9_out, and_11_out, and_20_out, and_22_out, and_23_out,
       and_24_out, and_25_out, and_26_out, and_27_out, and_28_out, and_29_out, and_30_out, and_44_out,
       bit_extender_13_out, bit_extender_23_out, comparator_1_eq, comparator_2_eq, comparator_3_eq,
       comparator_4_eq, comparator_5_eq, comparator_6_eq, comparator_7_eq, comparator_8_eq, comparator_9_eq,
       comparator_10_eq, comparator_11_eq, comparator_12_eq, comparator_13_eq, comparator_14_eq,
       comparator_15_eq, comparator_16_eq, comparator_18_eq, comparator_19_eq, comparator_20_eq,
       comparator_21_eq, comparator_22_eq, comparator_23_eq, comparator_24_eq, comparator_25_eq,
       comparator_26_eq, comparator_28_eq, comparator_28_gt, comparator_29_eq, comparator_29_lt,
       comparator_30_eq, comparator_31_eq, comparator_32_eq, comparator_33_eq, comparator_34_eq,
       comparator_35_eq, comparator_36_eq, comparator_37_eq, comparator_38_eq, comparator_39_eq,
       comparator_40_eq, comparator_41_eq, comparator_42_eq, comparator_43_eq, comparator_44_eq,
       comparator_45_eq, comparator_46_eq, comparator_47_eq, comparator_48_eq, comparator_49_eq,
       n1_bit_mem_1_out_4, n1_bit_mem_2_out_4, n1_bit_mem_3_out_4, n1_bit_mem_4_out_4, n1_bit_mem_5_out_4,
       n1_bit_mem_6_out_4, not_1_out, not_2_out, not_3_out, not_5_out, not_6_out, or_1_out_2, or_2_out,
       or_4_out_2, or_6_out_2, or_7_out, or_9_out_2, or_10_out, or_11_out, or_12_out, or_13_out, or_14_out,
       or_15_out, or_16_out, or_17_out, or_18_out, or_19_out, or_20_out, or_21_out, or_22_out, or_24_out,
       or_28_out, or_30_out, or_32_out, or_33_out, or_34_out, or_35_out, or_36_out, or_37_out, or_38_out,
       or_39_out, or_40_out, or_41_out, or_42_out, or_43_out, or_45_out, or_46_out, or_48_out, or_49_out,
       or_50_out, or_51_out, or_52_out, or_53_out, or_54_out, or_55_out, or_56_out, or_57_out, or_59_out,
       or_60_out, or_61_out_2, or_63_out, or_66_out, or_70_out, or_72_out, register_1_q, register_2_q,
       register_3_q, register_4_q, register_5_q, register_6_q, register_7_q, register_8_q, t_ff_1_q,
       t_ff_2_q, t_ff_11_q, transistor_1_out, transistor_2_out, transistor_3_out, transistor_4_out;
  wire [1:0] and_12_out, and_13_out, and_14_out, and_15_out, and_16_out, and_17_out, and_18_out, and_19_out,
       and_36_out, and_37_out, and_38_out, and_39_out, and_40_out, and_41_out, and_42_out, and_43_out,
       bit_extender_5_out, bit_extender_6_out, bit_extender_7_out, bit_extender_8_out, bit_extender_9_out,
       bit_extender_10_out, bit_extender_11_out, bit_extender_12_out, bit_extender_15_out,
       bit_extender_16_out, bit_extender_17_out, bit_extender_18_out, bit_extender_19_out,
       bit_extender_20_out, bit_extender_21_out, bit_extender_22_out, counter_2_q, n2_bit_mem_1_out_4,
       n2_bit_mem_2_out_4, or_23_out, or_25_out, or_26_out, or_27_out, or_29_out, or_31_out, or_44_out,
       or_47_out, or_58_out, or_62_out, or_64_out, or_65_out, or_67_out, or_69_out, or_71_out;
  wire [3:0] counter_1_q, counter_3_q, counter_4_q, counter_5_q;
  wire [7:0] adder_1_out, adder_2_out, and_2_out, and_3_out, and_6_out, and_7_out, and_8_out, and_31_out,
       and_32_out, and_33_out, bit_extender_1_out, bit_extender_2_out, bit_extender_3_out,
       bit_extender_4_out, bit_extender_14_out, or_3_out, ram_1_data, ram_2_data, ram_3_data;

  OR or_1 (.in_1(and_3_out), .out_2(or_1_out_2));
  and and_1 (and_1_out, not_1_out, or_6_out_2);
  not not_1 (not_1_out, register_4_q);
  assign bit_extender_1_out = {{7{MOV_B_FROM}}, MOV_B_FROM};  // Bit_Extender bit_extender_1
  assign bit_extender_2_out = {{7{MOV_DATA}}, MOV_DATA};  // Bit_Extender bit_extender_2
  assign and_2_out = bit_extender_2_out & DATA;  // AND_Gate and_2, 8 bits wide
  assign bit_extender_3_out = {{7{MOV_B_FROM}}, MOV_B_FROM};  // Bit_Extender bit_extender_3
  assign and_3_out = and_6_out & bit_extender_3_out;  // AND_Gate and_3, 8 bits wide
  Register #(.width(1), .trigger("high")) register_1 (
    .D(or_1_out_2), .Q(register_1_q), .clk(or_1_out_2), .clr(CLR));  // open: en
  Adder adder_1 (.a(ram_1_data), .b(8'h1), .out(adder_1_out));  // open: cin, cout
  Comparator comparator_1 (.a(adder_1_out), .b(PC_IN), .eq(comparator_1_eq));  // open: gt, lt
  Comparator comparator_2 (.a(PC_IN), .b({8{1'b0}}), .eq(comparator_2_eq));  // open: gt, lt
  Register #(.width(1), .trigger("high")) register_2 (.D(MOV_DATA), .Q(register_2_q), .clk(MOV_DATA));  // open: en, clr
  Register #(.width(1), .trigger("high")) register_3 (
    .D(or_9_out_2), .Q(register_3_q), .clk(or_9_out_2), .clr(or_19_out));  // open: en
  Counter #(.width(4), .max('hf)) counter_1 (
    .Q(counter_1_q), .clk(transistor_1_out), .clr(or_7_out));  // open: load, D, count, carry
  Transistor #(.\type ("n")) transistor_1 (.in(CLK), .out(transistor_1_out), .gate(and_1_out));
  Counter #(.width(2), .max('h3)) counter_2 (
    .Q(counter_2_q), .clk(transistor_2_out), .clr(or_2_out));  // open: load, D, count, carry
  Transistor #(.\type ("n")) transistor_2 (.in(CLK), .out(transistor_2_out), .gate(and_22_out));
  or or_2 (or_2_out, or_7_out, comparator_5_eq);
  and and_4 (and_4_out, MOV_B_FROM, or_4_out_2);
  and and_5 (and_5_out, or_4_out_2, MOV_B_TO);
  assign and_6_out = DATA & bit_extender_1_out;  // AND_Gate and_6, 8 bits wide
  assign and_7_out = DATA_1 & bit_extender_1_out;  // AND_Gate and_7, 8 bits wide
  assign and_8_out = DATA_2 & bit_extender_1_out;  // AND_Gate and_8, 8 bits wide
  assign or_3_out = and_7_out | DATA_1;  // OR_Gate or_3, 8 bits wide
  OR or_4 (.in_1(and_8_out), .out_2(or_4_out_2));
  RAM #(.addrWidth(2), .bus("separate")) ram_1 (
    .addr(2'b00), .din(and_3_out), .data(ram_1_data), .str(or_1_out_2), .clk(register_1_q), .clr(CLR));  // open: sel, ld
  and and_9 (and_9_out, comparator_1_eq, not_2_out);
  not not_2 (not_2_out, comparator_2_eq);
  OR or_5 (.in_1(ram_2_data), .out_2(PC_2_EN));
  RAM #(.addrWidth(2), .bus("separate")) ram_2 (
    .addr(2'b00), .din(PC_1), .data(ram_2_data), .str(or_9_out_2), .clk(register_3_q), .clr(or_19_out));  // open: sel, ld
  OR or_6 (.in_1(ram_2_data), .out_2(or_6_out_2));
  Comparator #(.width(4)) comparator_3 (.a(counter_1_q), .b(4'b0010), .eq(comparator_3_eq));  // open: gt, lt
  Register #(.width(1), .trigger("high")) register_4 (
    .D(comparator_3_eq), .Q(register_4_q), .clk(comparator_3_eq), .clr(or_7_out));  // open: en
  Comparator #(.width(2)) comparator_4 (.a(counter_2_q), .b(2'b10), .eq(comparator_4_eq));  // open: gt, lt
  Comparator #(.width(2)) comparator_5 (.a(counter_2_q), .b(2'b11), .eq(comparator_5_eq));  // open: gt, lt
  or or_7 (or_7_out, CLR, and_22_out);
  assign bit_extender_4_out = {{7{MOV_DATA}}, MOV_DATA};  // Bit_Extender bit_extender_4
  assign ADDR = and_31_out | and_2_out | and_6_out;  // OR_Gate or_8, 8 bits wide
  Comparator comparator_6 (.a(and_7_out), .b(8'h53), .eq(comparator_6_eq));  // open: gt, lt
  Comparator comparator_7 (.a(and_7_out), .b(8'h54), .eq(comparator_7_eq));  // open: gt, lt
  Comparator comparator_8 (.a(and_7_out), .b(8'h57), .eq(comparator_8_eq));  // open: gt, lt
  Comparator comparator_9 (.a(and_8_out), .b(8'ha), .eq(comparator_9_eq));  // open: gt, lt
  Comparator comparator_10 (.a(and_8_out), .b(8'hb), .eq(comparator_10_eq));  // open: gt, lt
  Comparator comparator_11 (.a(and_8_out), .b(8'hc), .eq(comparator_11_eq));  // open: gt, lt
  Comparator comparator_12 (.a(and_8_out), .b(8'hd), .eq(comparator_12_eq));  // open: gt, lt
  Comparator comparator_13 (.a(and_8_out), .b(8'he), .eq(comparator_13_eq));  // open: gt, lt
  Comparator comparator_14 (.a(and_8_out), .b(8'hf), .eq(comparator_14_eq));  // open: gt, lt
  Comparator comparator_15 (.a(and_8_out), .b(8'h11), .eq(comparator_15_eq));  // open: gt, lt
  Comparator comparator_16 (.a(and_8_out), .b(8'h12), .eq(comparator_16_eq));  // open: gt, lt
  Comparator comparator_17 (.a(and_8_out), .b(8'h15), .eq(PC_ENABLE));  // open: gt, lt
  assign PC_1 = DATA_2 & bit_extender_4_out;  // AND_Gate and_10, 8 bits wide
  OR or_9 (.in_1(PC_1), .out_2(or_9_out_2));
  or or_10 (or_10_out, or_43_out, and_11_out);
  and and_11 (and_11_out, register_2_q, comparator_3_eq);
  Comparator comparator_18 (.a(or_3_out), .b(8'h70), .eq(comparator_18_eq));  // open: gt, lt
  or or_11 (or_11_out, comparator_18_eq, comparator_19_eq, comparator_22_eq);
  Comparator comparator_19 (.a(or_3_out), .b(8'h79), .eq(comparator_19_eq));  // open: gt, lt
  Comparator comparator_20 (.a(or_3_out), .b(8'h72), .eq(comparator_20_eq));  // open: gt, lt
  Comparator comparator_21 (.a(or_3_out), .b(8'h71), .eq(comparator_21_eq));  // open: gt, lt
  Comparator comparator_22 (.a(or_3_out), .b(8'h78), .eq(comparator_22_eq));  // open: gt, lt
  Comparator comparator_23 (.a(or_3_out), .b(8'h76), .eq(comparator_23_eq));  // open: gt, lt
  Comparator comparator_24 (.a(or_3_out), .b(8'h77), .eq(comparator_24_eq));  // open: gt, lt
  Comparator comparator_25 (.a(or_3_out), .b(8'ha3), .eq(comparator_25_eq));  // open: gt, lt
  Comparator comparator_26 (.a(or_3_out), .b(8'ha4), .eq(comparator_26_eq));  // open: gt, lt
  Comparator comparator_27 (.a(or_3_out), .b(8'ha5), .eq(_13));  // open: gt, lt
  _1_BIT_MEM u_1_bit_mem_1 (.in_1(comparator_6_eq), .EN(comparator_28_eq), .CLR(CLR), .out_4(n1_bit_mem_1_out_4));
  _1_BIT_MEM u_1_bit_mem_2 (.in_1(comparator_7_eq), .EN(comparator_28_eq), .CLR(CLR), .out_4(n1_bit_mem_2_out_4));
  or or_12 (or_12_out, n1_bit_mem_2_out_4, n1_bit_mem_5_out_4);
  _1_BIT_MEM u_1_bit_mem_3 (.in_1(comparator_8_eq), .EN(comparator_28_eq), .CLR(CLR), .out_4(n1_bit_mem_3_out_4));
  assign and_12_out = 2'b00 & bit_extender_5_out;  // AND_Gate and_12, 2 bits wide
  assign bit_extender_5_out = {{1{comparator_9_eq}}, comparator_9_eq};  // Bit_Extender bit_extender_5
  or or_13 (or_13_out, comparator_9_eq, comparator_10_eq);
  assign and_13_out = 2'b01 & bit_extender_6_out;  // AND_Gate and_13, 2 bits wide
  assign bit_extender_6_out = {{1{comparator_10_eq}}, comparator_10_eq};  // Bit_Extender bit_extender_6
  assign and_14_out = 2'b10 & bit_extender_7_out;  // AND_Gate and_14, 2 bits wide
  assign bit_extender_7_out = {{1{comparator_11_eq}}, comparator_11_eq};  // Bit_Extender bit_extender_7
  or or_14 (or_14_out, comparator_11_eq, comparator_12_eq);
  assign and_15_out = 2'b11 & bit_extender_8_out;  // AND_Gate and_15, 2 bits wide
  assign bit_extender_8_out = {{1{comparator_12_eq}}, comparator_12_eq};  // Bit_Extender bit_extender_8
  assign and_16_out = 2'b00 & bit_extender_9_out;  // AND_Gate and_16, 2 bits wide
  assign bit_extender_9_out = {{1{comparator_13_eq}}, comparator_13_eq};  // Bit_Extender bit_extender_9
  or or_15 (or_15_out, comparator_13_eq, comparator_14_eq);
  assign and_17_out = 2'b01 & bit_extender_10_out;  // AND_Gate and_17, 2 bits wide
  assign bit_extender_10_out = {{1{comparator_14_eq}}, comparator_14_eq};  // Bit_Extender bit_extender_10
  assign and_18_out = 2'b10 & bit_extender_11_out;  // AND_Gate and_18, 2 bits wide
  assign bit_extender_11_out = {{1{comparator_15_eq}}, comparator_15_eq};  // Bit_Extender bit_extender_11
  or or_16 (or_16_out, comparator_15_eq, comparator_16_eq);
  assign and_19_out = 2'b11 & bit_extender_12_out;  // AND_Gate and_19, 2 bits wide
  assign bit_extender_12_out = {{1{comparator_16_eq}}, comparator_16_eq};  // Bit_Extender bit_extender_12
  Bit_Extender #(.in_width(2), .out_width(1), .\type ("sign")) bit_extender_13 (
    .in(or_31_out), .out(bit_extender_13_out));
  Counter #(.width(4), .max('hf)) counter_3 (
    .Q(counter_3_q), .clk(and_20_out), .clr(or_18_out));  // open: load, D, count, carry
  or or_17 (or_17_out, bit_extender_13_out, or_30_out);
  and and_20 (and_20_out, or_17_out, not_5_out, CLK);
  or or_18 (or_18_out, or_7_out, comparator_29_eq);
  or or_19 (or_19_out, or_7_out, comparator_4_eq);
  or or_20 (or_20_out, comparator_20_eq, comparator_26_eq, comparator_25_eq);
  assign bit_extender_14_out = {{7{MOV_B_TO}}, MOV_B_TO};  // Bit_Extender bit_extender_14
  or or_21 (or_21_out, n1_bit_mem_4_out_4, n1_bit_mem_1_out_4);
  or or_22 (or_22_out, n1_bit_mem_3_out_4, n1_bit_mem_6_out_4);
  assign or_23_out = and_12_out | and_13_out;  // OR_Gate or_23, 2 bits wide
  or or_24 (or_24_out, or_13_out, or_14_out);
  assign or_25_out = and_14_out | and_15_out;  // OR_Gate or_25, 2 bits wide
  assign or_26_out = and_16_out | and_17_out;  // OR_Gate or_26, 2 bits wide
  assign or_27_out = or_26_out | or_29_out;  // OR_Gate or_27, 2 bits wide
  or or_28 (or_28_out, or_15_out, or_16_out);
  assign or_29_out = and_18_out | and_19_out;  // OR_Gate or_29, 2 bits wide
  or or_30 (or_30_out, or_28_out, or_24_out);
  assign or_31_out = or_27_out | or_47_out;  // OR_Gate or_31, 2 bits wide
  // AND_Gate and_21 has open pins: in0=comparator_28_gt, in1=comparator_29_lt, out=open
  Comparator #(.width(4)) comparator_28 (
    .a(counter_3_q), .b(4'b0101), .gt(comparator_28_gt), .eq(comparator_28_eq));  // open: lt
  Comparator #(.width(4)) comparator_29 (
    .a(counter_3_q), .b(4'b0111), .eq(comparator_29_eq), .lt(comparator_29_lt));  // open: gt
  Comparator comparator_30 (.a(PC_IN), .b(ram_2_data), .eq(comparator_30_eq));  // open: gt, lt
  and and_22 (and_22_out, comparator_30_eq, not_3_out);
  not not_3 (not_3_out, comparator_31_eq);
  Comparator comparator_31 (.a(PC_IN), .b({8{1'b0}}), .eq(comparator_31_eq));  // open: gt, lt
  Counter #(.width(4), .max('hf)) counter_4 (
    .Q(counter_4_q), .clk(transistor_3_out), .clr(or_48_out));  // open: load, D, count, carry
  Transistor #(.\type ("n")) transistor_3 (.in(CLK), .out(transistor_3_out), .gate(t_ff_1_q));
  T_Flip_Flop t_ff_1 (.clk(or_49_out), .T(or_49_out), .Q(t_ff_1_q), .reset(or_48_out));  // open: Qn, preset, en
  or or_32 (or_32_out, _13, comparator_24_eq);
  and and_23 (and_23_out, or_33_out, or_10_out);
  or or_33 (or_33_out, or_21_out, or_32_out, comparator_21_eq);
  and and_24 (and_24_out, or_34_out, or_10_out);
  or or_34 (or_34_out, or_12_out, comparator_20_eq, or_11_out);
  and and_25 (and_25_out, or_35_out, or_10_out);
  or or_35 (or_35_out, or_22_out, or_20_out, comparator_19_eq);
  or or_36 (or_36_out, comparator_19_eq, comparator_23_eq, n1_bit_mem_5_out_4);
  and and_26 (and_26_out, or_36_out, or_10_out);
  or or_37 (or_37_out, comparator_20_eq, n1_bit_mem_6_out_4);
  and and_27 (and_27_out, or_37_out, or_10_out);
  or or_38 (or_38_out, comparator_18_eq, _13, comparator_26_eq);
  and and_28 (and_28_out, or_38_out, or_10_out);
  or or_39 (or_39_out, comparator_22_eq, comparator_20_eq);
  and and_29 (and_29_out, or_39_out, or_10_out);
  or or_40 (or_40_out, comparator_19_eq, comparator_21_eq);
  and and_30 (and_30_out, or_10_out, or_41_out);
  or or_41 (or_41_out, comparator_22_eq, comparator_25_eq, comparator_24_eq);
  assign and_31_out = DATA & bit_extender_14_out;  // AND_Gate and_31, 8 bits wide
  assign and_32_out = DATA_1 & bit_extender_14_out;  // AND_Gate and_32, 8 bits wide
  assign and_33_out = DATA_2 & bit_extender_14_out;  // AND_Gate and_33, 8 bits wide
  T_Flip_Flop t_ff_2 (.clk(or_42_out), .T(or_42_out), .Q(t_ff_2_q), .reset(or_50_out));  // open: Qn, preset, en
  or or_42 (or_42_out, comparator_3_eq, and_5_out, and_4_out, or_49_out);
  or or_43 (or_43_out, or_21_out, or_12_out, or_22_out);
  _2_BIT_MEM u_2_bit_mem_1 (
    .in_1(or_44_out), .CLR(or_46_out), .EN(comparator_28_eq), .out_4(n2_bit_mem_1_out_4), .out_5(SEL_1));
  assign or_44_out = or_23_out | or_25_out;  // OR_Gate or_44, 2 bits wide
  Register #(.width(1), .trigger("high")) register_5 (
    .D(or_24_out), .Q(register_5_q), .clk(or_24_out), .clr(or_46_out));  // open: en
  or or_45 (or_45_out, or_24_out, or_28_out);
  Register #(.width(1), .trigger("high")) register_6 (
    .D(or_28_out), .Q(register_6_q), .clk(or_28_out), .clr(or_46_out));  // open: en
  _2_BIT_MEM u_2_bit_mem_2 (
    .in_1(or_27_out), .CLR(or_46_out), .EN(comparator_28_eq), .out_4(n2_bit_mem_2_out_4), .out_5(SEL_2));
  or or_46 (or_46_out, and_9_out, or_7_out);
  assign or_47_out = or_44_out | n2_bit_mem_1_out_4 | n2_bit_mem_2_out_4;  // OR_Gate or_47, 2 bits wide
  Comparator #(.width(4)) comparator_32 (.a(counter_4_q), .b(4'b1010), .eq(comparator_32_eq));  // open: gt, lt
  Comparator #(.width(4)) comparator_33 (.a(counter_4_q), .b(4'b1011), .eq(comparator_33_eq));  // open: gt, lt
  or or_48 (or_48_out, or_7_out, comparator_33_eq);
  T_Flip_Flop t_ff_3 (
    .clk(and_23_out), .T(and_23_out), .Q(BIOS), .reset(or_51_out), .en(or_10_out));  // open: Qn, preset
  T_Flip_Flop t_ff_4 (
    .clk(and_24_out), .T(and_24_out), .Q(RAM), .reset(or_51_out), .en(or_10_out));  // open: Qn, preset
  T_Flip_Flop t_ff_5 (
    .clk(and_25_out), .T(and_25_out), .Q(MEM), .reset(or_51_out), .en(or_10_out));  // open: Qn, preset
  T_Flip_Flop t_ff_6 (
    .clk(and_26_out), .T(and_26_out), .Q(RAM_WRITE), .reset(or_51_out), .en(or_10_out));  // open: Qn, preset
  T_Flip_Flop t_ff_7 (
    .clk(and_27_out), .T(and_27_out), .Q(MEM_WRITE), .reset(or_51_out), .en(or_10_out));  // open: Qn, preset
  T_Flip_Flop t_ff_8 (
    .clk(and_28_out), .T(and_28_out), .Q(ENABLE_MATRIX), .reset(or_51_out), .en(or_10_out));  // open: Qn, preset
  T_Flip_Flop t_ff_9 (
    .clk(and_29_out), .T(and_29_out), .Q(RAM_READ), .reset(or_51_out), .en(or_10_out));  // open: Qn, preset
  T_Flip_Flop t_ff_10 (
    .clk(or_40_out), .T(or_40_out), .Q(MEM_READ), .reset(or_51_out), .en(or_10_out));  // open: Qn, preset
  T_Flip_Flop t_ff_11 (
    .clk(and_30_out), .T(and_30_out), .Q(t_ff_11_q), .reset(or_51_out), .en(or_10_out));  // open: Qn, preset
  T_Flip_Flop t_ff_12 (
    .clk(comparator_23_eq), .T(comparator_23_eq), .Q(KYBD_ENABLE), .reset(or_51_out), .en(or_10_out));  // open: Qn, preset
  not not_4 (STATUS, t_ff_2_q);
  or or_49 (or_49_out, or_45_out, or_70_out);
  or or_50 (or_50_out, and_22_out, comparator_32_eq, or_52_out);
  or or_51 (or_51_out, or_7_out, and_9_out, and_22_out);
  Comparator comparator_34 (.a(and_32_out), .b(8'h16), .eq(comparator_34_eq));  // open: gt, lt
  Comparator comparator_35 (.a(and_32_out), .b(8'h17), .eq(comparator_35_eq));  // open: gt, lt
  Comparator comparator_36 (.a(and_32_out), .b(8'h18), .eq(comparator_36_eq));  // open: gt, lt
  Comparator comparator_37 (.a(and_33_out), .b(8'ha), .eq(comparator_37_eq));  // open: gt, lt
  Comparator comparator_38 (.a(and_33_out), .b(8'hb), .eq(comparator_38_eq));  // open: gt, lt
  and and_34 (SEL_REGS, comparator_28_eq, register_5_q);
  Comparator comparator_39 (.a(and_33_out), .b(8'hc), .eq(comparator_39_eq));  // open: gt, lt
  Comparator comparator_40 (.a(and_33_out), .b(8'hd), .eq(comparator_40_eq));  // open: gt, lt
  Comparator comparator_41 (.a(and_33_out), .b(8'he), .eq(comparator_41_eq));  // open: gt, lt
  Comparator comparator_42 (.a(and_33_out), .b(8'hf), .eq(comparator_42_eq));  // open: gt, lt
  and and_35 (SEL_TEMP_2, register_6_q, comparator_28_eq);
  Comparator comparator_43 (.a(and_33_out), .b(8'h11), .eq(comparator_43_eq));  // open: gt, lt
  Comparator comparator_44 (.a(and_33_out), .b(8'h12), .eq(comparator_44_eq));  // open: gt, lt
  Register #(.width(1), .trigger("high")) register_7 (
    .D(comparator_29_eq), .Q(register_7_q), .clk(comparator_29_eq), .clr(or_7_out));  // open: en
  Comparator comparator_45 (.a(and_33_out), .b(8'h14), .eq(comparator_45_eq));  // open: gt, lt
  or or_52 (or_52_out, or_7_out, comparator_47_eq);
  _1_BIT_MEM u_1_bit_mem_4 (
    .in_1(comparator_34_eq), .EN(comparator_46_eq), .CLR(or_72_out), .out_4(n1_bit_mem_4_out_4));
  _1_BIT_MEM u_1_bit_mem_5 (
    .in_1(comparator_35_eq), .EN(comparator_46_eq), .CLR(or_72_out), .out_4(n1_bit_mem_5_out_4));
  _1_BIT_MEM u_1_bit_mem_6 (
    .in_1(comparator_36_eq), .EN(comparator_46_eq), .CLR(or_72_out), .out_4(n1_bit_mem_6_out_4));
  assign and_36_out = 2'b00 & bit_extender_15_out;  // AND_Gate and_36, 2 bits wide
  assign bit_extender_15_out = {{1{comparator_37_eq}}, comparator_37_eq};  // Bit_Extender bit_extender_15
  or or_53 (or_53_out, comparator_37_eq, comparator_38_eq);
  assign and_37_out = 2'b01 & bit_extender_16_out;  // AND_Gate and_37, 2 bits wide
  assign bit_extender_16_out = {{1{comparator_38_eq}}, comparator_38_eq};  // Bit_Extender bit_extender_16
  assign and_38_out = 2'b10 & bit_extender_17_out;  // AND_Gate and_38, 2 bits wide
  assign bit_extender_17_out = {{1{comparator_39_eq}}, comparator_39_eq};  // Bit_Extender bit_extender_17
  or or_54 (or_54_out, comparator_39_eq, comparator_40_eq);
  assign and_39_out = 2'b11 & bit_extender_18_out;  // AND_Gate and_39, 2 bits wide
  assign bit_extender_18_out = {{1{comparator_40_eq}}, comparator_40_eq};  // Bit_Extender bit_extender_18
  assign and_40_out = 2'b00 & bit_extender_19_out;  // AND_Gate and_40, 2 bits wide
  assign bit_extender_19_out = {{1{comparator_41_eq}}, comparator_41_eq};  // Bit_Extender bit_extender_19
  or or_55 (or_55_out, comparator_41_eq, comparator_42_eq);
  assign and_41_out = 2'b01 & bit_extender_20_out;  // AND_Gate and_41, 2 bits wide
  assign bit_extender_20_out = {{1{comparator_42_eq}}, comparator_42_eq};  // Bit_Extender bit_extender_20
  assign and_42_out = 2'b10 & bit_extender_21_out;  // AND_Gate and_42, 2 bits wide
  assign bit_extender_21_out = {{1{comparator_43_eq}}, comparator_43_eq};  // Bit_Extender bit_extender_21
  or or_56 (or_56_out, comparator_43_eq, comparator_44_eq);
  assign and_43_out = 2'b11 & bit_extender_22_out;  // AND_Gate and_43, 2 bits wide
  assign bit_extender_22_out = {{1{comparator_44_eq}}, comparator_44_eq};  // Bit_Extender bit_extender_22
  or or_57 (or_57_out, or_63_out, or_66_out);
  assign or_58_out = or_69_out | or_71_out;  // OR_Gate or_58, 2 bits wide
  not not_5 (not_5_out, register_7_q);
  Counter #(.width(4), .max('hf)) counter_5 (
    .Q(counter_5_q), .clk(transistor_4_out), .clr(or_60_out));  // open: load, D, count, carry
  or or_59 (or_59_out, or_57_out, bit_extender_23_out);
  Transistor #(.\type ("n")) transistor_4 (.in(CLK), .out(transistor_4_out), .gate(or_59_out));
  or or_60 (or_60_out, or_7_out, comparator_47_eq);
  OR or_61 (.in_1(and_31_out), .out_2(or_61_out_2));
  Register #(.width(1), .trigger("high")) register_8 (
    .D(or_61_out_2), .Q(register_8_q), .clk(or_61_out_2), .clr(or_7_out));  // open: en
  assign or_62_out = and_36_out | and_37_out;  // OR_Gate or_62, 2 bits wide
  or or_63 (or_63_out, or_53_out, or_54_out);
  assign or_64_out = and_38_out | and_39_out;  // OR_Gate or_64, 2 bits wide
  assign or_65_out = and_40_out | and_41_out;  // OR_Gate or_65, 2 bits wide
  or or_66 (or_66_out, or_55_out, or_56_out);
  assign or_67_out = and_42_out | and_43_out;  // OR_Gate or_67, 2 bits wide
  Bit_Extender #(.in_width(2), .out_width(1), .\type ("sign")) bit_extender_23 (
    .in(or_58_out), .out(bit_extender_23_out));
  or or_68 (TTY_ENABLE, comparator_45_eq, t_ff_11_q);
  Comparator #(.width(4)) comparator_46 (.a(counter_5_q), .b(4'b1001), .eq(comparator_46_eq));  // open: gt, lt
  Comparator #(.width(4)) comparator_47 (.a(counter_5_q), .b(4'b1010), .eq(comparator_47_eq));  // open: gt, lt
  RAM #(.addrWidth(2), .bus("separate")) ram_3 (
    .addr(2'b00), .din(and_31_out), .data(ram_3_data), .str(or_61_out_2), .clk(register_8_q), .clr(or_7_out));  // open: sel, ld
  Adder adder_2 (.a(ram_3_data), .b(8'h1), .out(adder_2_out));  // open: cin, cout
  Comparator comparator_48 (.a(adder_2_out), .b(PC_IN), .eq(comparator_48_eq));  // open: gt, lt
  not not_6 (not_6_out, comparator_49_eq);
  Comparator comparator_49 (.a(PC_IN), .b({8{1'b0}}), .eq(comparator_49_eq));  // open: gt, lt
  assign or_69_out = or_62_out | or_64_out;  // OR_Gate or_69, 2 bits wide
  _2_BIT_MEM u_2_bit_mem_3 (.in_1(or_69_out), .CLR(or_72_out), .EN(comparator_46_eq), .out_5(REGS));  // open: out_4
  or or_70 (or_70_out, or_63_out, or_66_out);
  assign or_71_out = or_65_out | or_67_out;  // OR_Gate or_71, 2 bits wide
  _2_BIT_MEM u_2_bit_mem_4 (.in_1(or_71_out), .CLR(or_72_out), .EN(comparator_46_eq), .out_5(TEMP));  // open: out_4
  or or_72 (or_72_out, or_7_out, and_44_out);
  and and_44 (and_44_out, comparator_48_eq, not_6_out);
  _1_BIT_MEM u_1_bit_mem_7 (.in_1(or_63_out), .EN(comparator_46_eq), .CLR(or_72_out), .out_4(SEL_REGS_2));
  _1_BIT_MEM u_1_bit_mem_8 (.in_1(or_66_out), .EN(comparator_46_eq), .CLR(or_72_out), .out_4(SEL_TEMP));
endmodule

module CALL_RET (
  input  RET,
  input  CALL,
  input  [7:0] DATA,
  input  [7:0] DATA_1,
  input  [7:0] DATA_2,
  input  [7:0] PC_IN,
  input  CLK,
  input  CLR,
  output [7:0] ADDR,
  output BIOS,
  output RAM,
  output MEM
);

  wire and_1_out, and_2_out, comparator_1_eq, comparator_2_eq, comparator_3_eq, comparator_4_eq,
       comparator_5_eq, comparator_6_eq, comparator_7_eq, comparator_8_eq, not_1_out, or_1_out_2, or_2_out,
       or_3_out, or_4_out, or_5_out, or_6_out, or_7_out, or_8_out, register_1_q, t_ff_1_q, t_ff_2_q,
       t_ff_3_q, transistor_1_out, transistor_2_out;
  wire [3:0] counter_1_q, counter_2_q;
  wire [7:0] adder_1_out, and_3_out, and_7_out, and_8_out, bit_extender_1_out, bit_extender_2_out,
       bit_extender_3_out, ram_1_data;

  Comparator comparator_1 (.a(DATA), .b(8'h9), .eq(comparator_1_eq));  // open: gt, lt
  Transistor #(.\type ("n")) transistor_1 (.in(CLK), .out(transistor_1_out), .gate(or_3_out));
  OR or_1 (.in_1(PC_IN), .out_2(or_1_out_2));
  Counter #(.width(4), .max('hf)) counter_1 (
    .Q(counter_1_q), .clk(transistor_1_out), .clr(comparator_6_eq));  // open: load, D, count, carry
  Comparator comparator_2 (.a(DATA_1), .b(8'h53), .eq(comparator_2_eq));  // open: gt, lt
  Comparator comparator_3 (.a(DATA_1), .b(8'h54), .eq(comparator_3_eq));  // open: gt, lt
  Comparator comparator_4 (.a(DATA_1), .b(8'h57), .eq(comparator_4_eq));  // open: gt, lt
  and and_1 (and_1_out, CALL, comparator_1_eq);
  and and_2 (and_2_out, CALL, or_1_out_2);
  Comparator #(.width(4)) comparator_5 (.a(counter_1_q), .b(4'b1011), .eq(comparator_5_eq));  // open: gt, lt
  T_Flip_Flop t_ff_1 (
    .clk(comparator_2_eq), .T(comparator_2_eq), .Q(t_ff_1_q), .reset(or_6_out));  // open: Qn, preset, en
  T_Flip_Flop t_ff_2 (
    .clk(comparator_3_eq), .T(comparator_3_eq), .Q(t_ff_2_q), .reset(or_5_out));  // open: Qn, preset, en
  T_Flip_Flop t_ff_3 (
    .clk(comparator_4_eq), .T(comparator_4_eq), .Q(t_ff_3_q), .reset(or_4_out));  // open: Qn, preset, en
  Comparator #(.width(4)) comparator_6 (.a(counter_1_q), .b(4'b1100), .eq(comparator_6_eq));  // open: gt, lt
  assign bit_extender_1_out = {{7{and_1_out}}, and_1_out};  // Bit_Extender bit_extender_1
  assign and_3_out = bit_extender_1_out & DATA_2;  // AND_Gate and_3, 8 bits wide
  Adder adder_1 (.a(PC_IN), .b(8'h2), .out(adder_1_out));  // open: cin, cout
  Transistor #(.\type ("n")) transistor_2 (.in(CLK), .out(transistor_2_out), .gate(RET));
  or or_2 (or_2_out, CLR, and_1_out, comparator_8_eq);
  or or_3 (or_3_out, BIOS, RAM, MEM);
  and and_4 (BIOS, t_ff_1_q, comparator_5_eq);
  and and_5 (RAM, t_ff_2_q, comparator_5_eq);
  and and_6 (MEM, t_ff_3_q, comparator_5_eq);
  or or_4 (or_4_out, RET, CLR);
  or or_5 (or_5_out, RET, CLR);
  or or_6 (or_6_out, RET, CLR);
  Counter #(.width(4), .max('hf)) counter_2 (
    .Q(counter_2_q), .clk(transistor_2_out), .clr(or_2_out));  // open: load, D, count, carry
  not not_1 (not_1_out, and_1_out);
  assign bit_extender_2_out = {{7{and_1_out}}, and_1_out};  // Bit_Extender bit_extender_2
  assign and_7_out = bit_extender_2_out & adder_1_out;  // AND_Gate and_7, 8 bits wide
  RAM #(.addrWidth(2), .bus("separate")) ram_1 (
    .addr(2'b00), .din(and_7_out), .data(ram_1_data), .str(and_2_out), .clk(register_1_q), .ld(RET),
    .clr(or_7_out));  // open: sel
  assign bit_extender_3_out = {{7{RET}}, RET};  // Bit_Extender bit_extender_3
  or or_7 (or_7_out, comparator_7_eq, CLR);
  Comparator #(.width(4)) comparator_7 (.a(counter_2_q), .b(4'b1010), .eq(comparator_7_eq));  // open: gt, lt
  Comparator #(.width(4)) comparator_8 (.a(counter_2_q), .b(4'b1011), .eq(comparator_8_eq));  // open: gt, lt
  Register #(.width(1), .trigger("high")) register_1 (
    .D(and_2_out), .Q(register_1_q), .clk(and_2_out), .clr(or_8_out));  // open: en
  or or_8 (or_8_out, not_1_out, CLR);
  assign and_8_out = ram_1_data & bit_extender_3_out;  // AND_Gate and_8, 8 bits wide
  assign ADDR = and_3_out | and_8_out;  // OR_Gate or_9, 8 bits wide
endmodule

module JUMP (
  input  CARRY_FLAG,
  input  ZERO_FLAG,
  input  SEL,
  input  [7:0] DATA,
  input  [7:0] DATA_1,
  input  [7:0] DATA_2,
  input  Hi,
  input  EQUAL,
  input  Lo,
  output [7:0] ADDR
);

  wire comparator_1_eq, comparator_2_eq, comparator_3_eq, comparator_4_eq, comparator_5_eq, comparator_6_eq,
       comparator_7_eq, comparator_8_eq, comparator_9_eq, comparator_10_eq, comparator_11_eq;
  wire [7:0] and_1_out, and_2_out, and_3_out, and_4_out, and_5_out, and_6_out, and_7_out, and_8_out,
       and_9_out, and_10_out, and_11_out, and_12_out, and_13_out, and_14_out, and_15_out, and_16_out,
       and_17_out, and_18_out, and_19_out, and_20_out, and_21_out, and_22_out, and_23_out, and_24_out,
       and_25_out, and_26_out, and_27_out, and_28_out, and_29_out, and_30_out, and_31_out, and_32_out,
       and_33_out, and_34_out, and_35_out, and_36_out, and_37_out, and_38_out, and_39_out, and_40_out,
       bit_extender_1_out, bit_extender_2_out, bit_extender_3_out, bit_extender_4_out, bit_extender_5_out,
       bit_extender_6_out, bit_extender_7_out, bit_extender_8_out, bit_extender_9_out, bit_extender_10_out,
       bit_extender_11_out, bit_extender_12_out, bit_extender_13_out, bit_extender_14_out,
       bit_extender_15_out, bit_extender_16_out, bit_extender_17_out, not_1_out, not_2_out, not_3_out,
       not_4_out, not_5_out, or_1_out, or_2_out, undriven, undriven_2;

  assign bit_extender_1_out = {{7{Hi}}, Hi};  // Bit_Extender bit_extender_1
  assign bit_extender_2_out = {{7{EQUAL}}, EQUAL};  // Bit_Extender bit_extender_2
  assign bit_extender_3_out = {{7{Lo}}, Lo};  // Bit_Extender bit_extender_3
  assign bit_extender_4_out = {{7{CARRY_FLAG}}, CARRY_FLAG};  // Bit_Extender bit_extender_4
  assign bit_extender_5_out = {{7{ZERO_FLAG}}, ZERO_FLAG};  // Bit_Extender bit_extender_5
  assign bit_extender_6_out = {{7{SEL}}, SEL};  // Bit_Extender bit_extender_6
  Comparator comparator_1 (.a(DATA), .b(8'h20), .eq(comparator_1_eq));  // open: gt, lt
  assign bit_extender_7_out = {{7{comparator_1_eq}}, comparator_1_eq};  // Bit_Extender bit_extender_7
  assign bit_extender_8_out = {{7{comparator_2_eq}}, comparator_2_eq};  // Bit_Extender bit_extender_8
  Comparator comparator_2 (.a(DATA_2), .b(8'h31), .eq(comparator_2_eq));  // open: gt, lt
  Comparator comparator_3 (.a(DATA_2), .b(8'h35), .eq(comparator_3_eq));  // open: gt, lt
  assign bit_extender_9_out = {{7{comparator_3_eq}}, comparator_3_eq};  // Bit_Extender bit_extender_9
  Comparator comparator_4 (.a(DATA_2), .b(8'h21), .eq(comparator_4_eq));  // open: gt, lt
  assign bit_extender_10_out = {{7{comparator_4_eq}}, comparator_4_eq};  // Bit_Extender bit_extender_10
  assign bit_extender_11_out = {{7{comparator_5_eq}}, comparator_5_eq};  // Bit_Extender bit_extender_11
  Comparator comparator_5 (.a(DATA_2), .b(8'h22), .eq(comparator_5_eq));  // open: gt, lt
  Comparator comparator_6 (.a(DATA_2), .b(8'hd1), .eq(comparator_6_eq));  // open: gt, lt
  assign bit_extender_12_out = {{7{comparator_6_eq}}, comparator_6_eq};  // Bit_Extender bit_extender_12
  Comparator comparator_7 (.a(DATA_2), .b(8'hd5), .eq(comparator_7_eq));  // open: gt, lt
  assign bit_extender_13_out = {{7{comparator_7_eq}}, comparator_7_eq};  // Bit_Extender bit_extender_13
  assign bit_extender_14_out = {{7{comparator_8_eq}}, comparator_8_eq};  // Bit_Extender bit_extender_14
  Comparator comparator_8 (.a(DATA_2), .b(8'hd2), .eq(comparator_8_eq));  // open: gt, lt
  Comparator comparator_9 (.a(DATA_2), .b(8'hc1), .eq(comparator_9_eq));  // open: gt, lt
  assign bit_extender_15_out = {{7{comparator_9_eq}}, comparator_9_eq};  // Bit_Extender bit_extender_15
  Comparator comparator_10 (.a(DATA_2), .b(8'hc5), .eq(comparator_10_eq));  // open: gt, lt
  assign bit_extender_16_out = {{7{comparator_10_eq}}, comparator_10_eq};  // Bit_Extender bit_extender_16
  assign bit_extender_17_out = {{7{comparator_11_eq}}, comparator_11_eq};  // Bit_Extender bit_extender_17
  Comparator comparator_11 (.a(DATA_2), .b(8'hc2), .eq(comparator_11_eq));  // open: gt, lt
  assign and_1_out = bit_extender_6_out & DATA_1;  // AND_Gate and_1, 8 bits wide
  assign and_2_out = bit_extender_6_out & DATA_1;  // AND_Gate and_2, 8 bits wide
  assign and_3_out = bit_extender_6_out & DATA_1;  // AND_Gate and_3, 8 bits wide
  assign and_4_out = bit_extender_7_out & and_5_out;  // AND_Gate and_4, 8 bits wide
  assign and_5_out = bit_extender_6_out & DATA_1;  // AND_Gate and_5, 8 bits wide
  assign and_6_out = bit_extender_6_out & DATA_1;  // AND_Gate and_6, 8 bits wide
  assign and_7_out = bit_extender_7_out & and_6_out;  // AND_Gate and_7, 8 bits wide
  assign and_8_out = bit_extender_7_out & and_9_out;  // AND_Gate and_8, 8 bits wide
  assign and_9_out = bit_extender_6_out & DATA_1;  // AND_Gate and_9, 8 bits wide
  assign and_10_out = bit_extender_7_out & and_11_out;  // AND_Gate and_10, 8 bits wide
  assign and_11_out = bit_extender_6_out & DATA_1;  // AND_Gate and_11, 8 bits wide
  assign and_12_out = bit_extender_6_out & DATA_1;  // AND_Gate and_12, 8 bits wide
  assign and_13_out = bit_extender_7_out & and_12_out;  // AND_Gate and_13, 8 bits wide
  assign and_14_out = bit_extender_6_out & DATA_1;  // AND_Gate and_14, 8 bits wide
  assign and_15_out = bit_extender_7_out & and_14_out;  // AND_Gate and_15, 8 bits wide
  assign and_16_out = bit_extender_6_out & DATA_1;  // AND_Gate and_16, 8 bits wide
  assign and_17_out = bit_extender_7_out & and_16_out;  // AND_Gate and_17, 8 bits wide
  assign and_18_out = undriven & and_1_out;  // AND_Gate and_18, 8 bits wide
  assign and_19_out = undriven & and_2_out;  // AND_Gate and_19, 8 bits wide
  assign and_20_out = undriven_2 & and_3_out;  // AND_Gate and_20, 8 bits wide
  assign and_21_out = bit_extender_5_out & and_4_out;  // AND_Gate and_21, 8 bits wide
  assign and_22_out = bit_extender_4_out & and_7_out;  // AND_Gate and_22, 8 bits wide
  assign not_1_out = ~bit_extender_5_out;  // NOT_Gate not_1, 8 bits wide
  assign and_23_out = not_1_out & and_8_out;  // AND_Gate and_23, 8 bits wide
  assign not_2_out = ~bit_extender_4_out;  // NOT_Gate not_2, 8 bits wide
  assign and_24_out = not_2_out & and_10_out;  // AND_Gate and_24, 8 bits wide
  assign and_25_out = bit_extender_1_out & and_13_out;  // AND_Gate and_25, 8 bits wide
  assign and_26_out = bit_extender_2_out & and_15_out;  // AND_Gate and_26, 8 bits wide
  assign and_27_out = bit_extender_3_out & and_17_out;  // AND_Gate and_27, 8 bits wide
  assign not_3_out = ~bit_extender_1_out;  // NOT_Gate not_3, 8 bits wide
  assign and_28_out = not_3_out & and_18_out;  // AND_Gate and_28, 8 bits wide
  assign not_4_out = ~bit_extender_2_out;  // NOT_Gate not_4, 8 bits wide
  assign and_29_out = not_4_out & and_19_out;  // AND_Gate and_29, 8 bits wide
  assign not_5_out = ~bit_extender_3_out;  // NOT_Gate not_5, 8 bits wide
  assign and_30_out = not_5_out & and_20_out;  // AND_Gate and_30, 8 bits wide
  assign and_31_out = bit_extender_10_out & and_21_out;  // AND_Gate and_31, 8 bits wide
  assign and_32_out = bit_extender_8_out & and_22_out;  // AND_Gate and_32, 8 bits wide
  assign and_33_out = bit_extender_11_out & and_23_out;  // AND_Gate and_33, 8 bits wide
  assign and_34_out = bit_extender_9_out & and_24_out;  // AND_Gate and_34, 8 bits wide
  assign and_35_out = bit_extender_12_out & and_25_out;  // AND_Gate and_35, 8 bits wide
  assign and_36_out = bit_extender_13_out & and_26_out;  // AND_Gate and_36, 8 bits wide
  assign and_37_out = bit_extender_14_out & and_27_out;  // AND_Gate and_37, 8 bits wide
  assign and_38_out = bit_extender_15_out & and_28_out;  // AND_Gate and_38, 8 bits wide
  assign and_39_out = bit_extender_16_out & and_29_out;  // AND_Gate and_39, 8 bits wide
  assign and_40_out = bit_extender_17_out & and_30_out;  // AND_Gate and_40, 8 bits wide
  assign or_1_out = and_31_out | and_32_out | and_33_out | and_34_out;  // OR_Gate or_1, 8 bits wide
  assign or_2_out = and_35_out | and_36_out | and_37_out | and_38_out | and_39_out | and_40_out;  // OR_Gate or_2, 8 bits wide
  assign ADDR = or_1_out | or_2_out;  // OR_Gate or_3, 8 bits wide
endmodule

module LOGIC (
  input  SEL_5,
  input  SEL_1,
  input  SEL_2,
  input  [7:0] DATA,
  input  [7:0] DATA_2,
  input  [7:0] DATA_3,
  input  [7:0] PC_IN,
  input  CLR,
  input  CLK,
  input  SEL_3,
  input  SEL_4,
  input  RAM_WRITE,
  input  MEM_WRITE,
  output MAIN_MUX,
  output [7:0] ADDR,
  output CLR_X,
  output CLR_PC,
  output CLK_KYBD,
  output CLR_TTY,
  output CLK_RAM,
  output CLR_LED_MATRIX,
  output CLK_MEM,
  output CLR_REGS,
  output SEL_BIOS,
  output SEL_RAM,
  output SEL_MEM,
  output CLR_PC_ALL,
  output ADDR_SEL
);

  wire and_1_out, and_2_out, and_3_out, and_4_out, and_5_out, and_6_out, and_7_out, and_8_out, and_9_out,
       and_10_out, and_11_out, and_12_out, and_13_out, and_16_out, and_17_out, and_18_out, and_19_out,
       and_20_out, and_21_out, and_22_out, and_23_out, and_24_out, and_25_out, and_26_out, and_27_out,
       and_29_out, and_30_out, and_31_out, and_32_out, and_33_out, and_36_out, and_37_out, and_38_out,
       and_40_out, comparator_1_eq, comparator_2_eq, comparator_3_eq, comparator_4_eq, comparator_5_eq,
       comparator_6_eq, comparator_7_eq, comparator_8_eq, comparator_9_eq, comparator_10_eq,
       comparator_11_eq, comparator_12_eq, comparator_13_eq, comparator_14_eq, comparator_15_eq,
       comparator_16_eq, comparator_17_eq, comparator_18_eq, comparator_19_eq, comparator_20_eq,
       comparator_21_eq, comparator_22_eq, comparator_23_eq, not_1_out, or_1_out, or_2_out, or_3_out,
       or_4_out, or_6_out, or_8_out_2, or_10_out, t_ff_2_q, transistor_1_out;
  wire [1:0] counter_1_q, counter_2_q;
  wire [7:0] bit_extender_1_out;

  Comparator comparator_1 (.a(DATA), .b(8'h40), .eq(comparator_1_eq));  // open: gt, lt
  Comparator comparator_2 (.a(DATA), .b(8'h50), .eq(comparator_2_eq));  // open: gt, lt
  Comparator comparator_3 (.a(DATA), .b(8'h60), .eq(comparator_3_eq));  // open: gt, lt
  Comparator comparator_4 (.a(DATA_2), .b(8'h45), .eq(comparator_4_eq));  // open: gt, lt
  Comparator comparator_5 (.a(DATA_2), .b(8'h55), .eq(comparator_5_eq));  // open: gt, lt
  Comparator comparator_6 (.a(DATA_2), .b(8'h65), .eq(comparator_6_eq));  // open: gt, lt
  Comparator comparator_7 (.a(DATA_3), .b(8'h43), .eq(comparator_7_eq));  // open: gt, lt
  Comparator comparator_8 (.a(DATA_3), .b(8'h44), .eq(comparator_8_eq));  // open: gt, lt
  Comparator comparator_9 (.a(DATA_3), .b(8'h47), .eq(comparator_9_eq));  // open: gt, lt
  Comparator comparator_10 (.a(DATA_3), .b(8'h53), .eq(comparator_10_eq));  // open: gt, lt
  Comparator comparator_11 (.a(DATA_3), .b(8'h54), .eq(comparator_11_eq));  // open: gt, lt
  Comparator comparator_12 (.a(DATA_3), .b(8'h57), .eq(comparator_12_eq));  // open: gt, lt
  not not_1 (not_1_out, or_1_out);
  and and_1 (and_1_out, not_1_out, comparator_13_eq);
  Comparator comparator_13 (.a(PC_IN), .b({8{1'b0}}), .eq(comparator_13_eq));  // open: gt, lt
  Comparator comparator_14 (.a(DATA), .b(8'h90), .eq(comparator_14_eq));  // open: gt, lt
  Comparator comparator_15 (.a(DATA_2), .b(8'h95), .eq(comparator_15_eq));  // open: gt, lt
  and and_2 (and_2_out, comparator_7_eq, SEL_1);
  and and_3 (and_3_out, and_2_out, comparator_1_eq);
  and and_4 (and_4_out, comparator_8_eq, SEL_1);
  and and_5 (and_5_out, and_4_out, comparator_1_eq);
  and and_6 (and_6_out, comparator_9_eq, SEL_1);
  and and_7 (and_7_out, and_6_out, comparator_1_eq);
  and and_8 (and_8_out, comparator_10_eq, SEL_2);
  and and_9 (and_9_out, and_8_out, comparator_2_eq);
  and and_10 (and_10_out, comparator_11_eq, SEL_2);
  and and_11 (and_11_out, and_10_out, comparator_2_eq);
  and and_12 (and_12_out, comparator_12_eq, SEL_2);
  and and_13 (and_13_out, and_12_out, comparator_2_eq);
  or or_1 (or_1_out, SEL_BIOS, SEL_RAM, SEL_MEM);
  Comparator comparator_16 (.a(DATA_3), .b(8'h93), .eq(comparator_16_eq));  // open: gt, lt
  Comparator comparator_17 (.a(DATA), .b(8'h70), .eq(comparator_17_eq));  // open: gt, lt
  Comparator comparator_18 (.a(DATA_2), .b(8'h75), .eq(comparator_18_eq));  // open: gt, lt
  and and_14 (CLR_TTY, and_3_out, comparator_4_eq);
  and and_15 (CLR_LED_MATRIX, and_5_out, comparator_4_eq);
  and and_16 (and_16_out, and_7_out, comparator_4_eq);
  and and_17 (and_17_out, and_9_out, comparator_5_eq);
  or or_2 (or_2_out, and_17_out, and_1_out);
  and and_18 (and_18_out, and_11_out, comparator_5_eq);
  and and_19 (and_19_out, and_13_out, comparator_5_eq);
  or or_3 (or_3_out, and_19_out, CLR, and_18_out);
  or or_4 (or_4_out, and_19_out, CLR, or_2_out);
  and and_20 (and_20_out, SEL_MEM, or_2_out);
  and and_21 (and_21_out, SEL_RAM, and_18_out);
  and and_22 (and_22_out, SEL_MEM, and_19_out);
  and and_23 (and_23_out, comparator_16_eq, SEL_4);
  Comparator comparator_19 (.a(DATA_3), .b(8'h63), .eq(comparator_19_eq));  // open: gt, lt
  Comparator comparator_20 (.a(DATA_3), .b(8'h64), .eq(comparator_20_eq));  // open: gt, lt
  Comparator comparator_21 (.a(DATA_3), .b(8'h67), .eq(comparator_21_eq));  // open: gt, lt
  or or_5 (CLR_REGS, and_16_out, CLR);
  Register #(.width(1), .trigger("high")) register_1 (
    .D(or_2_out), .Q(SEL_BIOS), .clk(or_2_out), .clr(or_3_out));  // open: en
  Register #(.width(1), .trigger("high")) register_2 (
    .D(and_18_out), .Q(SEL_RAM), .clk(and_18_out), .clr(or_4_out));  // open: en
  Register #(.width(1), .trigger("high")) register_3 (
    .D(and_19_out), .Q(SEL_MEM), .clk(and_19_out), .clr(or_6_out));  // open: en
  or or_6 (or_6_out, and_18_out, CLR, or_2_out);
  or or_7 (CLR_PC_ALL, and_20_out, and_21_out, and_22_out, CLR);
  and and_24 (and_24_out, and_23_out, comparator_14_eq);
  Comparator comparator_22 (.a(DATA_3), .b(8'h73), .eq(comparator_22_eq));  // open: gt, lt
  and and_25 (and_25_out, comparator_19_eq, SEL_5);
  and and_26 (and_26_out, comparator_20_eq, SEL_5);
  and and_27 (and_27_out, comparator_21_eq, SEL_5);
  and and_28 (ADDR_SEL, and_24_out, comparator_15_eq);
  and and_29 (and_29_out, comparator_22_eq, SEL_3);
  and and_30 (and_30_out, and_29_out, comparator_17_eq);
  OR or_8 (.in_1(PC_IN), .out_2(or_8_out_2));
  and and_31 (and_31_out, and_25_out, comparator_3_eq);
  and and_32 (and_32_out, and_26_out, comparator_3_eq);
  and and_33 (and_33_out, and_27_out, comparator_3_eq);
  and and_34 (CLK_RAM, RAM_WRITE, CLK);
  and and_35 (CLK_MEM, MEM_WRITE, CLK);
  and and_36 (and_36_out, and_30_out, comparator_18_eq);
  Counter #(.width(2), .max('h3)) counter_1 (
    .Q(counter_1_q), .clk(transistor_1_out), .clr(and_37_out));  // open: load, D, count, carry
  Transistor #(.\type ("n")) transistor_1 (.in(or_8_out_2), .out(transistor_1_out), .gate(MAIN_MUX));
  and and_37 (and_37_out, counter_1_q[1], counter_1_q[0]);
  and and_38 (and_38_out, and_31_out, comparator_6_eq);
  or or_9 (CLR_PC, and_38_out, CLR);
  and and_39 (CLR_X, and_32_out, comparator_6_eq);
  assign bit_extender_1_out = {{7{CLR_X}}, CLR_X};  // Bit_Extender bit_extender_1
  and and_40 (and_40_out, and_33_out, comparator_6_eq);
  T_Flip_Flop t_ff_1 (.clk(and_36_out), .T(and_36_out), .Q(MAIN_MUX), .reset(counter_1_q[1]));  // open: Qn, preset, en
  assign ADDR = DATA_2 & bit_extender_1_out;  // AND_Gate and_41, 8 bits wide
  T_Flip_Flop t_ff_2 (.clk(and_40_out), .T(and_40_out), .Q(t_ff_2_q), .reset(or_10_out));  // open: Qn, preset, en
  or or_10 (or_10_out, CLR, comparator_23_eq);
  Counter #(.width(2), .max('h3)) counter_2 (
    .Q(counter_2_q), .clk(and_40_out), .clr(comparator_23_eq));  // open: load, D, count, carry
  Comparator #(.width(2)) comparator_23 (.a(counter_2_q), .b(2'b10), .eq(comparator_23_eq));  // open: gt, lt
  and and_42 (CLK_KYBD, t_ff_2_q, CLK);
endmodule

module CORE (
  input  [7:0] D_BUS_IN,
  input  CLK,
  input  SELECT,
  input  RESET,
  input  [6:0] KYBD,
  output CLR_TTY,
  output [7:0] D_BUS_OUT,
  output [6:0] TTY,
  output [7:0] ADDRESS,
  output CLK_TTY,
  output LED_MATRIX_ENABLE,
  output CLK_KYBD,
  output SEL_BIOS,
  output SEL_RAM,
  output SEL_MEM,
  output MEM_WRITE,
  output CLK_RAM,
  output CLK_MEM,
  output CLR_LED_MATRIX,
  output CLR_BIOS,
  output CLR_RAM,
  output CLR_MEM,
  output RAM_WRITE,
  output RAM_READ,
  output MEM_READ
);

  wire _5, _6, _7, alu_1_p5, alu_1_p7, alu_1_p8, alu_1_p9, alu_1_p10, CLR_X, control_unit_1_p1,
       control_unit_1_p4, control_unit_1_p5, control_unit_1_p9, control_unit_1_p14, control_unit_1_p28,
       control_unit_1_p29, control_unit_1_p32, control_unit_1_p36, control_unit_1_p37, not_1_out, not_2_out,
       not_3_out, or_1_out, or_2_out, or_3_out_2, or_4_out, or_5_out_2, or_7_1_out_3, tunnel, tunnel_t,
       tunnel_t_t;
  wire [1:0] control_unit_1_p6, control_unit_1_p11, control_unit_1_p13, control_unit_1_p31,
       control_unit_1_p33, control_unit_1_p34, control_unit_1_p35;
  wire [1:1] control_unit_1_p27;
  wire [7:0] A, accumialtor_1_alu_out, alu_1_p6, B, bit_extender_1_out, control_unit_1_p30,
       multiplexer_1_out, multiplexer_2_out, multiplexer_3_out, multiplexer_4_out, register_file_1_out,
       registers_1_c, transistor_1_out, transistor_2_out;

  Transistor #(.\type ("n"), .width(8)) transistor_1 (
    .in(bit_extender_1_out), .out(transistor_1_out), .gate(control_unit_1_p28));
  assign bit_extender_1_out = {{1{1'b0}}, KYBD};  // Bit_Extender bit_extender_1
  and and_1 (CLR_BIOS, SEL_BIOS, CLR_X);
  and and_2 (CLR_RAM, SEL_RAM, CLR_X);
  and and_3 (CLR_MEM, SEL_MEM, CLR_X);
  Multiplexer #(.width(8), .enable("false")) multiplexer_1 (
    .in0(D_BUS_IN), .in1(transistor_1_out), .out(multiplexer_1_out), .sel(control_unit_1_p28));
  Multiplexer #(.width(8), .enable("false")) multiplexer_2 (
    .in0(multiplexer_1_out), .in1(accumialtor_1_alu_out), .out(multiplexer_2_out), .sel(control_unit_1_p37));
  // CONTROL_UNIT control_unit_1: pin names not known; wires that end beside it: control_unit_1_p1, D_BUS_IN, SELECT, control_unit_1_p4, control_unit_1_p5, control_unit_1_p6, RESET, CLK, control_unit_1_p9, MEM_WRITE, control_unit_1_p11, CLR_LED_MATRIX, control_unit_1_p13, control_unit_1_p14, _5, tunnel_t_t, SEL_MEM, CLR_X, _6, tunnel_t, SEL_RAM, CLK_RAM, _7, tunnel, SEL_BIOS, CLK_MEM, {control_unit_1_p27[1], LED_MATRIX_ENABLE}, control_unit_1_p28, control_unit_1_p29, control_unit_1_p30, control_unit_1_p31, control_unit_1_p32, control_unit_1_p33, control_unit_1_p34, control_unit_1_p35, control_unit_1_p36, control_unit_1_p37
  not not_1 (not_1_out, _7);
  or or_1 (or_1_out, not_1_out, _6);
  or or_2 (or_2_out, _5, not_2_out);
  not not_2 (not_2_out, MEM_WRITE);
  REGISTER_FILE register_file_1 (
    .SEL_TEMP(control_unit_1_p29), .TEMP(control_unit_1_p31), .SEL_2(control_unit_1_p11),
    .D_BUS_IN(D_BUS_IN), .OUT(register_file_1_out), .CLK(RESET));  // open: CLR, TEMP_SEL
  Multiplexer #(.width(8), .enable("false")) multiplexer_3 (
    .in0(multiplexer_2_out), .in1(register_file_1_out), .out(multiplexer_3_out), .sel(control_unit_1_p29));
  and and_4 (CLK_KYBD, control_unit_1_p9, SELECT);
  and and_5 (RAM_WRITE, _7, SEL_RAM);
  and and_6 (RAM_READ, SEL_RAM, or_1_out);
  and and_7 (MEM_READ, or_2_out, SEL_MEM);
  Multiplexer #(.width(8), .enable("false")) multiplexer_4 (
    .in0(D_BUS_IN), .in1(transistor_1_out), .out(multiplexer_4_out));  // open: sel
  OR or_3 (.in_1(A), .out_2(or_3_out_2));
  or or_4 (or_4_out, or_3_out_2, or_5_out_2);
  OR or_5 (.in_1(B), .out_2(or_5_out_2));
  REGISTERS registers_1 (
    .SEL_REGS(control_unit_1_p36), .SEL_1(control_unit_1_p13), .A_SEL(control_unit_1_p33),
    .D_BUS_IN(multiplexer_3_out), .REGS(control_unit_1_p35), .CLR(control_unit_1_p14),
    .B_SEL(control_unit_1_p34), .CLK(CLK), .A(A), .C(registers_1_c), .B(B));  // open: SEL_REG, SEL_A_B, SUM_UPDATE
  not not_3 (not_3_out, control_unit_1_p6[1]);
  Multiplexer #(.width(8), .enable("false")) multiplexer_5 (
    .in0(multiplexer_4_out), .in1(registers_1_c), .out(D_BUS_OUT), .sel(control_unit_1_p6[1]));
  // ALU alu_1: pin names not known; wires that end beside it: A, B, control_unit_1_p32, {8{1'b0}}, alu_1_p5, alu_1_p6, alu_1_p7, alu_1_p8, alu_1_p9, alu_1_p10
  KYBD_MANAGEMENT kybd_management_1 (
    .KYBD_ENABLE(not_3_out), .KYBD_IN(KYBD), .TTY_ENABLE(control_unit_1_p27[1]), .OUT(TTY));
  Transistor #(.\type ("n"), .width(8)) transistor_2 (
    .in(D_BUS_OUT), .out(transistor_2_out), .gate(control_unit_1_p27[1]));
  Bit_Extender #(.out_width(7)) bit_extender_2 (.in(transistor_2_out), .out(TTY));
  OR_7 or_7_1 (.in_1(TTY), .out_3(or_7_1_out_3));  // open: in_2
  ACCUMIALTOR accumialtor_1 (
    .ALU_IN(alu_1_p6), .ALU_OUT(accumialtor_1_alu_out), .CLR(control_unit_1_p14), .ZERO_IN(alu_1_p7),
    .ZERO_OUT(control_unit_1_p4), .CARRY_IN(alu_1_p5), .CARRY_OUT(control_unit_1_p5), .Hi_IN(alu_1_p8),
    .Hi_OUT(tunnel_t_t), .EQUAL_IN(alu_1_p9), .EQUAL_OUT(tunnel_t), .Lo_IN(alu_1_p10), .Lo_OUT(tunnel));  // open: SUM_UPDATE
  Multiplexer #(.width(8), .enable("false")) multiplexer_6 (
    .in0(control_unit_1_p30), .in1(accumialtor_1_alu_out), .out(ADDRESS), .sel(control_unit_1_p6[0]));
  and and_8 (CLK_TTY, control_unit_1_p27[1], or_7_1_out_3, SELECT);
  or or_6 (CLR_TTY, RESET, control_unit_1_p1);
endmodule

module REGISTER_FILE (
  input  SEL_TEMP,
  input  [1:0] TEMP,
  input  [1:0] SEL_2,
  input  TEMP_SEL,
  input  [7:0] D_BUS_IN,
  input  CLR,
  input  CLK,
  output [7:0] OUT
);

  wire demultiplexer_1_out0, demultiplexer_1_out1, demultiplexer_1_out2, demultiplexer_1_out3;
  wire [7:0] E_q, F_q, G_q, H_q;

  Demultiplexer #(.select(2), .enable("false")) demultiplexer_1 (
    .out0(demultiplexer_1_out0), .out1(demultiplexer_1_out1), .out2(demultiplexer_1_out2),
    .out3(demultiplexer_1_out3), .in(SEL_TEMP), .sel(SEL_2));
  Register #(.trigger("high")) E (.D(D_BUS_IN), .en(demultiplexer_1_out0), .Q(E_q), .clk(CLK), .clr(CLR));
  Register #(.trigger("high")) F (.D(D_BUS_IN), .en(demultiplexer_1_out1), .Q(F_q), .clk(CLK), .clr(CLR));
  Register #(.trigger("high")) G (.D(D_BUS_IN), .en(demultiplexer_1_out2), .Q(G_q), .clk(CLK), .clr(CLR));
  Register #(.trigger("high")) H (.D(D_BUS_IN), .en(demultiplexer_1_out3), .Q(H_q), .clk(CLK), .clr(CLR));
  Multiplexer #(.select(2), .width(8)) multiplexer_1 (
    .in0(E_q), .in1(F_q), .in2(G_q), .in3(H_q), .out(OUT), .sel(TEMP), .en(TEMP_SEL));
endmodule

module TEST2 (
  input  in_1,
  input  in_2,
  input  in_3,
  input  in_4,
  input  in_5,
  input  in_6,
  output out_7,
  output out_8
);

  wire _2, and_1_out, and_5_out, comparator_1_eq, comparator_2_eq, comparator_3_eq, demultiplexer_1_out1,
       demultiplexer_1_out2, demultiplexer_1_out3, mov_batch_1_bios, mov_batch_1_mem_write, mov_batch_1_ram,
       mov_batch_1_ram_write, mov_batch_1_sel_regs, mov_batch_1_sel_regs_2, mov_batch_1_sel_temp,
       mov_batch_1_sel_temp_2, mov_batch_1_status, or_1_out_2, or_2_out_2, transistor_1_out,
       transistor_2_out, undriven;
  wire [1:0] and_2_out, and_3_out, and_4_out, bit_extender_1_out, bit_extender_2_out, bit_extender_3_out,
       mov_batch_1_sel_1, mov_batch_1_sel_2, or_3_out, REGS, TEMP;
  wire [7:0] mov_batch_1_addr, multiplexer_1_out, multiplexer_2_out, pc_1_address, pc_1_out_1, pc_1_out_2,
       pc_1_out_3, pc_1_out_4, register_file_1_out, registers_1_c, rom_1_data;

  Demultiplexer #(.select(2), .enable("false")) demultiplexer_1 (
    .out1(demultiplexer_1_out1), .out2(demultiplexer_1_out2), .out3(demultiplexer_1_out3), .in(in_1),
    .sel(or_3_out));  // open: out0
  MOV_BATCH mov_batch_1 (
    .MOV_B_TO(demultiplexer_1_out1), .MOV_B_FROM(demultiplexer_1_out2), .DATA(pc_1_out_2),
    .DATA_1(pc_1_out_3), .DATA_2(pc_1_out_4), .ADDR(mov_batch_1_addr), .BIOS(mov_batch_1_bios),
    .RAM(mov_batch_1_ram), .MEM(out_8), .SEL_1(mov_batch_1_sel_1), .REGS(REGS), .SEL_2(mov_batch_1_sel_2),
    .TEMP(TEMP), .SEL_TEMP_2(mov_batch_1_sel_temp_2), .SEL_REGS(mov_batch_1_sel_regs),
    .STATUS(mov_batch_1_status), .PC_IN(pc_1_address), .CLR(in_2), .CLK(in_3),
    .MOV_DATA(demultiplexer_1_out3), .RAM_WRITE(mov_batch_1_ram_write), .MEM_WRITE(mov_batch_1_mem_write),
    .RAM_READ(_2), .MEM_READ(out_7), .SEL_TEMP(mov_batch_1_sel_temp), .SEL_REGS_2(mov_batch_1_sel_regs_2));  // open: TTY_ENABLE, PC_ENABLE, ENABLE_MATRIX, KYBD_ENABLE, PC_1, PC_2_EN
  PC pc_1 (
    .CLR_PC(in_2), .CLK(in_3), .D_BUS_IN(rom_1_data), .SEL_2(in_4), .ADDRESS(pc_1_address),
    .OUT_1(pc_1_out_1), .OUT_2(pc_1_out_2), .OUT_3(pc_1_out_3), .OUT_4(pc_1_out_4),
    .PC_IN_2(mov_batch_1_addr), .CLR_ALL(in_2), .D_BUS_ENABLE(mov_batch_1_status));  // open: LOAD, PC_IN_1, SEL
  // Probe on mov_batch_1_addr
  // Probe on pc_1_address
  ROM rom_1 (.addr(pc_1_address), .data(rom_1_data), .sel(mov_batch_1_bios));
  OR or_1 (.in_1(registers_1_c), .out_2(or_1_out_2));
  Multiplexer #(.width(8), .enable("false")) multiplexer_1 (
    .in0(rom_1_data), .in1(registers_1_c), .out(multiplexer_1_out), .sel(or_1_out_2));
  and and_1 (and_1_out, mov_batch_1_mem_write, in_3);
  OR or_2 (.in_1(register_file_1_out), .out_2(or_2_out_2));
  Multiplexer #(.width(8), .enable("false")) multiplexer_2 (
    .in0(rom_1_data), .in1(register_file_1_out), .out(multiplexer_2_out), .sel(or_2_out_2));
  REGISTER_FILE register_file_1 (
    .SEL_TEMP(mov_batch_1_sel_temp_2), .TEMP(TEMP), .SEL_2(mov_batch_1_sel_2), .D_BUS_IN(multiplexer_1_out),
    .CLR(in_2), .OUT(register_file_1_out), .CLK(in_3), .TEMP_SEL(mov_batch_1_sel_temp));
  Comparator comparator_1 (.a(pc_1_out_1), .b(8'he), .eq(comparator_1_eq));  // open: gt, lt
  assign bit_extender_1_out = {{1{comparator_1_eq}}, comparator_1_eq};  // Bit_Extender bit_extender_1
  Comparator comparator_2 (.a(pc_1_out_1), .b(8'h3), .eq(comparator_2_eq));  // open: gt, lt
  assign bit_extender_2_out = {{1{comparator_2_eq}}, comparator_2_eq};  // Bit_Extender bit_extender_2
  Comparator comparator_3 (.a(pc_1_out_1), .b(8'h4), .eq(comparator_3_eq));  // open: gt, lt
  assign bit_extender_3_out = {{1{comparator_3_eq}}, comparator_3_eq};  // Bit_Extender bit_extender_3
  // Probe on rom_1_data
  RAM #(.bus("separate")) ram_1 (
    .addr(pc_1_address), .din(rom_1_data), .data(rom_1_data), .str(mov_batch_1_mem_write), .sel(in_5),
    .clk(and_1_out), .ld(undriven));  // open: clr
  REGISTERS registers_1 (
    .SEL_REGS(mov_batch_1_sel_regs), .SEL_1(mov_batch_1_sel_1), .D_BUS_IN(multiplexer_2_out), .REGS(REGS),
    .CLR(in_2), .CLK(in_3), .C(registers_1_c));  // open: A_SEL, B_SEL, A, B, SEL_REG, SEL_A_B, SUM_UPDATE
  // Probe on registers_1_c
  assign and_2_out = bit_extender_1_out & 2'b11;  // AND_Gate and_2, 2 bits wide
  assign and_3_out = bit_extender_2_out & 2'b01;  // AND_Gate and_3, 2 bits wide
  assign and_4_out = bit_extender_3_out & 2'b10;  // AND_Gate and_4, 2 bits wide
  and and_5 (and_5_out, mov_batch_1_ram_write, in_3);
  Counter counter_1 (.clk(transistor_1_out));  // open: load, D, count, Q, carry, clr
  Transistor #(.\type ("n")) transistor_1 (.in(in_3), .out(transistor_1_out), .gate(mov_batch_1_sel_regs));
  Counter counter_2 (.clk(transistor_2_out));  // open: load, D, count, Q, carry, clr
  Transistor #(.\type ("n")) transistor_2 (.in(in_3), .out(transistor_2_out), .gate(mov_batch_1_sel_regs_2));
  assign or_3_out = and_3_out | and_2_out | and_4_out;  // OR_Gate or_3, 2 bits wide
  RAM #(.bus("separate")) ram_2 (
    .addr(pc_1_address), .din(registers_1_c), .data(rom_1_data), .str(mov_batch_1_ram_write),
    .sel(mov_batch_1_ram), .clk(and_5_out), .ld(_2), .clr(in_6));

  // Other names for the same wires on the sheet: _1 = out_7

  // Notes on the sheet:
  //   ROM
  //   MEM
  //   RAM
endmodule

module KYBD_MANAGEMENT (
  input  KYBD_ENABLE,
  input  [6:0] KYBD_IN,
  input  TTY_ENABLE,
  output [6:0] OUT
);

  wire and_1_out, and_2_out, and_3_out, not_1_out, not_2_out, not_3_out, not_4_out, or_1_out, t_ff_1_q;
  wire [6:0] bit_extender_1_out;

  not not_1 (not_1_out, or_1_out);
  and and_1 (and_1_out, not_1_out, KYBD_ENABLE);
  and and_2 (and_2_out, TTY_ENABLE, not_2_out);
  not not_2 (not_2_out, or_1_out);
  and and_3 (and_3_out, and_1_out, and_2_out);
  not not_3 (not_3_out, KYBD_ENABLE);
  or or_1 (or_1_out, not_3_out, not_4_out);
  not not_4 (not_4_out, TTY_ENABLE);
  T_Flip_Flop t_ff_1 (.clk(and_3_out), .T(and_3_out), .Q(t_ff_1_q), .reset(or_1_out));  // open: Qn, preset, en
  assign bit_extender_1_out = {{6{t_ff_1_q}}, t_ff_1_q};  // Bit_Extender bit_extender_1
  assign OUT = bit_extender_1_out & KYBD_IN;  // AND_Gate and_4, 7 bits wide
endmodule

module OR_7 (
  input  [6:0] in_1,
  input  in_2,
  output out_3
);

  wire or_1_out;

  or or_1 (or_1_out, in_1[0], in_1[1], in_1[2], in_1[3], in_1[4], in_1[5], in_1[6]);
  and and_1 (out_3, or_1_out, in_2);
endmodule
module TTY_MEMORY_CELL (
  input  W_R,
  input  ENABLE,
  input  [4:0] CUSTOM_ADDR,
  input  [6:0] DATA,
  input  CLR,
  input  CLK,
  input  C_IN,
  output [6:0] out_8,
  output C_OUT
);

  wire and_1_out, and_2_out, and_3_out, and_4_out, and_7_out, comparator_1_eq, comparator_2_eq,
       counter_2_carry, counter_3_q, demultiplexer_2_out0, demultiplexer_2_out1, demultiplexer_2_out2,
       demultiplexer_2_out3, demultiplexer_2_out4, demultiplexer_2_out5, demultiplexer_2_out6,
       demultiplexer_2_out7, demultiplexer_2_out8, demultiplexer_2_out9, demultiplexer_2_out10,
       demultiplexer_2_out11, demultiplexer_2_out12, demultiplexer_2_out13, demultiplexer_2_out14,
       demultiplexer_2_out15, demultiplexer_2_out16, demultiplexer_2_out17, demultiplexer_2_out18,
       demultiplexer_2_out19, demultiplexer_2_out20, demultiplexer_2_out21, demultiplexer_2_out22,
       demultiplexer_2_out23, demultiplexer_2_out24, demultiplexer_2_out25, demultiplexer_2_out26,
       demultiplexer_2_out27, demultiplexer_2_out28, demultiplexer_2_out29, demultiplexer_2_out30,
       demultiplexer_2_out31, EN, not_1_out, not_2_out, or_1_out, or_2_out, or_3_out, or_7_1_out_3;
  wire [1:0] counter_1_q;
  wire [4:0] counter_2_q, demultiplexer_1_out0, demultiplexer_1_out1, transistor_1_out;
  wire [6:0] and_5_out, bit_extender_1_out, bit_extender_2_out, multiplexer_1_out, register_1_q,
       register_2_q, register_3_q, register_4_q, register_5_q, register_6_q, register_7_q, register_8_q,
       register_9_q, register_10_q, register_11_q, register_12_q, register_13_q, register_14_q,
       register_15_q, register_16_q, register_17_q, register_18_q, register_19_q, register_20_q,
       register_21_q, register_22_q, register_23_q, register_24_q, register_25_q, register_26_q,
       register_27_q, register_28_q, register_29_q, register_30_q, register_31_q, register_32_q;

  or or_1 (or_1_out, EN, CLR);
  and and_1 (and_1_out, and_3_out, CLK);
  OR_7 or_7_1 (.in_1(and_5_out), .out_3(or_7_1_out_3));  // open: in_2
  Comparator #(.width(5)) comparator_1 (.a(counter_2_q), .b({5{1'b0}}), .eq(comparator_1_eq));  // open: gt, lt
  and and_2 (and_2_out, comparator_1_eq, CLK);
  Counter #(.width(2), .max('h3)) counter_1 (
    .Q(counter_1_q), .clk(and_2_out), .clr(or_1_out));  // open: load, D, count, carry
  and and_3 (and_3_out, W_R, ENABLE);
  Transistor #(.\type ("n"), .width(5)) transistor_1 (.in(CUSTOM_ADDR), .out(transistor_1_out), .gate(ENABLE));
  or or_2 (or_2_out, and_4_out, and_1_out);
  assign bit_extender_1_out = {{6{not_1_out}}, not_1_out};  // Bit_Extender bit_extender_1
  Counter #(.width(5), .max('h1f)) counter_2 (
    .D(transistor_1_out), .Q(counter_2_q), .carry(counter_2_carry), .clk(or_2_out), .clr(or_3_out));  // open: load, count
  Demultiplexer #(.width(5), .enable("false")) demultiplexer_1 (
    .out0(demultiplexer_1_out0), .out1(demultiplexer_1_out1), .in(counter_2_q), .sel(and_3_out));
  and and_4 (and_4_out, or_7_1_out_3, CLK, C_IN);
  or or_3 (or_3_out, CLR, counter_3_q);
  not not_1 (not_1_out, counter_3_q);
  Counter #(.width(1), .max('h1)) counter_3 (.Q(counter_3_q), .clk(C_OUT), .clr(CLR));  // open: load, D, count, carry
  T_Flip_Flop t_ff_1 (.clk(counter_2_carry), .T(counter_2_carry), .Q(C_OUT), .reset(CLR));  // open: Qn, preset, en
  assign bit_extender_2_out = {{6{and_3_out}}, and_3_out};  // Bit_Extender bit_extender_2
  Comparator #(.width(2)) comparator_2 (.a(counter_1_q), .b(2'b10), .eq(comparator_2_eq));  // open: gt, lt
  T_Flip_Flop t_ff_2 (.clk(comparator_2_eq), .T(comparator_2_eq), .Q(EN), .reset(CLR));  // open: Qn, preset, en
  Register #(.width(7), .trigger("high")) register_1 (
    .D(and_5_out), .Q(register_1_q), .clk(demultiplexer_2_out0), .clr(CLR));  // open: en
  assign and_5_out = bit_extender_1_out & DATA;  // AND_Gate and_5, 7 bits wide
  Register #(.width(7)) register_2 (
    .D(and_5_out), .Q(register_2_q), .clk(demultiplexer_2_out1), .clr(CLR));  // open: en
  assign out_8 = bit_extender_2_out & multiplexer_1_out;  // AND_Gate and_6, 7 bits wide
  Multiplexer #(.select(5), .width(7), .enable("false")) multiplexer_1 (
    .in0(register_1_q), .in1(register_2_q), .in2(register_3_q), .in3(register_4_q), .in4(register_5_q),
    .in5(register_6_q), .in6(register_7_q), .in7(register_8_q), .in8(register_9_q), .in9(register_10_q),
    .in10(register_11_q), .in11(register_12_q), .in12(register_13_q), .in13(register_14_q),
    .in14(register_15_q), .in15(register_17_q), .in16(register_16_q), .in17(register_18_q),
    .in18(register_19_q), .in19(register_21_q), .in20(register_20_q), .in21(register_22_q),
    .in22(register_23_q), .in23(register_25_q), .in24(register_24_q), .in25(register_26_q),
    .in26(register_27_q), .in27(register_29_q), .in28(register_28_q), .in29(register_30_q),
    .in30(register_31_q), .in31(register_32_q), .out(multiplexer_1_out), .sel(demultiplexer_1_out1));
  Register #(.width(7)) register_3 (
    .D(and_5_out), .Q(register_3_q), .clk(demultiplexer_2_out2), .clr(CLR));  // open: en
  and and_7 (and_7_out, not_2_out, 1'b1);
  Demultiplexer #(.select(5), .enable("false")) demultiplexer_2 (
    .out0(demultiplexer_2_out0), .out1(demultiplexer_2_out1), .out2(demultiplexer_2_out2),
    .out3(demultiplexer_2_out3), .out4(demultiplexer_2_out4), .out5(demultiplexer_2_out5),
    .out6(demultiplexer_2_out6), .out7(demultiplexer_2_out7), .out8(demultiplexer_2_out8),
    .out9(demultiplexer_2_out9), .out10(demultiplexer_2_out10), .out11(demultiplexer_2_out11),
    .out12(demultiplexer_2_out12), .out13(demultiplexer_2_out13), .out14(demultiplexer_2_out14),
    .out15(demultiplexer_2_out15), .out16(demultiplexer_2_out16), .out17(demultiplexer_2_out17),
    .out18(demultiplexer_2_out18), .out19(demultiplexer_2_out19), .out20(demultiplexer_2_out20),
    .out21(demultiplexer_2_out21), .out22(demultiplexer_2_out22), .out23(demultiplexer_2_out23),
    .out24(demultiplexer_2_out24), .out25(demultiplexer_2_out25), .out26(demultiplexer_2_out26),
    .out27(demultiplexer_2_out27), .out28(demultiplexer_2_out28), .out29(demultiplexer_2_out29),
    .out30(demultiplexer_2_out30), .out31(demultiplexer_2_out31), .in(and_7_out), .sel(demultiplexer_1_out0));
  not not_2 (not_2_out, and_3_out);
  Register #(.width(7)) register_4 (
    .D(and_5_out), .Q(register_4_q), .clk(demultiplexer_2_out3), .clr(CLR));  // open: en
  Register #(.width(7)) register_5 (
    .D(and_5_out), .Q(register_5_q), .clk(demultiplexer_2_out4), .clr(CLR));  // open: en
  Register #(.width(7)) register_6 (
    .D(and_5_out), .Q(register_6_q), .clk(demultiplexer_2_out5), .clr(CLR));  // open: en
  Register #(.width(7)) register_7 (
    .D(and_5_out), .Q(register_7_q), .clk(demultiplexer_2_out6), .clr(CLR));  // open: en
  Register #(.width(7)) register_8 (
    .D(and_5_out), .Q(register_8_q), .clk(demultiplexer_2_out7), .clr(CLR));  // open: en
  Register #(.width(7)) register_9 (
    .D(and_5_out), .Q(register_9_q), .clk(demultiplexer_2_out8), .clr(CLR));  // open: en
  Register #(.width(7)) register_10 (
    .D(and_5_out), .Q(register_10_q), .clk(demultiplexer_2_out9), .clr(CLR));  // open: en
  Register #(.width(7)) register_11 (
    .D(and_5_out), .Q(register_11_q), .clk(demultiplexer_2_out10), .clr(CLR));  // open: en
  Register #(.width(7)) register_12 (
    .D(and_5_out), .Q(register_12_q), .clk(demultiplexer_2_out11), .clr(CLR));  // open: en
  Register #(.width(7)) register_13 (
    .D(and_5_out), .Q(register_13_q), .clk(demultiplexer_2_out12), .clr(CLR));  // open: en
  Register #(.width(7)) register_14 (
    .D(and_5_out), .Q(register_14_q), .clk(demultiplexer_2_out13), .clr(CLR));  // open: en
  Register #(.width(7)) register_15 (
    .D(and_5_out), .Q(register_15_q), .clk(demultiplexer_2_out14), .clr(CLR));  // open: en
  Register #(.width(7)) register_16 (
    .D(and_5_out), .Q(register_16_q), .clk(demultiplexer_2_out16), .clr(CLR));  // open: en
  Register #(.width(7)) register_17 (
    .D(and_5_out), .Q(register_17_q), .clk(demultiplexer_2_out15), .clr(CLR));  // open: en
  Register #(.width(7)) register_18 (
    .D(and_5_out), .Q(register_18_q), .clk(demultiplexer_2_out17), .clr(CLR));  // open: en
  Register #(.width(7)) register_19 (
    .D(and_5_out), .Q(register_19_q), .clk(demultiplexer_2_out18), .clr(CLR));  // open: en
  Register #(.width(7)) register_20 (
    .D(and_5_out), .Q(register_20_q), .clk(demultiplexer_2_out20), .clr(CLR));  // open: en
  Register #(.width(7)) register_21 (
    .D(and_5_out), .Q(register_21_q), .clk(demultiplexer_2_out19), .clr(CLR));  // open: en
  Register #(.width(7)) register_22 (
    .D(and_5_out), .Q(register_22_q), .clk(demultiplexer_2_out21), .clr(CLR));  // open: en
  Register #(.width(7)) register_23 (
    .D(and_5_out), .Q(register_23_q), .clk(demultiplexer_2_out22), .clr(CLR));  // open: en
  Register #(.width(7)) register_24 (
    .D(and_5_out), .Q(register_24_q), .clk(demultiplexer_2_out24), .clr(CLR));  // open: en
  Register #(.width(7)) register_25 (
    .D(and_5_out), .Q(register_25_q), .clk(demultiplexer_2_out23), .clr(CLR));  // open: en
  Register #(.width(7)) register_26 (
    .D(and_5_out), .Q(register_26_q), .clk(demultiplexer_2_out25), .clr(CLR));  // open: en
  Register #(.width(7)) register_27 (
    .D(and_5_out), .Q(register_27_q), .clk(demultiplexer_2_out26), .clr(CLR));  // open: en
  Register #(.width(7)) register_28 (
    .D(and_5_out), .Q(register_28_q), .clk(demultiplexer_2_out28), .clr(CLR));  // open: en
  Register #(.width(7)) register_29 (
    .D(and_5_out), .Q(register_29_q), .clk(demultiplexer_2_out27), .clr(CLR));  // open: en
  Register #(.width(7)) register_30 (
    .D(and_5_out), .Q(register_30_q), .clk(demultiplexer_2_out29), .clr(CLR));  // open: en
  Register #(.width(7)) register_31 (
    .D(and_5_out), .Q(register_31_q), .clk(demultiplexer_2_out30), .clr(CLR));  // open: en
  Register #(.width(7)) register_32 (
    .D(and_5_out), .Q(register_32_q), .clk(demultiplexer_2_out31), .clr(CLR));  // open: en

  // Notes on the sheet:
  //   Write OFF
  //   Read ON
endmodule

module TTY_MEMORY_UNIT (
  input  [4:0] CUSTOM_ADDR_SEL,
  input  W_R,
  input  [4:0] CUSTOM_ADDR,
  input  CLK,
  input  CLR,
  input  [6:0] DATA,
  output [5:0] STATUS,
  output [6:0] OUT
);

  wire and_1_out, comparator_1_eq, demultiplexer_1_out0, demultiplexer_1_out1, demultiplexer_1_out2,
       demultiplexer_1_out3, demultiplexer_1_out4, demultiplexer_1_out5, demultiplexer_1_out6,
       demultiplexer_1_out7, demultiplexer_1_out8, demultiplexer_1_out9, demultiplexer_1_out10,
       demultiplexer_1_out11, demultiplexer_1_out12, demultiplexer_1_out13, demultiplexer_1_out14,
       demultiplexer_1_out15, demultiplexer_1_out16, demultiplexer_1_out17, demultiplexer_1_out18,
       demultiplexer_1_out19, demultiplexer_1_out20, demultiplexer_1_out21, demultiplexer_1_out22,
       demultiplexer_1_out23, demultiplexer_1_out24, demultiplexer_1_out25, demultiplexer_1_out26,
       demultiplexer_1_out27, demultiplexer_1_out28, demultiplexer_1_out29, demultiplexer_1_out30,
       demultiplexer_1_out31, tty_memory_cell_1_c_out, tty_memory_cell_2_c_out, tty_memory_cell_3_c_out,
       tty_memory_cell_4_c_out, tty_memory_cell_5_c_out, tty_memory_cell_6_c_out, tty_memory_cell_7_c_out,
       tty_memory_cell_8_c_out, tty_memory_cell_9_c_out, tty_memory_cell_10_c_out, tty_memory_cell_11_c_out,
       tty_memory_cell_12_c_out, tty_memory_cell_13_c_out, tty_memory_cell_14_c_out,
       tty_memory_cell_15_c_out, tty_memory_cell_16_c_out, tty_memory_cell_17_c_out,
       tty_memory_cell_18_c_out, tty_memory_cell_19_c_out, tty_memory_cell_20_c_out,
       tty_memory_cell_21_c_out, tty_memory_cell_22_c_out, tty_memory_cell_23_c_out,
       tty_memory_cell_24_c_out, tty_memory_cell_25_c_out, tty_memory_cell_26_c_out,
       tty_memory_cell_27_c_out, tty_memory_cell_28_c_out, tty_memory_cell_29_c_out,
       tty_memory_cell_30_c_out, tty_memory_cell_31_c_out;
  wire [4:0] counter_2_q;
  wire [5:0] bit_extender_1_out, counter_1_q;
  wire [6:0] tty_memory_cell_1_out_8, tty_memory_cell_2_out_8, tty_memory_cell_3_out_8,
       tty_memory_cell_4_out_8, tty_memory_cell_5_out_8, tty_memory_cell_6_out_8, tty_memory_cell_7_out_8,
       tty_memory_cell_8_out_8, tty_memory_cell_9_out_8, tty_memory_cell_10_out_8, tty_memory_cell_11_out_8,
       tty_memory_cell_12_out_8, tty_memory_cell_13_out_8, tty_memory_cell_14_out_8,
       tty_memory_cell_15_out_8, tty_memory_cell_16_out_8, tty_memory_cell_17_out_8,
       tty_memory_cell_18_out_8, tty_memory_cell_19_out_8, tty_memory_cell_20_out_8,
       tty_memory_cell_21_out_8, tty_memory_cell_22_out_8, tty_memory_cell_23_out_8,
       tty_memory_cell_24_out_8, tty_memory_cell_25_out_8, tty_memory_cell_26_out_8,
       tty_memory_cell_27_out_8, tty_memory_cell_28_out_8, tty_memory_cell_29_out_8,
       tty_memory_cell_30_out_8, tty_memory_cell_31_out_8, tty_memory_cell_32_out_8;

  and and_1 (and_1_out, W_R, CLK);
  Counter #(.width(6), .max('h3f)) counter_1 (.Q(counter_1_q), .clk(and_1_out));  // open: load, D, count, carry, clr
  Comparator #(.width(6)) comparator_1 (.a(counter_1_q), .b(6'b100000), .eq(comparator_1_eq));  // open: gt, lt
  TTY_MEMORY_CELL tty_memory_cell_1 (
    .W_R(W_R), .ENABLE(demultiplexer_1_out0), .CUSTOM_ADDR(CUSTOM_ADDR), .DATA(DATA), .CLR(CLR), .CLK(CLK),
    .C_IN(1'b1), .C_OUT(tty_memory_cell_1_c_out), .out_8(tty_memory_cell_1_out_8));
  Counter #(.width(5), .max('h1f)) counter_2 (
    .Q(counter_2_q), .clk(comparator_1_eq));  // open: load, D, count, carry, clr
  assign bit_extender_1_out = {{1{1'b0}}, counter_2_q};  // Bit_Extender bit_extender_1
  TTY_MEMORY_CELL tty_memory_cell_2 (
    .W_R(W_R), .ENABLE(demultiplexer_1_out1), .CUSTOM_ADDR(CUSTOM_ADDR), .DATA(DATA), .CLR(CLR), .CLK(CLK),
    .C_IN(tty_memory_cell_1_c_out), .C_OUT(tty_memory_cell_2_c_out), .out_8(tty_memory_cell_2_out_8));
  TTY_MEMORY_CELL tty_memory_cell_3 (
    .W_R(W_R), .ENABLE(demultiplexer_1_out2), .CUSTOM_ADDR(CUSTOM_ADDR), .DATA(DATA), .CLR(CLR), .CLK(CLK),
    .C_IN(tty_memory_cell_2_c_out), .C_OUT(tty_memory_cell_3_c_out), .out_8(tty_memory_cell_3_out_8));
  Adder #(.width(6)) adder_1 (.a(bit_extender_1_out), .b(6'b000001), .out(STATUS));  // open: cin, cout
  Demultiplexer #(.select(5), .enable("false")) demultiplexer_1 (
    .out0(demultiplexer_1_out0), .out1(demultiplexer_1_out1), .out2(demultiplexer_1_out2),
    .out3(demultiplexer_1_out3), .out4(demultiplexer_1_out4), .out5(demultiplexer_1_out5),
    .out6(demultiplexer_1_out6), .out7(demultiplexer_1_out7), .out8(demultiplexer_1_out8),
    .out9(demultiplexer_1_out9), .out10(demultiplexer_1_out10), .out11(demultiplexer_1_out11),
    .out12(demultiplexer_1_out12), .out13(demultiplexer_1_out13), .out14(demultiplexer_1_out14),
    .out15(demultiplexer_1_out15), .out16(demultiplexer_1_out16), .out17(demultiplexer_1_out17),
    .out18(demultiplexer_1_out18), .out19(demultiplexer_1_out19), .out20(demultiplexer_1_out20),
    .out21(demultiplexer_1_out21), .out22(demultiplexer_1_out22), .out23(demultiplexer_1_out23),
    .out24(demultiplexer_1_out24), .out25(demultiplexer_1_out25), .out26(demultiplexer_1_out26),
    .out27(demultiplexer_1_out27), .out28(demultiplexer_1_out28), .out29(demultiplexer_1_out29),
    .out30(demultiplexer_1_out30), .out31(demultiplexer_1_out31), .in(1'b1), .sel(CUSTOM_ADDR_SEL));
  TTY_MEMORY_CELL tty_memory_cell_4 (
    .W_R(W_R), .ENABLE(demultiplexer_1_out3), .CUSTOM_ADDR(CUSTOM_ADDR), .DATA(DATA), .CLR(CLR), .CLK(CLK),
    .C_IN(tty_memory_cell_3_c_out), .C_OUT(tty_memory_cell_4_c_out), .out_8(tty_memory_cell_4_out_8));
  Multiplexer #(.select(5), .width(7), .enable("false")) multiplexer_1 (
    .in0(tty_memory_cell_1_out_8), .in1(tty_memory_cell_2_out_8), .in2(tty_memory_cell_3_out_8),
    .in3(tty_memory_cell_4_out_8), .in4(tty_memory_cell_5_out_8), .in5(tty_memory_cell_7_out_8),
    .in6(tty_memory_cell_6_out_8), .in7(tty_memory_cell_8_out_8), .in8(tty_memory_cell_9_out_8),
    .in9(tty_memory_cell_10_out_8), .in10(tty_memory_cell_11_out_8), .in11(tty_memory_cell_12_out_8),
    .in12(tty_memory_cell_13_out_8), .in13(tty_memory_cell_14_out_8), .in14(tty_memory_cell_15_out_8),
    .in15(tty_memory_cell_16_out_8), .in16(tty_memory_cell_17_out_8), .in17(tty_memory_cell_18_out_8),
    .in18(tty_memory_cell_19_out_8), .in19(tty_memory_cell_20_out_8), .in20(tty_memory_cell_21_out_8),
    .in21(tty_memory_cell_22_out_8), .in22(tty_memory_cell_23_out_8), .in23(tty_memory_cell_24_out_8),
    .in24(tty_memory_cell_25_out_8), .in25(tty_memory_cell_27_out_8), .in26(tty_memory_cell_26_out_8),
    .in27(tty_memory_cell_28_out_8), .in28(tty_memory_cell_29_out_8), .in29(tty_memory_cell_30_out_8),
    .in30(tty_memory_cell_31_out_8), .in31(tty_memory_cell_32_out_8), .out(OUT), .sel(counter_2_q));
  TTY_MEMORY_CELL tty_memory_cell_5 (
    .W_R(W_R), .ENABLE(demultiplexer_1_out4), .CUSTOM_ADDR(CUSTOM_ADDR), .DATA(DATA), .CLR(CLR), .CLK(CLK),
    .C_IN(tty_memory_cell_4_c_out), .C_OUT(tty_memory_cell_5_c_out), .out_8(tty_memory_cell_5_out_8));
  TTY_MEMORY_CELL tty_memory_cell_6 (
    .W_R(W_R), .ENABLE(demultiplexer_1_out6), .CUSTOM_ADDR(CUSTOM_ADDR), .DATA(DATA), .CLR(CLR), .CLK(CLK),
    .C_IN(tty_memory_cell_7_c_out), .C_OUT(tty_memory_cell_6_c_out), .out_8(tty_memory_cell_6_out_8));
  TTY_MEMORY_CELL tty_memory_cell_7 (
    .W_R(W_R), .ENABLE(demultiplexer_1_out5), .CUSTOM_ADDR(CUSTOM_ADDR), .DATA(DATA), .CLR(CLR), .CLK(CLK),
    .C_IN(tty_memory_cell_5_c_out), .C_OUT(tty_memory_cell_7_c_out), .out_8(tty_memory_cell_7_out_8));
  TTY_MEMORY_CELL tty_memory_cell_8 (
    .W_R(W_R), .ENABLE(demultiplexer_1_out7), .CUSTOM_ADDR(CUSTOM_ADDR), .DATA(DATA), .CLR(CLR), .CLK(CLK),
    .C_IN(tty_memory_cell_6_c_out), .C_OUT(tty_memory_cell_8_c_out), .out_8(tty_memory_cell_8_out_8));
  TTY_MEMORY_CELL tty_memory_cell_9 (
    .W_R(W_R), .ENABLE(demultiplexer_1_out8), .CUSTOM_ADDR(CUSTOM_ADDR), .DATA(DATA), .CLR(CLR), .CLK(CLK),
    .C_IN(tty_memory_cell_8_c_out), .C_OUT(tty_memory_cell_9_c_out), .out_8(tty_memory_cell_9_out_8));
  TTY_MEMORY_CELL tty_memory_cell_10 (
    .W_R(W_R), .ENABLE(demultiplexer_1_out9), .CUSTOM_ADDR(CUSTOM_ADDR), .DATA(DATA), .CLR(CLR), .CLK(CLK),
    .C_IN(tty_memory_cell_9_c_out), .C_OUT(tty_memory_cell_10_c_out), .out_8(tty_memory_cell_10_out_8));
  TTY_MEMORY_CELL tty_memory_cell_11 (
    .W_R(W_R), .ENABLE(demultiplexer_1_out10), .CUSTOM_ADDR(CUSTOM_ADDR), .DATA(DATA), .CLR(CLR), .CLK(CLK),
    .C_IN(tty_memory_cell_10_c_out), .C_OUT(tty_memory_cell_11_c_out), .out_8(tty_memory_cell_11_out_8));
  TTY_MEMORY_CELL tty_memory_cell_12 (
    .W_R(W_R), .ENABLE(demultiplexer_1_out11), .CUSTOM_ADDR(CUSTOM_ADDR), .DATA(DATA), .CLR(CLR), .CLK(CLK),
    .C_IN(tty_memory_cell_11_c_out), .C_OUT(tty_memory_cell_12_c_out), .out_8(tty_memory_cell_12_out_8));
  TTY_MEMORY_CELL tty_memory_cell_13 (
    .W_R(W_R), .ENABLE(demultiplexer_1_out12), .CUSTOM_ADDR(CUSTOM_ADDR), .DATA(DATA), .CLR(CLR), .CLK(CLK),
    .C_IN(tty_memory_cell_12_c_out), .C_OUT(tty_memory_cell_13_c_out), .out_8(tty_memory_cell_13_out_8));
  TTY_MEMORY_CELL tty_memory_cell_14 (
    .W_R(W_R), .ENABLE(demultiplexer_1_out13), .CUSTOM_ADDR(CUSTOM_ADDR), .DATA(DATA), .CLR(CLR), .CLK(CLK),
    .C_IN(tty_memory_cell_13_c_out), .C_OUT(tty_memory_cell_14_c_out), .out_8(tty_memory_cell_14_out_8));
  TTY_MEMORY_CELL tty_memory_cell_15 (
    .W_R(W_R), .ENABLE(demultiplexer_1_out14), .CUSTOM_ADDR(CUSTOM_ADDR), .DATA(DATA), .CLR(CLR), .CLK(CLK),
    .C_IN(tty_memory_cell_14_c_out), .C_OUT(tty_memory_cell_15_c_out), .out_8(tty_memory_cell_15_out_8));
  TTY_MEMORY_CELL tty_memory_cell_16 (
    .W_R(W_R), .ENABLE(demultiplexer_1_out15), .CUSTOM_ADDR(CUSTOM_ADDR), .DATA(DATA), .CLR(CLR), .CLK(CLK),
    .C_IN(tty_memory_cell_15_c_out), .C_OUT(tty_memory_cell_16_c_out), .out_8(tty_memory_cell_16_out_8));
  TTY_MEMORY_CELL tty_memory_cell_17 (
    .W_R(W_R), .ENABLE(demultiplexer_1_out16), .CUSTOM_ADDR(CUSTOM_ADDR), .DATA(DATA), .CLR(CLR), .CLK(CLK),
    .C_IN(tty_memory_cell_16_c_out), .C_OUT(tty_memory_cell_17_c_out), .out_8(tty_memory_cell_17_out_8));
  TTY_MEMORY_CELL tty_memory_cell_18 (
    .W_R(W_R), .ENABLE(demultiplexer_1_out17), .CUSTOM_ADDR(CUSTOM_ADDR), .DATA(DATA), .CLR(CLR), .CLK(CLK),
    .C_IN(tty_memory_cell_17_c_out), .C_OUT(tty_memory_cell_18_c_out), .out_8(tty_memory_cell_18_out_8));
  TTY_MEMORY_CELL tty_memory_cell_19 (
    .W_R(W_R), .ENABLE(demultiplexer_1_out18), .CUSTOM_ADDR(CUSTOM_ADDR), .DATA(DATA), .CLR(CLR), .CLK(CLK),
    .C_IN(tty_memory_cell_18_c_out), .C_OUT(tty_memory_cell_19_c_out), .out_8(tty_memory_cell_19_out_8));
  TTY_MEMORY_CELL tty_memory_cell_20 (
    .W_R(W_R), .ENABLE(demultiplexer_1_out19), .CUSTOM_ADDR(CUSTOM_ADDR), .DATA(DATA), .CLR(CLR), .CLK(CLK),
    .C_IN(tty_memory_cell_19_c_out), .C_OUT(tty_memory_cell_20_c_out), .out_8(tty_memory_cell_20_out_8));
  TTY_MEMORY_CELL tty_memory_cell_21 (
    .W_R(W_R), .ENABLE(demultiplexer_1_out20), .CUSTOM_ADDR(CUSTOM_ADDR), .DATA(DATA), .CLR(CLR), .CLK(CLK),
    .C_IN(tty_memory_cell_20_c_out), .C_OUT(tty_memory_cell_21_c_out), .out_8(tty_memory_cell_21_out_8));
  TTY_MEMORY_CELL tty_memory_cell_22 (
    .W_R(W_R), .ENABLE(demultiplexer_1_out21), .CUSTOM_ADDR(CUSTOM_ADDR), .DATA(DATA), .CLR(CLR), .CLK(CLK),
    .C_IN(tty_memory_cell_21_c_out), .C_OUT(tty_memory_cell_22_c_out), .out_8(tty_memory_cell_22_out_8));
  TTY_MEMORY_CELL tty_memory_cell_23 (
    .W_R(W_R), .ENABLE(demultiplexer_1_out22), .CUSTOM_ADDR(CUSTOM_ADDR), .DATA(DATA), .CLR(CLR), .CLK(CLK),
    .C_IN(tty_memory_cell_22_c_out), .C_OUT(tty_memory_cell_23_c_out), .out_8(tty_memory_cell_23_out_8));
  TTY_MEMORY_CELL tty_memory_cell_24 (
    .W_R(W_R), .ENABLE(demultiplexer_1_out23), .CUSTOM_ADDR(CUSTOM_ADDR), .DATA(DATA), .CLR(CLR), .CLK(CLK),
    .C_IN(tty_memory_cell_23_c_out), .C_OUT(tty_memory_cell_24_c_out), .out_8(tty_memory_cell_24_out_8));
  TTY_MEMORY_CELL tty_memory_cell_25 (
    .W_R(W_R), .ENABLE(demultiplexer_1_out24), .CUSTOM_ADDR(CUSTOM_ADDR), .DATA(DATA), .CLR(CLR), .CLK(CLK),
    .C_IN(tty_memory_cell_24_c_out), .C_OUT(tty_memory_cell_25_c_out), .out_8(tty_memory_cell_25_out_8));
  TTY_MEMORY_CELL tty_memory_cell_26 (
    .W_R(W_R), .ENABLE(demultiplexer_1_out26), .CUSTOM_ADDR(CUSTOM_ADDR), .DATA(DATA), .CLR(CLR), .CLK(CLK),
    .C_IN(tty_memory_cell_27_c_out), .C_OUT(tty_memory_cell_26_c_out), .out_8(tty_memory_cell_26_out_8));
  TTY_MEMORY_CELL tty_memory_cell_27 (
    .W_R(W_R), .ENABLE(demultiplexer_1_out25), .CUSTOM_ADDR(CUSTOM_ADDR), .DATA(DATA), .CLR(CLR), .CLK(CLK),
    .C_IN(tty_memory_cell_25_c_out), .C_OUT(tty_memory_cell_27_c_out), .out_8(tty_memory_cell_27_out_8));
  TTY_MEMORY_CELL tty_memory_cell_28 (
    .W_R(W_R), .ENABLE(demultiplexer_1_out27), .CUSTOM_ADDR(CUSTOM_ADDR), .DATA(DATA), .CLR(CLR), .CLK(CLK),
    .C_IN(tty_memory_cell_26_c_out), .C_OUT(tty_memory_cell_28_c_out), .out_8(tty_memory_cell_28_out_8));
  TTY_MEMORY_CELL tty_memory_cell_29 (
    .W_R(W_R), .ENABLE(demultiplexer_1_out28), .CUSTOM_ADDR(CUSTOM_ADDR), .DATA(DATA), .CLR(CLR), .CLK(CLK),
    .C_IN(tty_memory_cell_28_c_out), .C_OUT(tty_memory_cell_29_c_out), .out_8(tty_memory_cell_29_out_8));
  TTY_MEMORY_CELL tty_memory_cell_30 (
    .W_R(W_R), .ENABLE(demultiplexer_1_out29), .CUSTOM_ADDR(CUSTOM_ADDR), .DATA(DATA), .CLR(CLR), .CLK(CLK),
    .C_IN(tty_memory_cell_29_c_out), .C_OUT(tty_memory_cell_30_c_out), .out_8(tty_memory_cell_30_out_8));
  TTY_MEMORY_CELL tty_memory_cell_31 (
    .W_R(W_R), .ENABLE(demultiplexer_1_out30), .CUSTOM_ADDR(CUSTOM_ADDR), .DATA(DATA), .CLR(CLR), .CLK(CLK),
    .C_IN(tty_memory_cell_30_c_out), .C_OUT(tty_memory_cell_31_c_out), .out_8(tty_memory_cell_31_out_8));
  TTY_MEMORY_CELL tty_memory_cell_32 (
    .W_R(W_R), .ENABLE(demultiplexer_1_out31), .CUSTOM_ADDR(CUSTOM_ADDR), .DATA(DATA), .CLR(CLR), .CLK(CLK),
    .C_IN(tty_memory_cell_31_c_out), .out_8(tty_memory_cell_32_out_8));  // open: C_OUT
endmodule

module TTY_CU (
  input  [6:0] DATA_IN,
  input  [7:0] D_BUS_IN,
  input  CLK,
  input  CLR,
  output SEL_MEM,
  output SEL_RAM,
  output [7:0] out_7
);

  wire comparator_1_eq, comparator_4_eq, comparator_5_eq, comparator_6_eq, comparator_7_eq, comparator_12_eq,
       or_1_out, t_ff_1_q;
  wire [0:0] comparator_9_eq;
  wire [1:0] and_1_out, and_2_out, and_3_out, and_4_out, bit_extender_1_out, bit_extender_2_out,
       bit_extender_3_out, bit_extender_4_out, counter_1_q, or_2_out;
  wire [1:1] comparator_10_eq, comparator_11_eq;
  wire [6:0] tty_memory_unit_1_out;
  wire [7:0] rom_1_data;
  wire [31:0] tty_alu_1_out;

  TTY_MEMORY_UNIT tty_memory_unit_1 (
    .W_R(t_ff_1_q), .CLK(CLK), .CLR(CLR), .DATA(DATA_IN), .OUT(tty_memory_unit_1_out));  // open: CUSTOM_ADDR_SEL, CUSTOM_ADDR, STATUS
  Comparator comparator_1 (.a(rom_1_data), .b(8'hf7), .eq(comparator_1_eq));  // open: gt, lt
  Comparator comparator_2 (.a(rom_1_data), .b(8'hf1), .eq(SEL_MEM));  // open: gt, lt
  Comparator comparator_3 (.a(rom_1_data), .b(8'hf2), .eq(SEL_RAM));  // open: gt, lt
  Comparator comparator_4 (.a(rom_1_data), .b(8'hf3), .eq(comparator_4_eq));  // open: gt, lt
  ROM rom_1 (.addr(D_BUS_IN), .data(rom_1_data));  // open: sel
  Comparator comparator_5 (.a(rom_1_data), .b(8'hf4), .eq(comparator_5_eq));  // open: gt, lt
  Comparator comparator_6 (.a(rom_1_data), .b(8'hf5), .eq(comparator_6_eq));  // open: gt, lt
  Comparator comparator_7 (.a(rom_1_data), .b(8'hf6), .eq(comparator_7_eq));  // open: gt, lt
  TTY_ALU tty_alu_1 (
    .ENABLE_1(1'b0), .DATA_IN(tty_memory_unit_1_out), .ENABLE(t_ff_1_q), .OP(or_2_out), .CLK(CLK), .CLR(CLR),
    .OUT(tty_alu_1_out));  // open: STATUS
  T_Flip_Flop t_ff_1 (
    .clk(comparator_1_eq), .T(comparator_1_eq), .Q(t_ff_1_q), .reset(or_1_out));  // open: Qn, preset, en
  or or_1 (or_1_out, CLR, comparator_12_eq);
  assign bit_extender_1_out = {{1{comparator_4_eq}}, comparator_4_eq};  // Bit_Extender bit_extender_1
  assign and_1_out = bit_extender_1_out & 2'b00;  // AND_Gate and_1, 2 bits wide
  assign bit_extender_2_out = {{1{comparator_5_eq}}, comparator_5_eq};  // Bit_Extender bit_extender_2
  assign and_2_out = bit_extender_2_out & 2'b01;  // AND_Gate and_2, 2 bits wide
  assign bit_extender_3_out = {{1{comparator_6_eq}}, comparator_6_eq};  // Bit_Extender bit_extender_3
  assign and_3_out = bit_extender_3_out & 2'b10;  // AND_Gate and_3, 2 bits wide
  assign bit_extender_4_out = {{1{comparator_7_eq}}, comparator_7_eq};  // Bit_Extender bit_extender_4
  assign and_4_out = bit_extender_4_out & 2'b11;  // AND_Gate and_4, 2 bits wide
  Bit_Extender #(.in_width(32), .out_width(8)) bit_extender_5 (.in(tty_alu_1_out), .out(out_7));
  Comparator #(.width(2)) comparator_8 (.a(and_1_out), .b(2'b00));  // open: gt, eq, lt
  Comparator #(.width(2)) comparator_9 (.a(and_2_out), .b(2'b01), .eq(comparator_9_eq[0]));  // open: gt, lt
  Comparator #(.width(2)) comparator_10 (.a(and_3_out), .b(2'b10), .eq(comparator_10_eq[1]));  // open: gt, lt
  Comparator #(.width(2)) comparator_11 (.a(and_4_out), .b(2'b11), .eq(comparator_11_eq[1]));  // open: gt, lt
  Counter #(.width(2), .max('h3)) counter_1 (
    .Q(counter_1_q), .clk(comparator_1_eq), .clr(comparator_12_eq));  // open: load, D, count, carry
  assign or_2_out = {1'b0, comparator_9_eq[0]} | {comparator_10_eq[1], 1'b0} | {2{comparator_11_eq[1]}};  // OR_Gate or_2, 2 bits wide
  Comparator #(.width(2)) comparator_12 (.a(counter_1_q), .b(2'b10), .eq(comparator_12_eq));  // open: gt, lt

  // Notes on the sheet:
  //   contents of rom_1 (hex, n*v repeats v):
  //   116*0 f1 f2 f3 f4 f5 f6 f7
endmodule

module TTY_ALU (
  input  ENABLE_1,
  input  [5:0] STATUS,
  input  [6:0] DATA_IN,
  input  ENABLE,
  input  [1:0] OP,
  input  CLK,
  input  CLR,
  output [31:0] OUT
);

  wire comparator_1_eq, comparator_2_eq, comparator_3_eq, comparator_3_gt, comparator_3_lt, comparator_4_eq,
       comparator_5_eq, comparator_6_eq, comparator_7_eq, or_1_out;
  wire [5:0] divider_1_rem;
  wire [6:0] and_1_out, and_2_out, bit_extender_1_out, bit_extender_2_out, bit_extender_3_out,
       multiplier_1_out;
  wire [31:0] adder_1_out, adder_2_out, and_3_out, and_4_out, and_5_out, and_6_out, and_7_out, and_8_out,
       and_9_out, bit_extender_4_out, bit_extender_5_out, bit_extender_6_out, bit_extender_7_out,
       bit_extender_8_out, bit_extender_9_out, bit_extender_10_out, bit_extender_11_out, bit_extender_12_out,
       bit_extender_13_out, bit_extender_14_out, bit_extender_15_out, or_2_out, register_1_q, register_2_q,
       register_3_q, subtractor_1_out;

  assign bit_extender_1_out = {{6{ENABLE}}, ENABLE};  // Bit_Extender bit_extender_1
  assign bit_extender_2_out = {{6{ENABLE}}, ENABLE};  // Bit_Extender bit_extender_2
  assign and_1_out = bit_extender_1_out & DATA_IN;  // AND_Gate and_1, 7 bits wide
  Comparator #(.width(7)) comparator_1 (.a(and_2_out), .b(7'b0100000), .eq(comparator_1_eq));  // open: gt, lt
  assign and_2_out = bit_extender_2_out & DATA_IN;  // AND_Gate and_2, 7 bits wide
  Comparator #(.width(2)) comparator_2 (.a(OP), .b(2'b11), .eq(comparator_2_eq));  // open: gt, lt
  assign bit_extender_3_out = {{1{1'b0}}, divider_1_rem};  // Bit_Extender bit_extender_3
  Divider #(.width(6)) divider_1 (.a(STATUS), .b(6'b100000), .rem(divider_1_rem));  // open: out, upper
  or or_1 (or_1_out, comparator_3_gt, comparator_3_lt);
  Comparator #(.width(7)) comparator_3 (
    .a(and_1_out), .b(7'b0100000), .gt(comparator_3_gt), .eq(comparator_3_eq), .lt(comparator_3_lt));
  assign bit_extender_4_out = {{31{1'b0}}, CLK};  // Bit_Extender bit_extender_4
  assign bit_extender_5_out = {{31{1'b0}}, comparator_1_eq};  // Bit_Extender bit_extender_5
  Adder #(.width(32)) adder_1 (.a(bit_extender_5_out), .b(register_1_q), .out(adder_1_out));  // open: cin, cout
  assign bit_extender_6_out = {{31{comparator_2_eq}}, comparator_2_eq};  // Bit_Extender bit_extender_6
  assign and_3_out = bit_extender_6_out & adder_1_out;  // AND_Gate and_3, 32 bits wide
  Multiplier #(.width(7)) multiplier_1 (
    .a(bit_extender_3_out), .b(7'b1100100), .out(multiplier_1_out));  // open: cin, cout
  assign bit_extender_7_out = {{31{1'b0}}, or_1_out};  // Bit_Extender bit_extender_7
  assign and_4_out = bit_extender_7_out & bit_extender_4_out & bit_extender_8_out;  // AND_Gate and_4, 32 bits wide
  assign bit_extender_8_out = {{31{ENABLE}}, ENABLE};  // Bit_Extender bit_extender_8
  // Probe on nothing
  Register #(.width(32), .trigger("falling")) register_1 (
    .D(and_3_out), .Q(register_1_q), .clk(CLK), .clr(CLR));  // open: en
  Comparator #(.width(2)) comparator_4 (.a(OP), .b(2'b01), .eq(comparator_4_eq));  // open: gt, lt
  Comparator #(.width(2)) comparator_5 (.a(OP), .b(2'b10), .eq(comparator_5_eq));  // open: gt, lt
  Adder #(.width(32)) adder_2 (.a(and_4_out), .b(or_2_out), .out(adder_2_out));  // open: cin, cout
  Subtractor #(.width(32)) subtractor_1 (
    .a(and_7_out), .b(bit_extender_9_out), .out(subtractor_1_out));  // open: bin, bout
  assign bit_extender_9_out = {{31{1'b0}}, comparator_3_eq};  // Bit_Extender bit_extender_9
  assign bit_extender_10_out = {{31{comparator_4_eq}}, comparator_4_eq};  // Bit_Extender bit_extender_10
  assign and_5_out = bit_extender_10_out & register_2_q;  // AND_Gate and_5, 32 bits wide
  assign bit_extender_11_out = {{31{comparator_5_eq}}, comparator_5_eq};  // Bit_Extender bit_extender_11
  assign and_6_out = bit_extender_11_out & register_3_q;  // AND_Gate and_6, 32 bits wide
  Register #(.width(32), .trigger("falling")) register_2 (
    .D(and_8_out), .Q(register_2_q), .clk(CLK), .clr(CLR));  // open: en
  Register #(.width(32), .trigger("falling")) register_3 (
    .D(subtractor_1_out), .Q(register_3_q), .clk(CLK), .clr(CLR));  // open: en
  assign bit_extender_12_out = {{31{comparator_6_eq}}, comparator_6_eq};  // Bit_Extender bit_extender_12
  Comparator #(.width(2)) comparator_6 (.a(OP), .b(2'b10), .eq(comparator_6_eq));  // open: gt, lt
  Comparator #(.width(2)) comparator_7 (.a(OP), .b(2'b01), .eq(comparator_7_eq));  // open: gt, lt
  assign bit_extender_13_out = {{31{comparator_7_eq}}, comparator_7_eq};  // Bit_Extender bit_extender_13
  assign or_2_out = and_5_out | and_6_out;  // OR_Gate or_2, 32 bits wide
  assign bit_extender_14_out = {{31{ENABLE_1}}, ENABLE_1};  // Bit_Extender bit_extender_14
  assign bit_extender_15_out = {{25{1'b0}}, multiplier_1_out};  // Bit_Extender bit_extender_15
  assign and_7_out = bit_extender_12_out & adder_2_out;  // AND_Gate and_7, 32 bits wide
  assign and_8_out = bit_extender_13_out & adder_2_out;  // AND_Gate and_8, 32 bits wide
  assign and_9_out = bit_extender_14_out & bit_extender_15_out;  // AND_Gate and_9, 32 bits wide
  Multiplexer #(.select(2), .width(32), .enable("false")) multiplexer_1 (
    .in0(and_9_out), .in1(register_2_q), .in2(register_3_q), .in3(register_1_q), .out(OUT), .sel(OP));

  // Notes on the sheet:
  //   0-backup percent
  //   1-characters
  //   2-characters without spaces
  //   3-words
endmodule

module _2_BIT_MEM (
  input  [1:0] in_1,
  input  CLR,
  input  EN,
  output [1:0] out_4,
  output [1:0] out_5
);

  wire and_1_out, or_1_out, or_2_out;
  wire [1:0] bit_extender_1_out;

  Register #(.width(2), .trigger("high")) register_1 (.D(in_1), .Q(out_4), .clk(and_1_out), .clr(CLR));  // open: en
  and and_1 (and_1_out, or_1_out, ~or_2_out);  // AND_Gate
  or or_1 (or_1_out, in_1[0], in_1[1]);
  or or_2 (or_2_out, out_4[0], out_4[1]);
  assign out_5 = out_4 & bit_extender_1_out;  // AND_Gate and_2, 2 bits wide
  assign bit_extender_1_out = {{1{EN}}, EN};  // Bit_Extender bit_extender_1
endmodule

module TEST_3 (
  input  in_1,
  input  in_2,
  input  in_3,
  input  in_4,
  output out_5,
  output out_6,
  output out_7
);

  wire transistor_1_out;
  wire [7:0] call_ret_1_addr, pc_1_address, pc_1_out_2, pc_1_out_3, pc_1_out_4, rom_1_data;

  Counter #(.width(4), .max('hf)) counter_1 ();  // open: load, D, count, Q, carry, clk, clr
  Transistor #(.\type ("n")) transistor_1 (.in(in_4), .out(transistor_1_out), .gate(out_5));
  // Probe on pc_1_address
  PC pc_1 (
    .PC_IN_1(call_ret_1_addr), .CLR_PC(in_3), .CLK(in_4), .D_BUS_IN(rom_1_data), .SEL_2(in_2),
    .ADDRESS(pc_1_address), .OUT_2(pc_1_out_2), .OUT_3(pc_1_out_3), .OUT_4(pc_1_out_4),
    .PC_IN_2(call_ret_1_addr), .CLR_ALL(in_3), .D_BUS_ENABLE(in_2));  // open: LOAD, OUT_1, SEL
  Counter #(.width(4), .max('hf)) counter_2 (.clk(transistor_1_out));  // open: load, D, count, Q, carry, clr
  CALL_RET call_ret_1 (
    .RET(in_1), .CALL(in_2), .DATA(pc_1_out_2), .DATA_1(pc_1_out_3), .DATA_2(pc_1_out_4),
    .PC_IN(pc_1_address), .CLK(in_4), .ADDR(call_ret_1_addr), .BIOS(out_6), .RAM(out_7), .MEM(out_5),
    .CLR(in_3));
  CORE core_1 ();  // open: D_BUS_IN, CLK, SELECT, RESET, KYBD, CLR_TTY, D_BUS_OUT, TTY, ADDRESS, CLK_KYBD, SEL_BIOS, SEL_RAM, SEL_MEM, MEM_WRITE, CLK_RAM, CLK_MEM, CLR_LED_MATRIX, CLR_BIOS, CLR_RAM, CLR_MEM, CLK_TTY, LED_MATRIX_ENABLE, RAM_READ, MEM_READ, RAM_WRITE
  ROM rom_1 (.addr(pc_1_address), .data(rom_1_data));  // open: sel
  CPU cpu_1 ();  // open: D_BUS_IN, KYBD_IN, SELECT, CLR, CLK, D_BUS_OUT, TTY_OUT, ADDRESS, MATRIX_ENABLE, SEL_BIOS, SEL_RAM, SEL_MEM, MEM_WRITE, CLK_RAM, CLK_MEM, CLR_LED_MATRIX, CLR_RAM, CLR_MEM, RAM_WRITE, RAM_READ, MEM_READ, CLK_KYBD, CLR_TTY, CLK_TTY, CLK_MATRIX, TEST, GRND_1, GRND_2
endmodule

module _1_BIT_MEM (
  input  in_1,
  input  EN,
  input  CLR,
  output out_4
);

  wire register_1_q;

  Register #(.width(1), .trigger("high")) register_1 (.D(in_1), .Q(register_1_q), .clk(in_1), .clr(CLR));  // open: en
  and and_1 (out_4, register_1_q, EN);
endmodule

module CPU (
  input  [7:0] D_BUS_IN,
  input  [6:0] KYBD_IN,
  input  TEST,
  input  SELECT,
  input  CLR,
  input  CLK,
  input  GRND_2,
  input  GRND_1,
  output [7:0] D_BUS_OUT,
  output [6:0] TTY_OUT,
  output [7:0] ADDRESS,
  output MATRIX_ENABLE,
  output CLK_MATRIX,
  output SEL_BIOS,
  output SEL_RAM,
  output SEL_MEM,
  output MEM_WRITE,
  output CLK_RAM,
  output CLK_MEM,
  output CLR_LED_MATRIX,
  output CLR_RAM,
  output CLR_MEM,
  output RAM_WRITE,
  output RAM_READ,
  output MEM_READ,
  output CLK_KYBD,
  output CLR_TTY,
  output CLK_TTY
);

  wire _5, _6, _7, A_B, accumialtor_1_carry_out, accumialtor_1_zero_out, alu_1_c_out, alu_1_equal, alu_1_hi,
       alu_1_lo, alu_1_zero, and_1_out, control_unit_1_addr_sel, control_unit_1_clr_regs,
       control_unit_1_clr_tty, control_unit_1_clr_x, control_unit_1_main_mux, control_unit_1_sel_regs,
       not_1_out, not_2_out, OP_MUX, or_2_out, or_3_out, or_7_1_out_3, registers_1_sum_update, SEL_REG,
       SEL_TEMPS, TEMPS, tunnel, tunnel_t, tunnel_t_t;
  wire [0:0] control_unit_1_tty_enable_and_matrx;
  wire [1:0] control_unit_1_a_sel, control_unit_1_b_sel, control_unit_1_mux_1, control_unit_1_mux_2,
       control_unit_1_tty_mux, REG, SEL_1, SEL_2, TEMP;
  wire [3:0] bit_extender_2_out, control_unit_1_op, multiplexer_3_out;
  wire [6:0] bit_extender_3_out, bit_extender_4_out, bit_extender_5_out, multiplexer_5_out;
  wire [7:0] accumialtor_1_alu_out, alu_1_result, bit_extender_1_out, control_unit_1_address,
       multiplexer_1_out, multiplexer_2_out, register_file_1_out, registers_1_a, registers_1_b, registers_1_c;

  assign bit_extender_1_out = {{1{KYBD_IN[6]}}, KYBD_IN};  // Bit_Extender bit_extender_1
  and and_1 (and_1_out, ~TEST, SELECT);  // AND_Gate
  Multiplexer #(.select(2), .width(8), .enable("false")) multiplexer_1 (
    .in0(D_BUS_IN), .in1(bit_extender_1_out), .in2(registers_1_c), .in3(register_file_1_out),
    .out(multiplexer_1_out), .sel(control_unit_1_mux_1));
  CONTROL_UNIT control_unit_1 (
    .D_BUS_IN(D_BUS_IN), .CLK(CLK), .CLR(CLR), .SELECT(and_1_out), .ZERO(accumialtor_1_zero_out),
    .CARRY(accumialtor_1_carry_out),
    .TTY_ENABLE_AND_MATRX({MATRIX_ENABLE, control_unit_1_tty_enable_and_matrx[0]}), .TEMP(TEMP),
    .OP(control_unit_1_op), .A_SEL(control_unit_1_a_sel), .B_SEL(control_unit_1_b_sel), .REGS(REG),
    .SEL_REGS(control_unit_1_sel_regs), .SEL_TEMPs(SEL_TEMPS), .SEL_BIOS(SEL_BIOS), .SEL_RAM(SEL_RAM),
    .SELMEM(SEL_MEM), .SEL_1(SEL_1), .SEL_2(SEL_2), .CLK_KYBD(CLK_KYBD), .CLR_TTY(control_unit_1_clr_tty),
    .CLR_LED_MATRIX(CLR_LED_MATRIX), .CLR_REGS(control_unit_1_clr_regs), .CLR_X(control_unit_1_clr_x),
    .CLK_RAM(CLK_RAM), .CLK_MEM(CLK_MEM), .ADDRESS(control_unit_1_address),
    .MAIN_MUX(control_unit_1_main_mux), .ADDR_SEL(control_unit_1_addr_sel), .MEM_READ(_5), .RAM_READ(_6),
    .RAM_WRITE(_7), .MEM_WRITE(MEM_WRITE), .Hi(tunnel_t_t), .EQUAL(tunnel_t), .Lo(tunnel), .SEL_REG(SEL_REG),
    .SEL_A_B(A_B), .SEL_TEMP(TEMPS), .MUX_1(control_unit_1_mux_1), .MUX_2(control_unit_1_mux_2),
    .TTY_MUX(control_unit_1_tty_mux), .OP_MUX(OP_MUX));
  or or_1 (CLR_TTY, control_unit_1_clr_tty, CLR);
  not not_1 (not_1_out, _7);
  or or_2 (or_2_out, not_1_out, _6);
  or or_3 (or_3_out, _5, not_2_out);
  not not_2 (not_2_out, MEM_WRITE);
  REGISTER_FILE register_file_1 (
    .SEL_TEMP(SEL_TEMPS), .TEMP(TEMP), .SEL_2(SEL_2), .D_BUS_IN(multiplexer_1_out),
    .CLR(control_unit_1_clr_regs), .OUT(register_file_1_out), .CLK(CLK), .TEMP_SEL(TEMPS));
  REGISTERS registers_1 (
    .SEL_REGS(control_unit_1_sel_regs), .SEL_1(SEL_1), .A_SEL(control_unit_1_a_sel),
    .D_BUS_IN(multiplexer_2_out), .REGS(REG), .CLR(control_unit_1_clr_regs), .B_SEL(control_unit_1_b_sel),
    .CLK(CLK), .A(registers_1_a), .C(registers_1_c), .B(registers_1_b), .SEL_REG(SEL_REG), .SEL_A_B(A_B),
    .SUM_UPDATE(registers_1_sum_update));
  Multiplexer #(.width(8), .enable("false")) multiplexer_2 (
    .in0(multiplexer_1_out), .in1(accumialtor_1_alu_out), .out(multiplexer_2_out),
    .sel(control_unit_1_main_mux));
  and and_2 (CLR_RAM, SEL_RAM, control_unit_1_clr_x);
  and and_3 (CLR_MEM, control_unit_1_clr_x, SEL_MEM);
  and and_4 (RAM_WRITE, _7, SEL_RAM);
  and and_5 (RAM_READ, SEL_RAM, or_2_out);
  and and_6 (MEM_READ, or_3_out, SEL_MEM);
  and and_7 (CLK_TTY, and_1_out, CLK, or_7_1_out_3);
  Multiplexer #(.width(4), .enable("false")) multiplexer_3 (
    .in0(control_unit_1_op), .in1(bit_extender_2_out), .out(multiplexer_3_out), .sel(OP_MUX));
  Bit_Extender #(.out_width(4)) bit_extender_2 (.in(register_file_1_out), .out(bit_extender_2_out));
  ALU alu_1 (
    .A(registers_1_a), .B(registers_1_b), .OP(multiplexer_3_out), .RESULT(alu_1_result), .ZERO(alu_1_zero),
    .C_OUT(alu_1_c_out), .Hi(alu_1_hi), .EQUAL(alu_1_equal), .Lo(alu_1_lo));  // open: C_IN, C_OUT_2
  Bit_Extender #(.out_width(7)) bit_extender_3 (.in(registers_1_c), .out(bit_extender_3_out));
  Bit_Extender #(.out_width(7)) bit_extender_4 (.in(register_file_1_out), .out(bit_extender_4_out));
  ACCUMIALTOR accumialtor_1 (
    .ALU_IN(alu_1_result), .ALU_OUT(accumialtor_1_alu_out), .CLR(control_unit_1_clr_regs),
    .ZERO_IN(alu_1_zero), .ZERO_OUT(accumialtor_1_zero_out), .CARRY_IN(alu_1_c_out),
    .CARRY_OUT(accumialtor_1_carry_out), .Hi_IN(alu_1_hi), .Hi_OUT(tunnel_t_t), .EQUAL_IN(alu_1_equal),
    .EQUAL_OUT(tunnel_t), .Lo_IN(alu_1_lo), .Lo_OUT(tunnel), .SUM_UPDATE(registers_1_sum_update));
  Bit_Extender #(.out_width(7)) bit_extender_5 (.in(multiplexer_1_out), .out(bit_extender_5_out));
  Multiplexer #(.select(2), .width(8), .enable("false")) multiplexer_4 (
    .in1(register_file_1_out), .in2(registers_1_c), .in3(multiplexer_1_out), .out(D_BUS_OUT),
    .sel(control_unit_1_mux_2));  // open: in0
  Transistor #(.\type ("n"), .width(7)) transistor_1 (
    .in(multiplexer_5_out), .out(TTY_OUT), .gate(control_unit_1_tty_enable_and_matrx[0]));
  Multiplexer #(.select(2), .width(7), .enable("false")) multiplexer_5 (
    .in0(bit_extender_5_out), .in1(bit_extender_3_out), .in2(bit_extender_4_out), .out(multiplexer_5_out),
    .sel(control_unit_1_tty_mux));  // open: in3
  Multiplexer #(.width(8), .enable("false")) multiplexer_6 (
    .in0(control_unit_1_address), .in1(accumialtor_1_alu_out), .out(ADDRESS), .sel(control_unit_1_addr_sel));
  OR_7 or_7_1 (.in_1(multiplexer_5_out), .in_2(control_unit_1_tty_enable_and_matrx[0]), .out_3(or_7_1_out_3));
  and and_8 (CLK_MATRIX, MATRIX_ENABLE, CLK);
  // also tied to GND on the sheet: {GRND_1, GRND_2}
endmodule

module JOYSTICK_LOGIC (
  input  [4:0] x,
  input  [4:0] y,
  output [31:0] out_3,
  output [31:0] out_4,
  output [31:0] out_5,
  output [31:0] out_6,
  output [31:0] out_7,
  output [31:0] out_8,
  output [31:0] out_9,
  output [31:0] out_10,
  output [31:0] out_11,
  output [31:0] out_12,
  output [31:0] out_13,
  output [31:0] out_14,
  output [31:0] out_15,
  output [31:0] out_16,
  output [31:0] out_17,
  output [31:0] out_18,
  output [31:0] out_19,
  output [31:0] out_20,
  output [31:0] out_21,
  output [31:0] out_22,
  output [31:0] out_23,
  output [31:0] out_24,
  output [31:0] out_25,
  output [31:0] out_26,
  output [31:0] out_27,
  output [31:0] out_28,
  output [31:0] out_29,
  output [31:0] out_30,
  output [31:0] out_31,
  output [31:0] out_32,
  output [31:0] out_33,
  output [31:0] out_34
);

  wire [31:0] x_axis_1_out_2;

  Directer directer_1 (
    .in_1(x_axis_1_out_2), .Vertical_Pos(y), .out_3(out_3), .out_4(out_4), .out_5(out_5), .out_6(out_6),
    .out_7(out_7), .out_8(out_8), .out_9(out_9), .out_10(out_10), .out_11(out_11), .out_12(out_12),
    .out_13(out_13), .out_14(out_14), .out_15(out_15), .out_16(out_16), .out_17(out_17), .out_18(out_18),
    .out_19(out_19), .out_20(out_20), .out_21(out_21), .out_22(out_22), .out_23(out_23), .out_24(out_24),
    .out_25(out_25), .out_26(out_26), .out_27(out_27), .out_28(out_28), .out_29(out_29), .out_30(out_30),
    .out_31(out_31), .out_32(out_32), .out_33(out_33), .out_34(out_34));
  X_Axis x_axis_1 (.Horizontal_Pos(x), .out_2(x_axis_1_out_2));
endmodule

module X_Axis (
  input  [4:0] Horizontal_Pos,
  output [31:0] out_2
);

  Comparator #(.width(5)) comparator_1 (.a(Horizontal_Pos), .b({5{1'b0}}), .eq(out_2[31]));  // open: gt, lt
  Comparator #(.width(5)) comparator_2 (.a(Horizontal_Pos), .b(5'b00001), .eq(out_2[30]));  // open: gt, lt
  Comparator #(.width(5)) comparator_3 (.a(Horizontal_Pos), .b(5'b00010), .eq(out_2[29]));  // open: gt, lt
  Comparator #(.width(5)) comparator_4 (.a(Horizontal_Pos), .b(5'b00011), .eq(out_2[28]));  // open: gt, lt
  Comparator #(.width(5)) comparator_5 (.a(Horizontal_Pos), .b(5'b00100), .eq(out_2[27]));  // open: gt, lt
  Comparator #(.width(5)) comparator_6 (.a(Horizontal_Pos), .b(5'b00101), .eq(out_2[26]));  // open: gt, lt
  Comparator #(.width(5)) comparator_7 (.a(Horizontal_Pos), .b(5'b00110), .eq(out_2[25]));  // open: gt, lt
  Comparator #(.width(5)) comparator_8 (.a(Horizontal_Pos), .b(5'b00111), .eq(out_2[24]));  // open: gt, lt
  Comparator #(.width(5)) comparator_9 (.a(Horizontal_Pos), .b(5'b01000), .eq(out_2[23]));  // open: gt, lt
  Comparator #(.width(5)) comparator_10 (.a(Horizontal_Pos), .b(5'b01001), .eq(out_2[22]));  // open: gt, lt
  Comparator #(.width(5)) comparator_11 (.a(Horizontal_Pos), .b(5'b01010), .eq(out_2[21]));  // open: gt, lt
  Comparator #(.width(5)) comparator_12 (.a(Horizontal_Pos), .b(5'b01011), .eq(out_2[20]));  // open: gt, lt
  Comparator #(.width(5)) comparator_13 (.a(Horizontal_Pos), .b(5'b01100), .eq(out_2[19]));  // open: gt, lt
  Comparator #(.width(5)) comparator_14 (.a(Horizontal_Pos), .b(5'b01101), .eq(out_2[18]));  // open: gt, lt
  Comparator #(.width(5)) comparator_15 (.a(Horizontal_Pos), .b(5'b01110), .eq(out_2[17]));  // open: gt, lt
  Comparator #(.width(5)) comparator_16 (.a(Horizontal_Pos), .b(5'b01111), .eq(out_2[16]));  // open: gt, lt
  Comparator #(.width(5)) comparator_17 (.a(Horizontal_Pos), .b(5'b10000), .eq(out_2[15]));  // open: gt, lt
  Comparator #(.width(5)) comparator_18 (.a(Horizontal_Pos), .b(5'b10001), .eq(out_2[14]));  // open: gt, lt
  Comparator #(.width(5)) comparator_19 (.a(Horizontal_Pos), .b(5'b10010), .eq(out_2[13]));  // open: gt, lt
  Comparator #(.width(5)) comparator_20 (.a(Horizontal_Pos), .b(5'b10011), .eq(out_2[12]));  // open: gt, lt
  Comparator #(.width(5)) comparator_21 (.a(Horizontal_Pos), .b(5'b10100), .eq(out_2[11]));  // open: gt, lt
  Comparator #(.width(5)) comparator_22 (.a(Horizontal_Pos), .b(5'b10101), .eq(out_2[10]));  // open: gt, lt
  Comparator #(.width(5)) comparator_23 (.a(Horizontal_Pos), .b(5'b10110), .eq(out_2[9]));  // open: gt, lt
  Comparator #(.width(5)) comparator_24 (.a(Horizontal_Pos), .b(5'b10111), .eq(out_2[8]));  // open: gt, lt
  Comparator #(.width(5)) comparator_25 (.a(Horizontal_Pos), .b(5'b11000), .eq(out_2[7]));  // open: gt, lt
  Comparator #(.width(5)) comparator_26 (.a(Horizontal_Pos), .b(5'b11001), .eq(out_2[6]));  // open: gt, lt
  Comparator #(.width(5)) comparator_27 (.a(Horizontal_Pos), .b(5'b11010), .eq(out_2[5]));  // open: gt, lt
  Comparator #(.width(5)) comparator_28 (.a(Horizontal_Pos), .b(5'b11011), .eq(out_2[4]));  // open: gt, lt
  Comparator #(.width(5)) comparator_29 (.a(Horizontal_Pos), .b(5'b11100), .eq(out_2[3]));  // open: gt, lt
  Comparator #(.width(5)) comparator_30 (.a(Horizontal_Pos), .b(5'b11101), .eq(out_2[2]));  // open: gt, lt
  Comparator #(.width(5)) comparator_31 (.a(Horizontal_Pos), .b(5'b11110), .eq(out_2[1]));  // open: gt, lt
  Comparator #(.width(5)) comparator_32 (.a(Horizontal_Pos), .b({5{1'b1}}), .eq(out_2[0]));  // open: gt, lt
endmodule

module Y_Axis (
  input  [31:0] Y_Axis,
  input  in_2,
  output [31:0] out_3
);

  and and_1 (out_3[31], Y_Axis[31], in_2);
  and and_2 (out_3[30], Y_Axis[30], in_2);
  and and_3 (out_3[29], Y_Axis[29], in_2);
  and and_4 (out_3[28], Y_Axis[28], in_2);
  and and_5 (out_3[27], Y_Axis[27], in_2);
  and and_6 (out_3[26], Y_Axis[26], in_2);
  and and_7 (out_3[25], Y_Axis[25], in_2);
  and and_8 (out_3[24], Y_Axis[24], in_2);
  and and_9 (out_3[23], Y_Axis[23], in_2);
  and and_10 (out_3[22], Y_Axis[22], in_2);
  and and_11 (out_3[21], Y_Axis[21], in_2);
  and and_12 (out_3[20], Y_Axis[20], in_2);
  and and_13 (out_3[19], Y_Axis[19], in_2);
  and and_14 (out_3[18], Y_Axis[18], in_2);
  and and_15 (out_3[17], Y_Axis[17], in_2);
  and and_16 (out_3[16], Y_Axis[16], in_2);
  and and_17 (out_3[15], Y_Axis[15], in_2);
  and and_18 (out_3[14], Y_Axis[14], in_2);
  and and_19 (out_3[13], Y_Axis[13], in_2);
  and and_20 (out_3[12], Y_Axis[12], in_2);
  and and_21 (out_3[11], Y_Axis[11], in_2);
  and and_22 (out_3[10], Y_Axis[10], in_2);
  and and_23 (out_3[9], Y_Axis[9], in_2);
  and and_24 (out_3[8], Y_Axis[8], in_2);
  and and_25 (out_3[7], Y_Axis[7], in_2);
  and and_26 (out_3[6], Y_Axis[6], in_2);
  and and_27 (out_3[5], Y_Axis[5], in_2);
  and and_28 (out_3[4], Y_Axis[4], in_2);
  and and_29 (out_3[3], Y_Axis[3], in_2);
  and and_30 (out_3[2], Y_Axis[2], in_2);
  and and_31 (out_3[1], Y_Axis[1], in_2);
  and and_32 (out_3[0], Y_Axis[0], in_2);

  // Other names for the same wires on the sheet: Block = in_2
endmodule

module Directer (
  input  [31:0] in_1,
  input  [4:0] Vertical_Pos,
  output [31:0] out_3,
  output [31:0] out_4,
  output [31:0] out_5,
  output [31:0] out_6,
  output [31:0] out_7,
  output [31:0] out_8,
  output [31:0] out_9,
  output [31:0] out_10,
  output [31:0] out_11,
  output [31:0] out_12,
  output [31:0] out_13,
  output [31:0] out_14,
  output [31:0] out_15,
  output [31:0] out_16,
  output [31:0] out_17,
  output [31:0] out_18,
  output [31:0] out_19,
  output [31:0] out_20,
  output [31:0] out_21,
  output [31:0] out_22,
  output [31:0] out_23,
  output [31:0] out_24,
  output [31:0] out_25,
  output [31:0] out_26,
  output [31:0] out_27,
  output [31:0] out_28,
  output [31:0] out_29,
  output [31:0] out_30,
  output [31:0] out_31,
  output [31:0] out_32,
  output [31:0] out_33,
  output [31:0] out_34
);

  wire comparator_1_eq, comparator_2_eq, comparator_3_eq, comparator_4_eq, comparator_5_eq, comparator_6_eq,
       comparator_7_eq, comparator_8_eq, comparator_9_eq, comparator_10_eq, comparator_11_eq,
       comparator_12_eq, comparator_13_eq, comparator_14_eq, comparator_15_eq, comparator_16_eq,
       comparator_17_eq, comparator_18_eq, comparator_19_eq, comparator_20_eq, comparator_21_eq,
       comparator_22_eq, comparator_23_eq, comparator_24_eq, comparator_25_eq, comparator_26_eq,
       comparator_27_eq, comparator_28_eq, comparator_29_eq, comparator_30_eq, comparator_31_eq,
       comparator_32_eq;

  Comparator #(.width(5)) comparator_1 (.a({5{1'b0}}), .b(Vertical_Pos), .eq(comparator_1_eq));  // open: gt, lt
  Comparator #(.width(5)) comparator_2 (.a(5'b00001), .b(Vertical_Pos), .eq(comparator_2_eq));  // open: gt, lt
  Comparator #(.width(5)) comparator_3 (.a(5'b00010), .b(Vertical_Pos), .eq(comparator_3_eq));  // open: gt, lt
  Comparator #(.width(5)) comparator_4 (.a(5'b00011), .b(Vertical_Pos), .eq(comparator_4_eq));  // open: gt, lt
  Comparator #(.width(5)) comparator_5 (.a(5'b00100), .b(Vertical_Pos), .eq(comparator_5_eq));  // open: gt, lt
  Comparator #(.width(5)) comparator_6 (.a(5'b00101), .b(Vertical_Pos), .eq(comparator_6_eq));  // open: gt, lt
  Comparator #(.width(5)) comparator_7 (.a(5'b00110), .b(Vertical_Pos), .eq(comparator_7_eq));  // open: gt, lt
  Comparator #(.width(5)) comparator_8 (.a(5'b00111), .b(Vertical_Pos), .eq(comparator_8_eq));  // open: gt, lt
  Comparator #(.width(5)) comparator_9 (.a(5'b01000), .b(Vertical_Pos), .eq(comparator_9_eq));  // open: gt, lt
  Comparator #(.width(5)) comparator_10 (.a(5'b01001), .b(Vertical_Pos), .eq(comparator_10_eq));  // open: gt, lt
  Comparator #(.width(5)) comparator_11 (.a(5'b01010), .b(Vertical_Pos), .eq(comparator_11_eq));  // open: gt, lt
  Comparator #(.width(5)) comparator_12 (.a(5'b01011), .b(Vertical_Pos), .eq(comparator_12_eq));  // open: gt, lt
  Comparator #(.width(5)) comparator_13 (.a(5'b01100), .b(Vertical_Pos), .eq(comparator_13_eq));  // open: gt, lt
  Comparator #(.width(5)) comparator_14 (.a(5'b01101), .b(Vertical_Pos), .eq(comparator_14_eq));  // open: gt, lt
  Comparator #(.width(5)) comparator_15 (.a(5'b01110), .b(Vertical_Pos), .eq(comparator_15_eq));  // open: gt, lt
  Comparator #(.width(5)) comparator_16 (.a(5'b01111), .b(Vertical_Pos), .eq(comparator_16_eq));  // open: gt, lt
  Comparator #(.width(5)) comparator_17 (.a(5'b10000), .b(Vertical_Pos), .eq(comparator_17_eq));  // open: gt, lt
  Comparator #(.width(5)) comparator_18 (.a(5'b10001), .b(Vertical_Pos), .eq(comparator_18_eq));  // open: gt, lt
  Comparator #(.width(5)) comparator_19 (.a(5'b10010), .b(Vertical_Pos), .eq(comparator_19_eq));  // open: gt, lt
  Comparator #(.width(5)) comparator_20 (.a(5'b10011), .b(Vertical_Pos), .eq(comparator_20_eq));  // open: gt, lt
  Comparator #(.width(5)) comparator_21 (.a(5'b10100), .b(Vertical_Pos), .eq(comparator_21_eq));  // open: gt, lt
  Comparator #(.width(5)) comparator_22 (.a(5'b10101), .b(Vertical_Pos), .eq(comparator_22_eq));  // open: gt, lt
  Comparator #(.width(5)) comparator_23 (.a(5'b10110), .b(Vertical_Pos), .eq(comparator_23_eq));  // open: gt, lt
  Comparator #(.width(5)) comparator_24 (.a(5'b10111), .b(Vertical_Pos), .eq(comparator_24_eq));  // open: gt, lt
  Comparator #(.width(5)) comparator_25 (.a(5'b11000), .b(Vertical_Pos), .eq(comparator_25_eq));  // open: gt, lt
  Comparator #(.width(5)) comparator_26 (.a(5'b11001), .b(Vertical_Pos), .eq(comparator_26_eq));  // open: gt, lt
  Comparator #(.width(5)) comparator_27 (.a(5'b11010), .b(Vertical_Pos), .eq(comparator_27_eq));  // open: gt, lt
  Comparator #(.width(5)) comparator_28 (.a(5'b11011), .b(Vertical_Pos), .eq(comparator_28_eq));  // open: gt, lt
  Comparator #(.width(5)) comparator_29 (.a(5'b11100), .b(Vertical_Pos), .eq(comparator_29_eq));  // open: gt, lt
  Comparator #(.width(5)) comparator_30 (.a(5'b11101), .b(Vertical_Pos), .eq(comparator_30_eq));  // open: gt, lt
  Comparator #(.width(5)) comparator_31 (.a(5'b11110), .b(Vertical_Pos), .eq(comparator_31_eq));  // open: gt, lt
  Comparator #(.width(5)) comparator_32 (.a({5{1'b1}}), .b(Vertical_Pos), .eq(comparator_32_eq));  // open: gt, lt
  Y_Axis y_axis_1 (.Y_Axis(in_1), .in_2(comparator_1_eq), .out_3(out_3));
  Y_Axis y_axis_2 (.Y_Axis(in_1), .in_2(comparator_2_eq), .out_3(out_4));
  Y_Axis y_axis_3 (.Y_Axis(in_1), .in_2(comparator_3_eq), .out_3(out_5));
  Y_Axis y_axis_4 (.Y_Axis(in_1), .in_2(comparator_4_eq), .out_3(out_6));
  Y_Axis y_axis_5 (.Y_Axis(in_1), .in_2(comparator_5_eq), .out_3(out_7));
  Y_Axis y_axis_6 (.Y_Axis(in_1), .in_2(comparator_6_eq), .out_3(out_8));
  Y_Axis y_axis_7 (.Y_Axis(in_1), .in_2(comparator_7_eq), .out_3(out_9));
  Y_Axis y_axis_8 (.Y_Axis(in_1), .in_2(comparator_8_eq), .out_3(out_10));
  Y_Axis y_axis_9 (.Y_Axis(in_1), .in_2(comparator_9_eq), .out_3(out_11));
  Y_Axis y_axis_10 (.Y_Axis(in_1), .in_2(comparator_10_eq), .out_3(out_12));
  Y_Axis y_axis_11 (.Y_Axis(in_1), .in_2(comparator_11_eq), .out_3(out_13));
  Y_Axis y_axis_12 (.Y_Axis(in_1), .in_2(comparator_12_eq), .out_3(out_14));
  Y_Axis y_axis_13 (.Y_Axis(in_1), .in_2(comparator_13_eq), .out_3(out_15));
  Y_Axis y_axis_14 (.Y_Axis(in_1), .in_2(comparator_14_eq), .out_3(out_16));
  Y_Axis y_axis_15 (.Y_Axis(in_1), .in_2(comparator_15_eq), .out_3(out_17));
  Y_Axis y_axis_16 (.Y_Axis(in_1), .in_2(comparator_16_eq), .out_3(out_18));
  Y_Axis y_axis_17 (.Y_Axis(in_1), .in_2(comparator_17_eq), .out_3(out_19));
  Y_Axis y_axis_18 (.Y_Axis(in_1), .in_2(comparator_18_eq), .out_3(out_20));
  Y_Axis y_axis_19 (.Y_Axis(in_1), .in_2(comparator_19_eq), .out_3(out_21));
  Y_Axis y_axis_20 (.Y_Axis(in_1), .in_2(comparator_20_eq), .out_3(out_22));
  Y_Axis y_axis_21 (.Y_Axis(in_1), .in_2(comparator_21_eq), .out_3(out_23));
  Y_Axis y_axis_22 (.Y_Axis(in_1), .in_2(comparator_22_eq), .out_3(out_24));
  Y_Axis y_axis_23 (.Y_Axis(in_1), .in_2(comparator_23_eq), .out_3(out_25));
  Y_Axis y_axis_24 (.Y_Axis(in_1), .in_2(comparator_24_eq), .out_3(out_26));
  Y_Axis y_axis_25 (.Y_Axis(in_1), .in_2(comparator_25_eq), .out_3(out_27));
  Y_Axis y_axis_26 (.Y_Axis(in_1), .in_2(comparator_26_eq), .out_3(out_28));
  Y_Axis y_axis_27 (.Y_Axis(in_1), .in_2(comparator_27_eq), .out_3(out_29));
  Y_Axis y_axis_28 (.Y_Axis(in_1), .in_2(comparator_28_eq), .out_3(out_30));
  Y_Axis y_axis_29 (.Y_Axis(in_1), .in_2(comparator_29_eq), .out_3(out_31));
  Y_Axis y_axis_30 (.Y_Axis(in_1), .in_2(comparator_30_eq), .out_3(out_32));
  Y_Axis y_axis_31 (.Y_Axis(in_1), .in_2(comparator_31_eq), .out_3(out_33));
  Y_Axis y_axis_32 (.Y_Axis(in_1), .in_2(comparator_32_eq), .out_3(out_34));
endmodule

module OR_2 (
  input  [1:0] in_1,
  output out_2
);

  or or_1 (out_2, in_1[0], in_1[1]);
endmodule

module Main (
  input  BIOS,
  input  Select
);

  wire and_1_out, clock_1_out, cpu_2_clk_kybd, cpu_2_clk_matrix, cpu_2_clk_mem, cpu_2_clk_ram, cpu_2_clk_tty,
       cpu_2_clr_led_matrix, cpu_2_clr_mem, cpu_2_clr_ram, cpu_2_clr_tty, cpu_2_matrix_enable,
       cpu_2_mem_read, cpu_2_ram_write, cpu_2_sel_bios, cpu_2_sel_mem, cpu_2_sel_ram, Reset_out, undriven,
       undriven_2;
  wire [6:0] cpu_2_tty_out, keyboard_1_data;
  wire [7:0] cpu_2_address, cpu_2_d_bus_out, rom_1_data;
  wire [31:0] led_matrix_ctrl_1_out_6, led_matrix_ctrl_1_out_7, led_matrix_ctrl_1_out_8,
       led_matrix_ctrl_1_out_9, led_matrix_ctrl_1_out_10, led_matrix_ctrl_1_out_11, led_matrix_ctrl_1_out_12,
       led_matrix_ctrl_1_out_13, led_matrix_ctrl_1_out_14, led_matrix_ctrl_1_out_15,
       led_matrix_ctrl_1_out_16, led_matrix_ctrl_1_out_17, led_matrix_ctrl_1_out_18,
       led_matrix_ctrl_1_out_19, led_matrix_ctrl_1_out_20, led_matrix_ctrl_1_out_21,
       led_matrix_ctrl_1_out_22, led_matrix_ctrl_1_out_23, led_matrix_ctrl_1_out_24,
       led_matrix_ctrl_1_out_25, led_matrix_ctrl_1_out_26, led_matrix_ctrl_1_out_27,
       led_matrix_ctrl_1_out_28, led_matrix_ctrl_1_out_29, led_matrix_ctrl_1_out_30,
       led_matrix_ctrl_1_out_31, led_matrix_ctrl_1_out_32, led_matrix_ctrl_1_out_33,
       led_matrix_ctrl_1_out_34, led_matrix_ctrl_1_out_35, led_matrix_ctrl_1_out_36, led_matrix_ctrl_1_out_37;

  CPU cpu_1 ();  // open: D_BUS_IN, KYBD_IN, SELECT, CLR, CLK, D_BUS_OUT, TTY_OUT, ADDRESS, MATRIX_ENABLE, SEL_BIOS, SEL_RAM, SEL_MEM, MEM_WRITE, CLK_RAM, CLK_MEM, CLR_LED_MATRIX, CLR_RAM, CLR_MEM, RAM_WRITE, RAM_READ, MEM_READ, CLK_KYBD, CLR_TTY, CLK_TTY, CLK_MATRIX, TEST, GRND_1, GRND_2
  ROM rom_1 (.addr(cpu_2_address), .data(rom_1_data), .sel(cpu_2_sel_bios));
  CPU cpu_2 (
    .D_BUS_IN(rom_1_data), .KYBD_IN(keyboard_1_data), .SELECT(Select), .CLR(Reset_out), .CLK(clock_1_out),
    .D_BUS_OUT(cpu_2_d_bus_out), .TTY_OUT(cpu_2_tty_out), .ADDRESS(cpu_2_address),
    .MATRIX_ENABLE(cpu_2_matrix_enable), .SEL_BIOS(cpu_2_sel_bios), .SEL_RAM(cpu_2_sel_ram),
    .SEL_MEM(cpu_2_sel_mem), .CLK_RAM(cpu_2_clk_ram), .CLK_MEM(cpu_2_clk_mem),
    .CLR_LED_MATRIX(cpu_2_clr_led_matrix), .CLR_RAM(cpu_2_clr_ram), .CLR_MEM(cpu_2_clr_mem),
    .RAM_WRITE(cpu_2_ram_write), .MEM_READ(cpu_2_mem_read), .CLK_KYBD(cpu_2_clk_kybd),
    .CLR_TTY(cpu_2_clr_tty), .CLK_TTY(cpu_2_clk_tty), .CLK_MATRIX(cpu_2_clk_matrix), .TEST(1'b0),
    .GRND_1(1'b0), .GRND_2(undriven));  // open: MEM_WRITE, RAM_READ
  Clock clock_1 (.out(clock_1_out));
  Counter #(.width(4), .max('hf)) counter_1 (.clk(and_1_out));  // open: load, D, count, Q, carry, clr
  and and_1 (and_1_out, BIOS, clock_1_out);
  RAM #(.bus("separate")) ram_1 (
    .addr(cpu_2_address), .din(cpu_2_d_bus_out), .data(rom_1_data), .str(undriven_2), .sel(cpu_2_sel_ram),
    .clk(cpu_2_clk_ram), .ld(cpu_2_mem_read), .clr(cpu_2_clr_ram));
  ROM rom_2 ();  // open: addr, data, sel
  RAM #(.bus("separate")) ram_2 (
    .addr(cpu_2_address), .din(cpu_2_d_bus_out), .data(rom_1_data), .str(cpu_2_ram_write),
    .sel(cpu_2_sel_mem), .clk(cpu_2_clk_mem), .clr(cpu_2_clr_mem));  // open: ld
  // Probe on cpu_2_address
  Button Reset (.out(Reset_out));
  LED_MATRIX_CTRL led_matrix_ctrl_1 (
    .DATA_IN(cpu_2_d_bus_out), .ADDRESS_IN(cpu_2_address), .out_6(led_matrix_ctrl_1_out_6),
    .out_7(led_matrix_ctrl_1_out_7), .out_8(led_matrix_ctrl_1_out_8), .out_9(led_matrix_ctrl_1_out_9),
    .out_10(led_matrix_ctrl_1_out_10), .out_11(led_matrix_ctrl_1_out_11), .out_12(led_matrix_ctrl_1_out_12),
    .out_13(led_matrix_ctrl_1_out_13), .out_14(led_matrix_ctrl_1_out_14), .out_15(led_matrix_ctrl_1_out_15),
    .out_16(led_matrix_ctrl_1_out_16), .out_17(led_matrix_ctrl_1_out_17), .out_18(led_matrix_ctrl_1_out_18),
    .out_19(led_matrix_ctrl_1_out_19), .out_20(led_matrix_ctrl_1_out_20), .out_21(led_matrix_ctrl_1_out_21),
    .out_22(led_matrix_ctrl_1_out_22), .out_23(led_matrix_ctrl_1_out_23), .out_24(led_matrix_ctrl_1_out_24),
    .out_25(led_matrix_ctrl_1_out_25), .out_26(led_matrix_ctrl_1_out_26), .out_27(led_matrix_ctrl_1_out_27),
    .out_28(led_matrix_ctrl_1_out_28), .out_29(led_matrix_ctrl_1_out_29), .out_30(led_matrix_ctrl_1_out_30),
    .out_31(led_matrix_ctrl_1_out_31), .out_32(led_matrix_ctrl_1_out_32), .out_33(led_matrix_ctrl_1_out_33),
    .out_34(led_matrix_ctrl_1_out_34), .out_35(led_matrix_ctrl_1_out_35), .out_36(led_matrix_ctrl_1_out_36),
    .out_37(led_matrix_ctrl_1_out_37), .Clock_IN(cpu_2_clk_matrix), .Select(cpu_2_matrix_enable),
    .CLEAR(cpu_2_clr_led_matrix));
  DotMatrix #(.inputtype("row"), .matrixcols(32), .matrixrows(32)) dotmatrix_1 (
    .row0(led_matrix_ctrl_1_out_6), .row1(led_matrix_ctrl_1_out_7), .row2(led_matrix_ctrl_1_out_8),
    .row3(led_matrix_ctrl_1_out_9), .row4(led_matrix_ctrl_1_out_10), .row5(led_matrix_ctrl_1_out_11),
    .row6(led_matrix_ctrl_1_out_12), .row7(led_matrix_ctrl_1_out_13), .row8(led_matrix_ctrl_1_out_14),
    .row9(led_matrix_ctrl_1_out_15), .row10(led_matrix_ctrl_1_out_16), .row11(led_matrix_ctrl_1_out_17),
    .row12(led_matrix_ctrl_1_out_18), .row13(led_matrix_ctrl_1_out_19), .row14(led_matrix_ctrl_1_out_20),
    .row15(led_matrix_ctrl_1_out_21), .row16(led_matrix_ctrl_1_out_22), .row17(led_matrix_ctrl_1_out_23),
    .row18(led_matrix_ctrl_1_out_24), .row19(led_matrix_ctrl_1_out_25), .row20(led_matrix_ctrl_1_out_26),
    .row21(led_matrix_ctrl_1_out_27), .row22(led_matrix_ctrl_1_out_28), .row23(led_matrix_ctrl_1_out_29),
    .row24(led_matrix_ctrl_1_out_30), .row25(led_matrix_ctrl_1_out_31), .row26(led_matrix_ctrl_1_out_32),
    .row27(led_matrix_ctrl_1_out_33), .row28(led_matrix_ctrl_1_out_34), .row29(led_matrix_ctrl_1_out_35),
    .row30(led_matrix_ctrl_1_out_36), .row31(led_matrix_ctrl_1_out_37));
  DotMatrix #(.inputtype("row"), .matrixcols(32), .matrixrows(1), .dotshape("circle")) dotmatrix_2 ();  // open: row0
  TTY tty_1 (.data(cpu_2_tty_out), .clk(cpu_2_clk_tty), .clr(cpu_2_clr_tty));  // open: we
  Keyboard keyboard_1 (.clk(cpu_2_clk_kybd), .data(keyboard_1_data));  // open: re, clr, avail
  _7_Segment_Display u_7_segment_display_1 ();  // open: g, f, a, b, e, d, c, dp
  Joystick #(.bits(5)) joystick_1 ();  // open: x, y
  _7_Segment_Display u_7_segment_display_2 ();  // open: g, f, a, b, e, d, c, dp
  _7_Segment_Display u_7_segment_display_3 ();  // open: g, f, a, b, e, d, c, dp

  // Notes on the sheet:
  //   contents of rom_1 (hex, n*v repeats v):
  //   e 4 77 38 4*5f 57 65 6c 63 6f 6d 65 4*5f 20 a a 38 2d 42 49 54 20 43 50 55 20 a 56 2e 31 2e 30 a 47
  //   65 74 74 69 6e 67 20 52 65 61 64 79 2e 2e 2e 0 4 3c 53 b 49 11*0 4 4c 53 c 32 11*0 4 5c 53 d 63 19*0
  //   9 40 45 43 0 50 55 57
  //   RAM
  //   MEM
  //   contents of rom_2 (hex, n*v repeats v):
  //   e 4 a3 50 43 68 6f 6f 73 65 20 50 72 6f 67 72 61 6d 3a a a 31 2e 43 50 55 20 49 4e 46 4f a 32 2e 43
  //   61 6c 63 75 6c 61 74 6f 72 a 33 2e 4d 6f 72 65 2e 2e 2e a a 45 6e 74 65 72 20 63 6f 6d 6d 61 6e 64
  //   20 6e 75 6d 62 65 72 3a 7*0 1 5 13 a 2 a a b 7 20 a0 d5 2 a a c 7 20 f0 d5 2 a a d 7 20 d0 d5 7 20
  //   50 c5
endmodule

module PC_2 (
  input  PC_2_EN,
  input  ENABLE,
  input  [7:0] PC_IN,
  input  SELECT,
  input  CLK,
  input  CLR,
  output [7:0] ADDRESS
);

  wire and_1_out, not_1_out, or_1_out_2;
  wire [7:0] bit_extender_1_out, counter_1_q;

  and and_1 (and_1_out, SELECT, PC_2_EN, not_1_out);
  not not_1 (not_1_out, ENABLE);
  assign bit_extender_1_out = {{7{and_1_out}}, and_1_out};  // Bit_Extender bit_extender_1
  OR or_1 (.in_1(PC_IN), .out_2(or_1_out_2));
  Counter counter_1 (
    .load(or_1_out_2), .D(PC_IN), .count(and_1_out), .Q(counter_1_q), .clk(CLK), .clr(CLR));  // open: carry
  assign ADDRESS = bit_extender_1_out & counter_1_q;  // AND_Gate and_2, 8 bits wide
endmodule

module VID_MEM (
  input  [7:0] DATA_IN,
  input  Clock,
  input  Clear,
  input  CT_4,
  input  CT_3,
  input  CT_2,
  input  CT_1,
  output [31:0] out_8,
  output [7:0] DATA_OUT,
  output Clock_Out,
  output Clear_Out
);

  Register register_1 (.D(DATA_IN), .en(CT_4), .Q(out_8[31:24]), .clk(Clock), .clr(Clear));
  Register register_2 (.D(DATA_IN), .en(CT_3), .Q(out_8[23:16]), .clk(Clock), .clr(Clear));
  Register register_3 (.D(DATA_IN), .en(CT_2), .Q(out_8[15:8]), .clk(Clock), .clr(Clear));
  Register register_4 (.D(DATA_IN), .en(CT_1), .Q(out_8[7:0]), .clk(Clock), .clr(Clear));

  assign Clear_Out = Clear;
  assign Clock_Out = Clock;
  assign DATA_OUT = DATA_IN;

  // Notes on the sheet:
  //   CT_2: pull=down
  //   DATA_IN: pull=down
  //   CT_4: pull=down
  //   Clock: pull=down
  //   CT_1: pull=down
  //   Clear: pull=down
  //   CT_3: pull=down
endmodule

module VID_MEM_32 (
  input  [7:0] DATA,
  input  Clock_In,
  input  Clear,
  input  [7:0] ADDRESS,
  input  ENABLE,
  output [31:0] OUT_1,
  output [31:0] OUT_2,
  output [31:0] OUT_3,
  output [31:0] OUT_4,
  output [31:0] OUT_5,
  output [31:0] OUT_6,
  output [31:0] OUT_7,
  output [7:0] DATA_2,
  output [31:0] OUT_8,
  output Clear_2,
  output Clock_Out
);

  wire demultiplexer_1_out0, demultiplexer_1_out1, demultiplexer_1_out2, demultiplexer_1_out3,
       demultiplexer_1_out4, demultiplexer_1_out5, demultiplexer_1_out6, demultiplexer_1_out7,
       demultiplexer_1_out8, demultiplexer_1_out9, demultiplexer_1_out10, demultiplexer_1_out11,
       demultiplexer_1_out12, demultiplexer_1_out13, demultiplexer_1_out14, demultiplexer_1_out15,
       demultiplexer_1_out16, demultiplexer_1_out17, demultiplexer_1_out18, demultiplexer_1_out19,
       demultiplexer_1_out20, demultiplexer_1_out21, demultiplexer_1_out22, demultiplexer_1_out23,
       demultiplexer_1_out24, demultiplexer_1_out25, demultiplexer_1_out26, demultiplexer_1_out27,
       demultiplexer_1_out28, demultiplexer_1_out29, demultiplexer_1_out30, demultiplexer_1_out31,
       vid_mem_1_clear_out, vid_mem_1_clock_out, vid_mem_2_clear_out, vid_mem_2_clock_out,
       vid_mem_3_clear_out, vid_mem_3_clock_out, vid_mem_4_clear_out, vid_mem_4_clock_out,
       vid_mem_5_clear_out, vid_mem_5_clock_out, vid_mem_6_clear_out, vid_mem_6_clock_out,
       vid_mem_7_clear_out, vid_mem_7_clock_out;
  wire [7:0] vid_mem_1_data_out, vid_mem_2_data_out, vid_mem_3_data_out, vid_mem_4_data_out,
       vid_mem_5_data_out, vid_mem_6_data_out, vid_mem_7_data_out;

  Demultiplexer #(.select(5)) demultiplexer_1 (
    .out0(demultiplexer_1_out0), .out1(demultiplexer_1_out1), .out2(demultiplexer_1_out2),
    .out3(demultiplexer_1_out3), .out4(demultiplexer_1_out4), .out5(demultiplexer_1_out5),
    .out6(demultiplexer_1_out6), .out7(demultiplexer_1_out7), .out8(demultiplexer_1_out8),
    .out9(demultiplexer_1_out9), .out10(demultiplexer_1_out10), .out11(demultiplexer_1_out11),
    .out12(demultiplexer_1_out12), .out13(demultiplexer_1_out13), .out14(demultiplexer_1_out14),
    .out15(demultiplexer_1_out15), .out16(demultiplexer_1_out16), .out17(demultiplexer_1_out17),
    .out18(demultiplexer_1_out18), .out19(demultiplexer_1_out19), .out20(demultiplexer_1_out20),
    .out21(demultiplexer_1_out21), .out22(demultiplexer_1_out22), .out23(demultiplexer_1_out23),
    .out24(demultiplexer_1_out24), .out25(demultiplexer_1_out25), .out26(demultiplexer_1_out26),
    .out27(demultiplexer_1_out27), .out28(demultiplexer_1_out28), .out29(demultiplexer_1_out29),
    .out30(demultiplexer_1_out30), .out31(demultiplexer_1_out31), .in(ENABLE), .sel(ADDRESS[4:0]));  // open: en
  VID_MEM vid_mem_1 (
    .DATA_IN(DATA), .Clock(Clock_In), .Clear(Clear), .out_8(OUT_1), .DATA_OUT(vid_mem_1_data_out),
    .Clock_Out(vid_mem_1_clock_out), .Clear_Out(vid_mem_1_clear_out), .CT_4(demultiplexer_1_out0),
    .CT_3(demultiplexer_1_out1), .CT_2(demultiplexer_1_out2), .CT_1(demultiplexer_1_out3));
  VID_MEM vid_mem_2 (
    .DATA_IN(vid_mem_1_data_out), .Clock(vid_mem_1_clock_out), .Clear(vid_mem_1_clear_out), .out_8(OUT_2),
    .DATA_OUT(vid_mem_2_data_out), .Clock_Out(vid_mem_2_clock_out), .Clear_Out(vid_mem_2_clear_out),
    .CT_4(demultiplexer_1_out4), .CT_3(demultiplexer_1_out5), .CT_2(demultiplexer_1_out6),
    .CT_1(demultiplexer_1_out7));
  VID_MEM vid_mem_3 (
    .DATA_IN(vid_mem_2_data_out), .Clock(vid_mem_2_clock_out), .Clear(vid_mem_2_clear_out), .out_8(OUT_3),
    .DATA_OUT(vid_mem_3_data_out), .Clock_Out(vid_mem_3_clock_out), .Clear_Out(vid_mem_3_clear_out),
    .CT_4(demultiplexer_1_out8), .CT_3(demultiplexer_1_out9), .CT_2(demultiplexer_1_out10),
    .CT_1(demultiplexer_1_out11));
  VID_MEM vid_mem_4 (
    .DATA_IN(vid_mem_3_data_out), .Clock(vid_mem_3_clock_out), .Clear(vid_mem_3_clear_out), .out_8(OUT_4),
    .DATA_OUT(vid_mem_4_data_out), .Clock_Out(vid_mem_4_clock_out), .Clear_Out(vid_mem_4_clear_out),
    .CT_4(demultiplexer_1_out12), .CT_3(demultiplexer_1_out13), .CT_2(demultiplexer_1_out14),
    .CT_1(demultiplexer_1_out15));
  VID_MEM vid_mem_5 (
    .DATA_IN(vid_mem_4_data_out), .Clock(vid_mem_4_clock_out), .Clear(vid_mem_4_clear_out), .out_8(OUT_5),
    .DATA_OUT(vid_mem_5_data_out), .Clock_Out(vid_mem_5_clock_out), .Clear_Out(vid_mem_5_clear_out),
    .CT_4(demultiplexer_1_out16), .CT_3(demultiplexer_1_out17), .CT_2(demultiplexer_1_out18),
    .CT_1(demultiplexer_1_out19));
  VID_MEM vid_mem_6 (
    .DATA_IN(vid_mem_5_data_out), .Clock(vid_mem_5_clock_out), .Clear(vid_mem_5_clear_out), .out_8(OUT_6),
    .DATA_OUT(vid_mem_6_data_out), .Clock_Out(vid_mem_6_clock_out), .Clear_Out(vid_mem_6_clear_out),
    .CT_4(demultiplexer_1_out20), .CT_3(demultiplexer_1_out21), .CT_2(demultiplexer_1_out22),
    .CT_1(demultiplexer_1_out23));
  VID_MEM vid_mem_7 (
    .DATA_IN(vid_mem_6_data_out), .Clock(vid_mem_6_clock_out), .Clear(vid_mem_6_clear_out), .out_8(OUT_7),
    .DATA_OUT(vid_mem_7_data_out), .Clock_Out(vid_mem_7_clock_out), .Clear_Out(vid_mem_7_clear_out),
    .CT_4(demultiplexer_1_out24), .CT_3(demultiplexer_1_out25), .CT_2(demultiplexer_1_out26),
    .CT_1(demultiplexer_1_out27));
  VID_MEM vid_mem_8 (
    .DATA_IN(vid_mem_7_data_out), .Clock(vid_mem_7_clock_out), .Clear(vid_mem_7_clear_out), .out_8(OUT_8),
    .DATA_OUT(DATA_2), .Clock_Out(Clock_Out), .Clear_Out(Clear_2), .CT_4(demultiplexer_1_out28),
    .CT_3(demultiplexer_1_out29), .CT_2(demultiplexer_1_out30), .CT_1(demultiplexer_1_out31));

  // Notes on the sheet:
  //   Clock_In: pull=down
  //   DATA: pull=down
  //   ENABLE: pull=down
  //   ADDRESS: pull=down
  //   Clear: pull=down
endmodule

module LED_MATRIX_CTRL (
  input  [7:0] DATA_IN,
  input  CLEAR,
  input  Select,
  input  Clock_IN,
  input  [7:0] ADDRESS_IN,
  output [31:0] out_6,
  output [31:0] out_7,
  output [31:0] out_8,
  output [31:0] out_9,
  output [31:0] out_10,
  output [31:0] out_11,
  output [31:0] out_12,
  output [31:0] out_13,
  output [31:0] out_14,
  output [31:0] out_15,
  output [31:0] out_16,
  output [31:0] out_17,
  output [31:0] out_18,
  output [31:0] out_19,
  output [31:0] out_20,
  output [31:0] out_21,
  output [31:0] out_22,
  output [31:0] out_23,
  output [31:0] out_24,
  output [31:0] out_25,
  output [31:0] out_26,
  output [31:0] out_27,
  output [31:0] out_28,
  output [31:0] out_29,
  output [31:0] out_30,
  output [31:0] out_31,
  output [31:0] out_32,
  output [31:0] out_33,
  output [31:0] out_34,
  output [31:0] out_35,
  output [31:0] out_36,
  output [31:0] out_37
);

  wire demultiplexer_1_out0, demultiplexer_1_out1, demultiplexer_1_out2, demultiplexer_1_out3,
       vid_mem_32_1_clear_2, vid_mem_32_1_clock_out, vid_mem_32_2_clear_2, vid_mem_32_2_clock_out,
       vid_mem_32_3_clear_2, vid_mem_32_3_clock_out;
  wire [7:0] vid_mem_32_1_data_2, vid_mem_32_2_data_2, vid_mem_32_3_data_2;

  Demultiplexer #(.select(3)) demultiplexer_1 (
    .out0(demultiplexer_1_out0), .out1(demultiplexer_1_out1), .out2(demultiplexer_1_out2),
    .out3(demultiplexer_1_out3), .in(Select), .sel(ADDRESS_IN[7:5]));  // open: out4, out5, out6, out7, en
  VID_MEM_32 vid_mem_32_1 (
    .DATA(DATA_IN), .OUT_1(out_6), .Clock_In(Clock_IN), .Clear(CLEAR), .OUT_2(out_7), .OUT_3(out_8),
    .ADDRESS(ADDRESS_IN), .ENABLE(demultiplexer_1_out0), .OUT_4(out_9), .OUT_5(out_10), .OUT_6(out_11),
    .OUT_7(out_12), .DATA_2(vid_mem_32_1_data_2), .OUT_8(out_13), .Clear_2(vid_mem_32_1_clear_2),
    .Clock_Out(vid_mem_32_1_clock_out));
  VID_MEM_32 vid_mem_32_2 (
    .DATA(vid_mem_32_1_data_2), .OUT_1(out_14), .Clock_In(vid_mem_32_1_clock_out),
    .Clear(vid_mem_32_1_clear_2), .OUT_2(out_15), .OUT_3(out_16), .ADDRESS(ADDRESS_IN),
    .ENABLE(demultiplexer_1_out1), .OUT_4(out_17), .OUT_5(out_18), .OUT_6(out_19), .OUT_7(out_20),
    .DATA_2(vid_mem_32_2_data_2), .OUT_8(out_21), .Clear_2(vid_mem_32_2_clear_2),
    .Clock_Out(vid_mem_32_2_clock_out));
  VID_MEM_32 vid_mem_32_3 (
    .DATA(vid_mem_32_2_data_2), .OUT_1(out_22), .Clock_In(vid_mem_32_2_clock_out),
    .Clear(vid_mem_32_2_clear_2), .OUT_2(out_23), .OUT_3(out_24), .ADDRESS(ADDRESS_IN),
    .ENABLE(demultiplexer_1_out2), .OUT_4(out_25), .OUT_5(out_26), .OUT_6(out_27), .OUT_7(out_28),
    .DATA_2(vid_mem_32_3_data_2), .OUT_8(out_29), .Clear_2(vid_mem_32_3_clear_2),
    .Clock_Out(vid_mem_32_3_clock_out));
  VID_MEM_32 vid_mem_32_4 (
    .DATA(vid_mem_32_3_data_2), .OUT_1(out_30), .Clock_In(vid_mem_32_3_clock_out),
    .Clear(vid_mem_32_3_clear_2), .OUT_2(out_31), .OUT_3(out_32), .ADDRESS(ADDRESS_IN),
    .ENABLE(demultiplexer_1_out3), .OUT_4(out_33), .OUT_5(out_34), .OUT_6(out_35), .OUT_7(out_36),
    .OUT_8(out_37));  // open: DATA_2, Clear_2, Clock_Out

  // Notes on the sheet:
  //   ADDRESS_IN: pull=down
  //   CLEAR: pull=down
  //   Select: pull=down
  //   Clock_IN: pull=down
  //   DATA_IN: pull=down
endmodule
